// Digital circuit traficDiodeInv.dig as structural Verilog
// simple red-yellow-green traffic light with wired and
module traficDiodeInv (
  input  clk
);

  wire _7476_1__1nq, _7476_1__1q, _7476_1__2nq, _7476_1__2q, diodeforward_1_out;

  _7476 _7476_1 (
    ._1J(1'b1), ._1Q(_7476_1__1q), ._1nQ(_7476_1__1nq), ._1nCLK(clk), ._1K(1'b1), ._1nC(1'b1), ._1nS(1'b1),
    ._2J(_7476_1__1q), ._2Q(_7476_1__2q), ._2nQ(_7476_1__2nq), ._2nCLK(clk), ._2K(_7476_1__1q), ._2nC(1'b1),
    ._2nS(1'b1), .VCC(1'b1), .GND(1'b0));
  DiodeForward diodeforward_1 (.in(_7476_1__1q), .out(diodeforward_1_out));
  DiodeForward diodeforward_2 (.in(_7476_1__2nq), .out(diodeforward_1_out));
  LightBulb lightbulb_1 (.A(_7476_1__2q), .B(1'b1));
  LightBulb lightbulb_2 (.A(_7476_1__1nq), .B(1'b1));
  LightBulb lightbulb_3 (.A(diodeforward_1_out), .B(1'b1));
  PullDown pulldown_1 (.out(diodeforward_1_out));
endmodule
