// Digital circuit sram_simple.dig as structural Verilog
module sram_simple (
  input  WL1,
  input  WE,
  input  Data,
  input  WL0,
  output D
);

  wire nfet_1_d, nfet_1_s, nfet_2_s, nfet_3_s, nfet_4_s, nfet_5_s, nfet_7_s, pfet_1_d, pfet_2_d,
       pullup_1_out, pullup_2_out, pullup_3_out, pullup_4_out, undriven;

  NFET nfet_1 (.G(WL0), .D(nfet_1_d), .S(nfet_1_s));
  NFET nfet_2 (.G(WL1), .D(nfet_1_d), .S(nfet_2_s));
  assign nfet_1_d = WE ? undriven : 1'bz;  // Driver driver_1
  // Not not_1 has open pins: in=Data, out=open
  PullUp pullup_1 (.out(pullup_1_out));
  PFET pfet_1 (.G(nfet_1_s), .S(pullup_1_out), .D(pfet_1_d));
  NFET nfet_3 (.G(nfet_1_s), .D(pfet_1_d), .S(nfet_3_s));
  PullDown pulldown_1 (.out(nfet_3_s));
  PullUp pullup_2 (.out(pullup_2_out));
  PFET pfet_2 (.G(nfet_2_s), .S(pullup_2_out), .D(pfet_2_d));
  NFET nfet_4 (.G(nfet_2_s), .D(pfet_2_d), .S(nfet_4_s));
  PullDown pulldown_2 (.out(nfet_4_s));
  PullUp pullup_3 (.out(pullup_3_out));
  LED led_1 (.in(pfet_1_d));
  PFET pfet_3 (.G(pfet_1_d), .S(pullup_3_out), .D(nfet_1_s));
  NFET nfet_5 (.G(pfet_1_d), .D(nfet_1_s), .S(nfet_5_s));
  NFET nfet_6 (.G(WL0), .D(pfet_1_d), .S(D));
  PullDown pulldown_3 (.out(nfet_5_s));
  PullUp pullup_4 (.out(pullup_4_out));
  LED led_2 (.in(pfet_2_d));
  PFET pfet_4 (.G(pfet_2_d), .S(pullup_4_out), .D(nfet_2_s));
  NFET nfet_7 (.G(pfet_2_d), .D(nfet_2_s), .S(nfet_7_s));
  NFET nfet_8 (.G(WL1), .D(pfet_2_d), .S(D));
  PullDown pulldown_4 (.out(nfet_7_s));
  assign D = WE ? Data : 1'bz;  // Driver driver_2

  // Notes on the sheet:
  //   WL1: row line 1
  //   {{de Wortleitung 1}}
  //   WE: Write Enable
  //   {{de Schreibfreigabe}}
  //   Data: Data Input {{de Dateneingang}}
  //   D: Data Output {{de Datenausgang}}
  //   WL0: row line 0
  //   {{de Wortleitung 0}}
endmodule

/* Test case:
WL1 WL0 WE Data D
# write both cells to one
 1   0  1   1   1
 0   1  1   1   1

# check both are one
 1   0  0   0   1
 0   1  0   0   1

# write cell 0 to zero
 1   0  1   0   0

# check
 1   0  0   0   0
 0   1  0   0   1

# write cell 1 to zero
 0   1  1   0   0

# check
 1   0  0   0   0
 0   1  0   0   0

# if no word line is high, output is in high Z state
 0   0  0   x   z
*/
