// Digital circuit Comp.dig as structural Verilog
// Simple comparator, which compares two bits.
// {{de Einfacher Vergleicher, welcher zwei Bits 
// miteinander vergleicht.}}
module Comp (
  input  P,
  input  Q,
  output P_lt_Q,
  output P_eq_Q,
  output P_gt_Q
);

  wire undriven, undriven_2;

  // Not not_1 has open pins: in=P, out=open
  // Not not_2 has open pins: in=Q, out=open
  // And and_1 has open pins: In_1=undriven, In_2=Q, out=open
  // And and_2 has open pins: In_1=P, In_2=undriven_2, out=open
  // NOr nor_1 has open pins: In_1=P_lt_Q, In_2=P_gt_Q, out=open

  // Notes on the sheet:
  //   P: First bit to compare.
  //   {{de Erstes zu vergleichendes Bit.}}
  //   Q: Second bit to compare.
  //   {{de Zweites zu vergleichendes Bit.}}
  //   P_lt_Q: This output is one if P<Q is true.
  //   {{de Das Bit ist Eins, wenn P<Q gilt.}}
  //   P_eq_Q: This output is one if P=Q is true.
  //   {{de Das Bit ist Eins, wenn P=Q gilt.}}
  //   P_gt_Q: This output is one if P>Q is true.
  //   {{de Das Bit ist Eins, wenn P>Q gilt.}}
endmodule

/* Test case:
P Q P<Q P=Q P>Q
0 0  0   1   0
0 1  1   0   0
1 0  0   0   1
1 1  0   1   0
*/
