// Digital circuit CompEN.dig as structural Verilog
// Compares two bits. Has an additional enable input.
// {{de Vergleicht zwei Bit miteinander. Besitzt einen 
// zusätzlichen Enable Eingang.}}
module CompEN (
  input  EN,
  input  P,
  input  Q,
  output P_lt_Q,
  output P_eq_Q,
  output P_gt_Q
);

  wire comp_1_p_eq_q, undriven, undriven_2;

  // And and_1 has open pins: In_1=P, In_2=EN, out=open
  // And and_2 has open pins: In_1=EN, In_2=Q, out=open
  Comp comp_1 (.P(undriven), .Q(undriven_2), .P_lt_Q(P_lt_Q), .P_eq_Q(comp_1_p_eq_q), .P_gt_Q(P_gt_Q));
  // And and_3 has open pins: In_1=comp_1_p_eq_q, In_2=EN, out=open

  // Notes on the sheet:
  //   P_lt_Q: Is set to one if P<Q is valid.
  //   {{de Das Bit ist Eins, wenn P<Q gilt.}}
  //   P_eq_Q: Is set to one if P=Q is valid.
  //   {{de Das Bit ist Eins, wenn P=Q gilt.}}
  //   P_gt_Q: Is set to one if P>Q is valid.
  //   {{de Das Bit ist Eins, wenn P>Q gilt.}}
  //   EN: Enable input. If this input goes to zero, all three output 
  //   bits are also zero. If this input is one, the comparator 
  //   has its normal function.
  //   {{de Enable Eingang. Geht dieser Eingang auf Null, sind 
  //   alle drei Ausgangsbit auch Null. Ist dieser Eingang 
  //   auf Eins, hat der Komparator seine normale 
  //   Funktion.}}
  //   P: First bit to compare.
  //   {{de Erstes zu vergleichendes Bit.}}
  //   Q: Second bit to compare.
  //   {{de Zweites zu vergleichendes Bit.}}
endmodule

/* Test case:
EN P Q P<Q P=Q P>Q
1  0 0  0   1   0
1  0 1  1   0   0
1  1 0  0   0   1
1  1 1  0   1   0
0  0 0  0   0   0
0  0 1  0   0   0
0  1 0  0   0   0
0  1 1  0   0   0
*/
