// Digital circuit FullAddSub_RC.dig as structural Verilog
module FullAddSub_RC (
  input  A_0,
  input  B_0,
  input  A_1,
  input  B_1,
  input  A_2,
  input  B_2,
  input  A_3,
  input  B_3,
  input  S,
  output S_0,
  output S_1,
  output S_2,
  output S_3
);

  wire fulladder_2_c_i, fulladder_3_c_i, fulladder_4_c_i, undriven, undriven_2, undriven_3, undriven_4;

  // XOr xor_1 has open pins: In_1=B_3, In_2=S, out=open
  // XOr xor_2 has open pins: In_1=B_2, In_2=S, out=open
  // XOr xor_3 has open pins: In_1=B_1, In_2=S, out=open
  // XOr xor_4 has open pins: In_1=B_0, In_2=S, out=open
  FullAdder fulladder_1 (.A_i(A_3), .B_i(undriven), .C_i_1(fulladder_2_c_i), .S_i(S_3));  // open: C_i
  FullAdder fulladder_2 (.A_i(A_2), .B_i(undriven_2), .C_i_1(fulladder_3_c_i), .C_i(fulladder_2_c_i), .S_i(S_2));
  FullAdder fulladder_3 (.A_i(A_1), .B_i(undriven_3), .C_i_1(fulladder_4_c_i), .C_i(fulladder_3_c_i), .S_i(S_1));
  FullAdder fulladder_4 (.A_i(A_0), .B_i(undriven_4), .C_i_1(S), .C_i(fulladder_4_c_i), .S_i(S_0));

  // Notes on the sheet:
  //   S: Input with which you can toggle between 
  //   addition (S = 0) and subtraction (S = 1).
  //   {{de Eingang mit welchem zwischen Addition (S=0) und 
  //   Subtraktion (S=1) umgeschaltet werden kann.}}
endmodule

/* Test case:
            S   A_3 A_2 A_1 A_0  B_3 B_2 B_1 B_0  S_3 S_2 S_1 S_0
repeat(256) 0   bits(4,n>>4)     bits(4,n)        bits(4,(n>>4)+(n&15))
repeat(256) 1   bits(4,n>>4)     bits(4,n)        bits(4,(n>>4)-(n&15))
*/
