// Digital circuit FullAdder.dig as structural Verilog
module FullAdder (
  input  A_i,
  input  B_i,
  input  C_i_1,
  output C_i,
  output S_i
);

  wire undriven, undriven_2, undriven_3;

  // And and_1 has open pins: In_1=A_i, In_2=B_i, out=open
  // XOr xor_1 has open pins: In_1=A_i, In_2=B_i, out=open
  // And and_2 has open pins: In_1=undriven_2, In_2=C_i_1, out=open
  // XOr xor_2 has open pins: In_1=undriven_2, In_2=C_i_1, out=open
  // Or or_1 has open pins: In_1=undriven, In_2=undriven_3, out=open

  // Notes on the sheet:
  //   A_i: first bit to add
  //   {{de Erstes zu addierendes Bit.}}
  //   B_i: second bit to add
  //   {{de Zweites zu addierendes Bit.}}
  //   C_i_1: carry in
  //   {{de Übertragsbit der Vorgängerschaltung.}}
  //   C_i: carry bit
  //   {{de Übertragsbit}}
  //   S_i: sum {{de Summe}}
endmodule

/* Test case:
  A_i B_i C_{i-1} C_i S_i

loop (A,2)
  loop (B,2)
    loop (Ci,2)
 (A) (B) (Ci)   bits(2, A+B+Ci)
    end loop
  end loop
end loop
*/
