// Digital circuit FullAdderCLA.dig as structural Verilog
// An adder implemented according to the carry-look-ahead method.
// {{de Ein Addierer der nach dem carry-look-ahead 
// Verfahren implementiert ist.}}
module FullAdderCLA (
  input  C_i_1,
  input  A_0,
  input  A_1,
  input  A_2,
  input  A_3,
  input  B_0,
  input  B_1,
  input  B_2,
  input  B_3,
  output S_0,
  output S_1,
  output S_2,
  output S_3,
  output C_i
);

  wire undriven, undriven_2, undriven_3, undriven_4, undriven_5, undriven_6, undriven_7, undriven_8,
       undriven_9, undriven_10, undriven_11, undriven_12, undriven_13, undriven_14, undriven_15, undriven_16,
       undriven_17, undriven_18, undriven_19, undriven_20, undriven_21, undriven_22, undriven_23,
       undriven_24, undriven_25;

  // Or or_1 has open pins: In_1=A_3, In_2=B_3, out=open
  // And and_1 has open pins: In_1=A_3, In_2=B_3, out=open
  // Or or_2 has open pins: In_1=A_2, In_2=B_2, out=open
  // And and_2 has open pins: In_1=A_2, In_2=B_2, out=open
  // Or or_3 has open pins: In_1=A_1, In_2=B_1, out=open
  // And and_3 has open pins: In_1=A_1, In_2=B_1, out=open
  // Or or_4 has open pins: In_1=A_0, In_2=B_0, out=open
  // And and_4 has open pins: In_1=A_0, In_2=B_0, out=open
  // And and_5 has open pins: In_1=C_i_1, In_2=undriven_7, In_3=undriven_5, In_4=undriven_3, In_5=undriven, out=open
  // And and_6 has open pins: In_1=undriven_6, In_2=undriven, In_3=undriven_3, In_4=undriven_5, out=open
  // And and_7 has open pins: In_1=undriven_4, In_2=undriven_3, In_3=undriven, out=open
  // And and_8 has open pins: In_1=undriven, In_2=undriven_2, out=open
  // XOr xor_1 has open pins: In_1=undriven, In_2=undriven_22, out=open
  // And and_9 has open pins: In_1=C_i_1, In_2=undriven_7, In_3=undriven_5, In_4=undriven_3, out=open
  // And and_10 has open pins: In_1=undriven_5, In_2=undriven_3, In_3=undriven_6, out=open
  // And and_11 has open pins: In_1=undriven_3, In_2=undriven_4, out=open
  // XOr xor_2 has open pins: In_1=undriven_3, In_2=undriven_2, out=open
  // And and_12 has open pins: In_1=C_i_1, In_2=undriven_7, In_3=undriven_5, out=open
  // And and_13 has open pins: In_1=undriven_5, In_2=undriven_6, out=open
  // XOr xor_3 has open pins: In_1=undriven_5, In_2=undriven_4, out=open
  // And and_14 has open pins: In_1=undriven_7, In_2=C_i_1, out=open
  // XOr xor_4 has open pins: In_1=undriven_7, In_2=undriven_6, out=open
  // Or or_5 has open pins: In_1=undriven_10, In_2=undriven_6, out=open
  // Or or_6 has open pins: In_1=undriven_21, In_2=undriven_20, In_3=undriven_19, In_4=undriven_18, In_5=undriven_22, out=open
  // Or or_7 has open pins: In_1=undriven_16, In_2=undriven_15, In_3=undriven_14, In_4=undriven_2, out=open
  // Or or_8 has open pins: In_1=undriven_12, In_2=undriven_8, In_3=undriven_4, out=open
  // XOr xor_5 has open pins: In_1=undriven_17, In_2=undriven_25, out=open
  // XOr xor_6 has open pins: In_1=undriven_13, In_2=undriven_24, out=open
  // XOr xor_7 has open pins: In_1=undriven_9, In_2=undriven_23, out=open
  // XOr xor_8 has open pins: In_1=undriven_11, In_2=C_i_1, out=open

  // Notes on the sheet:
  //   C_i_1: The carry of adding the low order bits. If the 
  //   least significant bits are added, this input is zero.
  //   {{de Der Übetrag vom Addierer welcher die 
  //   niederwertigeren Bits addiert. Werden die 
  //   niederwertigsten Bits addiert, ist dieser Eingang 
  //   Null.}}
  //   A_0: The 0. bit of the first value to add.
  //   {{de Das 0. Bit des ersten zu addierenden Wertes.}}
  //   A_1: The 1. bit of the first value to add.
  //   {{de Das 1. Bit des ersten zu addierenden Wertes.}}
  //   S_0: The 0. bit of the sum.
  //   {{de Das 0. Bit der Summe.}}
  //   A_2: The 2. bit of the first value to add.
  //   {{de Das 2. Bit des ersten zu addierenden Wertes.}}
  //   A_3: The 3. bit of the first value to add.
  //   {{de Das 3. Bit des ersten zu addierenden 
  //   Wertes.}}
  //   S_1: The 1. bit of the sum.
  //   {{de Das 1. Bit der Summe.}}
  //   S_2: The 2. bit of the sum.
  //   {{de Das 2. Bit der Summe.}}
  //   B_0: The 0. bit of the second value to add.
  //   {{de Das 0. Bit des zweiten zu addierenden Wertes.}}
  //   B_1: The 1. bit of the second value to add.
  //   {{de Das 1. Bit des zweiten zu addierenden Wertes.}}
  //   B_2: The 2. bit of the second value to add.
  //   {{de Das 2. Bit des zweiten zu addierenden Wertes.}}
  //   B_3: The 3. bit of the second value to add.
  //   {{de Das 3. Bit des zweiten zu addierenden Wertes.}}
  //   S_3: The 3. bit of the sum.
  //   {{de Das 3. Bit der Summe.}}
  //   C_i: The carry bit, which is passed to the adiator for the 
  //   next most significant bits.
  //   {{de Das Übertragsbit, welches an den Adiierer für die
  //   nächst höherwertigen Bits weitergegeben wird.}}
endmodule

/* Test case:
# A complete test of all 512 possible additions
#
# All created test vectors are shown in the result table.

C_i-1  A_3 A_2 A_1 A_0  B_3 B_2 B_1 B_0  C_i S_3 S_2 S_1 S_0

loop(a,16)
 loop(b,16)
  0    bits(4,a)        bits(4,b)        bits(5,a+b)
  1    bits(4,a)        bits(4,b)        bits(5,a+b+1)
 end loop
end loop
*/
