// Digital circuit FullAdderRCSig.dig as structural Verilog
// 4-bit ripple carry adder, consisting of four full adders.
// {{de 4-Bit Ripple-Carry addierer bestehend aus vier 
// Volladdierern.}}
module FullAdderRCSig (
  input  C__1,
  input  A_0,
  input  B_0,
  input  A_1,
  input  B_1,
  input  A_2,
  input  B_2,
  input  A_3,
  input  B_3,
  output S_0,
  output S_1,
  output S_2,
  output C_3,
  output S_3
);

  wire undriven, undriven_2, undriven_3, undriven_4, undriven_5, undriven_6, undriven_7, undriven_8,
       undriven_9, undriven_10, undriven_11, undriven_12, undriven_13, undriven_14, undriven_15;

  // And and_1 has open pins: In_1=A_3, In_2=B_3, out=open
  // XOr xor_1 has open pins: In_1=A_3, In_2=B_3, out=open
  // And and_2 has open pins: In_1=A_2, In_2=B_2, out=open
  // XOr xor_2 has open pins: In_1=A_2, In_2=B_2, out=open
  // And and_3 has open pins: In_1=A_1, In_2=B_1, out=open
  // XOr xor_3 has open pins: In_1=A_1, In_2=B_1, out=open
  // And and_4 has open pins: In_1=A_0, In_2=B_0, out=open
  // XOr xor_4 has open pins: In_1=A_0, In_2=B_0, out=open
  // And and_5 has open pins: In_1=undriven_11, In_2=undriven_15, out=open
  // XOr xor_5 has open pins: In_1=undriven_11, In_2=undriven_15, out=open
  // And and_6 has open pins: In_1=undriven_9, In_2=undriven_14, out=open
  // XOr xor_6 has open pins: In_1=undriven_9, In_2=undriven_14, out=open
  // And and_7 has open pins: In_1=undriven_5, In_2=undriven_13, out=open
  // XOr xor_7 has open pins: In_1=undriven_5, In_2=undriven_13, out=open
  // And and_8 has open pins: In_1=undriven_7, In_2=C__1, out=open
  // XOr xor_8 has open pins: In_1=undriven_7, In_2=C__1, out=open
  // Or or_1 has open pins: In_1=undriven_12, In_2=undriven_4, out=open
  // Or or_2 has open pins: In_1=undriven_10, In_2=undriven_3, out=open
  // Or or_3 has open pins: In_1=undriven_8, In_2=undriven, out=open
  // Or or_4 has open pins: In_1=undriven_6, In_2=undriven_2, out=open

  // Notes on the sheet:
  //   A_0: default 1
  //   B_1: default 1
  //   A_2: default 1
  //   B_3: default 1
endmodule

/* Test case:
# complete test of all 512 possible additions
C_-1 A_3 A_2 A_1 A_0 B_3 B_2 B_1 B_0 C_3 S_3 S_2 S_1 S_0
repeat(256) 0 bits(4,n>>4) bits(4,n) bits(5,(n>>4)+(n&15))
repeat(256) 1 bits(4,n>>4) bits(4,n) bits(5,(n>>4)+(n&15)+1)
*/
