// Digital circuit FullAdderRC_CLA.dig as structural Verilog
// Example to compare RC and CLA adders.
// {{de Beispiel um RC- und CLA-Addierer zu vergleichen.}}
module FullAdderRC_CLA (
  input  C0,
  input  A0,
  input  B0,
  input  A1,
  input  B1,
  input  A2,
  input  B2,
  input  A3,
  input  B3,
  input  A0_2,
  input  B0_2,
  input  C0_2,
  input  A1_2,
  input  B1_2,
  input  A2_2,
  input  B2_2,
  input  A3_2,
  input  B3_2,
  output S0,
  output S1,
  output S2,
  output C3,
  output S3,
  output S0_2,
  output S1_2,
  output S2_2,
  output S3_2,
  output C3_2
);

  wire undriven, undriven_2, undriven_3, undriven_4, undriven_5, undriven_6, undriven_7, undriven_8,
       undriven_9, undriven_10, undriven_11, undriven_12, undriven_13, undriven_14, undriven_15, undriven_16,
       undriven_17, undriven_18, undriven_19, undriven_20, undriven_21, undriven_22, undriven_23,
       undriven_24, undriven_25, undriven_26, undriven_27, undriven_28, undriven_29, undriven_30,
       undriven_31, undriven_32, undriven_33, undriven_34, undriven_35, undriven_36, undriven_37,
       undriven_38, undriven_39, undriven_40;

  // And and_1 has open pins: In_1=A3, In_2=B3, out=open
  // XOr xor_1 has open pins: In_1=A3, In_2=B3, out=open
  // And and_2 has open pins: In_1=A2, In_2=B2, out=open
  // XOr xor_2 has open pins: In_1=A2, In_2=B2, out=open
  // And and_3 has open pins: In_1=A1, In_2=B1, out=open
  // XOr xor_3 has open pins: In_1=A1, In_2=B1, out=open
  // And and_4 has open pins: In_1=A0, In_2=B0, out=open
  // XOr xor_4 has open pins: In_1=A0, In_2=B0, out=open
  // And and_5 has open pins: In_1=undriven_36, In_2=undriven_40, out=open
  // XOr xor_5 has open pins: In_1=undriven_36, In_2=undriven_40, out=open
  // And and_6 has open pins: In_1=undriven_34, In_2=undriven_39, out=open
  // XOr xor_6 has open pins: In_1=undriven_34, In_2=undriven_39, out=open
  // And and_7 has open pins: In_1=undriven_30, In_2=undriven_38, out=open
  // XOr xor_7 has open pins: In_1=undriven_30, In_2=undriven_38, out=open
  // And and_8 has open pins: In_1=undriven_32, In_2=C0, out=open
  // XOr xor_8 has open pins: In_1=undriven_32, In_2=C0, out=open
  // Or or_1 has open pins: In_1=undriven_37, In_2=undriven_4, out=open
  // Or or_2 has open pins: In_1=undriven_35, In_2=undriven_3, out=open
  // Or or_3 has open pins: In_1=undriven_33, In_2=undriven, out=open
  // Or or_4 has open pins: In_1=undriven_31, In_2=undriven_2, out=open
  // Or or_5 has open pins: In_1=A3_2, In_2=B3_2, out=open
  // And and_9 has open pins: In_1=A3_2, In_2=B3_2, out=open
  // Or or_6 has open pins: In_1=A2_2, In_2=B2_2, out=open
  // And and_10 has open pins: In_1=A2_2, In_2=B2_2, out=open
  // Or or_7 has open pins: In_1=A1_2, In_2=B1_2, out=open
  // And and_11 has open pins: In_1=A1_2, In_2=B1_2, out=open
  // Or or_8 has open pins: In_1=A0_2, In_2=B0_2, out=open
  // And and_12 has open pins: In_1=A0_2, In_2=B0_2, out=open
  // And and_13 has open pins: In_1=C0_2, In_2=undriven_9, In_3=undriven_7, In_4=undriven_6, In_5=undriven_5, out=open
  // And and_14 has open pins: In_1=undriven_8, In_2=undriven_5, In_3=undriven_6, In_4=undriven_7, out=open
  // And and_15 has open pins: In_1=undriven_24, In_2=undriven_6, In_3=undriven_5, out=open
  // And and_16 has open pins: In_1=undriven_5, In_2=undriven_25, out=open
  // XOr xor_9 has open pins: In_1=undriven_5, In_2=undriven_26, out=open
  // And and_17 has open pins: In_1=C0_2, In_2=undriven_9, In_3=undriven_7, In_4=undriven_6, out=open
  // And and_18 has open pins: In_1=undriven_7, In_2=undriven_6, In_3=undriven_8, out=open
  // And and_19 has open pins: In_1=undriven_6, In_2=undriven_24, out=open
  // XOr xor_10 has open pins: In_1=undriven_6, In_2=undriven_25, out=open
  // And and_20 has open pins: In_1=C0_2, In_2=undriven_9, In_3=undriven_7, out=open
  // And and_21 has open pins: In_1=undriven_7, In_2=undriven_8, out=open
  // XOr xor_11 has open pins: In_1=undriven_7, In_2=undriven_24, out=open
  // And and_22 has open pins: In_1=undriven_9, In_2=C0_2, out=open
  // XOr xor_12 has open pins: In_1=undriven_9, In_2=undriven_8, out=open
  // Or or_9 has open pins: In_1=undriven_23, In_2=undriven_22, In_3=undriven_21, In_4=undriven_20, In_5=undriven_26, out=open
  // Or or_10 has open pins: In_1=undriven_18, In_2=undriven_17, In_3=undriven_16, In_4=undriven_25, out=open
  // Or or_11 has open pins: In_1=undriven_14, In_2=undriven_10, In_3=undriven_24, out=open
  // Or or_12 has open pins: In_1=undriven_12, In_2=undriven_8, out=open
  // XOr xor_13 has open pins: In_1=undriven_15, In_2=undriven_28, out=open
  // XOr xor_14 has open pins: In_1=undriven_11, In_2=undriven_27, out=open
  // XOr xor_15 has open pins: In_1=undriven_13, In_2=C0_2, out=open
  // XOr xor_16 has open pins: In_1=undriven_19, In_2=undriven_29, out=open

  // Notes on the sheet:
  //   A0: default 1
  //   B1: default 1
  //   B2: default 1
  //   A3: default 1
  //   A0_2: default 1
  //   B1_2: default 1
  //   B2_2: default 1
  //   A3_2: default 1
endmodule
