// Digital circuit FullSub2.dig as structural Verilog
module FullSub2 (
  input  A_i,
  input  B_i,
  input  BO_i_1,
  output S_i,
  output BO_i
);

  wire halfsub_1_bo, halfsub_1_s, halfsub_2_bo;

  HalfSub halfsub_1 (.A(A_i), .B(B_i), .S(halfsub_1_s), .BO(halfsub_1_bo));
  HalfSub halfsub_2 (.A(halfsub_1_s), .B(BO_i_1), .S(S_i), .BO(halfsub_2_bo));
  // Or or_1 has open pins: In_1=halfsub_2_bo, In_2=halfsub_1_bo, out=open
endmodule

/* Test case:
A_i B_i BO_i-1  BO_i S_i
 0   0   0        0   0
 0   0   1        1   1
 0   1   0        1   1
 0   1   1        1   0
 1   0   0        0   1
 1   0   1        0   0
 1   1   0        0   0
 1   1   1        1   1
*/
