// Digital circuit FullSubNaive.dig as structural Verilog
module FullSubNaive (
  input  A_i,
  input  B_i,
  input  BO_i_1,
  output S_i,
  output BO_i
);

  wire undriven, undriven_2, undriven_3, undriven_4, undriven_5, undriven_6, undriven_7, undriven_8,
       undriven_9, undriven_10;

  // Not not_1 has open pins: in=A_i, out=open
  // Not not_2 has open pins: in=B_i, out=open
  // Not not_3 has open pins: in=BO_i_1, out=open
  // And and_1 has open pins: In_1=undriven, In_2=undriven_2, In_3=BO_i_1, out=open
  // And and_2 has open pins: In_1=undriven, In_2=B_i, In_3=undriven_3, out=open
  // And and_3 has open pins: In_1=A_i, In_2=undriven_2, In_3=undriven_3, out=open
  // And and_4 has open pins: In_1=A_i, In_2=B_i, In_3=BO_i_1, out=open
  // And and_5 has open pins: In_1=undriven, In_2=BO_i_1, out=open
  // And and_6 has open pins: In_1=undriven, In_2=B_i, out=open
  // And and_7 has open pins: In_1=B_i, In_2=BO_i_1, out=open
  // Or or_1 has open pins: In_1=undriven_4, In_2=undriven_5, In_3=undriven_8, In_4=undriven_10, out=open
  // Or or_2 has open pins: In_1=undriven_6, In_2=undriven_7, In_3=undriven_9, out=open
endmodule

/* Test case:
A_i B_i BO_i-1  BO_i S_i
 0   0   0        0   0
 0   0   1        1   1
 0   1   0        1   1
 0   1   1        1   0
 1   0   0        0   1
 1   0   1        0   0
 1   1   0        0   0
 1   1   1        1   1
*/
