// Digital circuit HalfAdder.dig as structural Verilog
module HalfAdder (
  input  A,
  input  B,
  output S,
  output C
);

  // XOr xor_1 has open pins: In_1=A, In_2=B, out=open
  // And and_1 has open pins: In_1=A, In_2=B, out=open
endmodule

/* Test case:
A B C S
0 0 0 0
0 1 0 1
1 0 0 1
1 1 1 0
*/
