// Digital circuit Multiply.dig as structural Verilog
// Simple 4-bit multiplier built from three 4-bit adders. 
// The actual 1-bit multiplications are implemented by the AND gates.
// {{de Einfacher 4-Bit Multiplikator aufgebaut aus drei 4-Bit
// Addierern. Die eigentlichen 1-Bit Multiplikationen 
// werden durch die Und-Gatter implementiert.}}
module Multiply (
  input  P_0,
  input  P_1,
  input  P_2,
  input  P_3,
  input  Q_0,
  input  Q_1,
  input  Q_2,
  input  Q_3,
  output S_0,
  output S_1,
  output S_2,
  output S_3,
  output S_4,
  output S_5,
  output S_6,
  output S_7
);

  wire fulladdercla_1_c_i, fulladdercla_1_s_1, fulladdercla_1_s_2, fulladdercla_1_s_3, fulladdercla_2_c_i,
       fulladdercla_2_s_1, fulladdercla_2_s_2, fulladdercla_2_s_3, undriven, undriven_2, undriven_3,
       undriven_4, undriven_5, undriven_6, undriven_7, undriven_8, undriven_9, undriven_10, undriven_11,
       undriven_12, undriven_13, undriven_14, undriven_15;

  // And and_1 has open pins: In_1=P_0, In_2=Q_0, out=open
  // And and_2 has open pins: In_1=P_0, In_2=Q_1, out=open
  // And and_3 has open pins: In_1=P_0, In_2=Q_2, out=open
  // And and_4 has open pins: In_1=P_0, In_2=Q_3, out=open
  // And and_5 has open pins: In_1=P_1, In_2=Q_0, out=open
  // And and_6 has open pins: In_1=P_1, In_2=Q_1, out=open
  // And and_7 has open pins: In_1=P_1, In_2=Q_2, out=open
  // And and_8 has open pins: In_1=P_1, In_2=Q_3, out=open
  // And and_9 has open pins: In_1=P_2, In_2=Q_0, out=open
  // And and_10 has open pins: In_1=P_2, In_2=Q_1, out=open
  // And and_11 has open pins: In_1=P_2, In_2=Q_2, out=open
  // And and_12 has open pins: In_1=P_2, In_2=Q_3, out=open
  // And and_13 has open pins: In_1=P_3, In_2=Q_0, out=open
  // And and_14 has open pins: In_1=P_3, In_2=Q_1, out=open
  // And and_15 has open pins: In_1=P_3, In_2=Q_2, out=open
  // And and_16 has open pins: In_1=P_3, In_2=Q_3, out=open
  FullAdderCLA fulladdercla_1 (
    .C_i_1(1'b0), .A_0(undriven), .A_1(undriven_2), .A_2(undriven_3), .A_3(1'b0), .B_0(undriven_4),
    .B_1(undriven_5), .B_2(undriven_6), .B_3(undriven_7), .S_0(S_1), .S_1(fulladdercla_1_s_1),
    .S_2(fulladdercla_1_s_2), .S_3(fulladdercla_1_s_3), .C_i(fulladdercla_1_c_i));
  FullAdderCLA fulladdercla_2 (
    .C_i_1(1'b0), .A_0(fulladdercla_1_s_1), .A_1(fulladdercla_1_s_2), .A_2(fulladdercla_1_s_3),
    .A_3(fulladdercla_1_c_i), .B_0(undriven_8), .B_1(undriven_9), .B_2(undriven_10), .B_3(undriven_11),
    .S_0(S_2), .S_1(fulladdercla_2_s_1), .S_2(fulladdercla_2_s_2), .S_3(fulladdercla_2_s_3),
    .C_i(fulladdercla_2_c_i));
  FullAdderCLA fulladdercla_3 (
    .C_i_1(1'b0), .A_0(fulladdercla_2_s_1), .A_1(fulladdercla_2_s_2), .A_2(fulladdercla_2_s_3),
    .A_3(fulladdercla_2_c_i), .B_0(undriven_12), .B_1(undriven_13), .B_2(undriven_14), .B_3(undriven_15),
    .S_0(S_3), .S_1(S_4), .S_2(S_5), .S_3(S_6), .C_i(S_7));

  // Notes on the sheet:
  //   P_0: First number to multiply.
  //   {{de Erste zu multiplizierende 4 Bit Zahl.}}
  //   Q_0: Second number to multiply.
  //   {{de Zweite zu multiplizierende 4 Bit Zahl.}}
  //   S_0: The result of the multiply operation.
  //   {{de Das 8-Bit Ergebnis der Multiplikation}}
endmodule

/* Test case:
  P_3 P_2 P_1 P_0   Q_3 Q_2 Q_1 Q_0   S_7 S_6 S_5 S_4 S_3 S_2 S_1 S_0
loop(P,16)
 loop(Q,16)
  bits(4,P)         bits(4,Q)         bits(8,P*Q)
 end loop
end loop
*/
