// Digital circuit Multiply16Bit.dig as structural Verilog
// O(ln n) 16 bit multiplyer
// {{de O(ln n) 16 Bit Multiplizierer}}
module Multiply16Bit (
  input  [15:0] A,
  input  [15:0] B,
  output [31:0] Y
);

  wire [15:0] bitextender_1_out, bitextender_2_out, bitextender_3_out, bitextender_4_out, bitextender_5_out,
       bitextender_6_out, bitextender_7_out, bitextender_8_out, bitextender_9_out, bitextender_10_out,
       bitextender_11_out, bitextender_12_out, bitextender_13_out, bitextender_14_out, bitextender_15_out,
       bitextender_16_out, undriven, undriven_2, undriven_3, undriven_4, undriven_5, undriven_6, undriven_7,
       undriven_8, undriven_9, undriven_10, undriven_11, undriven_12, undriven_13, undriven_14, undriven_15,
       undriven_16;
  wire [16:0] add_1_s, add_2_s, add_3_s, add_4_s, add_5_s, add_6_s, add_7_s, add_8_s;
  wire [17:17] add_1_c_o, add_3_c_o, add_5_c_o, add_7_c_o;
  wire [19:0] add_9_s, add_10_s, add_11_s, add_12_s;
  wire [19:19] add_2_c_o, add_4_c_o, add_6_c_o, add_8_c_o;
  wire [20:20] add_9_c_o, add_11_c_o;
  wire [23:0] add_13_s, add_14_s;
  wire [24:24] add_13_c_o;

  BitExtender #(.inputBits(1)) bitextender_1 (.in(B[0]), .out(bitextender_1_out));
  BitExtender #(.inputBits(1)) bitextender_2 (.in(B[1]), .out(bitextender_2_out));
  BitExtender #(.inputBits(1)) bitextender_3 (.in(B[2]), .out(bitextender_3_out));
  BitExtender #(.inputBits(1)) bitextender_4 (.in(B[3]), .out(bitextender_4_out));
  BitExtender #(.inputBits(1)) bitextender_5 (.in(B[4]), .out(bitextender_5_out));
  BitExtender #(.inputBits(1)) bitextender_6 (.in(B[5]), .out(bitextender_6_out));
  BitExtender #(.inputBits(1)) bitextender_7 (.in(B[6]), .out(bitextender_7_out));
  BitExtender #(.inputBits(1)) bitextender_8 (.in(B[7]), .out(bitextender_8_out));
  BitExtender #(.inputBits(1)) bitextender_9 (.in(B[8]), .out(bitextender_9_out));
  BitExtender #(.inputBits(1)) bitextender_10 (.in(B[9]), .out(bitextender_10_out));
  BitExtender #(.inputBits(1)) bitextender_11 (.in(B[10]), .out(bitextender_11_out));
  BitExtender #(.inputBits(1)) bitextender_12 (.in(B[11]), .out(bitextender_12_out));
  BitExtender #(.inputBits(1)) bitextender_13 (.in(B[12]), .out(bitextender_13_out));
  BitExtender #(.inputBits(1)) bitextender_14 (.in(B[13]), .out(bitextender_14_out));
  BitExtender #(.inputBits(1)) bitextender_15 (.in(B[14]), .out(bitextender_15_out));
  BitExtender #(.inputBits(1)) bitextender_16 (.in(B[15]), .out(bitextender_16_out));
  // And and_1 has open pins: In_1=A, In_2=bitextender_1_out, out=open
  // And and_2 has open pins: In_1=A, In_2=bitextender_2_out, out=open
  // And and_3 has open pins: In_1=A, In_2=bitextender_3_out, out=open
  // And and_4 has open pins: In_1=A, In_2=bitextender_4_out, out=open
  // And and_5 has open pins: In_1=A, In_2=bitextender_5_out, out=open
  // And and_6 has open pins: In_1=A, In_2=bitextender_6_out, out=open
  // And and_7 has open pins: In_1=A, In_2=bitextender_7_out, out=open
  // And and_8 has open pins: In_1=A, In_2=bitextender_8_out, out=open
  // And and_9 has open pins: In_1=A, In_2=bitextender_9_out, out=open
  // And and_10 has open pins: In_1=A, In_2=bitextender_10_out, out=open
  // And and_11 has open pins: In_1=A, In_2=bitextender_11_out, out=open
  // And and_12 has open pins: In_1=A, In_2=bitextender_12_out, out=open
  // And and_13 has open pins: In_1=A, In_2=bitextender_13_out, out=open
  // And and_14 has open pins: In_1=A, In_2=bitextender_14_out, out=open
  // And and_15 has open pins: In_1=A, In_2=bitextender_15_out, out=open
  // And and_16 has open pins: In_1=A, In_2=bitextender_16_out, out=open
  Add #(.Bits(17)) add_1 (.a({1'b0, undriven}), .b({undriven_2, 1'b0}), .c_i(1'b0), .s(add_1_s), .c_o(add_1_c_o[17]));
  Add #(.Bits(17)) add_2 (.a({1'b0, undriven_3}), .b({undriven_4, 1'b0}), .c_i(1'b0), .s(add_2_s), .c_o(add_2_c_o[19]));
  Add #(.Bits(17)) add_3 (.a({1'b0, undriven_5}), .b({undriven_6, 1'b0}), .c_i(1'b0), .s(add_3_s), .c_o(add_3_c_o[17]));
  Add #(.Bits(17)) add_4 (.a({1'b0, undriven_7}), .b({undriven_8, 1'b0}), .c_i(1'b0), .s(add_4_s), .c_o(add_4_c_o[19]));
  Add #(.Bits(17)) add_5 (
    .a({1'b0, undriven_9}), .b({undriven_10, 1'b0}), .c_i(1'b0), .s(add_5_s), .c_o(add_5_c_o[17]));
  Add #(.Bits(17)) add_6 (
    .a({1'b0, undriven_11}), .b({undriven_12, 1'b0}), .c_i(1'b0), .s(add_6_s), .c_o(add_6_c_o[19]));
  Add #(.Bits(17)) add_7 (
    .a({1'b0, undriven_13}), .b({undriven_14, 1'b0}), .c_i(1'b0), .s(add_7_s), .c_o(add_7_c_o[17]));
  Add #(.Bits(17)) add_8 (
    .a({1'b0, undriven_15}), .b({undriven_16, 1'b0}), .c_i(1'b0), .s(add_8_s), .c_o(add_8_c_o[19]));
  Add #(.Bits(20)) add_9 (
    .a({2'b00, add_1_c_o[17], add_1_s}), .b({add_2_c_o[19], add_2_s, 2'b00}), .c_i(1'b0), .s(add_9_s),
    .c_o(add_9_c_o[20]));
  Add #(.Bits(20)) add_10 (
    .a({2'b00, add_3_c_o[17], add_3_s}), .b({add_4_c_o[19], add_4_s, 2'b00}), .c_i(1'b0), .s(add_10_s));  // open: c_o
  Add #(.Bits(20)) add_11 (
    .a({2'b00, add_5_c_o[17], add_5_s}), .b({add_6_c_o[19], add_6_s, 2'b00}), .c_i(1'b0), .s(add_11_s),
    .c_o(add_11_c_o[20]));
  Add #(.Bits(20)) add_12 (
    .a({2'b00, add_7_c_o[17], add_7_s}), .b({add_8_c_o[19], add_8_s, 2'b00}), .c_i(1'b0), .s(add_12_s));  // open: c_o
  Add #(.Bits(24)) add_13 (
    .a({3'b000, add_9_c_o[20], add_9_s}), .b({add_10_s, 4'b0000}), .c_i(1'b0), .s(add_13_s),
    .c_o(add_13_c_o[24]));
  Add #(.Bits(24)) add_14 (
    .a({3'b000, add_11_c_o[20], add_11_s}), .b({add_12_s, 4'b0000}), .c_i(1'b0), .s(add_14_s));  // open: c_o
  Add #(.Bits(32)) add_15 (
    .a({{7{1'b0}}, add_13_c_o[24], add_13_s}), .b({add_14_s, {8{1'b0}}}), .c_i(1'b0), .s(Y));  // open: c_o

  // Notes on the sheet:
  //   A: default 65535
  //   B: default 65535
endmodule

/* Test case:
   A    B      Y
loop(i,100000)
  let a = random(1<<16);
  let b = random(1<<16);
  (a)  (b)   (a*b)
end loop
*/
