// Digital circuit Multiply8Bit.dig as structural Verilog
// O(ln n) 8 bit multiplyer
// {{de O(ln n) 8 Bit Multiplizierer}}
module Multiply8Bit (
  input  [7:0] A,
  input  [7:0] B,
  output [15:0] Y
);

  wire [7:0] bitextender_1_out, bitextender_2_out, bitextender_3_out, bitextender_4_out, bitextender_5_out,
       bitextender_6_out, bitextender_7_out, bitextender_8_out, undriven, undriven_2, undriven_3, undriven_4,
       undriven_5, undriven_6, undriven_7, undriven_8;
  wire [8:0] add_1_s, add_2_s, add_3_s, add_4_s;
  wire [9:9] add_1_c_o, add_3_c_o;
  wire [11:0] add_5_s, add_6_s;
  wire [11:11] add_2_c_o, add_4_c_o;
  wire [12:12] add_5_c_o;

  BitExtender #(.inputBits(1), .outputBits(8)) bitextender_1 (.in(B[0]), .out(bitextender_1_out));
  BitExtender #(.inputBits(1), .outputBits(8)) bitextender_2 (.in(B[1]), .out(bitextender_2_out));
  BitExtender #(.inputBits(1), .outputBits(8)) bitextender_3 (.in(B[2]), .out(bitextender_3_out));
  BitExtender #(.inputBits(1), .outputBits(8)) bitextender_4 (.in(B[3]), .out(bitextender_4_out));
  BitExtender #(.inputBits(1), .outputBits(8)) bitextender_5 (.in(B[4]), .out(bitextender_5_out));
  BitExtender #(.inputBits(1), .outputBits(8)) bitextender_6 (.in(B[5]), .out(bitextender_6_out));
  BitExtender #(.inputBits(1), .outputBits(8)) bitextender_7 (.in(B[6]), .out(bitextender_7_out));
  BitExtender #(.inputBits(1), .outputBits(8)) bitextender_8 (.in(B[7]), .out(bitextender_8_out));
  // And and_1 has open pins: In_1=A, In_2=bitextender_1_out, out=open
  // And and_2 has open pins: In_1=A, In_2=bitextender_2_out, out=open
  // And and_3 has open pins: In_1=A, In_2=bitextender_3_out, out=open
  // And and_4 has open pins: In_1=A, In_2=bitextender_4_out, out=open
  // And and_5 has open pins: In_1=A, In_2=bitextender_5_out, out=open
  // And and_6 has open pins: In_1=A, In_2=bitextender_6_out, out=open
  // And and_7 has open pins: In_1=A, In_2=bitextender_7_out, out=open
  // And and_8 has open pins: In_1=A, In_2=bitextender_8_out, out=open
  Add #(.Bits(9)) add_1 (.a({1'b0, undriven}), .b({undriven_2, 1'b0}), .c_i(1'b0), .s(add_1_s), .c_o(add_1_c_o[9]));
  Add #(.Bits(9)) add_2 (.a({1'b0, undriven_3}), .b({undriven_4, 1'b0}), .c_i(1'b0), .s(add_2_s), .c_o(add_2_c_o[11]));
  Add #(.Bits(9)) add_3 (.a({1'b0, undriven_5}), .b({undriven_6, 1'b0}), .c_i(1'b0), .s(add_3_s), .c_o(add_3_c_o[9]));
  Add #(.Bits(9)) add_4 (.a({1'b0, undriven_7}), .b({undriven_8, 1'b0}), .c_i(1'b0), .s(add_4_s), .c_o(add_4_c_o[11]));
  Add #(.Bits(12)) add_5 (
    .a({2'b00, add_1_c_o[9], add_1_s}), .b({add_2_c_o[11], add_2_s, 2'b00}), .c_i(1'b0), .s(add_5_s),
    .c_o(add_5_c_o[12]));
  Add #(.Bits(12)) add_6 (
    .a({2'b00, add_3_c_o[9], add_3_s}), .b({add_4_c_o[11], add_4_s, 2'b00}), .c_i(1'b0), .s(add_6_s));  // open: c_o
  Add #(.Bits(16)) add_7 (
    .a({3'b000, add_5_c_o[12], add_5_s}), .b({add_6_s, 4'b0000}), .c_i(1'b0), .s(Y));  // open: c_o

  // Notes on the sheet:
  //   A: default 3
  //   B: default 8
  //   8 bit inputs
  //   {{de 8 Bit Eingänge}}
  //   9 bit, {{de 9 Bit,}}
  //   12 bit, {{de 12 Bit,}}
  //   16 bit adders {{de 16 Bit Addierer}}
endmodule

/* Test case:
     A   B   Y
loop(a,1<<8)
  loop(b,1<<8)
     (a) (b) (a*b)
  end loop
end loop
*/
