// Digital circuit Xor1.dig as structural Verilog
module Xor1 (
  input  A,
  input  B,
  output Y
);

  wire undriven, undriven_2;

  // Or or_1 has open pins: In_1=A, In_2=B, out=open
  // NAnd nand_1 has open pins: In_1=A, In_2=B, out=open
  // And and_1 has open pins: In_1=undriven, In_2=undriven_2, out=open
endmodule

/* Test case:
A B Y
0 0 0
0 1 1
1 0 1
1 1 0
*/
