// Digital circuit Xor2.dig as structural Verilog
module Xor2 (
  input  A,
  input  B,
  output Y
);

  wire undriven, undriven_2, undriven_3, undriven_4;

  // Not not_1 has open pins: in=A, out=open
  // Not not_2 has open pins: in=B, out=open
  // And and_1 has open pins: In_1=undriven, In_2=B, out=open
  // And and_2 has open pins: In_1=A, In_2=undriven_2, out=open
  // Or or_1 has open pins: In_1=undriven_3, In_2=undriven_4, out=open
endmodule

/* Test case:
A B Y
0 0 0
0 1 1
1 0 1
1 1 0
*/
