// Digital circuit Xor3.dig as structural Verilog
module Xor3 (
  input  A,
  input  B,
  output Y
);

  wire undriven, undriven_2, undriven_3;

  // NAnd nand_1 has open pins: In_1=A, In_2=B, out=open
  // NAnd nand_2 has open pins: In_1=A, In_2=undriven, out=open
  // NAnd nand_3 has open pins: In_1=undriven, In_2=B, out=open
  // NAnd nand_4 has open pins: In_1=undriven_2, In_2=undriven_3, out=open
endmodule

/* Test case:
A B Y
0 0 0
0 1 1
1 0 1
1 1 0
*/
