// Digital circuit demux.dig as structural Verilog
// A 4-bit demultiplexer. The two input bits A_0 and A_1 specify 
// on which of the 4 output lines Y_0 to Y_3 the input D is output.
// {{de Ein 4-Bit Demultiplexer. Die zwei Eingangsbits A_0 
// und A_1 legen fest, auf welche der 4 
// Ausgangsleitungen Y_0 bis Y_3  der Eingang D 
// ausgegeben wird.}}
module demux (
  input  A_0,
  input  A_1,
  input  D,
  output Y_0,
  output Y_1,
  output Y_2,
  output Y_3
);

  wire undriven, undriven_2;

  // Not not_1 has open pins: in=A_1, out=open
  // Not not_2 has open pins: in=A_0, out=open
  // And and_1 has open pins: In_1=undriven_2, In_2=undriven, In_3=D, out=open
  // And and_2 has open pins: In_1=A_0, In_2=undriven, In_3=D, out=open
  // And and_3 has open pins: In_1=undriven_2, In_2=A_1, In_3=D, out=open
  // And and_4 has open pins: In_1=A_0, In_2=A_1, In_3=D, out=open

  // Notes on the sheet:
  //   A_0: selection bit 0
  //   {{de Das 0. Auswahlbit.}}
  //   A_1: election bit 1
  //   {{de Das 1. Auswahlbit.}}
  //   D: The data bit which is output to one of the four 
  //   outputs.
  //   {{de Das Datenbit welches auf einen der vier 
  //   Ausgänge ausgegeben wird.}}
  //   Y_0: output bit 0
  //   {{de Das 0. Ausgangsbit.}}
  //   Y_1: output bit 1
  //   {{de Das 1. Ausgangsbit.}}
  //   Y_2: output bit 2
  //   {{de Das 2. Ausgangsbit.}}
  //   Y_3: output bit 3
  //   {{de Das 3. Ausgangsbit.}}
endmodule

/* Test case:
A_1 A_0 D Y_3 Y_2 Y_1 Y_0
 0   0  0  0   0   0   0
 0   0  1  0   0   0   1
 0   1  0  0   0   0   0
 0   1  1  0   0   1   0
 1   0  0  0   0   0   0
 1   0  1  0   1   0   0
 1   1  0  0   0   0   0
 1   1  1  1   0   0   0
*/
