// Digital circuit mux.dig as structural Verilog
// 4-bit multiplexer.
// One of the data bits D_0 to D_3 is output at the output Y. Which 
// output is determined by the two inputs A_0 and A_1.
// {{de Diskret aufgebauter 4-Bit Multiplexer.
// Es wird immer eines der Datenbits D_0 bis D_3 am
// Ausgang Y ausgegeben. Welches ausgegeben wird,
// legen die beiden Eingänge A_0 und A_1 fest.}}
module mux (
  input  A_0,
  input  A_1,
  input  D_0,
  input  D_1,
  input  D_2,
  input  D_3,
  output Y
);

  wire undriven, undriven_2, undriven_3, undriven_4, undriven_5, undriven_6;

  // Not not_1 has open pins: in=A_1, out=open
  // Not not_2 has open pins: in=A_0, out=open
  // And and_1 has open pins: In_1=undriven_2, In_2=undriven, In_3=D_0, out=open
  // And and_2 has open pins: In_1=A_0, In_2=undriven, In_3=D_1, out=open
  // And and_3 has open pins: In_1=undriven_2, In_2=A_1, In_3=D_2, out=open
  // And and_4 has open pins: In_1=A_0, In_2=A_1, In_3=D_3, out=open
  // Or or_1 has open pins: In_1=undriven_3, In_2=undriven_4, In_3=undriven_5, In_4=undriven_6, out=open

  // Notes on the sheet:
  //   A_0: Bit 0 of the input selection.
  //   {{de Bit 0 der Signalauswahl.}}
  //   A_1: Bit 1 of the input selection.
  //   {{de Bit 1 der Signalauswahl.}}
  //   D_0: data bit 0.
  //   {{de Das 0. Datenbit.}}
  //   D_1: data bit 1.
  //   {{de Das 1. Datenbit.}}
  //   D_2: data bit 2.
  //   {{de Das 2. Datenbit.}}
  //   D_3: data bit 3.
  //   {{de Das 3. Datenbit.}}
  //   Y: Output bit. One of the data bits is always output 
  //   here. Which one is set by the inputs A_0 and A_1.
  //   {{de Ausgangsbit. Es wird immer eines der Datenbits 
  //   hier ausgegeben. Welches das ist, legen die 
  //   Eingänge A_0 und A_1 fest.}}
endmodule

/* Test case:
A_1 A_0 D_3 D_2 D_1 D_0 Y
 0   0   X   X   X   0  0
 0   0   X   X   X   1  1
 0   1   X   X   0   X  0
 0   1   X   X   1   X  1
 1   0   X   0   X   X  0
 1   0   X   1   X   X  1
 1   1   0   X   X   X  0
 1   1   1   X   X   X  1
*/
