// Digital circuit Hazard.dig as structural Verilog
module Hazard (
  input  In,
  output Out
);

  wire delay_1_out, undriven;

  Delay delay_1 (.in(In), .out(delay_1_out));
  // XOr xor_1 has open pins: In_1=delay_1_out, In_2=In, out=open
  // XOr xor_2 has open pins: In_1=undriven, In_2=In, out=open
endmodule
