// Digital circuit HazardB.dig as structural Verilog
module HazardB (
  input  x_2,
  input  x_0,
  input  x_1,
  output y
);

  wire undriven, undriven_2, undriven_3, undriven_4;

  // Not not_1 has open pins: in=x_0, out=open
  // And and_1 has open pins: In_1=x_2, In_2=undriven, out=open
  // And and_2 has open pins: In_1=x_0, In_2=x_1, out=open
  // And and_3 has open pins: In_1=x_1, In_2=x_2, out=open
  // Or or_1 has open pins: In_1=undriven_2, In_2=undriven_3, In_3=undriven_4, out=open

  // Notes on the sheet:
  //   x_2: default 1
  //   x_1: default 1
endmodule
