// Digital circuit Oscillation.dig as structural Verilog
module Oscillation (
  input  in_1,
  output out_2
);

  wire undriven, undriven_2;

  // XOr xor_1 has open pins: In_1=in_1, In_2=out_2, out=open
  // Not not_1 has open pins: in=undriven, out=open
  // Not not_2 has open pins: in=undriven_2, out=open
endmodule
