// Digital circuit 74147.dig as structural Verilog
// 10-line to 4-line priority encoder
module _74147 (
  input  I9,
  input  I8,
  input  I7,
  input  I6,
  input  I5,
  input  I4,
  input  I3,
  input  I2,
  input  I1,
  input  VCC,
  input  GND,
  output A,
  output B,
  output C,
  output D
);

  wire undriven, undriven_2, undriven_3, undriven_4, undriven_5, undriven_6, undriven_7, undriven_8,
       undriven_9, undriven_10, undriven_11, undriven_12, undriven_13, undriven_14, undriven_15;

  // Not not_1 has open pins: in=I9, out=open
  // Not not_2 has open pins: in=I8, out=open
  // Not not_3 has open pins: in=I6, out=open
  // Not not_4 has open pins: in=I5, out=open
  // Not not_5 has open pins: in=I4, out=open
  // Not not_6 has open pins: in=I2, out=open
  // And and_1 has open pins: In_1=I1, In_2=I3, In_3=I5, In_4=I7, In_5=I9, out=open
  // And and_2 has open pins: In_1=undriven_10, In_2=I3, In_3=I5, In_4=I7, In_5=I9, out=open
  // And and_3 has open pins: In_1=undriven_11, In_2=I5, In_3=I7, In_4=I9, out=open
  // And and_4 has open pins: In_1=undriven_13, In_2=I7, In_3=I9, out=open
  // And and_5 has open pins: In_1=undriven_14, In_2=I9, out=open
  // And and_6 has open pins: In_1=I2, In_2=I3, In_3=I6, In_4=I7, out=open
  // And and_7 has open pins: In_1=undriven_11, In_2=I6, In_3=I7, out=open
  // And and_8 has open pins: In_1=undriven_12, In_2=I6, In_3=I7, out=open
  // And and_9 has open pins: In_1=I4, In_2=I5, In_3=I6, In_4=I7, out=open
  // And and_10 has open pins: In_1=I8, In_2=I9, out=open
  // Or or_1 has open pins: In_1=undriven, In_2=undriven_2, In_3=undriven_3, In_4=undriven_8, In_5=undriven_9, out=open
  // Or or_2 has open pins: In_1=undriven_4, In_2=undriven_5, In_3=undriven_6, In_4=undriven_14, In_5=undriven_15, out=open
  // Or or_3 has open pins: In_1=undriven_7, In_2=undriven_14, In_3=undriven_15, out=open
  PowerSupply powersupply_1 (.VDD(VCC), .GND(GND));

  // Notes on the sheet:
  //   I9: pin 10
  //   I8: pin 5
  //   I7: pin 4
  //   I6: pin 3
  //   I5: pin 2
  //   I4: pin 1
  //   I3: pin 13
  //   I2: pin 12
  //   I1: pin 11
  //   A: pin 9
  //   B: pin 7
  //   C: pin 6
  //   D: pin 14
  //   VCC: pin 16, default 1
  //   GND: pin 8
endmodule

/* Test case:
I1 I2 I3 I4 I5 I6 I7 I8 I9   D C B A
1  1  1  1  1  1  1  1  1    1 1 1 1
x  x  x  x  x  x  x  x  0    0 1 1 0
x  x  x  x  x  x  x  0  1    0 1 1 1
x  x  x  x  x  x  0  1  1    1 0 0 0
x  x  x  x  x  0  1  1  1    1 0 0 1
x  x  x  x  0  1  1  1  1    1 0 1 0
x  x  x  0  1  1  1  1  1    1 0 1 1
x  x  0  1  1  1  1  1  1    1 1 0 0
x  0  1  1  1  1  1  1  1    1 1 0 1
0  1  1  1  1  1  1  1  1    1 1 1 0
*/
