// Digital circuit 74148.dig as structural Verilog
// 8-line to 3-Line priority encoder
module _74148 (
  input  EI,
  input  _0,
  input  _1,
  input  _2,
  input  _3,
  input  _4,
  input  _5,
  input  _6,
  input  _7,
  input  VCC,
  input  GND,
  output A2,
  output A1,
  output A0,
  output GS,
  output E0
);

  wire undriven, undriven_2, undriven_3, undriven_4, undriven_5, undriven_6, undriven_7, undriven_8,
       undriven_9, undriven_10, undriven_11, undriven_12, undriven_13, undriven_14, undriven_15, undriven_16,
       undriven_17;

  // Not not_1 has open pins: in=_0, out=open
  // Not not_2 has open pins: in=_1, out=open
  // Not not_3 has open pins: in=_2, out=open
  // Not not_4 has open pins: in=_3, out=open
  // Not not_5 has open pins: in=_4, out=open
  // Not not_6 has open pins: in=_5, out=open
  // Not not_7 has open pins: in=_6, out=open
  // Not not_8 has open pins: in=_7, out=open
  // And and_1 has open pins: In_1=_4, In_2=_5, In_3=_6, In_4=_7, out=open
  // And and_2 has open pins: In_1=_2, In_2=_3, In_3=_6, In_4=_7, out=open
  // And and_3 has open pins: In_1=undriven_13, In_2=_6, In_3=_7, out=open
  // And and_4 has open pins: In_1=undriven_12, In_2=_6, In_3=_7, out=open
  // And and_5 has open pins: In_1=_1, In_2=_3, In_3=_5, In_4=_7, out=open
  // And and_6 has open pins: In_1=undriven_15, In_2=_3, In_3=_5, In_4=_7, out=open
  // And and_7 has open pins: In_1=undriven_13, In_2=_5, In_3=_7, out=open
  // And and_8 has open pins: In_1=undriven_11, In_2=_7, out=open
  // And and_9 has open pins: In_1=_0, In_2=_1, In_3=_2, In_4=_3, In_5=_4, In_6=_5, In_7=_6, In_8=_7, out=open
  // Or or_1 has open pins: In_1=undriven_17, In_2=undriven_16, In_3=undriven_15, In_4=undriven_14, In_5=undriven_13, In_6=undriven_12, In_7=undriven_11, In_8=undriven_10, In_9=EI, out=open
  // Or or_2 has open pins: In_1=undriven, In_2=EI, out=open
  // Or or_3 has open pins: In_1=undriven_7, In_2=EI, out=open
  // Or or_4 has open pins: In_1=undriven_2, In_2=undriven_3, In_3=undriven_8, In_4=EI, out=open
  // Or or_5 has open pins: In_1=undriven_4, In_2=undriven_5, In_3=undriven_6, In_4=undriven_9, In_5=EI, out=open
  PowerSupply powersupply_1 (.VDD(VCC), .GND(GND));

  // Notes on the sheet:
  //   A2: pin 6
  //   A1: pin 7
  //   A0: pin 9
  //   GS: pin 14
  //   E0: pin 15
  //   EI: pin 5
  //   _0: pin 10
  //   _1: pin 11
  //   _2: pin 12
  //   _3: pin 13
  //   _4: pin 1
  //   _5: pin 2
  //   _6: pin 3
  //   _7: pin 4
  //   VCC: pin 16, default 1
  //   GND: pin 8
endmodule

/* Test case:
EI 0 1 2 3 4 5 6 7   A2 A1 A0   GS E0
1  x x x x x x x x   1  1  1    1  1
0  1 1 1 1 1 1 1 1   1  1  1    1  0
0  x x x x x x x 0   0  0  0    0  1
0  x x x x x x 0 1   0  0  1    0  1
0  x x x x x 0 1 1   0  1  0    0  1
0  x x x x 0 1 1 1   0  1  1    0  1
0  x x x 0 1 1 1 1   1  0  0    0  1
0  x x 0 1 1 1 1 1   1  0  1    0  1
0  x 0 1 1 1 1 1 1   1  1  0    0  1
0  0 1 1 1 1 1 1 1   1  1  1    0  1
*/
