// Digital circuit 74181.dig as structural Verilog
// 4-bit arithmetic logic unit
module _74181 (
  input  Cn,
  input  nA0,
  input  nA1,
  input  nA2,
  input  nA3,
  input  nB0,
  input  nB1,
  input  nB2,
  input  nB3,
  input  S0,
  input  S1,
  input  S2,
  input  S3,
  input  M,
  input  VCC,
  input  GND,
  output nG,
  output nP,
  output nF0,
  output nF1,
  output nF2,
  output nF3,
  output A_eq_B,
  output Cn_plus_4
);

  wire undriven, undriven_2, undriven_3, undriven_4, undriven_5, undriven_6, undriven_7, undriven_8,
       undriven_9, undriven_10, undriven_11, undriven_12, undriven_13, undriven_14, undriven_15, undriven_16,
       undriven_17, undriven_18, undriven_19, undriven_20, undriven_21, undriven_22, undriven_23,
       undriven_24, undriven_25, undriven_26, undriven_27, undriven_28, undriven_29, undriven_30,
       undriven_31, undriven_32, undriven_33, undriven_34, undriven_35, undriven_36, undriven_37,
       undriven_38, undriven_39, undriven_40, undriven_41, undriven_42, undriven_43, undriven_44,
       undriven_45, undriven_46, undriven_47, undriven_48, undriven_49, undriven_50, undriven_51,
       undriven_52, undriven_53, undriven_54;

  PowerSupply powersupply_1 (.VDD(VCC), .GND(GND));
  // Not not_1 has open pins: in=nB3, out=open
  // Not not_2 has open pins: in=nB2, out=open
  // Not not_3 has open pins: in=nB1, out=open
  // Not not_4 has open pins: in=nB0, out=open
  // Not not_5 has open pins: in=M, out=open
  // And and_1 has open pins: In_1=S3, In_2=nB3, In_3=nA3, out=open
  // And and_2 has open pins: In_1=nA3, In_2=S2, In_3=undriven, out=open
  // And and_3 has open pins: In_1=undriven, In_2=S1, out=open
  // And and_4 has open pins: In_1=S0, In_2=nB3, out=open
  // And and_5 has open pins: In_1=nB2, In_2=S3, In_3=nA2, out=open
  // And and_6 has open pins: In_1=nA2, In_2=S2, In_3=undriven_2, out=open
  // And and_7 has open pins: In_1=undriven_2, In_2=S1, out=open
  // And and_8 has open pins: In_1=S0, In_2=nB2, out=open
  // And and_9 has open pins: In_1=nB1, In_2=S3, In_3=nA1, out=open
  // And and_10 has open pins: In_1=nA1, In_2=S2, In_3=undriven_3, out=open
  // And and_11 has open pins: In_1=undriven_3, In_2=S1, out=open
  // And and_12 has open pins: In_1=S0, In_2=nB1, out=open
  // And and_13 has open pins: In_1=S3, In_2=nB0, In_3=nA0, out=open
  // And and_14 has open pins: In_1=nA0, In_2=S2, In_3=undriven_4, out=open
  // And and_15 has open pins: In_1=undriven_4, In_2=S1, out=open
  // And and_16 has open pins: In_1=S0, In_2=nB0, out=open
  // NOr nor_1 has open pins: In_1=undriven_5, In_2=undriven_17, out=open
  // NOr nor_2 has open pins: In_1=undriven_6, In_2=undriven_7, In_3=nA3, out=open
  // NOr nor_3 has open pins: In_1=undriven_8, In_2=undriven_18, out=open
  // NOr nor_4 has open pins: In_1=undriven_9, In_2=undriven_10, In_3=nA2, out=open
  // NOr nor_5 has open pins: In_1=undriven_11, In_2=undriven_19, out=open
  // NOr nor_6 has open pins: In_1=undriven_12, In_2=undriven_13, In_3=nA1, out=open
  // NOr nor_7 has open pins: In_1=undriven_14, In_2=undriven_20, out=open
  // NOr nor_8 has open pins: In_1=undriven_15, In_2=undriven_16, In_3=nA0, out=open
  // And and_17 has open pins: In_1=undriven_22, In_2=undriven_23, out=open
  // And and_18 has open pins: In_1=undriven_22, In_2=undriven_24, In_3=undriven_25, out=open
  // And and_19 has open pins: In_1=undriven_22, In_2=undriven_24, In_3=undriven_26, In_4=undriven_27, out=open
  // NAnd nand_1 has open pins: In_1=undriven_22, In_2=undriven_24, In_3=undriven_26, In_4=undriven_28, In_5=Cn, out=open
  // NAnd nand_2 has open pins: In_1=undriven_22, In_2=undriven_24, In_3=undriven_26, In_4=undriven_28, out=open
  // And and_20 has open pins: In_1=undriven_24, In_2=undriven_26, In_3=undriven_28, In_4=Cn, In_5=undriven_29, out=open
  // And and_21 has open pins: In_1=undriven_24, In_2=undriven_26, In_3=undriven_27, In_4=undriven_29, out=open
  // And and_22 has open pins: In_1=undriven_24, In_2=undriven_25, In_3=undriven_29, out=open
  // And and_23 has open pins: In_1=undriven_23, In_2=undriven_29, out=open
  // And and_24 has open pins: In_1=undriven_26, In_2=undriven_28, In_3=Cn, In_4=undriven_29, out=open
  // And and_25 has open pins: In_1=undriven_26, In_2=undriven_27, In_3=undriven_29, out=open
  // And and_26 has open pins: In_1=undriven_25, In_2=undriven_29, out=open
  // And and_27 has open pins: In_1=Cn, In_2=undriven_28, In_3=undriven_29, out=open
  // And and_28 has open pins: In_1=undriven_27, In_2=undriven_29, out=open
  // NAnd nand_3 has open pins: In_1=undriven_29, In_2=Cn, out=open
  // Not not_6 has open pins: in=undriven_21, out=open
  // Not not_7 has open pins: in=undriven_23, out=open
  // Not not_8 has open pins: in=undriven_25, out=open
  // Not not_9 has open pins: in=undriven_27, out=open
  // NOr nor_9 has open pins: In_1=undriven_21, In_2=undriven_40, In_3=undriven_43, In_4=undriven_44, out=open
  // And and_29 has open pins: In_1=undriven_22, In_2=undriven_30, out=open
  // NOr nor_10 has open pins: In_1=undriven_31, In_2=undriven_32, In_3=undriven_33, In_4=undriven_45, out=open
  // And and_30 has open pins: In_1=undriven_24, In_2=undriven_34, out=open
  // NOr nor_11 has open pins: In_1=undriven_35, In_2=undriven_36, In_3=undriven_46, out=open
  // And and_31 has open pins: In_1=undriven_26, In_2=undriven_37, out=open
  // NOr nor_12 has open pins: In_1=undriven_38, In_2=undriven_47, out=open
  // And and_32 has open pins: In_1=undriven_28, In_2=undriven_39, out=open
  // Or or_1 has open pins: In_1=nG, In_2=undriven_41, out=open
  // XOr xor_1 has open pins: In_1=undriven_48, In_2=undriven_52, out=open
  // XOr xor_2 has open pins: In_1=undriven_49, In_2=undriven_53, out=open
  // XOr xor_3 has open pins: In_1=undriven_50, In_2=undriven_54, out=open
  // XOr xor_4 has open pins: In_1=undriven_51, In_2=undriven_42, out=open
  // And and_33 has open pins: In_1=nF3, In_2=nF2, In_3=nF1, In_4=nF0, out=open

  // Notes on the sheet:
  //   Cn: pin 7
  //   nA0: pin 2
  //   nA1: pin 23
  //   nA2: pin 21
  //   nA3: pin 19
  //   nB0: pin 1
  //   nB1: pin 22
  //   nB2: pin 20
  //   nB3: pin 18
  //   S0: pin 6
  //   S1: pin 5
  //   S2: pin 4
  //   S3: pin 3
  //   M: pin 8
  //   nG: pin 17
  //   nP: pin 15
  //   nF0: pin 9
  //   nF1: pin 10
  //   nF2: pin 11
  //   nF3: pin 13
  //   A_eq_B: pin 14
  //   Cn_plus_4: pin 16
  //   VCC: pin 24, default 1
  //   GND: pin 12
  //   Logic Tests
  //       (M=1)
  //   Arithmetic Tests
  //     (M=0, Cn=1)
endmodule

/* Test case !A (L0000):
S3 S2 S1 S0 M Cn ~A3 ~A2 ~A1 ~A0 ~B3 ~B2 ~B1 ~B0 ~F3 ~F2 ~F1 ~F0
# M=1, Cn=X MEANS LOGIC MODE
# !A
loop(a,16)
          0  0  0  0  1  0    bits(4,a)   X X X X       bits(4,~a)
end loop
*/

/* Test case !A AND !B (L0001):
S3 S2 S1 S0 M Cn ~A3 ~A2 ~A1 ~A0 ~B3 ~B2 ~B1 ~B0 ~F3 ~F2 ~F1 ~F0
# !A AND !B
loop(a,16)
  loop(b,16)
          0  0  0  1  1  0    bits(4,a)   bits(4,b)       bits(4,(~a)&(~b))
  end loop
end loop
*/

/* Test case !A AND B (L0010):
S3 S2 S1 S0 M Cn ~A3 ~A2 ~A1 ~A0 ~B3 ~B2 ~B1 ~B0 ~F3 ~F2 ~F1 ~F0
# !A AND B
loop(a,16)
  loop(b,16)
          0  0  1  0  1  0    bits(4,a)   bits(4,b)       bits(4,~a&b)
  end loop
end loop
*/

/* Test case "logic 0" (L0011):
S3 S2 S1 S0 M Cn ~A3 ~A2 ~A1 ~A0 ~B3 ~B2 ~B1 ~B0 ~F3 ~F2 ~F1 ~F0
# MINUS 1
0  0  1  1  1  0   X   X   X   X   X   X   X   X   0   0   0   0
*/

/* Test case !(A AND B) (L0100):
S3 S2 S1 S0 M Cn ~A3 ~A2 ~A1 ~A0 ~B3 ~B2 ~B1 ~B0 ~F3 ~F2 ~F1 ~F0
# !(A AND B)
loop(a,16)
  loop(b,16)
          0  1  0  0  1  0    bits(4,a)   bits(4,b)       bits(4,~(a&b))
  end loop
end loop
*/

/* Test case !B (L0101):
S3 S2 S1 S0 M Cn ~A3 ~A2 ~A1 ~A0 ~B3 ~B2 ~B1 ~B0 ~F3 ~F2 ~F1 ~F0
# !B
loop(a,16)
  loop(b,16)
          0  1  0  1  1  0    bits(4,a)   bits(4,b)       bits(4,~b)
  end loop
end loop
*/

/* Test case A XOR B (L0110):
S3 S2 S1 S0 M Cn ~A3 ~A2 ~A1 ~A0 ~B3 ~B2 ~B1 ~B0 ~F3 ~F2 ~F1 ~F0
# A XOR B 
loop(a,16)
  loop(b,16)
          0  1  1  0  1  0    bits(4,a)   bits(4,b)       bits(4,a^b)
  end loop
end loop
*/

/* Test case A AND !B (L0111):
S3 S2 S1 S0 M Cn ~A3 ~A2 ~A1 ~A0 ~B3 ~B2 ~B1 ~B0 ~F3 ~F2 ~F1 ~F0
# (A AND !B)
loop(a,16)
  loop(b,16)
          0  1  1  1  1  0    bits(4,a)   bits(4,b)       bits(4,(a&~b))
 end loop
end loop
*/

/* Test case !A OR B (L1000):
S3 S2 S1 S0 M Cn ~A3 ~A2 ~A1 ~A0 ~B3 ~B2 ~B1 ~B0 ~F3 ~F2 ~F1 ~F0
# !A OR B
loop(a,16)
  loop(b,16)
          1  0  0  0  1  1    bits(4,a)   bits(4,b)       bits(4,~a|b)
  end loop
end loop
*/

/* Test case !(A XOR B) (L1001):
S3 S2 S1 S0 M Cn ~A3 ~A2 ~A1 ~A0 ~B3 ~B2 ~B1 ~B0 ~F3 ~F2 ~F1 ~F0
# !(A XOR B)
loop(a,16)
  loop(b,16)
          1  0  0  1  1  0    bits(4,a)   bits(4,b)       bits(4,~(a^b))
  end loop
end loop
*/

/* Test case B (L1010):
S3 S2 S1 S0 M Cn ~A3 ~A2 ~A1 ~A0 ~B3 ~B2 ~B1 ~B0 ~F3 ~F2 ~F1 ~F0
# B
loop(a,16)
  loop(b,16)
          1  0  1  0  1  0    bits(4,a)   bits(4,b)       bits(4,b)
  end loop
end loop
*/

/* Test case A AND B (L1011):
S3 S2 S1 S0 M Cn ~A3 ~A2 ~A1 ~A0 ~B3 ~B2 ~B1 ~B0 ~F3 ~F2 ~F1 ~F0
# A AND B
loop(a,16)
  loop(b,16)
          1  0  1  1  1  0    bits(4,a)   bits(4,b)       bits(4,a&b)
  end loop
end loop
*/

/* Test case "logic 1" (L1100):
S3 S2 S1 S0 M Cn ~A3 ~A2 ~A1 ~A0 ~B3 ~B2 ~B1 ~B0 ~F3 ~F2 ~F1 ~F0
# A plus A

          1  1  0  0  1  0    X X X X   X X X X       1 1 1 1
*/

/* Test case A OR !B (L1101):
S3 S2 S1 S0 M Cn ~A3 ~A2 ~A1 ~A0 ~B3 ~B2 ~B1 ~B0 ~F3 ~F2 ~F1 ~F0
# A OR !B
loop(a,16)
  loop(b,16)
          1  1  0  1  1  0    bits(4,a)   bits(4,b)       bits(4,a|~b)
  end loop
end loop
*/

/* Test case A OR B (L1110):
S3 S2 S1 S0 M Cn ~A3 ~A2 ~A1 ~A0 ~B3 ~B2 ~B1 ~B0 ~F3 ~F2 ~F1 ~F0
# A OR B
loop(a,16)
  loop(b,16)
          1  1  1  0  1  0    bits(4,a)   bits(4,b)       bits(4,a|b)
  end loop
end loop
*/

/* Test case A (L1111):
S3 S2 S1 S0 M Cn ~A3 ~A2 ~A1 ~A0 ~B3 ~B2 ~B1 ~B0 ~F3 ~F2 ~F1 ~F0
# A 
loop(a,16)
          1  1  1  1  1  0    bits(4,a)  X X X X       bits(4,a)
end loop
*/

/* Test case A (A0000):
S3 S2 S1 S0 M Cn ~A3 ~A2 ~A1 ~A0 ~B3 ~B2 ~B1 ~B0 ~F3 ~F2 ~F1 ~F0
# M=0, Cn=1 MEANS ARITHMETIC MODE
# A
repeat(16) 0  0  0  0  0  1   bits(4,n)   X   X   X   X   bits(4,n)
*/

/* Test case A OR B (A0001):
S3 S2 S1 S0 M Cn ~A3 ~A2 ~A1 ~A0 ~B3 ~B2 ~B1 ~B0 ~F3 ~F2 ~F1 ~F0
# A OR B
loop(a,16)
  loop(b,16)
          0  0  0  1  0  1    bits(4,a)   bits(4,b)       bits(4,a|b)
  end loop
end loop
*/

/* Test case A OR !B (A0010):
S3 S2 S1 S0 M Cn ~A3 ~A2 ~A1 ~A0 ~B3 ~B2 ~B1 ~B0 ~F3 ~F2 ~F1 ~F0
# A OR !B
loop(a,16)
  loop(b,16)
          0  0  1  0  0  1    bits(4,a)   bits(4,b)       bits(4,a|~b)
  end loop
end loop
*/

/* Test case "minus 1" (A0011):
S3 S2 S1 S0 M Cn ~A3 ~A2 ~A1 ~A0 ~B3 ~B2 ~B1 ~B0 ~F3 ~F2 ~F1 ~F0
# MINUS 1
0  0  1  1  0  1   X   X   X   X   X   X   X   X   1   1   1   1
*/

/* Test case A plus (A AND !B) (A0100):
S3 S2 S1 S0 M Cn ~A3 ~A2 ~A1 ~A0 ~B3 ~B2 ~B1 ~B0 ~F3 ~F2 ~F1 ~F0
# A plus (A AND !B)
#0  1  0  0  0  1   1   0   0   1   0   1   0   1   0   0   0   1
loop(a,16)
  loop(b,16)
          0  1  0  0  0  1    bits(4,a)   bits(4,b)       bits(4,a+(a&~b))
  end loop
end loop
*/

/* Test case (A OR B) plus (A AND !B) (A0101):
S3 S2 S1 S0 M Cn ~A3 ~A2 ~A1 ~A0 ~B3 ~B2 ~B1 ~B0 ~F3 ~F2 ~F1 ~F0
# (A OR B) plus (A AND !B)
loop(a,16)
  loop(b,16)
          0  1  0  1  0  1    bits(4,a)   bits(4,b)       bits(4,(a|b)+(a&~b))
  end loop
end loop
*/

/* Test case A minus B minus 1 (A0110):
S3 S2 S1 S0 M Cn ~A3 ~A2 ~A1 ~A0 ~B3 ~B2 ~B1 ~B0 ~F3 ~F2 ~F1 ~F0
# A minus B minus 1
loop(a,16)
  loop(b,16)
          0  1  1  0  0  1    bits(4,a)   bits(4,b)       bits(4,a-b-1)
  end loop
end loop
*/

/* Test case (A AND !B) minus 1 (A0111):
S3 S2 S1 S0 M Cn ~A3 ~A2 ~A1 ~A0 ~B3 ~B2 ~B1 ~B0 ~F3 ~F2 ~F1 ~F0
# (A AND !B) minus 1
loop(a,16)
  loop(b,16)
          0  1  1  1  0  1    bits(4,a)   bits(4,b)       bits(4,(a&~b)-1)
 end loop
end loop
*/

/* Test case A plus (A AND B) (A1000):
S3 S2 S1 S0 M Cn ~A3 ~A2 ~A1 ~A0 ~B3 ~B2 ~B1 ~B0 ~F3 ~F2 ~F1 ~F0
# A plus (A AND B)
1  0  0  0  0  1   0   1   1   1   0   0   0   1   1   0   0   0
loop(a,16)
  loop(b,16)
          1  0  0  0  0  1    bits(4,a)   bits(4,b)       bits(4,a+(a&b))
  end loop
end loop
*/

/* Test case A plus B (A1001):
S3 S2 S1 S0 M Cn ~A3 ~A2 ~A1 ~A0 ~B3 ~B2 ~B1 ~B0 Cn+4 ~F3 ~F2 ~F1 ~F0
# A plus B
loop(a,16)
  loop(b,16)
          1  0  0  1  0  1    bits(4,a)   bits(4,b)   ((~((a+b)>>4))&1) bits(4,a+b)
  end loop
end loop

# A plus B plus 1
loop(a,16)
  loop(b,16)
          1  0  0  1  0  0    bits(4,a)   bits(4,b)   ((~((a+b+1)>>4))&1) bits(4,a+b+1)
  end loop
end loop
*/

/* Test case (A OR !B) plus (A AND B) (A1010):
S3 S2 S1 S0 M Cn ~A3 ~A2 ~A1 ~A0 ~B3 ~B2 ~B1 ~B0 ~F3 ~F2 ~F1 ~F0
# (A OR !B) plus (A AND B)
loop(a,16)
  loop(b,16)
          1  0  1  0  0  1    bits(4,a)   bits(4,b)       bits(4,(a|~b)+(a&b))
  end loop
end loop
*/

/* Test case (A AND B) minus 1 (A1011):
S3 S2 S1 S0 M Cn ~A3 ~A2 ~A1 ~A0 ~B3 ~B2 ~B1 ~B0 ~F3 ~F2 ~F1 ~F0
# (A AND B) minus 1
loop(a,16)
  loop(b,16)
          1  0  1  1  0  1    bits(4,a)   bits(4,b)       bits(4,(a&b)-1)
  end loop
end loop
*/

/* Test case A plus A (A1100):
S3 S2 S1 S0 M Cn ~A3 ~A2 ~A1 ~A0 ~B3 ~B2 ~B1 ~B0 ~F3 ~F2 ~F1 ~F0
# A plus A
loop(a,16)
          1  1  0  0  0  1    bits(4,a)   X X X X       bits(4,a+a)
end loop
*/

/* Test case (A OR B) plus A (A1101):
S3 S2 S1 S0 M Cn ~A3 ~A2 ~A1 ~A0 ~B3 ~B2 ~B1 ~B0 ~F3 ~F2 ~F1 ~F0
# (A OR B) plus A
loop(a,16)
  loop(b,16)
          1  1  0  1  0  1    bits(4,a)   bits(4,b)       bits(4,(a|b)+a)
  end loop
end loop
*/

/* Test case (A OR !B) plus A (A1110):
S3 S2 S1 S0 M Cn ~A3 ~A2 ~A1 ~A0 ~B3 ~B2 ~B1 ~B0 ~F3 ~F2 ~F1 ~F0
# (A OR !B) plus A
loop(a,16)
  loop(b,16)
          1  1  1  0  0  1    bits(4,a)   bits(4,b)       bits(4,(a|~b)+a)
  end loop
end loop
*/

/* Test case A minus 1 (A1111):
S3 S2 S1 S0 M Cn ~A3 ~A2 ~A1 ~A0 ~B3 ~B2 ~B1 ~B0 ~F3 ~F2 ~F1 ~F0
# A minus 1
loop(a,16)
          1  1  1  1  0  1    bits(4,a)  X X X X       bits(4,a-1)
end loop
*/
