// Digital circuit 74182.dig as structural Verilog
// look-ahead carry generator
module _74182 (
  input  C_n,
  input  nG0,
  input  nP0,
  input  nG1,
  input  nP1,
  input  nG2,
  input  nP2,
  input  nG3,
  input  nP3,
  input  VCC,
  input  GND,
  output nP,
  output nG,
  output C_n_plus_z,
  output C_n_plus_y,
  output C_n_plus_x
);

  wire undriven, undriven_2, undriven_3, undriven_4, undriven_5, undriven_6, undriven_7, undriven_8,
       undriven_9, undriven_10, undriven_11, undriven_12, undriven_13, undriven_14;

  PowerSupply powersupply_1 (.VDD(VCC), .GND(GND));
  // Not not_1 has open pins: in=C_n, out=open
  // Or or_1 has open pins: In_1=nP0, In_2=nP1, In_3=nP2, In_4=nP3, out=open
  // And and_1 has open pins: In_1=nG0, In_2=nG1, In_3=nG2, In_4=nG3, out=open
  // And and_2 has open pins: In_1=nP1, In_2=nG3, In_3=nG2, In_4=nG1, out=open
  // And and_3 has open pins: In_1=nP2, In_2=nG3, In_3=nG2, out=open
  // And and_4 has open pins: In_1=nP3, In_2=nG3, out=open
  // And and_5 has open pins: In_1=nG2, In_2=nG1, In_3=nG0, In_4=undriven, out=open
  // And and_6 has open pins: In_1=nP0, In_2=nG2, In_3=nG1, In_4=nG0, out=open
  // And and_7 has open pins: In_1=nP1, In_2=nG2, In_3=nG1, out=open
  // And and_8 has open pins: In_1=nP2, In_2=nG2, out=open
  // And and_9 has open pins: In_1=nG1, In_2=nG0, In_3=undriven, out=open
  // And and_10 has open pins: In_1=nP0, In_2=nG1, In_3=nG0, out=open
  // And and_11 has open pins: In_1=nP1, In_2=nG1, out=open
  // And and_12 has open pins: In_1=nG0, In_2=undriven, out=open
  // And and_13 has open pins: In_1=nP0, In_2=nG0, out=open
  // Or or_2 has open pins: In_1=undriven_2, In_2=undriven_3, In_3=undriven_9, In_4=undriven_13, out=open
  // NOr nor_1 has open pins: In_1=undriven_4, In_2=undriven_5, In_3=undriven_10, In_4=undriven_14, out=open
  // NOr nor_2 has open pins: In_1=undriven_6, In_2=undriven_7, In_3=undriven_11, out=open
  // NOr nor_3 has open pins: In_1=undriven_8, In_2=undriven_12, out=open

  // Notes on the sheet:
  //   C_n: pin 13
  //   nG0: pin 3
  //   nP0: pin 4
  //   nG1: pin 1
  //   nP1: pin 2
  //   nG2: pin 14
  //   nP2: pin 15
  //   nG3: pin 5
  //   nP3: pin 6
  //   nP: pin 7
  //   nG: pin 10
  //   C_n_plus_z: pin 9
  //   C_n_plus_y: pin 11
  //   C_n_plus_x: pin 12
  //   VCC: pin 16, default 1
  //   GND: pin 8
endmodule

/* Test case:
C_n ~G0 ~P0 ~G1 ~P1 ~G2 ~P2 ~G3 ~P3 C_{n+x} C_{n+y} C_{n+z} ~G ~P
#
X   1   1   X   X   X   X   X   X   0       X       X       X  X
0   1   X   X   X   X   X   X   X   0       X       X       X  X
X   0   X   X   X   X   X   X   X   1       X       X       X  X
1   X   0   X   X   X   X   X   X   1       X       X       X  X
#
X   X   X   1   1   X   X   X   X   X       0       X       X  X
X   1   1   1   X   X   X   X   X   X       0       X       X  X
0   1   X   1   X   X   X   X   X   X       0       X       X  X
X   X   X   0   X   X   X   X   X   X       1       X       X  X
X   0   X   X   0   X   X   X   X   X       1       X       X  X
1   X   0   X   0   X   X   X   X   X       1       X       X  X
#
X   X   X   X   X   1   1   X   X   X       X       0       X  X
X   X   X   1   1   1   X   X   X   X       X       0       X  X
X   1   1   1   X   1   X   X   X   X       X       0       X  X
0   1   X   1   X   1   X   X   X   X       X       0       X  X
X   X   X   X   X   0   X   X   X   X       X       1       X  X
X   X   X   0   X   X   0   X   X   X       X       1       X  X
X   0   X   X   0   X   0   X   X   X       X       1       X  X
1   X   0   X   0   X   0   X   X   X       X       1       X  X
#
X   X   X   X   X   X   X   1   1   X       X       X       1  X
X   X   X   X   X   1   1   1   X   X       X       X       1  X
X   X   X   1   1   1   X   1   X   X       X       X       1  X
X   1   X   1   X   1   X   1   X   X       X       X       1  X
X   X   X   X   X   X   X   0   X   X       X       X       0  X
X   X   X   X   X   0   X   X   0   X       X       X       0  X
X   X   X   0   X   X   0   X   0   X       X       X       0  X
X   0   X   X   0   X   0   X   0   X       X       X       0  X
#
X   X   1   X   X   X   X   X   X   X       X       X       X  1
X   X   X   X   1   X   X   X   X   X       X       X       X  1
X   X   X   X   X   X   1   X   X   X       X       X       X  1
X   X   X   X   X   X   X   X   1   X       X       X       X  1
X   X   0   X   0   X   0   X   0   X       X       X       X  0
*/
