// Digital circuit 74280.dig as structural Verilog
// 9 bit Odd-Even Parity Generator-Checker
module _74280 (
  input  A,
  input  B,
  input  C,
  input  D,
  input  E,
  input  F,
  input  G,
  input  H,
  input  I,
  input  VCC,
  input  GND,
  output EVEN,
  output ODD
);

  wire undriven, undriven_2, undriven_3, undriven_4, undriven_5, undriven_6, undriven_7, undriven_8,
       undriven_9, undriven_10, undriven_11, undriven_12, undriven_13, undriven_14, undriven_15, undriven_16,
       undriven_17, undriven_18, undriven_19, undriven_20, undriven_21, undriven_22, undriven_23,
       undriven_24, undriven_25, undriven_26, undriven_27, undriven_28, undriven_29, undriven_30,
       undriven_31, undriven_32, undriven_33, undriven_34, undriven_35, undriven_36, undriven_37,
       undriven_38, undriven_39, undriven_40, undriven_41, undriven_42, undriven_43, undriven_44;

  // Not not_1 has open pins: in=A, out=open
  // Not not_2 has open pins: in=B, out=open
  // Not not_3 has open pins: in=C, out=open
  // Not not_4 has open pins: in=D, out=open
  // Not not_5 has open pins: in=E, out=open
  // Not not_6 has open pins: in=F, out=open
  // Not not_7 has open pins: in=G, out=open
  // Not not_8 has open pins: in=H, out=open
  // Not not_9 has open pins: in=I, out=open
  // Not not_10 has open pins: in=undriven, out=open
  // Not not_11 has open pins: in=undriven_4, out=open
  // Not not_12 has open pins: in=undriven_7, out=open
  // Not not_13 has open pins: in=undriven_2, out=open
  // Not not_14 has open pins: in=undriven_5, out=open
  // Not not_15 has open pins: in=undriven_8, out=open
  // Not not_16 has open pins: in=undriven_3, out=open
  // Not not_17 has open pins: in=undriven_6, out=open
  // Not not_18 has open pins: in=undriven_9, out=open
  // And and_1 has open pins: In_1=undriven_4, In_2=undriven_7, In_3=undriven_10, out=open
  // And and_2 has open pins: In_1=undriven, In_2=undriven_7, In_3=undriven_13, out=open
  // And and_3 has open pins: In_1=undriven_4, In_2=undriven, In_3=undriven_16, out=open
  // And and_4 has open pins: In_1=undriven_16, In_2=undriven_13, In_3=undriven_10, out=open
  // And and_5 has open pins: In_1=undriven_5, In_2=undriven_8, In_3=undriven_11, out=open
  // And and_6 has open pins: In_1=undriven_2, In_2=undriven_8, In_3=undriven_14, out=open
  // And and_7 has open pins: In_1=undriven_5, In_2=undriven_2, In_3=undriven_17, out=open
  // And and_8 has open pins: In_1=undriven_17, In_2=undriven_14, In_3=undriven_11, out=open
  // And and_9 has open pins: In_1=undriven_6, In_2=undriven_9, In_3=undriven_12, out=open
  // And and_10 has open pins: In_1=undriven_3, In_2=undriven_9, In_3=undriven_15, out=open
  // And and_11 has open pins: In_1=undriven_6, In_2=undriven_3, In_3=undriven_18, out=open
  // And and_12 has open pins: In_1=undriven_18, In_2=undriven_15, In_3=undriven_12, out=open
  // NOr nor_1 has open pins: In_1=undriven_19, In_2=undriven_20, In_3=undriven_25, In_4=undriven_28, out=open
  // NOr nor_2 has open pins: In_1=undriven_21, In_2=undriven_22, In_3=undriven_26, In_4=undriven_29, out=open
  // NOr nor_3 has open pins: In_1=undriven_23, In_2=undriven_24, In_3=undriven_27, In_4=undriven_30, out=open
  // Not not_19 has open pins: in=undriven_31, out=open
  // Not not_20 has open pins: in=undriven_32, out=open
  // Not not_21 has open pins: in=undriven_33, out=open
  // And and_13 has open pins: In_1=undriven_32, In_2=undriven_33, In_3=undriven_34, out=open
  // And and_14 has open pins: In_1=undriven_31, In_2=undriven_33, In_3=undriven_35, out=open
  // And and_15 has open pins: In_1=undriven_31, In_2=undriven_32, In_3=undriven_36, out=open
  // And and_16 has open pins: In_1=undriven_34, In_2=undriven_35, In_3=undriven_36, out=open
  // And and_17 has open pins: In_1=undriven_35, In_2=undriven_36, In_3=undriven_31, out=open
  // And and_18 has open pins: In_1=undriven_32, In_2=undriven_34, In_3=undriven_36, out=open
  // And and_19 has open pins: In_1=undriven_35, In_2=undriven_34, In_3=undriven_33, out=open
  // And and_20 has open pins: In_1=undriven_32, In_2=undriven_31, In_3=undriven_33, out=open
  PowerSupply powersupply_1 (.VDD(VCC), .GND(GND));
  // NOr nor_4 has open pins: In_1=undriven_37, In_2=undriven_38, In_3=undriven_41, In_4=undriven_43, out=open
  // NOr nor_5 has open pins: In_1=undriven_39, In_2=undriven_40, In_3=undriven_42, In_4=undriven_44, out=open

  // Notes on the sheet:
  //   A: pin 8
  //   B: pin 9
  //   C: pin 10
  //   D: pin 11
  //   E: pin 12
  //   F: pin 13
  //   G: pin 1
  //   H: pin 2
  //   I: pin 4
  //   EVEN: pin 5
  //   ODD: pin 6
  //   VCC: pin 14, default 1
  //   GND: pin 7
endmodule

/* Test case:
A B C D E F G H I EVEN ODD

loop (n,256)
  let p=((n&1)^((n>>1)&1)^((n>>2)&1)^((n>>3)&1)^((n>>4)&1)^((n>>5)&1)^((n>>6)&1)^((n>>7)&1)^((n>>8)&1));
  bits(9,n) (~p) (p)
end loop
*/
