// Digital circuit 74382.dig as structural Verilog
// 4-Bit Arithmetic Logic Unit
module _74382 (
  input  Cin,
  input  B0,
  input  A0,
  input  B1,
  input  A1,
  input  B2,
  input  A2,
  input  B3,
  input  A3,
  input  S0,
  input  S1,
  input  S2,
  input  VCC,
  input  GND,
  output CO,
  output OVR,
  output F0,
  output F1,
  output F2,
  output F3
);

  wire undriven, undriven_2, undriven_3, undriven_4, undriven_5, undriven_6, undriven_7, undriven_8,
       undriven_9, undriven_10, undriven_11, undriven_12, undriven_13, undriven_14, undriven_15, undriven_16,
       undriven_17, undriven_18, undriven_19, undriven_20, undriven_21, undriven_22, undriven_23,
       undriven_24, undriven_25, undriven_26, undriven_27, undriven_28, undriven_29, undriven_30,
       undriven_31, undriven_32, undriven_33, undriven_34, undriven_35, undriven_36, undriven_37,
       undriven_38, undriven_39, undriven_40, undriven_41, undriven_42, undriven_43, undriven_44,
       undriven_45, undriven_46, undriven_47, undriven_48, undriven_49, undriven_50, undriven_51,
       undriven_52, undriven_53, undriven_54, undriven_55, undriven_56, undriven_57, undriven_58,
       undriven_59, undriven_60, undriven_61, undriven_62, undriven_63, undriven_64, undriven_65,
       undriven_66, undriven_67, undriven_68, undriven_69, undriven_70, undriven_71, undriven_72,
       undriven_73, undriven_74, undriven_75, undriven_76, undriven_77, undriven_78, undriven_79;

  // Not not_1 has open pins: in=S0, out=open
  // Not not_2 has open pins: in=S1, out=open
  // Not not_3 has open pins: in=S2, out=open
  // Not not_4 has open pins: in=undriven, out=open
  // Not not_5 has open pins: in=undriven_13, out=open
  // Not not_6 has open pins: in=undriven_18, out=open
  // Not not_7 has open pins: in=B0, out=open
  // Not not_8 has open pins: in=A0, out=open
  // Not not_9 has open pins: in=B1, out=open
  // Not not_10 has open pins: in=A1, out=open
  // Not not_11 has open pins: in=B2, out=open
  // Not not_12 has open pins: in=A2, out=open
  // Not not_13 has open pins: in=B3, out=open
  // Not not_14 has open pins: in=A3, out=open
  // NAnd nand_1 has open pins: In_1=undriven, In_2=undriven_13, out=open
  // NAnd nand_2 has open pins: In_1=undriven_13, In_2=undriven_18, out=open
  // And and_1 has open pins: In_1=undriven_3, In_2=undriven_7, In_3=undriven_14, In_4=undriven_12, out=open
  // And and_2 has open pins: In_1=undriven_11, In_2=undriven_14, In_3=undriven_15, In_4=undriven_7, In_5=A0, out=open
  // And and_3 has open pins: In_1=undriven_12, In_2=undriven_15, In_3=B0, In_4=undriven_3, out=open
  // And and_4 has open pins: In_1=undriven_3, In_2=undriven_7, In_3=undriven_11, In_4=undriven_15, In_5=undriven_17, out=open
  // And and_5 has open pins: In_1=undriven_12, In_2=undriven_14, In_3=undriven_7, In_4=A0, out=open
  // And and_6 has open pins: In_1=undriven_12, In_2=undriven_14, In_3=B0, In_4=undriven_3, out=open
  // And and_7 has open pins: In_1=undriven_11, In_2=undriven_15, In_3=B0, In_4=A0, out=open
  // And and_8 has open pins: In_1=undriven_4, In_2=undriven_8, In_3=undriven_14, In_4=undriven_12, out=open
  // And and_9 has open pins: In_1=undriven_11, In_2=undriven_14, In_3=undriven_15, In_4=undriven_8, In_5=A1, out=open
  // And and_10 has open pins: In_1=undriven_12, In_2=undriven_15, In_3=B1, In_4=undriven_4, out=open
  // And and_11 has open pins: In_1=undriven_4, In_2=undriven_8, In_3=undriven_11, In_4=undriven_15, In_5=undriven_17, out=open
  // And and_12 has open pins: In_1=undriven_12, In_2=undriven_14, In_3=undriven_8, In_4=A1, out=open
  // And and_13 has open pins: In_1=undriven_12, In_2=undriven_14, In_3=B1, In_4=undriven_4, out=open
  // And and_14 has open pins: In_1=undriven_11, In_2=undriven_15, In_3=B1, In_4=A1, out=open
  // And and_15 has open pins: In_1=undriven_5, In_2=undriven_9, In_3=undriven_14, In_4=undriven_12, out=open
  // And and_16 has open pins: In_1=undriven_11, In_2=undriven_14, In_3=undriven_15, In_4=undriven_9, In_5=A2, out=open
  // And and_17 has open pins: In_1=undriven_12, In_2=undriven_15, In_3=B2, In_4=undriven_5, out=open
  // And and_18 has open pins: In_1=undriven_5, In_2=undriven_9, In_3=undriven_11, In_4=undriven_15, In_5=undriven_17, out=open
  // And and_19 has open pins: In_1=undriven_12, In_2=undriven_14, In_3=undriven_9, In_4=A2, out=open
  // And and_20 has open pins: In_1=undriven_12, In_2=undriven_14, In_3=B2, In_4=undriven_5, out=open
  // And and_21 has open pins: In_1=undriven_11, In_2=undriven_15, In_3=B2, In_4=A2, out=open
  // And and_22 has open pins: In_1=undriven_6, In_2=undriven_10, In_3=undriven_14, In_4=undriven_12, out=open
  // And and_23 has open pins: In_1=undriven_11, In_2=undriven_14, In_3=undriven_15, In_4=undriven_10, In_5=A3, out=open
  // And and_24 has open pins: In_1=undriven_12, In_2=undriven_15, In_3=B3, In_4=undriven_6, out=open
  // And and_25 has open pins: In_1=undriven_6, In_2=undriven_10, In_3=undriven_11, In_4=undriven_15, In_5=undriven_17, out=open
  // And and_26 has open pins: In_1=undriven_12, In_2=undriven_14, In_3=undriven_10, In_4=A3, out=open
  // And and_27 has open pins: In_1=undriven_12, In_2=undriven_14, In_3=B3, In_4=undriven_6, out=open
  // And and_28 has open pins: In_1=undriven_11, In_2=undriven_15, In_3=B3, In_4=A3, out=open
  // And and_29 has open pins: In_1=undriven, In_2=undriven_13, out=open
  // NAnd nand_3 has open pins: In_1=undriven, In_2=undriven_16, out=open
  // NAnd nand_4 has open pins: In_1=undriven_2, In_2=undriven_16, In_3=undriven_18, out=open
  // And and_30 has open pins: In_1=undriven_13, In_2=undriven_19, out=open
  // And and_31 has open pins: In_1=undriven, In_2=undriven_19, out=open
  // NOr nor_1 has open pins: In_1=undriven_20, In_2=undriven_21, In_3=undriven_41, out=open
  // NOr nor_2 has open pins: In_1=undriven_22, In_2=undriven_23, In_3=undriven_36, In_4=undriven_42, out=open
  // NOr nor_3 has open pins: In_1=undriven_24, In_2=undriven_25, In_3=undriven_43, out=open
  // NOr nor_4 has open pins: In_1=undriven_26, In_2=undriven_27, In_3=undriven_37, In_4=undriven_44, out=open
  // NOr nor_5 has open pins: In_1=undriven_28, In_2=undriven_29, In_3=undriven_45, out=open
  // NOr nor_6 has open pins: In_1=undriven_30, In_2=undriven_31, In_3=undriven_38, In_4=undriven_46, out=open
  // NOr nor_7 has open pins: In_1=undriven_32, In_2=undriven_33, In_3=undriven_47, out=open
  // NOr nor_8 has open pins: In_1=undriven_34, In_2=undriven_35, In_3=undriven_39, In_4=undriven_48, out=open
  // NOr nor_9 has open pins: In_1=undriven_49, In_2=undriven_40, out=open
  // NOr nor_10 has open pins: In_1=undriven_58, In_2=undriven_19, out=open
  // And and_32 has open pins: In_1=Cin, In_2=undriven_54, In_3=undriven_59, out=open
  // And and_33 has open pins: In_1=undriven_54, In_2=undriven_55, In_3=undriven_59, out=open
  // And and_34 has open pins: In_1=Cin, In_2=undriven_54, In_3=undriven_56, In_4=undriven_59, out=open
  // And and_35 has open pins: In_1=undriven_54, In_2=undriven_56, In_3=undriven_55, In_4=undriven_59, out=open
  // And and_36 has open pins: In_1=undriven_56, In_2=undriven_57, In_3=undriven_59, out=open
  // And and_37 has open pins: In_1=Cin, In_2=undriven_54, In_3=undriven_56, In_4=undriven_50, In_5=undriven_59, out=open
  // And and_38 has open pins: In_1=undriven_54, In_2=undriven_56, In_3=undriven_50, In_4=undriven_55, In_5=undriven_59, out=open
  // And and_39 has open pins: In_1=undriven_56, In_2=undriven_50, In_3=undriven_57, In_4=undriven_59, out=open
  // And and_40 has open pins: In_1=undriven_50, In_2=undriven_51, In_3=undriven_59, out=open
  // And and_41 has open pins: In_1=undriven_54, In_2=undriven_56, In_3=undriven_50, In_4=undriven_52, In_5=undriven_55, out=open
  // And and_42 has open pins: In_1=undriven_56, In_2=undriven_50, In_3=undriven_52, In_4=undriven_57, out=open
  // And and_43 has open pins: In_1=undriven_50, In_2=undriven_52, In_3=undriven_51, out=open
  // And and_44 has open pins: In_1=undriven_52, In_2=undriven_53, out=open
  // NAnd nand_5 has open pins: In_1=Cin, In_2=undriven_54, In_3=undriven_56, In_4=undriven_50, In_5=undriven_52, out=open
  PowerSupply powersupply_1 (.VDD(VCC), .GND(GND));
  // NAnd nand_6 has open pins: In_1=Cin, In_2=undriven_59, out=open
  // NOr nor_11 has open pins: In_1=undriven_60, In_2=undriven_66, out=open
  // NOr nor_12 has open pins: In_1=undriven_63, In_2=undriven_64, In_3=undriven_65, In_4=undriven_69, out=open
  // NOr nor_13 has open pins: In_1=undriven_61, In_2=undriven_62, In_3=undriven_72, out=open
  // NOr nor_14 has open pins: In_1=undriven_67, In_2=undriven_68, In_3=undriven_70, In_4=undriven_71, out=open
  // XOr xor_1 has open pins: In_1=undriven_76, In_2=undriven_55, out=open
  // XOr xor_2 has open pins: In_1=undriven_74, In_2=undriven_57, out=open
  // And and_45 has open pins: In_1=undriven_77, In_2=undriven_73, out=open
  // NAnd nand_7 has open pins: In_1=undriven_77, In_2=undriven_73, out=open
  // XOr xor_3 has open pins: In_1=undriven_78, In_2=undriven_51, out=open
  // XOr xor_4 has open pins: In_1=undriven_75, In_2=undriven_53, out=open
  // XOr xor_5 has open pins: In_1=undriven_75, In_2=undriven_79, out=open

  // Notes on the sheet:
  //   CO: pin 14
  //   OVR: pin 13
  //   F0: pin 8
  //   F1: pin 9
  //   F2: pin 11
  //   F3: pin 12
  //   Cin: pin 15
  //   B0: pin 4
  //   A0: pin 3
  //   B1: pin 2
  //   A1: pin 1
  //   B2: pin 18
  //   A2: pin 19
  //   B3: pin 16
  //   A3: pin 17
  //   S0: pin 5
  //   S1: pin 6
  //   S2: pin 7
  //   VCC: pin 20, default 1
  //   GND: pin 10
endmodule

/* Test case Fairchild:
S0 S1 S2  Cin  A3 A2 A1 A0  B3 B2 B1 B0  F0 F1 F2 F3 OVR CO
# Clear
0  0  0   0    x  x  x  x   x  x  x  x   0  0  0  0   1   1
# B MINUS A
1  0  0   0    0  0  0  0   0  0  0  0   1  1  1  1   0   0
1  0  0   0    0  0  0  0   1  1  1  1   0  1  1  1   0   1
1  0  0   0    1  1  1  1   0  0  0  0   0  0  0  0   0   0
1  0  0   0    1  1  1  1   1  1  1  1   1  1  1  1   0   0
1  0  0   1    0  0  0  0   0  0  0  0   0  0  0  0   0   1
1  0  0   1    0  0  0  0   1  1  1  1   1  1  1  1   0   1
1  0  0   1    1  1  1  1   0  0  0  0   1  0  0  0   0   0
1  0  0   1    1  1  1  1   1  1  1  1   0  0  0  0   0   1
# A MINUS B
0  1  0   0    0  0  0  0   0  0  0  0   1  1  1  1   0   0
0  1  0   0    0  0  0  0   1  1  1  1   0  0  0  0   0   0
0  1  0   0    1  1  1  1   0  0  0  0   0  1  1  1   0   1
0  1  0   0    1  1  1  1   1  1  1  1   1  1  1  1   0   0
0  1  0   1    0  0  0  0   0  0  0  0   0  0  0  0   0   1
0  1  0   1    0  0  0  0   1  1  1  1   1  0  0  0   0   0
0  1  0   1    1  1  1  1   0  0  0  0   1  1  1  1   0   1
0  1  0   1    1  1  1  1   1  1  1  1   0  0  0  0   0   1
# A PLUS B
1  1  0   0    0  0  0  0   0  0  0  0   0  0  0  0   0   0
1  1  0   0    0  0  0  0   1  1  1  1   1  1  1  1   0   0
1  1  0   0    1  1  1  1   0  0  0  0   1  1  1  1   0   0
1  1  0   0    1  1  1  1   1  1  1  1   0  1  1  1   0   1
1  1  0   1    0  0  0  0   0  0  0  0   1  0  0  0   0   0
1  1  0   1    0  0  0  0   1  1  1  1   0  0  0  0   0   1
1  1  0   1    1  1  1  1   0  0  0  0   0  0  0  0   0   1
1  1  0   1    1  1  1  1   1  1  1  1   1  1  1  1   0   1
# A XOR B
0  0  1   x    0  0  0  0   0  0  0  0   0  0  0  0   0   0
0  0  1   x    0  0  0  0   1  1  1  1   1  1  1  1   0   0
0  0  1   0    1  1  1  1   0  0  0  0   1  1  1  1   0   0
0  0  1   x    1  1  1  1   1  1  1  1   0  0  0  0   1   1
0  0  1   1    1  1  1  1   0  0  0  0   1  1  1  1   1   1
# A OR B
1  0  1   x    0  0  0  0   0  0  0  0   0  0  0  0   0  0
1  0  1   x    0  0  0  0   1  1  1  1   1  1  1  1   0  0
1  0  1   x    1  1  1  1   0  0  0  0   1  1  1  1   0  0
1  0  1   0    1  1  1  1   1  1  1  1   1  1  1  1   0  0
1  0  1   1    1  1  1  1   1  1  1  1   1  1  1  1   1  1
# A AND B
0  1  1   x    0  0  0  0   0  0  0  0   0  0  0  0   1  1
0  1  1   x    0  0  0  0   1  1  1  1   0  0  0  0   0  0
0  1  1   x    1  1  1  1   0  0  0  0   0  0  0  0   1  1
0  1  1   0    1  1  1  1   1  1  1  1   1  1  1  1   0  0
0  1  1   1    1  1  1  1   1  1  1  1   1  1  1  1   1  1
# Preset
1  1  1   x    0  0  0  0   0  0  0  0   1  1  1  1   0  0
1  1  1   x    0  0  0  0   1  1  1  1   1  1  1  1   0  0
1  1  1   x    1  1  1  1   0  0  0  0   1  1  1  1   0  0
1  1  1   0    1  1  1  1   1  1  1  1   1  1  1  1   0  0
1  1  1   1    1  1  1  1   1  1  1  1   1  1  1  1   1  1
*/

/* Test case Add:
S0 S1 S2  Cin  A3 A2 A1 A0  B3 B2 B1 B0  CO F3 F2 F1 F0 
# A PLUS B
loop (a,16)
loop (b,16)
1  1  0   0    bits(4,a)    bits(4,b)    bits(5,a+b)    
1  1  0   1    bits(4,a)    bits(4,b)    bits(5,a+b+1)    
end loop
end loop
*/

/* Test case Sub:
S0 S1 S2  Cin  A3 A2 A1 A0  B3 B2 B1 B0  CO F3 F2 F1 F0
# A MINUS B
loop (a,16)
loop (b,16)
0  1  0   1    bits(4,a)    bits(4,b)  bits(1,~((a-b)>>4))    bits(4,a-b)    
0  1  0   0    bits(4,a)    bits(4,b)  bits(1,~((a-b-1)>>4))  bits(4,a-b-1)  
end loop
end loop
*/

/* Test case Sub Signed:
S0 S1 S2  Cin  A3 A2 A1 A0  B3 B2 B1 B0  F3 F2 F1 F0 OVR
# A MINUS B
loop (ua,16)
loop (ub,16)
let a = ua - 8;
let b = ub - 8;
let d = a - b;
let dc = a - b - 1;
0  1  0   1    bits(4,a)    bits(4,b)   bits(4,d)    (!(signExt(4,d)=d))
0  1  0   0    bits(4,a)    bits(4,b)   bits(4,dc)   (!(signExt(4,dc)=dc))
end loop
end loop
*/
