// Digital circuit 74688.dig as structural Verilog
// 8-bit identity comparator
module _74688 (
  input  P_0,
  input  Q_0,
  input  P_1,
  input  Q_1,
  input  P_2,
  input  Q_2,
  input  P_3,
  input  Q_3,
  input  P_4,
  input  Q_4,
  input  P_5,
  input  Q_5,
  input  P_6,
  input  Q_6,
  input  P_7,
  input  Q_7,
  input  nOE,
  input  VCC,
  input  GND,
  output nEQ
);

  wire undriven, undriven_2, undriven_3, undriven_4, undriven_5, undriven_6, undriven_7, undriven_8,
       undriven_9, undriven_10, undriven_11;

  // XOr xor_1 has open pins: In_1=P_0, In_2=Q_0, out=open
  // XOr xor_2 has open pins: In_1=P_1, In_2=Q_1, out=open
  // XOr xor_3 has open pins: In_1=P_2, In_2=Q_2, out=open
  // XOr xor_4 has open pins: In_1=P_3, In_2=Q_3, out=open
  // XOr xor_5 has open pins: In_1=P_4, In_2=Q_4, out=open
  // XOr xor_6 has open pins: In_1=P_5, In_2=Q_5, out=open
  // XOr xor_7 has open pins: In_1=P_6, In_2=Q_6, out=open
  // XOr xor_8 has open pins: In_1=P_7, In_2=Q_7, out=open
  PowerSupply powersupply_1 (.VDD(VCC), .GND(GND));
  // NOr nor_1 has open pins: In_1=undriven, In_2=undriven_2, In_3=undriven_6, out=open
  // NOr nor_2 has open pins: In_1=undriven_3, In_2=undriven_4, In_3=undriven_7, out=open
  // NOr nor_3 has open pins: In_1=undriven_5, In_2=undriven_8, out=open
  // NAnd nand_1 has open pins: In_1=nOE, In_2=undriven_9, In_3=undriven_10, In_4=undriven_11, out=open

  // Notes on the sheet:
  //   P_0: pin 2
  //   Q_0: pin 3
  //   P_1: pin 4
  //   Q_1: pin 5
  //   P_2: pin 6
  //   Q_2: pin 7
  //   P_3: pin 8
  //   Q_3: pin 9
  //   P_4: pin 11
  //   Q_4: pin 12
  //   P_5: pin 13
  //   Q_5: pin 14
  //   P_6: pin 15
  //   Q_6: pin 16
  //   P_7: pin 17
  //   Q_7: pin 18
  //   nOE: pin 1
  //   nEQ: pin 19
  //   VCC: pin 20, default 1
  //   GND: pin 10
endmodule

/* Test case:
~OE P_7 P_6 P_5 P_4 P_3 P_2 P_1 P_0 Q_7 Q_6 Q_5 Q_4 Q_3 Q_2 Q_1 Q_0 ~EQ
loop(P,16)
loop(Q,16)
0 bits(8,P) bits(8,Q) (~(P=Q))
1 bits(8,P) bits(8,Q) (1)
end loop
end loop
*/
