// Digital circuit 7480.dig as structural Verilog
// Gated Full Adder with Complementary Inputs
// and Complementary Sum Outputs
module _7480 (
  input  A1,
  input  A2,
  input  AC,
  input  A,
  input  B1,
  input  B2,
  input  BC,
  input  B,
  input  Cn,
  input  VCC,
  input  GND,
  output nCn_plus_1,
  output S,
  output nS
);

  wire undriven, undriven_2, undriven_3, undriven_4, undriven_5, undriven_6, undriven_7;

  PowerSupply powersupply_1 (.VDD(VCC), .GND(GND));
  // And and_1 has open pins: In_1=A1, In_2=A2, out=open
  // And and_2 has open pins: In_1=B1, In_2=B2, out=open
  // Or or_1 has open pins: In_1=undriven, In_2=AC, In_3=A, out=open
  // Or or_2 has open pins: In_1=undriven_2, In_2=BC, In_3=B, out=open
  // And and_3 has open pins: In_1=undriven_3, In_2=undriven_4, out=open
  // XOr xor_1 has open pins: In_1=undriven_3, In_2=undriven_4, out=open
  // And and_4 has open pins: In_1=undriven_6, In_2=Cn, out=open
  // XOr xor_2 has open pins: In_1=undriven_6, In_2=Cn, out=open
  // NOr nor_1 has open pins: In_1=undriven_5, In_2=undriven_7, out=open
  // Not not_1 has open pins: in=S, out=open

  // Notes on the sheet:
  //   A1: pin 8
  //   A2: pin 9
  //   AC: pin 11
  //   A: pin 10
  //   B1: pin 12
  //   B2: pin 13
  //   BC: pin 2
  //   B: pin 1
  //   Cn: pin 3
  //   nCn_plus_1: pin 4
  //   S: pin 6
  //   nS: pin 5
  //   VCC: pin 14, default 1
  //   GND: pin 7
endmodule

/* Test case:
B* A* Cn AC BC ~Cn+1 S ~S
1  1  0  1  1  1     0  1
1  1  0  1  0  1     1  0
1  1  0  0  1  1     1  0
1  1  0  0  0  0     0  1
1  1  1  1  1  1     1  0
1  1  1  1  0  0     0  1
1  1  1  0  1  0     0  1
1  1  1  0  0  0     1  0
*/
