// Digital circuit 7483Real.dig as structural Verilog
// 4-bit binary full adder, real gates
module _7483Real (
  input  C0,
  input  B1,
  input  B2,
  input  B3,
  input  B4,
  input  A1,
  input  A2,
  input  A3,
  input  A4,
  input  VCC,
  input  GND,
  output S1,
  output S2,
  output S3,
  output S4,
  output C4
);

  wire undriven, undriven_2, undriven_3, undriven_4, undriven_5, undriven_6, undriven_7, undriven_8,
       undriven_9, undriven_10, undriven_11, undriven_12, undriven_13, undriven_14, undriven_15, undriven_16,
       undriven_17, undriven_18, undriven_19, undriven_20, undriven_21, undriven_22, undriven_23,
       undriven_24, undriven_25;

  PowerSupply powersupply_1 (.VDD(VCC), .GND(GND));
  // Or or_1 has open pins: In_1=B4, In_2=A4, out=open
  // And and_1 has open pins: In_1=B4, In_2=A4, out=open
  // Or or_2 has open pins: In_1=B3, In_2=A3, out=open
  // And and_2 has open pins: In_1=B3, In_2=A3, out=open
  // Or or_3 has open pins: In_1=B2, In_2=A2, out=open
  // And and_3 has open pins: In_1=B2, In_2=A2, out=open
  // Or or_4 has open pins: In_1=B1, In_2=A1, out=open
  // And and_4 has open pins: In_1=B1, In_2=A1, out=open
  // And and_5 has open pins: In_1=C0, In_2=undriven_5, In_3=undriven_3, In_4=undriven_2, In_5=undriven, out=open
  // And and_6 has open pins: In_1=undriven_4, In_2=undriven, In_3=undriven_2, In_4=undriven_3, out=open
  // And and_7 has open pins: In_1=undriven_20, In_2=undriven_2, In_3=undriven, out=open
  // And and_8 has open pins: In_1=undriven, In_2=undriven_21, out=open
  // XOr xor_1 has open pins: In_1=undriven, In_2=undriven_22, out=open
  // And and_9 has open pins: In_1=C0, In_2=undriven_5, In_3=undriven_3, In_4=undriven_2, out=open
  // And and_10 has open pins: In_1=undriven_3, In_2=undriven_2, In_3=undriven_4, out=open
  // And and_11 has open pins: In_1=undriven_2, In_2=undriven_20, out=open
  // XOr xor_2 has open pins: In_1=undriven_2, In_2=undriven_21, out=open
  // And and_12 has open pins: In_1=C0, In_2=undriven_5, In_3=undriven_3, out=open
  // And and_13 has open pins: In_1=undriven_3, In_2=undriven_4, out=open
  // XOr xor_3 has open pins: In_1=undriven_3, In_2=undriven_20, out=open
  // And and_14 has open pins: In_1=undriven_5, In_2=C0, out=open
  // XOr xor_4 has open pins: In_1=undriven_5, In_2=undriven_4, out=open
  // Or or_5 has open pins: In_1=undriven_19, In_2=undriven_18, In_3=undriven_17, In_4=undriven_16, In_5=undriven_22, out=open
  // Or or_6 has open pins: In_1=undriven_14, In_2=undriven_13, In_3=undriven_12, In_4=undriven_21, out=open
  // Or or_7 has open pins: In_1=undriven_10, In_2=undriven_6, In_3=undriven_20, out=open
  // Or or_8 has open pins: In_1=undriven_8, In_2=undriven_4, out=open
  // XOr xor_5 has open pins: In_1=undriven_11, In_2=undriven_24, out=open
  // XOr xor_6 has open pins: In_1=undriven_7, In_2=undriven_23, out=open
  // XOr xor_7 has open pins: In_1=undriven_9, In_2=C0, out=open
  // XOr xor_8 has open pins: In_1=undriven_15, In_2=undriven_25, out=open

  // Notes on the sheet:
  //   C0: pin 13
  //   B1: pin 11
  //   B2: pin 7
  //   S1: pin 9
  //   B3: pin 4
  //   B4: pin 16
  //   S2: pin 6
  //   S3: pin 2
  //   A1: pin 10
  //   A2: pin 8
  //   A3: pin 3
  //   A4: pin 1
  //   S4: pin 15
  //   C4: pin 14
  //   VCC: pin 5, default 1
  //   GND: pin 12
endmodule

/* Test case:
# A complete test of all 512 possible additions
#
# A line that begins with "repeat([i])" is repeated [i] times.
# In this case 256 times. Then the variable n goes from 0 to 255.
# So the values for the inputs are calculated depending on n.
# The function "bits([m],[v])" takes the lowest m bits from the value v.
# The expression "bits(4,n>>4)" takes the lowest 4 bits of the value
# n>>4. Then the resulting bits are used for the inputs A_3 to A_0.
# All created test vectors are shown in the result table.

             C0   A4 A3 A2 A1   B4 B3 B2 B1  C4 S4 S3 S2 S1
repeat(256)  0    bits(4,n>>4)  bits(4,n)    bits(5,(n>>4)+(n&15))
repeat(256)  1    bits(4,n>>4)  bits(4,n)    bits(5,(n>>4)+(n&15)+1)
*/
