// Digital circuit 7485.dig as structural Verilog
// 4-bit comparator
module _7485 (
  input  P_lt_Q_i,
  input  P_eq_Q_i,
  input  P_gt_Q_i,
  input  P_0,
  input  P_1,
  input  P_2,
  input  P_3,
  input  Q_0,
  input  Q_1,
  input  Q_2,
  input  Q_3,
  input  VCC,
  input  GND,
  output P_lt_Q,
  output P_eq_Q,
  output P_gt_Q
);

  wire undriven, undriven_2, undriven_3, undriven_4, undriven_5, undriven_6, undriven_7, undriven_8,
       undriven_9, undriven_10, undriven_11, undriven_12, undriven_13, undriven_14, undriven_15, undriven_16,
       undriven_17, undriven_18, undriven_19, undriven_20, undriven_21, undriven_22, undriven_23,
       undriven_24, undriven_25, undriven_26, undriven_27, undriven_28;

  PowerSupply powersupply_1 (.VDD(VCC), .GND(GND));
  // NAnd nand_1 has open pins: In_1=P_3, In_2=Q_3, out=open
  // NAnd nand_2 has open pins: In_1=P_2, In_2=Q_2, out=open
  // NAnd nand_3 has open pins: In_1=P_1, In_2=Q_1, out=open
  // NAnd nand_4 has open pins: In_1=P_0, In_2=Q_0, out=open
  // And and_1 has open pins: In_1=P_3, In_2=undriven, out=open
  // And and_2 has open pins: In_1=undriven, In_2=Q_3, out=open
  // And and_3 has open pins: In_1=P_2, In_2=undriven_2, out=open
  // And and_4 has open pins: In_1=undriven_2, In_2=Q_2, out=open
  // And and_5 has open pins: In_1=P_1, In_2=undriven_3, out=open
  // And and_6 has open pins: In_1=undriven_3, In_2=Q_1, out=open
  // And and_7 has open pins: In_1=P_0, In_2=undriven_4, out=open
  // And and_8 has open pins: In_1=undriven_4, In_2=Q_0, out=open
  // NOr nor_1 has open pins: In_1=undriven_8, In_2=undriven_12, out=open
  // NOr nor_2 has open pins: In_1=undriven_7, In_2=undriven_11, out=open
  // NOr nor_3 has open pins: In_1=undriven_5, In_2=undriven_9, out=open
  // NOr nor_4 has open pins: In_1=undriven_6, In_2=undriven_10, out=open
  // NAnd nand_5 has open pins: In_1=Q_3, In_2=undriven, out=open
  // NAnd nand_6 has open pins: In_1=Q_2, In_2=undriven_2, In_3=undriven_13, out=open
  // NAnd nand_7 has open pins: In_1=Q_1, In_2=undriven_3, In_3=undriven_13, In_4=undriven_14, out=open
  // NAnd nand_8 has open pins: In_1=Q_0, In_2=undriven_4, In_3=undriven_13, In_4=undriven_14, In_5=undriven_15, out=open
  // NAnd nand_9 has open pins: In_1=undriven_13, In_2=undriven_14, In_3=undriven_15, In_4=undriven_16, In_5=P_lt_Q_i, out=open
  // NAnd nand_10 has open pins: In_1=undriven_13, In_2=undriven_14, In_3=undriven_15, In_4=undriven_16, In_5=P_eq_Q_i, out=open
  // And and_9 has open pins: In_1=undriven_13, In_2=undriven_14, In_3=P_eq_Q_i, In_4=undriven_15, In_5=undriven_16, out=open
  // NAnd nand_11 has open pins: In_1=P_eq_Q_i, In_2=undriven_16, In_3=undriven_15, In_4=undriven_14, In_5=undriven_13, out=open
  // NAnd nand_12 has open pins: In_1=P_gt_Q_i, In_2=undriven_16, In_3=undriven_14, In_4=undriven_15, In_5=undriven_13, out=open
  // NAnd nand_13 has open pins: In_1=undriven_15, In_2=undriven_14, In_3=undriven_13, In_4=undriven_4, In_5=P_0, out=open
  // NAnd nand_14 has open pins: In_1=undriven_14, In_2=undriven_13, In_3=undriven_3, In_4=P_1, out=open
  // NAnd nand_15 has open pins: In_1=undriven_13, In_2=undriven_2, In_3=P_2, out=open
  // NAnd nand_16 has open pins: In_1=undriven, In_2=P_3, out=open
  // And and_10 has open pins: In_1=undriven_22, In_2=undriven_21, In_3=undriven_20, In_4=undriven_24, In_5=undriven_26, In_6=undriven_28, out=open
  // And and_11 has open pins: In_1=undriven_17, In_2=undriven_18, In_3=undriven_19, In_4=undriven_23, In_5=undriven_25, In_6=undriven_27, out=open

  // Notes on the sheet:
  //   P_lt_Q_i: pin 2
  //   P_eq_Q_i: pin 3
  //   P_gt_Q_i: pin 4
  //   P_lt_Q: pin 7
  //   P_eq_Q: pin 6
  //   P_gt_Q: pin 5
  //   P_0: pin 10
  //   P_1: pin 12
  //   P_2: pin 13
  //   P_3: pin 15
  //   Q_0: pin 9
  //   Q_1: pin 11
  //   Q_2: pin 14
  //   Q_3: pin 1
  //   VCC: pin 16, default 1
  //   GND: pin 8
endmodule

/* Test case:
   P<Q_i P=Q_i P>Q_i  P_3 P_2 P_1 P_0   Q_3 Q_2 Q_1 Q_0  P<Q   P=Q   P>Q
loop(P,16)
  loop(Q,16)
    0    1     0      bits(4,P)         bits(4,Q)        (P<Q) (P=Q) (P>Q)
  end loop
end loop

loop (i,16)
    0    1     0      bits(4,i)         bits(4,i)        0    1     0
    1    0     0      bits(4,i)         bits(4,i)        1    0     0
    0    0     1      bits(4,i)         bits(4,i)        0    0     1
end loop
*/
