// Digital circuit 7401.dig as structural Verilog
// quad 2-input NAND gate with open-collector outputs
module _7401 (
  input  _2A,
  input  _2B,
  input  VCC,
  input  GND,
  input  _3A,
  input  _3B,
  input  _4A,
  input  _4B,
  input  _1A,
  input  _1B,
  output _2Y,
  output _3Y,
  output _4Y,
  output _1Y
);

  wire undriven, undriven_2, undriven_3, undriven_4;

  // And and_1 has open pins: In_1=_1A, In_2=_1B, out=open
  // And and_2 has open pins: In_1=_2A, In_2=_2B, out=open
  // And and_3 has open pins: In_1=_3A, In_2=_3B, out=open
  // And and_4 has open pins: In_1=_4A, In_2=_4B, out=open
  PowerSupply powersupply_1 (.VDD(VCC), .GND(GND));
  NFET nfet_1 (.G(undriven), .D(_1Y), .S(1'b0));
  NFET nfet_2 (.G(undriven_2), .D(_2Y), .S(1'b0));
  NFET nfet_3 (.G(undriven_3), .D(_3Y), .S(1'b0));
  NFET nfet_4 (.G(undriven_4), .D(_4Y), .S(1'b0));

  // Notes on the sheet:
  //   _2A: pin 5
  //   _2B: pin 6
  //   _2Y: pin 4
  //   VCC: pin 14, default 1
  //   GND: pin 7
  //   _3A: pin 8
  //   _3B: pin 9
  //   _3Y: pin 10
  //   _4A: pin 11
  //   _4B: pin 12
  //   _4Y: pin 13
  //   _1A: pin 2
  //   _1B: pin 3
  //   _1Y: pin 1
endmodule
