// Digital circuit 7412.dig as structural Verilog
// triple 3-input NAND gate with open-collector outputs
module _7412 (
  input  _1A,
  input  _1C,
  input  _2A,
  input  _2C,
  input  _3C,
  input  _3A,
  input  _1B,
  input  _2B,
  input  _3B,
  input  VCC,
  input  GND,
  output _1Y,
  output _2Y,
  output _3Y
);

  wire undriven, undriven_2, undriven_3;

  // And and_1 has open pins: In_1=_1A, In_2=_1B, In_3=_1C, out=open
  // And and_2 has open pins: In_1=_2A, In_2=_2B, In_3=_2C, out=open
  // And and_3 has open pins: In_1=_3A, In_2=_3B, In_3=_3C, out=open
  PowerSupply powersupply_1 (.VDD(VCC), .GND(GND));
  NFET nfet_1 (.G(undriven), .D(_1Y), .S(1'b0));
  NFET nfet_2 (.G(undriven_2), .D(_2Y), .S(1'b0));
  NFET nfet_3 (.G(undriven_3), .D(_3Y), .S(1'b0));

  // Notes on the sheet:
  //   _1A: pin 1
  //   _1C: pin 13
  //   _1Y: pin 12
  //   _2A: pin 3
  //   _2C: pin 5
  //   _2Y: pin 6
  //   _3C: pin 11
  //   _3A: pin 9
  //   _3Y: pin 8
  //   _1B: pin 2
  //   _2B: pin 4
  //   _3B: pin 10
  //   VCC: pin 14, default 1
  //   GND: pin 7
endmodule
