// Digital circuit 7413.dig as structural Verilog
// dual 4-input NAND gate, Schmitt trigger
module _7413 (
  input  _1A,
  input  _1C,
  input  _2A,
  input  _2C,
  input  _1B,
  input  _2B,
  input  _1D,
  input  _2D,
  input  VCC,
  input  GND,
  output _1Y,
  output _2Y
);

  // NAnd nand_1 has open pins: In_1=_1A, In_2=_1B, In_3=_1C, In_4=_1D, out=open
  // NAnd nand_2 has open pins: In_1=_2A, In_2=_2B, In_3=_2C, In_4=_2D, out=open
  PowerSupply powersupply_1 (.VDD(VCC), .GND(GND));

  // Notes on the sheet:
  //   _1A: pin 1
  //   _1C: pin 4
  //   _1Y: pin 6
  //   _2A: pin 9
  //   _2C: pin 12
  //   _2Y: pin 8
  //   _1B: pin 2
  //   _2B: pin 10
  //   _1D: pin 5
  //   _2D: pin 13
  //   VCC: pin 14, default 1
  //   GND: pin 7
endmodule
