// Digital circuit 7414.dig as structural Verilog
// hex inverter, Schmitt trigger
module _7414 (
  input  _1A,
  input  _2A,
  input  _3A,
  input  _4A,
  input  _5A,
  input  _6A,
  input  VCC,
  input  GND,
  output _1Y,
  output _2Y,
  output _3Y,
  output _4Y,
  output _5Y,
  output _6Y
);

  // Not not_1 has open pins: in=_1A, out=open
  // Not not_2 has open pins: in=_2A, out=open
  // Not not_3 has open pins: in=_3A, out=open
  // Not not_4 has open pins: in=_4A, out=open
  // Not not_5 has open pins: in=_5A, out=open
  // Not not_6 has open pins: in=_6A, out=open
  PowerSupply powersupply_1 (.VDD(VCC), .GND(GND));

  // Notes on the sheet:
  //   _1A: pin 1
  //   _1Y: pin 2
  //   _2A: pin 3
  //   _2Y: pin 4
  //   _3A: pin 5
  //   _3Y: pin 6
  //   _4A: pin 9
  //   _4Y: pin 8
  //   _5A: pin 11
  //   _5Y: pin 10
  //   _6A: pin 13
  //   _6Y: pin 12
  //   VCC: pin 14, default 1
  //   GND: pin 7
endmodule
