// Digital circuit 74260.dig as structural Verilog
// dual 5-input NOR gate
module _74260 (
  input  _1A,
  input  _1B,
  input  _1C,
  input  _1D,
  input  _1E,
  input  _2A,
  input  _2B,
  input  _2C,
  input  _2D,
  input  _2E,
  input  VCC,
  input  GND,
  output _1Y,
  output _2Y
);

  // NOr nor_1 has open pins: In_1=_1A, In_2=_1B, In_3=_1C, In_4=_1D, In_5=_1E, out=open
  // NOr nor_2 has open pins: In_1=_2A, In_2=_2B, In_3=_2C, In_4=_2D, In_5=_2E, out=open
  PowerSupply powersupply_1 (.VDD(VCC), .GND(GND));

  // Notes on the sheet:
  //   _1A: pin 1
  //   _1B: pin 2
  //   _1C: pin 3
  //   _1D: pin 12
  //   _1E: pin 13
  //   _1Y: pin 5
  //   _2A: pin 4
  //   _2B: pin 11
  //   _2C: pin 10
  //   _2D: pin 9
  //   _2E: pin 8
  //   _2Y: pin 6
  //   VCC: pin 14, default 1
  //   GND: pin 7
endmodule
