// Digital circuit 7428.dig as structural Verilog
// quad 2-input NOR buffer
module _7428 (
  input  _1A,
  input  _1B,
  input  _2A,
  input  _2B,
  input  _3B,
  input  _3A,
  input  _4A,
  input  _4B,
  input  VCC,
  input  GND,
  output _1Y,
  output _2Y,
  output _3Y,
  output _4Y
);

  // NOr nor_1 has open pins: In_1=_1A, In_2=_1B, out=open
  // NOr nor_2 has open pins: In_1=_2A, In_2=_2B, out=open
  // NOr nor_3 has open pins: In_1=_3A, In_2=_3B, out=open
  // NOr nor_4 has open pins: In_1=_4A, In_2=_4B, out=open
  PowerSupply powersupply_1 (.VDD(VCC), .GND(GND));

  // Notes on the sheet:
  //   _1A: pin 2
  //   _1B: pin 3
  //   _1Y: pin 1
  //   _2A: pin 5
  //   _2B: pin 6
  //   _2Y: pin 4
  //   _3B: pin 9
  //   _3A: pin 8
  //   _3Y: pin 10
  //   _4A: pin 11
  //   _4B: pin 12
  //   _4Y: pin 13
  //   VCC: pin 14, default 1
  //   GND: pin 7
endmodule
