// Digital circuit 7430.dig as structural Verilog
// 8-input NAND gate
module _7430 (
  input  _1A,
  input  _1C,
  input  _1B,
  input  _1D,
  input  _1E,
  input  _1G,
  input  _1F,
  input  _1H,
  input  VCC,
  input  GND,
  output _1Y
);

  // NAnd nand_1 has open pins: In_1=_1A, In_2=_1B, In_3=_1C, In_4=_1D, In_5=_1E, In_6=_1F, In_7=_1G, In_8=_1H, out=open
  PowerSupply powersupply_1 (.VDD(VCC), .GND(GND));

  // Notes on the sheet:
  //   _1A: pin 1
  //   _1C: pin 3
  //   _1Y: pin 8
  //   _1B: pin 2
  //   _1D: pin 4
  //   _1E: pin 5
  //   _1G: pin 11
  //   _1F: pin 6
  //   _1H: pin 12
  //   VCC: pin 14, default 1
  //   GND: pin 7
endmodule
