// Digital circuit 7451.dig as structural Verilog
// 2-input/3-input AND-NOR gate
module _7451 (
  input  _1A,
  input  _1C,
  input  _1D,
  input  _1F,
  input  _1B,
  input  _1E,
  input  _2A,
  input  _2B,
  input  _2C,
  input  _2D,
  input  VCC,
  input  GND,
  output _1Q,
  output _2Q
);

  wire undriven, undriven_2, undriven_3, undriven_4;

  // And and_1 has open pins: In_1=_1A, In_2=_1B, In_3=_1C, out=open
  // And and_2 has open pins: In_1=_1D, In_2=_1E, In_3=_1F, out=open
  // And and_3 has open pins: In_1=_2A, In_2=_2B, out=open
  // And and_4 has open pins: In_1=_2C, In_2=_2D, out=open
  PowerSupply powersupply_1 (.VDD(VCC), .GND(GND));
  // NOr nor_1 has open pins: In_1=undriven, In_2=undriven_3, out=open
  // NOr nor_2 has open pins: In_1=undriven_2, In_2=undriven_4, out=open

  // Notes on the sheet:
  //   _1Q: pin 8
  //   _1A: pin 1
  //   _1C: pin 12
  //   _1D: pin 11
  //   _1F: pin 9
  //   _1B: pin 13
  //   _1E: pin 10
  //   _2Q: pin 6
  //   _2A: pin 2
  //   _2B: pin 3
  //   _2C: pin 4
  //   _2D: pin 5
  //   VCC: pin 14, default 1
  //   GND: pin 7
endmodule
