// Digital circuit 7454.dig as structural Verilog
// 2-3-2-3-line AND NOR gate
module _7454 (
  input  _1A,
  input  _1B,
  input  _3A,
  input  _3B,
  input  _2A,
  input  _2C,
  input  _2B,
  input  _4A,
  input  _4C,
  input  _4B,
  input  VCC,
  input  GND,
  output Y
);

  wire undriven, undriven_2, undriven_3, undriven_4;

  // And and_1 has open pins: In_1=_1A, In_2=_1B, out=open
  // And and_2 has open pins: In_1=_2A, In_2=_2B, In_3=_2C, out=open
  // And and_3 has open pins: In_1=_3A, In_2=_3B, out=open
  // And and_4 has open pins: In_1=_4A, In_2=_4B, In_3=_4C, out=open
  PowerSupply powersupply_1 (.VDD(VCC), .GND(GND));
  // NOr nor_1 has open pins: In_1=undriven, In_2=undriven_2, In_3=undriven_3, In_4=undriven_4, out=open

  // Notes on the sheet:
  //   Y: pin 6
  //   _1A: pin 1
  //   _1B: pin 2
  //   _3A: pin 13
  //   _3B: pin 12
  //   _2A: pin 3
  //   _2C: pin 5
  //   _2B: pin 4
  //   _4A: pin 9
  //   _4C: pin 11
  //   _4B: pin 10
  //   VCC: pin 14, default 1
  //   GND: pin 7
endmodule
