// Digital circuit 7455.dig as structural Verilog
// 2 wide 4-input AND-NOR gate
module _7455 (
  input  _1A,
  input  _1C,
  input  _1B,
  input  _1D,
  input  _2A,
  input  _2C,
  input  _2B,
  input  _2D,
  input  VCC,
  input  GND,
  output Y
);

  wire undriven, undriven_2;

  // And and_1 has open pins: In_1=_1A, In_2=_1B, In_3=_1C, In_4=_1D, out=open
  // And and_2 has open pins: In_1=_2A, In_2=_2B, In_3=_2C, In_4=_2D, out=open
  PowerSupply powersupply_1 (.VDD(VCC), .GND(GND));
  // NOr nor_1 has open pins: In_1=undriven, In_2=undriven_2, out=open

  // Notes on the sheet:
  //   Y: pin 8
  //   _1A: pin 1
  //   _1C: pin 3
  //   _1B: pin 2
  //   _1D: pin 4
  //   _2A: pin 10
  //   _2C: pin 12
  //   _2B: pin 11
  //   _2D: pin 13
  //   VCC: pin 14, default 1
  //   GND: pin 7
endmodule
