// Digital circuit 7458.dig as structural Verilog
// dual AND OR gate
module _7458 (
  input  _1A,
  input  _1B,
  input  _1C,
  input  _1D,
  input  _2D,
  input  _2F,
  input  _2E,
  input  _2A,
  input  _2C,
  input  _2B,
  input  VCC,
  input  GND,
  output _1Y,
  output _2Y
);

  wire undriven, undriven_2, undriven_3, undriven_4;

  // And and_1 has open pins: In_1=_1A, In_2=_1B, out=open
  // And and_2 has open pins: In_1=_1C, In_2=_1D, out=open
  // And and_3 has open pins: In_1=_2A, In_2=_2B, In_3=_2C, out=open
  // And and_4 has open pins: In_1=_2D, In_2=_2E, In_3=_2F, out=open
  PowerSupply powersupply_1 (.VDD(VCC), .GND(GND));
  // Or or_1 has open pins: In_1=undriven, In_2=undriven_3, out=open
  // Or or_2 has open pins: In_1=undriven_2, In_2=undriven_4, out=open

  // Notes on the sheet:
  //   _1Y: pin 6
  //   _1A: pin 2
  //   _1B: pin 3
  //   _1C: pin 4
  //   _1D: pin 5
  //   _2D: pin 11
  //   _2F: pin 9
  //   _2E: pin 10
  //   _2A: pin 1
  //   _2C: pin 12
  //   _2B: pin 13
  //   _2Y: pin 8
  //   VCC: pin 14, default 1
  //   GND: pin 7
endmodule
