// Digital circuit 74162Real.dig as structural Verilog
// decimal synchronous counter, real gates
module _74162Real (
  input  nMR,
  input  nPE,
  input  D_0,
  input  D_1,
  input  D_2,
  input  D_3,
  input  CET,
  input  CEP,
  input  CP,
  input  VCC,
  input  GND,
  output Q_0,
  output Q_1,
  output Q_2,
  output Q_3,
  output TC
);

  wire d_ff_1_nq, d_ff_2_nq, d_ff_3_nq, d_ff_4_nq, undriven, undriven_2, undriven_3, undriven_4, undriven_5,
       undriven_6, undriven_7, undriven_8, undriven_9, undriven_10, undriven_11, undriven_12, undriven_13,
       undriven_14, undriven_15, undriven_16, undriven_17, undriven_18, undriven_19, undriven_20,
       undriven_21, undriven_22, undriven_23, undriven_24, undriven_25, undriven_26, undriven_27, undriven_28;

  PowerSupply powersupply_1 (.VDD(VCC), .GND(GND));
  // NAnd nand_1 has open pins: In_1=CET, In_2=CEP, out=open
  // NOr nor_1 has open pins: In_1=nPE, In_2=undriven_28, out=open
  // Not not_1 has open pins: in=nMR, out=open
  // NOr nor_2 has open pins: In_1=undriven, In_2=undriven_28, out=open
  // Not not_2 has open pins: in=undriven_2, out=open
  // XNOr xnor_1 has open pins: In_1=d_ff_1_nq, In_2=undriven_6, out=open
  // And and_1 has open pins: In_1=undriven, In_2=D_0, out=open
  // Or or_1 has open pins: In_1=undriven_8, In_2=undriven_4, out=open
  D_FF d_ff_1 (.D(undriven_5), .C(CP), .Q(Q_0), .nQ(d_ff_1_nq));
  // And and_2 has open pins: In_1=undriven_3, In_2=undriven_7, out=open
  // NOr nor_3 has open pins: In_1=Q_3, In_2=undriven_2, In_3=d_ff_1_nq, out=open
  // And and_3 has open pins: In_1=undriven, In_2=D_1, out=open
  // Or or_2 has open pins: In_1=undriven_13, In_2=undriven_9, out=open
  D_FF d_ff_2 (.D(undriven_10), .C(CP), .Q(Q_1), .nQ(d_ff_2_nq));
  // XNOr xnor_2 has open pins: In_1=d_ff_2_nq, In_2=undriven_11, out=open
  // And and_4 has open pins: In_1=undriven_3, In_2=undriven_12, out=open
  // And and_5 has open pins: In_1=undriven, In_2=D_2, out=open
  // NOr nor_4 has open pins: In_1=d_ff_1_nq, In_2=d_ff_2_nq, In_3=undriven_2, out=open
  // XNOr xnor_3 has open pins: In_1=d_ff_3_nq, In_2=undriven_16, out=open
  // And and_6 has open pins: In_1=undriven_3, In_2=undriven_17, out=open
  // Or or_3 has open pins: In_1=undriven_18, In_2=undriven_14, out=open
  D_FF d_ff_3 (.D(undriven_15), .C(CP), .Q(Q_2), .nQ(d_ff_3_nq));
  // And and_7 has open pins: In_1=undriven, In_2=D_3, out=open
  // NOr nor_5 has open pins: In_1=d_ff_1_nq, In_2=d_ff_2_nq, In_3=d_ff_3_nq, In_4=undriven_2, out=open
  // And and_8 has open pins: In_1=d_ff_4_nq, In_2=undriven_21, out=open
  // And and_9 has open pins: In_1=undriven_24, In_2=undriven_3, out=open
  // Or or_4 has open pins: In_1=undriven_23, In_2=undriven_19, out=open
  D_FF d_ff_4 (.D(undriven_20), .C(CP), .Q(Q_3), .nQ(d_ff_4_nq));
  // NOr nor_6 has open pins: In_1=undriven_27, In_2=undriven_2, out=open
  // NOr nor_7 has open pins: In_1=undriven_26, In_2=d_ff_4_nq, out=open
  // Or or_5 has open pins: In_1=undriven_25, In_2=undriven_22, out=open
  // NOr nor_8 has open pins: In_1=d_ff_4_nq, In_2=Q_0, out=open
  // And and_10 has open pins: In_1=CET, In_2=Q_0, In_3=d_ff_2_nq, In_4=d_ff_3_nq, In_5=Q_3, out=open

  // Notes on the sheet:
  //   Q_0: flip-flop outputs, pin 14
  //   Q_1: flip-flop outputs, pin 13
  //   Q_2: flip-flop outputs, pin 12
  //   Q_3: flip-flop outputs, pin 11
  //   nMR: Reset, pin 1
  //   nPE: parallel enable input (active LOW), pin 9
  //   D_0: data inputs, pin 3
  //   D_1: data inputs, pin 4
  //   D_2: data inputs, pin 5
  //   D_3: data inputs, pin 6
  //   TC: terminal count output, pin 15
  //   CET: count enable carry input, pin 10
  //   CEP: count enable input, pin 7
  //   CP: pin 2, Hz: 2
  //   VCC: pin 16, default 1
  //   GND: pin 8
endmodule

/* Test case:
CP ~MR ~PE CET CEP   D_3 D_2 D_1 D_0 Q_3 Q_2 Q_1 Q_0

# load
loop(i,4)
loop(n,16)
C  1   0   bits(2,i) bits(4,n)   bits(4,n)
end loop
end loop

# reset
loop(i,8)
loop(n,16)
C  1   0   0   0     bits(4,n)   bits(4,n)
C  0   bits(3,i)     bits(4,n)   bits(4,0)
end loop
end loop

# count
loop(n,16)
C  1   1   1   1     bits(4,0)   bits(4,(n+1)%10)
end loop

# hold
loop(n,16)
C  1   0   0   0     bits(4,n)   bits(4,n)
C  1   1   0   0     bits(4,n)   bits(4,n)
C  1   1   1   0     bits(4,n)   bits(4,n)
C  1   1   0   1     bits(4,n)   bits(4,n)
end loop
*/
