// Digital circuit 74191.dig as structural Verilog
// Presettable synchronous 4-bit binary up/down counter
module _74191 (
  input  D0,
  input  nPL,
  input  nU_D,
  input  CP,
  input  nCE,
  input  D1,
  input  D2,
  input  D3,
  input  VCC,
  input  GND,
  output Q0,
  output Q1,
  output Q2,
  output Q3,
  output TC,
  output nRC
);

  wire jk_ff_as_1_nq, jk_ff_as_2_nq, jk_ff_as_3_nq, jk_ff_as_4_nq, undriven, undriven_2, undriven_3,
       undriven_4, undriven_5, undriven_6, undriven_7, undriven_8, undriven_9, undriven_10, undriven_11,
       undriven_12, undriven_13, undriven_14, undriven_15, undriven_16, undriven_17, undriven_18,
       undriven_19, undriven_20, undriven_21, undriven_22, undriven_23;

  // Not not_1 has open pins: in=nPL, out=open
  // Not not_2 has open pins: in=nCE, out=open
  // And and_1 has open pins: In_1=undriven_3, In_2=nU_D, out=open
  PowerSupply powersupply_1 (.VDD(VCC), .GND(GND));
  // And and_2 has open pins: In_1=nU_D, In_2=undriven_3, out=open
  // And and_3 has open pins: In_1=nU_D, In_2=Q1, In_3=Q0, In_4=Q2, In_5=Q3, out=open
  // And and_4 has open pins: In_1=nU_D, In_2=jk_ff_as_1_nq, In_3=jk_ff_as_2_nq, In_4=jk_ff_as_3_nq, In_5=jk_ff_as_4_nq, out=open
  // And and_5 has open pins: In_1=D0, In_2=undriven, out=open
  // And and_6 has open pins: In_1=D1, In_2=undriven, out=open
  // And and_7 has open pins: In_1=undriven_4, In_2=jk_ff_as_1_nq, out=open
  // And and_8 has open pins: In_1=Q0, In_2=undriven_2, out=open
  // And and_9 has open pins: In_1=D2, In_2=undriven, out=open
  // And and_10 has open pins: In_1=undriven_4, In_2=jk_ff_as_1_nq, In_3=jk_ff_as_2_nq, out=open
  // And and_11 has open pins: In_1=Q0, In_2=Q1, In_3=undriven_2, out=open
  // And and_12 has open pins: In_1=D3, In_2=undriven, out=open
  // And and_13 has open pins: In_1=undriven_4, In_2=jk_ff_as_1_nq, In_3=jk_ff_as_2_nq, In_4=jk_ff_as_3_nq, out=open
  // And and_14 has open pins: In_1=Q0, In_2=Q1, In_3=Q2, In_4=undriven_2, out=open
  // Or or_1 has open pins: In_1=undriven_12, In_2=undriven_13, out=open
  // Or or_2 has open pins: In_1=undriven_7, In_2=undriven_14, out=open
  // Or or_3 has open pins: In_1=undriven_9, In_2=undriven_15, out=open
  // Or or_4 has open pins: In_1=undriven_11, In_2=undriven_16, out=open
  // And and_15 has open pins: In_1=undriven_5, In_2=undriven, out=open
  // And and_16 has open pins: In_1=undriven_6, In_2=undriven, out=open
  // And and_17 has open pins: In_1=undriven_8, In_2=undriven, out=open
  // And and_18 has open pins: In_1=undriven_10, In_2=undriven, out=open
  // NAnd nand_1 has open pins: In_1=CP, In_2=undriven_3, In_3=TC, out=open
  JK_FF_AS jk_ff_as_1 (
    .Set(undriven_5), .J(undriven_3), .C(CP), .K(undriven_3), .Clr(undriven_17), .Q(Q0), .nQ(jk_ff_as_1_nq));
  JK_FF_AS jk_ff_as_2 (
    .Set(undriven_6), .J(undriven_21), .C(CP), .K(undriven_21), .Clr(undriven_18), .Q(Q1), .nQ(jk_ff_as_2_nq));
  JK_FF_AS jk_ff_as_3 (
    .Set(undriven_8), .J(undriven_22), .C(CP), .K(undriven_22), .Clr(undriven_19), .Q(Q2), .nQ(jk_ff_as_3_nq));
  JK_FF_AS jk_ff_as_4 (
    .Set(undriven_10), .J(undriven_23), .C(CP), .K(undriven_23), .Clr(undriven_20), .Q(Q3), .nQ(jk_ff_as_4_nq));

  // Notes on the sheet:
  //   Q0: pin 3
  //   Q1: pin 2
  //   Q2: pin 6
  //   Q3: pin 7
  //   TC: pin 12
  //   D0: pin 15
  //   nPL: pin 11
  //   nU_D: pin 5
  //   CP: pin 14
  //   nCE: pin 4
  //   nRC: pin 13
  //   D1: pin 1
  //   D2: pin 10
  //   D3: pin 9
  //   VCC: pin 16, default 1
  //   GND: pin 8
endmodule

/* Test case Count:
~U/D	~CE	~PL	CP	D0	D1	D2	D3	Q0	Q1	Q2	Q3
# Pre-Load & Hold
X	X	0	C	1	1	1	1	1	1	1	1
X	1	1	C	1	1	1	1	1	1	1	1
X	X	0	C	1	0	1	0	1	0	1	0
X	1	1	C	1	0	1	0	1	0	1	0
X	X	0	C	0	1	0	1	0	1	0	1
X	1	1	C	0	1	0	1	0	1	0	1
X	X	0	C	0	0	0	0	0	0	0	0
X	1	1	C	0	0	0	0	0	0	0	0

# Count Up
0	0	1	C	0	0	0	0	1	0	0	0
0	0	1	C	0	0	0	0	0	1	0	0
0	0	1	C	0	0	0	0	1	1	0	0
0	0	1	C	0	0	0	0	0	0	1	0
0	0	1	C	0	0	0	0	1	0	1	0
0	0	1	C	0	0	0	0	0	1	1	0
0	0	1	C	0	0	0	0	1	1	1	0
0	0	1	C	0	0	0	0	0	0	0	1
0	0	1	C	0	0	0	0	1	0	0	1
0	0	1	C	0	0	0	0	0	1	0	1
0	0	1	C	0	0	0	0	1	1	0	1
0	0	1	C	0	0	0	0	0	0	1	1
0	0	1	C	0	0	0	0	1	0	1	1
0	0	1	C	0	0	0	0	0	1	1	1
0	0	1	C	0	0	0	0	1	1	1	1
0	0	1	C	0	0	0	0	0	0	0	0

# Count Down
1	0	1	C	0	0	0	0	1	1	1	1
1	0	1	C	0	0	0	0	0	1	1	1
1	0	1	C	0	0	0	0	1	0	1	1
1	0	1	C	0	0	0	0	0	0	1	1
1	0	1	C	0	0	0	0	1	1	0	1
1	0	1	C	0	0	0	0	0	1	0	1
1	0	1	C	0	0	0	0	1	0	0	1
1	0	1	C	0	0	0	0	0	0	0	1
1	0	1	C	0	0	0	0	1	1	1	0
1	0	1	C	0	0	0	0	0	1	1	0
1	0	1	C	0	0	0	0	1	0	1	0
1	0	1	C	0	0	0	0	0	0	1	0
1	0	1	C	0	0	0	0	1	1	0	0
1	0	1	C	0	0	0	0	0	1	0	0
1	0	1	C	0	0	0	0	1	0	0	0
*/

/* Test case Carry:
~U/D	~CE	~PL	CP	D0	D1	D2	D3	Q0	Q1	Q2	Q3	TC	~RC
1	1	0	C	1	1	1	1	1	1	1	1	X	X
1	1	1	C	1	1	1	1	1	1	1	1	0	1
0	1	1	C	1	1	1	1	1	1	1	1	1	1

1	1	0	C	0	0	0	0	0	0	0	0	X	X
0	1	1	C	0	0	0	0	0	0	0	0	0	1
1	1	1	C	0	0	0	0	0	0	0	0	1	1
*/
