// Digital circuit 74590.dig as structural Verilog
// 8-bit binary counter with tri-state output registers
module _74590 (
  input  nOE,
  input  RCLK,
  input  nCCKEN,
  input  CCLK,
  input  nCCLR,
  input  VCC,
  input  GND,
  output nRCO,
  output QA,
  output QB,
  output QC,
  output QD,
  output QE,
  output QF,
  output QG,
  output QH
);

  wire d_ff_1_q, d_ff_2_q, d_ff_3_q, d_ff_4_q, d_ff_5_q, d_ff_6_q, d_ff_7_q, d_ff_8_q, jk_ff_as_1_q,
       jk_ff_as_2_q, jk_ff_as_3_q, jk_ff_as_4_q, jk_ff_as_5_q, jk_ff_as_6_q, jk_ff_as_7_q, jk_ff_as_8_q,
       undriven, undriven_2, undriven_3, undriven_4, undriven_5, undriven_6, undriven_7, undriven_8,
       undriven_9, undriven_10, undriven_11, undriven_12, undriven_13, undriven_14, undriven_15;

  PowerSupply powersupply_1 (.VDD(VCC), .GND(GND));
  // Not not_1 has open pins: in=nCCKEN, out=open
  // Not not_2 has open pins: in=nCCLR, out=open
  // And and_1 has open pins: In_1=jk_ff_as_1_q, In_2=undriven_8, out=open
  // And and_2 has open pins: In_1=jk_ff_as_2_q, In_2=jk_ff_as_1_q, out=open
  // And and_3 has open pins: In_1=undriven_2, In_2=undriven_8, out=open
  // And and_4 has open pins: In_1=jk_ff_as_3_q, In_2=undriven_2, out=open
  // And and_5 has open pins: In_1=undriven_3, In_2=undriven_8, out=open
  // And and_6 has open pins: In_1=jk_ff_as_4_q, In_2=undriven_3, out=open
  // And and_7 has open pins: In_1=undriven_4, In_2=undriven_8, out=open
  // And and_8 has open pins: In_1=jk_ff_as_5_q, In_2=undriven_4, out=open
  // And and_9 has open pins: In_1=undriven_5, In_2=undriven_8, out=open
  // And and_10 has open pins: In_1=jk_ff_as_6_q, In_2=undriven_5, out=open
  // And and_11 has open pins: In_1=undriven_6, In_2=undriven_8, out=open
  // And and_12 has open pins: In_1=jk_ff_as_7_q, In_2=undriven_6, out=open
  // And and_13 has open pins: In_1=undriven_7, In_2=undriven_8, out=open
  JK_FF_AS jk_ff_as_1 (
    .Set(1'b0), .J(undriven_8), .C(CCLK), .K(undriven_8), .Clr(undriven), .Q(jk_ff_as_1_q));  // open: nQ
  JK_FF_AS jk_ff_as_2 (
    .Set(1'b0), .J(undriven_9), .C(CCLK), .K(undriven_9), .Clr(undriven), .Q(jk_ff_as_2_q));  // open: nQ
  JK_FF_AS jk_ff_as_3 (
    .Set(1'b0), .J(undriven_10), .C(CCLK), .K(undriven_10), .Clr(undriven), .Q(jk_ff_as_3_q));  // open: nQ
  JK_FF_AS jk_ff_as_4 (
    .Set(1'b0), .J(undriven_11), .C(CCLK), .K(undriven_11), .Clr(undriven), .Q(jk_ff_as_4_q));  // open: nQ
  JK_FF_AS jk_ff_as_5 (
    .Set(1'b0), .J(undriven_12), .C(CCLK), .K(undriven_12), .Clr(undriven), .Q(jk_ff_as_5_q));  // open: nQ
  JK_FF_AS jk_ff_as_6 (
    .Set(1'b0), .J(undriven_13), .C(CCLK), .K(undriven_13), .Clr(undriven), .Q(jk_ff_as_6_q));  // open: nQ
  JK_FF_AS jk_ff_as_7 (
    .Set(1'b0), .J(undriven_14), .C(CCLK), .K(undriven_14), .Clr(undriven), .Q(jk_ff_as_7_q));  // open: nQ
  JK_FF_AS jk_ff_as_8 (
    .Set(1'b0), .J(undriven_15), .C(CCLK), .K(undriven_15), .Clr(undriven), .Q(jk_ff_as_8_q));  // open: nQ
  D_FF d_ff_1 (.D(jk_ff_as_1_q), .C(RCLK), .Q(d_ff_1_q));  // open: nQ
  D_FF d_ff_2 (.D(jk_ff_as_2_q), .C(RCLK), .Q(d_ff_2_q));  // open: nQ
  D_FF d_ff_3 (.D(jk_ff_as_3_q), .C(RCLK), .Q(d_ff_3_q));  // open: nQ
  D_FF d_ff_4 (.D(jk_ff_as_4_q), .C(RCLK), .Q(d_ff_4_q));  // open: nQ
  D_FF d_ff_5 (.D(jk_ff_as_5_q), .C(RCLK), .Q(d_ff_5_q));  // open: nQ
  D_FF d_ff_6 (.D(jk_ff_as_6_q), .C(RCLK), .Q(d_ff_6_q));  // open: nQ
  D_FF d_ff_7 (.D(jk_ff_as_7_q), .C(RCLK), .Q(d_ff_7_q));  // open: nQ
  D_FF d_ff_8 (.D(jk_ff_as_8_q), .C(RCLK), .Q(d_ff_8_q));  // open: nQ
  // NAnd nand_1 has open pins: In_1=jk_ff_as_8_q, In_2=undriven_7, out=open
  assign QA = ~nOE ? d_ff_1_q : 1'bz;  // DriverInvSel driverinvsel_1
  assign QB = ~nOE ? d_ff_2_q : 1'bz;  // DriverInvSel driverinvsel_2
  assign QC = ~nOE ? d_ff_3_q : 1'bz;  // DriverInvSel driverinvsel_3
  assign QD = ~nOE ? d_ff_4_q : 1'bz;  // DriverInvSel driverinvsel_4
  assign QE = ~nOE ? d_ff_5_q : 1'bz;  // DriverInvSel driverinvsel_5
  assign QF = ~nOE ? d_ff_6_q : 1'bz;  // DriverInvSel driverinvsel_6
  assign QG = ~nOE ? d_ff_7_q : 1'bz;  // DriverInvSel driverinvsel_7
  assign QH = ~nOE ? d_ff_8_q : 1'bz;  // DriverInvSel driverinvsel_8

  // Notes on the sheet:
  //   nOE: pin 14
  //   RCLK: pin 13
  //   nRCO: pin 9
  //   nCCKEN: pin 12
  //   CCLK: pin 11, Hz: 5
  //   nCCLR: pin 10
  //   QA: pin 15
  //   QB: pin 1
  //   QC: pin 2
  //   QD: pin 3
  //   QE: pin 4
  //   QF: pin 5
  //   QG: pin 6
  //   QH: pin 7
  //   VCC: pin 16, default 1
  //   GND: pin 8
endmodule
