// Digital circuit 74779-inc.dig as structural Verilog
// flip flop part of 74779
module _74779_inc (
  input  DATA,
  input  LOAD,
  input  nTOGGLE,
  input  CP,
  output Q,
  output nQ
);

  wire undriven, undriven_2, undriven_3, undriven_4, undriven_5, undriven_6;

  // Not not_1 has open pins: in=LOAD, out=open
  // Not not_2 has open pins: in=nTOGGLE, out=open
  // And and_1 has open pins: In_1=DATA, In_2=LOAD, out=open
  // And and_2 has open pins: In_1=undriven, In_2=nTOGGLE, In_3=Q, out=open
  // And and_3 has open pins: In_1=undriven, In_2=undriven_2, In_3=nQ, out=open
  // Or or_1 has open pins: In_1=undriven_3, In_2=undriven_4, In_3=undriven_5, out=open
  D_FF d_ff_1 (.D(undriven_6), .C(CP), .Q(Q), .nQ(nQ));

  // Notes on the sheet:
  //   DATA: pin 1
  //   LOAD: pin 2
  //   Q: pin 4
  //   nQ: pin 3
endmodule
