// Digital circuit 74779.dig as structural Verilog
// 8-Bit Bidirectional Binary Counter with 3-STATE Outputs
module _74779 (
  input  CP,
  input  S0,
  input  S1,
  input  nOE,
  input  I_O0,
  input  I_O1,
  input  I_O2,
  input  I_O3,
  input  I_O4,
  input  I_O5,
  input  I_O6,
  input  I_O7,
  input  nCET,
  input  VCC,
  input  GND,
  output nTC
);

  wire _74779_inc_1_nq, _74779_inc_1_q, _74779_inc_2_nq, _74779_inc_2_q, _74779_inc_3_nq, _74779_inc_3_q,
       _74779_inc_4_nq, _74779_inc_4_q, _74779_inc_5_nq, _74779_inc_5_q, _74779_inc_6_nq, _74779_inc_6_q,
       _74779_inc_7_nq, _74779_inc_7_q, _74779_inc_8_nq, _74779_inc_8_q, undriven, undriven_2, undriven_3,
       undriven_4, undriven_5, undriven_6, undriven_7, undriven_8, undriven_9, undriven_10, undriven_11,
       undriven_12, undriven_13, undriven_14, undriven_15, undriven_16, undriven_17, undriven_18,
       undriven_19, undriven_20, undriven_21, undriven_22, undriven_23, undriven_24, undriven_25,
       undriven_26, undriven_27, undriven_28, undriven_29, undriven_30, undriven_31, undriven_32,
       undriven_33, undriven_34, undriven_35, undriven_36, undriven_37, undriven_38, undriven_39,
       undriven_40, undriven_41, undriven_42, undriven_43, undriven_44, undriven_45, undriven_46,
       undriven_47, undriven_48, undriven_49, undriven_50, undriven_51, undriven_52, undriven_53,
       undriven_54, undriven_55, undriven_56, undriven_57, undriven_58, undriven_59, undriven_60, undriven_61;

  // Not not_1 has open pins: in=S0, out=open
  // Not not_2 has open pins: in=S1, out=open
  // Not not_3 has open pins: in=nOE, out=open
  assign I_O0 = undriven_59 ? undriven_58 : 1'bz;  // Driver driver_1
  assign I_O1 = undriven_59 ? undriven_57 : 1'bz;  // Driver driver_2
  assign I_O2 = undriven_59 ? undriven_56 : 1'bz;  // Driver driver_3
  assign I_O3 = undriven_59 ? undriven_55 : 1'bz;  // Driver driver_4
  assign I_O4 = undriven_59 ? undriven_51 : 1'bz;  // Driver driver_5
  assign I_O5 = undriven_59 ? undriven_52 : 1'bz;  // Driver driver_6
  assign I_O6 = undriven_59 ? undriven_53 : 1'bz;  // Driver driver_7
  assign I_O7 = undriven_59 ? undriven_54 : 1'bz;  // Driver driver_8
  // Not not_4 has open pins: in=undriven_60, out=open
  // Not not_5 has open pins: in=undriven_61, out=open
  // Not not_6 has open pins: in=nCET, out=open
  // And and_1 has open pins: In_1=undriven_61, In_2=undriven_60, out=open
  // And and_2 has open pins: In_1=undriven_50, In_2=undriven_61, out=open
  // And and_3 has open pins: In_1=undriven_60, In_2=undriven_49, out=open
  // Not not_7 has open pins: in=_74779_inc_1_nq, out=open
  // Not not_8 has open pins: in=_74779_inc_2_nq, out=open
  // Not not_9 has open pins: in=_74779_inc_3_nq, out=open
  // Not not_10 has open pins: in=_74779_inc_4_nq, out=open
  // Not not_11 has open pins: in=_74779_inc_5_nq, out=open
  // Not not_12 has open pins: in=_74779_inc_6_nq, out=open
  // Not not_13 has open pins: in=_74779_inc_7_nq, out=open
  // Not not_14 has open pins: in=_74779_inc_8_nq, out=open
  // And and_4 has open pins: In_1=_74779_inc_3_nq, In_2=_74779_inc_2_nq, In_3=_74779_inc_1_nq, In_4=undriven_46, In_5=undriven_45, out=open
  // And and_5 has open pins: In_1=undriven_42, In_2=undriven_44, out=open
  // And and_6 has open pins: In_1=_74779_inc_1_nq, In_2=undriven_46, In_3=undriven_45, out=open
  // And and_7 has open pins: In_1=_74779_inc_8_nq, In_2=_74779_inc_7_nq, In_3=_74779_inc_6_nq, In_4=_74779_inc_5_nq, In_5=_74779_inc_4_nq, out=open
  // And and_8 has open pins: In_1=_74779_inc_2_nq, In_2=_74779_inc_1_nq, In_3=undriven_46, In_4=undriven_45, out=open
  // And and_9 has open pins: In_1=_74779_inc_3_nq, In_2=_74779_inc_2_nq, In_3=_74779_inc_1_nq, In_4=undriven_46, In_5=undriven_45, out=open
  // And and_10 has open pins: In_1=_74779_inc_4_nq, In_2=_74779_inc_3_nq, In_3=_74779_inc_2_nq, out=open
  // And and_11 has open pins: In_1=_74779_inc_1_nq, In_2=undriven_46, In_3=undriven_45, out=open
  // And and_12 has open pins: In_1=_74779_inc_5_nq, In_2=_74779_inc_4_nq, In_3=_74779_inc_3_nq, out=open
  // And and_13 has open pins: In_1=_74779_inc_2_nq, In_2=_74779_inc_1_nq, In_3=undriven_46, In_4=undriven_45, out=open
  // And and_14 has open pins: In_1=_74779_inc_6_nq, In_2=_74779_inc_5_nq, In_3=_74779_inc_4_nq, In_4=_74779_inc_3_nq, out=open
  // And and_15 has open pins: In_1=_74779_inc_2_nq, In_2=_74779_inc_1_nq, In_3=undriven_46, In_4=undriven_45, out=open
  // And and_16 has open pins: In_1=_74779_inc_7_nq, In_2=_74779_inc_6_nq, In_3=_74779_inc_5_nq, In_4=_74779_inc_4_nq, out=open
  // And and_17 has open pins: In_1=_74779_inc_3_nq, In_2=_74779_inc_2_nq, In_3=_74779_inc_1_nq, In_4=undriven_46, In_5=undriven_45, out=open
  // And and_18 has open pins: In_1=undriven, In_2=undriven_7, out=open
  // And and_19 has open pins: In_1=undriven_2, In_2=undriven_8, out=open
  // And and_20 has open pins: In_1=undriven_3, In_2=undriven_9, out=open
  // And and_21 has open pins: In_1=undriven_4, In_2=undriven_10, out=open
  // And and_22 has open pins: In_1=_74779_inc_3_q, In_2=_74779_inc_2_q, In_3=_74779_inc_1_q, In_4=undriven_47, In_5=undriven_45, out=open
  // And and_23 has open pins: In_1=undriven_17, In_2=undriven_15, out=open
  // And and_24 has open pins: In_1=_74779_inc_8_q, In_2=_74779_inc_7_q, In_3=_74779_inc_6_q, In_4=_74779_inc_5_q, In_5=_74779_inc_4_q, out=open
  PowerSupply powersupply_1 (.VDD(VCC), .GND(GND));
  // And and_25 has open pins: In_1=undriven_45, In_2=_74779_inc_1_q, In_3=undriven_47, out=open
  // And and_26 has open pins: In_1=undriven_45, In_2=_74779_inc_2_q, In_3=_74779_inc_1_q, In_4=undriven_47, out=open
  // And and_27 has open pins: In_1=undriven_45, In_2=_74779_inc_3_q, In_3=_74779_inc_2_q, In_4=_74779_inc_1_q, In_5=undriven_47, out=open
  // And and_28 has open pins: In_1=undriven_45, In_2=_74779_inc_4_q, In_3=_74779_inc_3_q, out=open
  // And and_29 has open pins: In_1=_74779_inc_2_q, In_2=_74779_inc_1_q, In_3=undriven_47, out=open
  // NOr nor_1 has open pins: In_1=undriven_16, In_2=undriven_43, out=open
  // And and_30 has open pins: In_1=undriven_45, In_2=_74779_inc_5_q, In_3=_74779_inc_4_q, out=open
  // And and_31 has open pins: In_1=_74779_inc_3_q, In_2=_74779_inc_2_q, In_3=_74779_inc_1_q, In_4=undriven_47, out=open
  // And and_32 has open pins: In_1=undriven_45, In_2=_74779_inc_6_q, In_3=_74779_inc_5_q, In_4=_74779_inc_4_q, out=open
  // And and_33 has open pins: In_1=_74779_inc_3_q, In_2=_74779_inc_2_q, In_3=_74779_inc_1_q, In_4=undriven_47, out=open
  // And and_34 has open pins: In_1=undriven_45, In_2=_74779_inc_7_q, In_3=_74779_inc_6_q, In_4=_74779_inc_5_q, out=open
  // And and_35 has open pins: In_1=_74779_inc_4_q, In_2=_74779_inc_3_q, In_3=_74779_inc_2_q, In_4=_74779_inc_1_q, In_5=undriven_47, out=open
  // And and_36 has open pins: In_1=undriven_20, In_2=undriven_21, out=open
  // And and_37 has open pins: In_1=undriven_23, In_2=undriven_26, out=open
  // And and_38 has open pins: In_1=undriven_24, In_2=undriven_27, out=open
  // And and_39 has open pins: In_1=undriven_25, In_2=undriven_28, out=open
  // Not not_15 has open pins: in=undriven_45, out=open
  // NOr nor_2 has open pins: In_1=undriven_18, In_2=undriven_41, out=open
  // NOr nor_3 has open pins: In_1=undriven_19, In_2=undriven_6, out=open
  // NOr nor_4 has open pins: In_1=undriven_22, In_2=undriven_5, out=open
  // NOr nor_5 has open pins: In_1=undriven_29, In_2=undriven_11, out=open
  // NOr nor_6 has open pins: In_1=undriven_30, In_2=undriven_12, out=open
  // NOr nor_7 has open pins: In_1=undriven_31, In_2=undriven_13, out=open
  // NOr nor_8 has open pins: In_1=undriven_32, In_2=undriven_14, out=open
  _74779_inc _74779_inc_1 (
    .DATA(I_O0), .LOAD(undriven_48), .nTOGGLE(undriven_33), .CP(CP), .Q(_74779_inc_1_q), .nQ(_74779_inc_1_nq));
  _74779_inc _74779_inc_2 (
    .DATA(I_O1), .LOAD(undriven_48), .nTOGGLE(undriven_39), .CP(CP), .Q(_74779_inc_2_q), .nQ(_74779_inc_2_nq));
  _74779_inc _74779_inc_3 (
    .DATA(I_O2), .LOAD(undriven_48), .nTOGGLE(undriven_40), .CP(CP), .Q(_74779_inc_3_q), .nQ(_74779_inc_3_nq));
  _74779_inc _74779_inc_4 (
    .DATA(I_O3), .LOAD(undriven_48), .nTOGGLE(undriven_38), .CP(CP), .Q(_74779_inc_4_q), .nQ(_74779_inc_4_nq));
  _74779_inc _74779_inc_5 (
    .DATA(I_O4), .LOAD(undriven_48), .nTOGGLE(undriven_35), .CP(CP), .Q(_74779_inc_5_q), .nQ(_74779_inc_5_nq));
  _74779_inc _74779_inc_6 (
    .DATA(I_O5), .LOAD(undriven_48), .nTOGGLE(undriven_36), .CP(CP), .Q(_74779_inc_6_q), .nQ(_74779_inc_6_nq));
  _74779_inc _74779_inc_7 (
    .DATA(I_O6), .LOAD(undriven_48), .nTOGGLE(undriven_37), .CP(CP), .Q(_74779_inc_7_q), .nQ(_74779_inc_7_nq));
  _74779_inc _74779_inc_8 (
    .DATA(I_O7), .LOAD(undriven_48), .nTOGGLE(undriven_34), .CP(CP), .Q(_74779_inc_8_q), .nQ(_74779_inc_8_nq));

  // Notes on the sheet:
  //   CP: pin 15
  //   S0: pin 11
  //   S1: pin 10
  //   nOE: pin 9, default 1
  //   I_O0: pin 16
  //   I_O1: pin 1
  //   I_O2: pin 2
  //   I_O3: pin 3
  //   I_O4: pin 5
  //   I_O5: pin 6
  //   I_O6: pin 7
  //   I_O7: pin 8
  //   nCET: pin 14, default 1
  //   nTC: pin 12
  //   VCC: pin 13, default 1
  //   GND: pin 4
endmodule

/* Test case:
S1 S0 ~CET ~OE CP I/O7 I/O6 I/O5 I/O4 I/O3 I/O2 I/O1 I/O0 I/O7_out I/O6_out I/O5_out I/O4_out I/O3_out I/O2_out I/O1_out I/O0_out ~TC
0  0    0   1   C  bits(8,1)          bits(8,1) 1
x  x    x   1   0  Z Z Z Z Z Z Z Z    Z Z Z Z Z Z Z Z 1
loop(n,256)
0  0    0   1   C  bits(8,n)          bits(8,n) 1
0  0    0   0   0  Z Z Z Z Z Z Z Z    bits(8,n) 1
0  0    1   1   C  bits(8,n)          bits(8,n) 1
0  0    1   0   0  Z Z Z Z Z Z Z Z    bits(8,n) 1

1  0    1   0   C  Z Z Z Z Z Z Z Z    bits(8,n) 1
0  1    1   0   C  Z Z Z Z Z Z Z Z    bits(8,n) 1
1  1    1   0   C  Z Z Z Z Z Z Z Z    bits(8,n) 1
end loop

loop(n,255)
1  0    0   0   C  Z Z Z Z Z Z Z Z    bits(8,n) 1
end loop
1  0    0   0   C  Z Z Z Z Z Z Z Z    bits(8,-1) 0

loop(n,254)
0  1    0   0   C  Z Z Z Z Z Z Z Z    bits(8,254-n) 1
end loop
0  1    0   0   C  Z Z Z Z Z Z Z Z    bits(8,0) 0
*/
