// Digital circuit 7447.dig as structural Verilog
// BCD to 7-segment decoder, active high
module _7447 (
  input  A,
  input  B,
  input  C,
  input  D,
  input  nRBI,
  input  nLT,
  input  VCC,
  input  GND,
  output nRBO,
  output a_2,
  output b_2,
  output c_2,
  output d_2,
  output e,
  output f,
  output g
);

  wire undriven, undriven_2, undriven_3, undriven_4, undriven_5, undriven_6, undriven_7, undriven_8,
       undriven_9, undriven_10, undriven_11, undriven_12, undriven_13, undriven_14, undriven_15, undriven_16,
       undriven_17, undriven_18, undriven_19, undriven_20, undriven_21, undriven_22, undriven_23,
       undriven_24, undriven_25, undriven_26, undriven_27, undriven_28, undriven_29, undriven_30,
       undriven_31, undriven_32, undriven_33, undriven_34, undriven_35, undriven_36, undriven_37;

  // NOr nor_1 has open pins: In_1=A, In_2=B, In_3=C, In_4=D, out=open
  // Not not_1 has open pins: in=nRBI, out=open
  PowerSupply powersupply_1 (.VDD(VCC), .GND(GND));
  // And and_1 has open pins: In_1=undriven_37, In_2=undriven_36, out=open
  // NAnd nand_1 has open pins: In_1=undriven_37, In_2=undriven_36, out=open
  // Or or_1 has open pins: In_1=D, In_2=undriven, out=open
  // Or or_2 has open pins: In_1=C, In_2=undriven, out=open
  // Or or_3 has open pins: In_1=B, In_2=undriven, out=open
  // Or or_4 has open pins: In_1=A, In_2=undriven, out=open
  // Not not_2 has open pins: in=undriven_2, out=open
  // Not not_3 has open pins: in=undriven_4, out=open
  // Not not_4 has open pins: in=undriven_6, out=open
  // Not not_5 has open pins: in=undriven_8, out=open
  // And and_2 has open pins: In_1=undriven_2, In_2=undriven_7, In_3=undriven_8, out=open
  // And and_3 has open pins: In_1=undriven_3, In_2=undriven_4, In_3=undriven_8, out=open
  // And and_4 has open pins: In_1=undriven_3, In_2=undriven_5, In_3=undriven_6, out=open
  // And and_5 has open pins: In_1=undriven_5, In_2=undriven_7, In_3=undriven_9, out=open
  // And and_6 has open pins: In_1=undriven_3, In_2=undriven_5, out=open
  // And and_7 has open pins: In_1=undriven_3, In_2=undriven_6, In_3=undriven_8, out=open
  // And and_8 has open pins: In_1=undriven_5, In_2=undriven_7, out=open
  // And and_9 has open pins: In_1=undriven_7, In_2=undriven_9, out=open
  // And and_10 has open pins: In_1=undriven_3, In_2=undriven_4, out=open
  // And and_11 has open pins: In_1=undriven_5, In_2=undriven_7, out=open
  // And and_12 has open pins: In_1=undriven_5, In_2=undriven_8, out=open
  // And and_13 has open pins: In_1=undriven_5, In_2=undriven_9, out=open
  // And and_14 has open pins: In_1=undriven_5, In_2=undriven_6, out=open
  // And and_15 has open pins: In_1=undriven_4, In_2=undriven_7, In_3=undriven_8, out=open
  // And and_16 has open pins: In_1=undriven_6, In_2=undriven_9, out=open
  // And and_17 has open pins: In_1=undriven_5, In_2=undriven_9, out=open
  // And and_18 has open pins: In_1=undriven_6, In_2=undriven_9, out=open
  // And and_19 has open pins: In_1=undriven_2, In_2=undriven_7, out=open
  // And and_20 has open pins: In_1=undriven_4, In_2=undriven_7, out=open
  // And and_21 has open pins: In_1=undriven_4, In_2=undriven_9, out=open
  // And and_22 has open pins: In_1=undriven_7, In_2=undriven_9, out=open
  // And and_23 has open pins: In_1=undriven_2, In_2=undriven_7, out=open
  // And and_24 has open pins: In_1=undriven_5, In_2=undriven_6, out=open
  // And and_25 has open pins: In_1=undriven_4, In_2=undriven_7, out=open
  // And and_26 has open pins: In_1=undriven_6, In_2=undriven_9, out=open
  // Not not_6 has open pins: in=nLT, out=open
  // Or or_5 has open pins: In_1=undriven_22, In_2=undriven_21, In_3=undriven_35, In_4=undriven_29, In_5=undriven_34, out=open
  // Or or_6 has open pins: In_1=undriven_20, In_2=undriven_19, In_3=undriven_35, In_4=undriven_28, In_5=undriven_33, out=open
  // Or or_7 has open pins: In_1=undriven_18, In_2=undriven_17, In_3=undriven_35, In_4=undriven_27, out=open
  // Or or_8 has open pins: In_1=undriven_16, In_2=undriven_15, In_3=undriven_35, In_4=undriven_26, In_5=undriven_32, out=open
  or or_9 (e, undriven_10, undriven_35, undriven_23);
  or or_10 (f, undriven_11, undriven_12, undriven_35, undriven_24, undriven_30);
  or or_11 (g, undriven_13, undriven_14, undriven_35, undriven_25, undriven_31);

  // Notes on the sheet:
  //   A: Bit 0, pin 7
  //   B: Bit 1, pin 1
  //   C: Bit 2, pin 2
  //   D: Bit 3, pin 6
  //   nRBO: ripple blanking output (LOW active), pin 4
  //   nRBI: ripple blanking input (LOW active), pin 5
  //   a_2: pin 13
  //   b_2: pin 12
  //   c_2: pin 11
  //   d_2: pin 10
  //   e: pin 9
  //   f: pin 15
  //   g: pin 14
  //   nLT: lamp test, pin 3
  //   VCC: pin 16, default 1
  //   GND: pin 8
endmodule
