// Digital circuit 7448.dig as structural Verilog
// BCD to 7-segment decoder, active low
module _7448 (
  input  A,
  input  B,
  input  C,
  input  D,
  input  nRBI,
  input  nLT,
  input  VCC,
  input  GND,
  output nRBO,
  output na,
  output nb,
  output nc,
  output nd,
  output ne,
  output nf,
  output ng
);

  wire a_t, b_t, c_t, d_t, undriven, undriven_2, undriven_3, undriven_4, undriven_5, undriven_6, undriven_7,
       undriven_8, undriven_9, undriven_10, undriven_11, undriven_12, undriven_13, undriven_14, undriven_15,
       undriven_16, undriven_17, undriven_18, undriven_19, undriven_20, undriven_21, undriven_22,
       undriven_23, undriven_24, undriven_25, undriven_26, undriven_27, undriven_28, undriven_29,
       undriven_30, undriven_31, undriven_32, undriven_33;

  PowerSupply powersupply_1 (.VDD(VCC), .GND(GND));
  // NOr nor_1 has open pins: In_1=A, In_2=B, In_3=C, In_4=D, out=open
  // Not not_1 has open pins: in=nRBI, out=open
  // And and_1 has open pins: In_1=undriven_33, In_2=undriven_32, out=open
  // NAnd nand_1 has open pins: In_1=undriven_33, In_2=undriven_32, out=open
  // Or or_1 has open pins: In_1=D, In_2=undriven_31, out=open
  // Or or_2 has open pins: In_1=C, In_2=undriven_31, out=open
  // Or or_3 has open pins: In_1=B, In_2=undriven_31, out=open
  // Or or_4 has open pins: In_1=A, In_2=undriven_31, out=open
  // Not not_2 has open pins: in=d_t, out=open
  // Not not_3 has open pins: in=c_t, out=open
  // Not not_4 has open pins: in=b_t, out=open
  // Not not_5 has open pins: in=a_t, out=open
  // And and_2 has open pins: In_1=d_t, In_2=undriven_3, In_3=a_t, out=open
  // And and_3 has open pins: In_1=undriven, In_2=c_t, In_3=a_t, out=open
  // And and_4 has open pins: In_1=undriven, In_2=undriven_2, In_3=b_t, out=open
  // And and_5 has open pins: In_1=undriven_2, In_2=undriven_3, In_3=undriven_4, out=open
  // And and_6 has open pins: In_1=undriven, In_2=undriven_2, out=open
  // And and_7 has open pins: In_1=undriven, In_2=b_t, In_3=a_t, out=open
  // And and_8 has open pins: In_1=undriven_2, In_2=undriven_3, out=open
  // And and_9 has open pins: In_1=undriven_3, In_2=undriven_4, out=open
  // And and_10 has open pins: In_1=undriven, In_2=c_t, out=open
  // And and_11 has open pins: In_1=undriven_2, In_2=undriven_3, out=open
  // And and_12 has open pins: In_1=undriven_2, In_2=a_t, out=open
  // And and_13 has open pins: In_1=undriven_2, In_2=undriven_4, out=open
  // And and_14 has open pins: In_1=undriven_2, In_2=b_t, out=open
  // And and_15 has open pins: In_1=c_t, In_2=undriven_3, In_3=a_t, out=open
  // And and_16 has open pins: In_1=b_t, In_2=undriven_4, out=open
  // And and_17 has open pins: In_1=undriven_2, In_2=undriven_4, out=open
  // And and_18 has open pins: In_1=b_t, In_2=undriven_4, out=open
  // And and_19 has open pins: In_1=d_t, In_2=undriven_3, out=open
  // And and_20 has open pins: In_1=c_t, In_2=undriven_3, out=open
  // And and_21 has open pins: In_1=c_t, In_2=undriven_4, out=open
  // And and_22 has open pins: In_1=undriven_3, In_2=undriven_4, out=open
  // And and_23 has open pins: In_1=d_t, In_2=undriven_3, out=open
  // And and_24 has open pins: In_1=undriven_2, In_2=b_t, out=open
  // And and_25 has open pins: In_1=c_t, In_2=undriven_3, out=open
  // And and_26 has open pins: In_1=b_t, In_2=undriven_4, out=open
  // Not not_6 has open pins: in=nLT, out=open
  // NOr nor_2 has open pins: In_1=undriven_17, In_2=undriven_16, In_3=undriven_30, In_4=undriven_24, In_5=undriven_29, out=open
  // NOr nor_3 has open pins: In_1=undriven_15, In_2=undriven_14, In_3=undriven_30, In_4=undriven_23, In_5=undriven_28, out=open
  // NOr nor_4 has open pins: In_1=undriven_13, In_2=undriven_12, In_3=undriven_30, In_4=undriven_22, out=open
  // NOr nor_5 has open pins: In_1=undriven_11, In_2=undriven_10, In_3=undriven_30, In_4=undriven_21, In_5=undriven_27, out=open
  // NOr nor_6 has open pins: In_1=undriven_5, In_2=undriven_30, In_3=undriven_18, out=open
  // NOr nor_7 has open pins: In_1=undriven_6, In_2=undriven_7, In_3=undriven_30, In_4=undriven_19, In_5=undriven_25, out=open
  // NOr nor_8 has open pins: In_1=undriven_8, In_2=undriven_9, In_3=undriven_30, In_4=undriven_20, In_5=undriven_26, out=open

  // Notes on the sheet:
  //   A: pin 7
  //   B: pin 1
  //   C: pin 2
  //   D: pin 6
  //   nRBO: ripple blanking output (LOW active), pin 4
  //   nRBI: ripple blanking input (LOW active), pin 5
  //   na: pin 13
  //   nb: pin 12
  //   nc: pin 11
  //   nd: pin 10
  //   ne: pin 9
  //   nf: pin 15
  //   ng: pin 14
  //   nLT: lamp test, pin 3
  //   VCC: pin 16, default 1
  //   GND: pin 8
endmodule
