// Digital circuit 7417.dig as structural Verilog
// hex buffer, open-collector output, same as 7407
module _7417 (
  input  _1A,
  input  _2A,
  input  _3A,
  input  _4A,
  input  _5A,
  input  _6A,
  input  VCC,
  input  GND,
  output _1Y,
  output _2Y,
  output _3Y,
  output _4Y,
  output _5Y,
  output _6Y
);

  wire undriven, undriven_2, undriven_3, undriven_4, undriven_5, undriven_6;

  // Not not_1 has open pins: in=_1A, out=open
  // Not not_2 has open pins: in=_2A, out=open
  // Not not_3 has open pins: in=_3A, out=open
  NFET nfet_1 (.G(undriven), .D(_1Y), .S(1'b0));
  NFET nfet_2 (.G(undriven_2), .D(_2Y), .S(1'b0));
  NFET nfet_3 (.G(undriven_3), .D(_3Y), .S(1'b0));
  PowerSupply powersupply_1 (.VDD(VCC), .GND(GND));
  // Not not_4 has open pins: in=_4A, out=open
  // Not not_5 has open pins: in=_5A, out=open
  // Not not_6 has open pins: in=_6A, out=open
  NFET nfet_4 (.G(undriven_4), .D(_4Y), .S(1'b0));
  NFET nfet_5 (.G(undriven_5), .D(_5Y), .S(1'b0));
  NFET nfet_6 (.G(undriven_6), .D(_6Y), .S(1'b0));

  // Notes on the sheet:
  //   _1A: pin 1
  //   _1Y: pin 2
  //   _2A: pin 3
  //   _2Y: pin 4
  //   _3A: pin 5
  //   _3Y: pin 6
  //   _4A: pin 9
  //   _4Y: pin 8
  //   _5A: pin 11
  //   _5Y: pin 10
  //   _6A: pin 13
  //   _6Y: pin 12
  //   VCC: pin 14, default 1
  //   GND: pin 7
endmodule
