// Digital circuit 74245.dig as structural Verilog
// octal bus transceivers with 3-state outputs
module _74245 (
  input  DIR,
  input  nOE,
  input  A1,
  input  B1,
  input  A2,
  input  B2,
  input  A3,
  input  B3,
  input  A4,
  input  B4,
  input  A5,
  input  B5,
  input  A6,
  input  B6,
  input  A7,
  input  B7,
  input  A8,
  input  B8,
  input  VCC,
  input  GND
);

  wire undriven, undriven_2;

  PowerSupply powersupply_1 (.VDD(VCC), .GND(GND));
  // And and_1 has open pins: In_1=DIR, In_2=nOE, out=open
  assign B1 = undriven ? A1 : 1'bz;  // Driver driver_1
  assign B2 = undriven ? A2 : 1'bz;  // Driver driver_2
  assign B3 = undriven ? A3 : 1'bz;  // Driver driver_3
  assign B4 = undriven ? A4 : 1'bz;  // Driver driver_4
  assign B5 = undriven ? A5 : 1'bz;  // Driver driver_5
  assign B6 = undriven ? A6 : 1'bz;  // Driver driver_6
  assign B7 = undriven ? A7 : 1'bz;  // Driver driver_7
  assign B8 = undriven ? A8 : 1'bz;  // Driver driver_8
  assign A1 = undriven_2 ? B1 : 1'bz;  // Driver driver_9
  assign A2 = undriven_2 ? B2 : 1'bz;  // Driver driver_10
  assign A3 = undriven_2 ? B3 : 1'bz;  // Driver driver_11
  assign A4 = undriven_2 ? B4 : 1'bz;  // Driver driver_12
  assign A5 = undriven_2 ? B5 : 1'bz;  // Driver driver_13
  assign A6 = undriven_2 ? B6 : 1'bz;  // Driver driver_14
  assign A7 = undriven_2 ? B7 : 1'bz;  // Driver driver_15
  assign A8 = undriven_2 ? B8 : 1'bz;  // Driver driver_16
  // And and_2 has open pins: In_1=nOE, In_2=DIR, out=open

  // Notes on the sheet:
  //   DIR: pin 1
  //   nOE: pin 19
  //   A1: pin 2
  //   B1: pin 18
  //   A2: pin 3
  //   B2: pin 17
  //   A3: pin 4
  //   B3: pin 16
  //   A4: pin 5
  //   B4: pin 15
  //   A5: pin 6
  //   B5: pin 14
  //   A6: pin 7
  //   B6: pin 13
  //   A7: pin 8
  //   B7: pin 12
  //   A8: pin 9
  //   B8: pin 11
  //   VCC: pin 20, default 1
  //   GND: pin 10
endmodule
