// Digital circuit 74541.dig as structural Verilog
// octal buffer/line driver
module _74541 (
  input  nOE1,
  input  nOE2,
  input  _0D,
  input  _1D,
  input  _2D,
  input  _3D,
  input  _4D,
  input  _5D,
  input  _6D,
  input  _7D,
  input  VCC,
  input  GND,
  output _0O,
  output _1O,
  output _2O,
  output _3O,
  output _4O,
  output _5O,
  output _6O,
  output _7O
);

  wire undriven;

  // NOr nor_1 has open pins: In_1=nOE1, In_2=nOE2, out=open
  PowerSupply powersupply_1 (.VDD(VCC), .GND(GND));
  assign _0O = undriven ? _0D : 1'bz;  // Driver driver_1
  assign _1O = undriven ? _1D : 1'bz;  // Driver driver_2
  assign _2O = undriven ? _2D : 1'bz;  // Driver driver_3
  assign _3O = undriven ? _3D : 1'bz;  // Driver driver_4
  assign _4O = undriven ? _4D : 1'bz;  // Driver driver_5
  assign _5O = undriven ? _5D : 1'bz;  // Driver driver_6
  assign _6O = undriven ? _6D : 1'bz;  // Driver driver_7
  assign _7O = undriven ? _7D : 1'bz;  // Driver driver_8

  // Notes on the sheet:
  //   nOE1: pin 1
  //   nOE2: pin 19
  //   _0D: pin 2
  //   _0O: pin 18
  //   _1D: pin 3
  //   _1O: pin 17
  //   _2D: pin 4
  //   _2O: pin 16
  //   _3D: pin 5
  //   _3O: pin 15
  //   _4D: pin 6
  //   _4O: pin 14
  //   _5D: pin 7
  //   _5O: pin 13
  //   _6D: pin 8
  //   _6O: pin 12
  //   _7D: pin 9
  //   _7O: pin 11
  //   VCC: pin 20, default 1
  //   GND: pin 10
endmodule
