// Digital circuit 74109.dig as structural Verilog
// Dual J-NOT-K flip-flop with set and reset; positive-edge-trigger
module _74109 (
  input  _1J,
  input  n1RD,
  input  _1CP,
  input  n1SD,
  input  n1K,
  input  VCC,
  input  GND,
  input  _2J,
  input  n2RD,
  input  _2CP,
  input  n2SD,
  input  n2K,
  output _1Q,
  output n1Q,
  output _2Q,
  output n2Q
);

  wire jk_ff_as_1_nq, jk_ff_as_2_nq, undriven, undriven_2;

  JK_FF_AS jk_ff_as_1 (.Set(~n1SD), .J(_1J), .C(_1CP), .K(~n1K), .Clr(~n1RD), .Q(_1Q), .nQ(jk_ff_as_1_nq));
  PowerSupply powersupply_1 (.VDD(VCC), .GND(GND));
  JK_FF_AS jk_ff_as_2 (.Set(~n2SD), .J(_2J), .C(_2CP), .K(~n2K), .Clr(~n2RD), .Q(_2Q), .nQ(jk_ff_as_2_nq));
  // And and_1 has open pins: In_1=n1SD, In_2=n1RD, out=open
  // And and_2 has open pins: In_1=n2SD, In_2=n2RD, out=open
  // Or or_1 has open pins: In_1=jk_ff_as_1_nq, In_2=undriven, out=open
  // Or or_2 has open pins: In_1=jk_ff_as_2_nq, In_2=undriven_2, out=open

  // Notes on the sheet:
  //   _1J: pin 2
  //   n1RD: pin 1
  //   _1CP: pin 4
  //   _1Q: pin 6
  //   n1Q: pin 7
  //   n1SD: pin 5
  //   n1K: pin 3
  //   VCC: pin 16, default 1
  //   GND: pin 8
  //   _2J: pin 14
  //   n2RD: pin 15
  //   _2CP: pin 12
  //   n2SD: pin 11
  //   n2K: pin 13
  //   _2Q: pin 10
  //   n2Q: pin 9
endmodule

/* Test case FF1:
~1RD ~1SD 1J ~1K 1CP 1Q ~1Q
0 1 X X X 0 1 
1 0 X X X 1 0 
0 0 X X X 1 1 
1 1 1 1 C 1 0 
1 1 0 0 C 0 1 

# Tests for "no change" and "toggle" states
1 1 0 1 C 0 1 
1 1 1 0 C 1 0 
*/

/* Test case FF2:
~2RD ~2SD 2J ~2K 2CP 2Q ~2Q
0 1 X X X 0 1 
1 0 X X X 1 0 
0 0 X X X 1 1 
1 1 1 1 C 1 0 
1 1 0 0 C 0 1 

# Tests for "no change" and "toggle" states
1 1 0 1 C 0 1 
1 1 1 0 C 1 0 
*/
