// Digital circuit 74112.dig as structural Verilog
// Dual J-K negative-edge-triggered flip-flop, clear and preset
module _74112 (
  input  n1CK,
  input  _1K,
  input  _1J,
  input  n1PR,
  input  n1CLR,
  input  n2CLR,
  input  n2CK,
  input  _2K,
  input  _2J,
  input  n2PR,
  input  VCC,
  input  GND,
  output _1Q,
  output n1Q,
  output _2Q,
  output n2Q
);

  wire jk_ff_as_1_nq, jk_ff_as_2_nq, undriven, undriven_2;

  JK_FF_AS jk_ff_as_1 (.Set(~n1PR), .J(_1J), .C(~n1CK), .K(_1K), .Clr(~n1CLR), .Q(_1Q), .nQ(jk_ff_as_1_nq));
  JK_FF_AS jk_ff_as_2 (.Set(~n2PR), .J(_2J), .C(~n2CK), .K(_2K), .Clr(~n2CLR), .Q(_2Q), .nQ(jk_ff_as_2_nq));
  PowerSupply powersupply_1 (.VDD(VCC), .GND(GND));
  // And and_1 has open pins: In_1=n1PR, In_2=n1CLR, out=open
  // And and_2 has open pins: In_1=n2PR, In_2=n2CLR, out=open
  // Or or_1 has open pins: In_1=jk_ff_as_1_nq, In_2=undriven, out=open
  // Or or_2 has open pins: In_1=jk_ff_as_2_nq, In_2=undriven_2, out=open

  // Notes on the sheet:
  //   n1CK: pin 1
  //   _1K: pin 2
  //   _1J: pin 3
  //   n1PR: pin 4
  //   n1CLR: pin 15
  //   n2CLR: pin 14
  //   n2CK: pin 13
  //   _2K: pin 12
  //   _2J: pin 11
  //   n2PR: pin 10
  //   _1Q: pin 5
  //   n1Q: pin 6
  //   _2Q: pin 9
  //   n2Q: pin 7
  //   VCC: pin 16, default 1
  //   GND: pin 8
  //   74112 - Dual J-K negative-edge-triggered flip-flop, clear and preset
endmodule

/* Test case 74112 - Flip Flop #1:
~1CLR ~1PR 1J 1K ~1CK 1Q ~1Q
0 1 X X X 0 1
1 0 X X X 1 0
0 0 X X X 1 1
1 1 1 0 C 1 0
1 1 0 1 C 0 1

# Tests for "no change" and "toggle" states
1 1 0 1 C 0 1
1 1 0 0 C 0 1
1 1 1 1 C 1 0
1 1 0 0 C 1 0
1 1 1 1 C 0 1
*/

/* Test case 74112 - Flip Flop #2:
~2CLR ~2PR 2J 2K ~2CK 2Q ~2Q
0 1 X X X 0 1
1 0 X X X 1 0
0 0 X X X 1 1
1 1 1 0 C 1 0
1 1 0 1 C 0 1

# Tests for "no change" and "toggle" states
1 1 0 1 C 0 1
1 1 0 0 C 0 1
1 1 1 1 C 1 0
1 1 0 0 C 1 0
1 1 1 1 C 0 1
*/
