// Digital circuit 74116.dig as structural Verilog
// dual 4-bit D-type latches
module _74116 (
  input  _1nCLR,
  input  _1nC1,
  input  _1nC2,
  input  _1D1,
  input  _1D2,
  input  _1D3,
  input  _1D4,
  input  _2nCLR,
  input  _2nC1,
  input  _2nC2,
  input  _2D1,
  input  _2D2,
  input  _2D3,
  input  _2D4,
  input  VCC,
  input  GND,
  output _1Q1,
  output _1Q2,
  output _1Q3,
  output _1Q4,
  output _2Q1,
  output _2Q2,
  output _2Q3,
  output _2Q4
);

  wire undriven, undriven_2, undriven_3, undriven_4, undriven_5, undriven_6, undriven_7, undriven_8,
       undriven_9, undriven_10, undriven_11, undriven_12, undriven_13, undriven_14, undriven_15, undriven_16,
       undriven_17, undriven_18, undriven_19, undriven_20, undriven_21, undriven_22, undriven_23,
       undriven_24, undriven_25, undriven_26, undriven_27, undriven_28, undriven_29, undriven_30,
       undriven_31, undriven_32, undriven_33, undriven_34, undriven_35, undriven_36, undriven_37,
       undriven_38, undriven_39, undriven_40, undriven_41, undriven_42, undriven_43, undriven_44;

  // Or or_1 has open pins: In_1=_1nC1, In_2=_1nC2, out=open
  // Not not_1 has open pins: in=undriven, out=open
  // And and_1 has open pins: In_1=_1Q1, In_2=undriven, out=open
  // And and_2 has open pins: In_1=_1Q1, In_2=_1D1, out=open
  // And and_3 has open pins: In_1=undriven_2, In_2=_1D1, out=open
  // And and_4 has open pins: In_1=_1Q2, In_2=undriven, out=open
  // And and_5 has open pins: In_1=_1Q2, In_2=_1D2, out=open
  // And and_6 has open pins: In_1=undriven_2, In_2=_1D2, out=open
  // And and_7 has open pins: In_1=_1Q3, In_2=undriven, out=open
  // And and_8 has open pins: In_1=_1Q3, In_2=_1D3, out=open
  // And and_9 has open pins: In_1=undriven_2, In_2=_1D3, out=open
  // And and_10 has open pins: In_1=_1Q4, In_2=undriven, out=open
  // And and_11 has open pins: In_1=_1Q4, In_2=_1D4, out=open
  // And and_12 has open pins: In_1=undriven_2, In_2=_1D4, out=open
  // Or or_2 has open pins: In_1=undriven_4, In_2=undriven_11, out=open
  // Or or_3 has open pins: In_1=undriven_6, In_2=undriven_12, out=open
  // Or or_4 has open pins: In_1=undriven_8, In_2=undriven_13, out=open
  // Or or_5 has open pins: In_1=undriven_10, In_2=undriven_14, out=open
  // Or or_6 has open pins: In_1=undriven_3, In_2=undriven_15, out=open
  // Or or_7 has open pins: In_1=undriven_5, In_2=undriven_16, out=open
  // Or or_8 has open pins: In_1=undriven_7, In_2=undriven_17, out=open
  // Or or_9 has open pins: In_1=undriven_9, In_2=undriven_18, out=open
  // And and_13 has open pins: In_1=_1nCLR, In_2=undriven_19, out=open
  // And and_14 has open pins: In_1=_1nCLR, In_2=undriven_20, out=open
  // And and_15 has open pins: In_1=_1nCLR, In_2=undriven_21, out=open
  // And and_16 has open pins: In_1=_1nCLR, In_2=undriven_22, out=open
  PowerSupply powersupply_1 (.VDD(VCC), .GND(GND));
  // Or or_10 has open pins: In_1=_2nC1, In_2=_2nC2, out=open
  // Not not_2 has open pins: in=undriven_23, out=open
  // And and_17 has open pins: In_1=_2Q1, In_2=undriven_23, out=open
  // And and_18 has open pins: In_1=_2Q1, In_2=_2D1, out=open
  // And and_19 has open pins: In_1=undriven_24, In_2=_2D1, out=open
  // And and_20 has open pins: In_1=_2Q2, In_2=undriven_23, out=open
  // And and_21 has open pins: In_1=_2Q2, In_2=_2D2, out=open
  // And and_22 has open pins: In_1=undriven_24, In_2=_2D2, out=open
  // And and_23 has open pins: In_1=_2Q3, In_2=undriven_23, out=open
  // And and_24 has open pins: In_1=_2Q3, In_2=_2D3, out=open
  // And and_25 has open pins: In_1=undriven_24, In_2=_2D3, out=open
  // And and_26 has open pins: In_1=_2Q4, In_2=undriven_23, out=open
  // And and_27 has open pins: In_1=_2Q4, In_2=_2D4, out=open
  // And and_28 has open pins: In_1=undriven_24, In_2=_2D4, out=open
  // Or or_11 has open pins: In_1=undriven_26, In_2=undriven_33, out=open
  // Or or_12 has open pins: In_1=undriven_28, In_2=undriven_34, out=open
  // Or or_13 has open pins: In_1=undriven_30, In_2=undriven_35, out=open
  // Or or_14 has open pins: In_1=undriven_32, In_2=undriven_36, out=open
  // Or or_15 has open pins: In_1=undriven_25, In_2=undriven_37, out=open
  // Or or_16 has open pins: In_1=undriven_27, In_2=undriven_38, out=open
  // Or or_17 has open pins: In_1=undriven_29, In_2=undriven_39, out=open
  // Or or_18 has open pins: In_1=undriven_31, In_2=undriven_40, out=open
  // And and_29 has open pins: In_1=_2nCLR, In_2=undriven_41, out=open
  // And and_30 has open pins: In_1=_2nCLR, In_2=undriven_42, out=open
  // And and_31 has open pins: In_1=_2nCLR, In_2=undriven_43, out=open
  // And and_32 has open pins: In_1=_2nCLR, In_2=undriven_44, out=open

  // Notes on the sheet:
  //   _1nCLR: not clear, pin 1
  //   _1Q1: pin 5
  //   _1nC1: pin 2
  //   _1nC2: pin 3
  //   _1D1: pin 4
  //   _1Q2: pin 7
  //   _1D2: pin 6
  //   _1Q3: pin 9
  //   _1D3: pin 8
  //   _1Q4: pin 11
  //   _1D4: pin 10
  //   _2nCLR: not clear, pin 13
  //   _2Q1: pin 17
  //   _2nC1: pin 14
  //   _2nC2: pin 15
  //   _2D1: pin 16
  //   _2Q2: pin 19
  //   _2D2: pin 18
  //   _2Q3: pin 21
  //   _2D3: pin 20
  //   _2Q4: pin 23
  //   _2D4: pin 22
  //   VCC: pin 24, default 1
  //   GND: pin 12
endmodule
