// Digital circuit 74173.dig as structural Verilog
// quad 3-state D flip-flop with common clock and reset
module _74173 (
  input  D0,
  input  VCC,
  input  GND,
  input  RES,
  input  D1,
  input  D2,
  input  D3,
  input  CLK,
  input  DE1,
  input  DE2,
  input  OE1,
  input  OE2,
  output Q0,
  output Q1,
  output Q2,
  output Q3
);

  wire d_ff_as_1_q, d_ff_as_2_q, d_ff_as_3_q, d_ff_as_4_q, undriven, undriven_2, undriven_3, undriven_4,
       undriven_5, undriven_6, undriven_7, undriven_8, undriven_9, undriven_10, undriven_11, undriven_12,
       undriven_13, undriven_14, undriven_15;

  // Or or_1 has open pins: In_1=DE1, In_2=DE2, out=open
  // NOr nor_1 has open pins: In_1=OE1, In_2=OE2, out=open
  PowerSupply powersupply_1 (.VDD(VCC), .GND(GND));
  // Not not_1 has open pins: in=undriven, out=open
  // And and_1 has open pins: In_1=d_ff_as_1_q, In_2=undriven, out=open
  // And and_2 has open pins: In_1=D0, In_2=undriven_2, out=open
  // And and_3 has open pins: In_1=d_ff_as_2_q, In_2=undriven, out=open
  // And and_4 has open pins: In_1=D1, In_2=undriven_2, out=open
  // And and_5 has open pins: In_1=d_ff_as_3_q, In_2=undriven, out=open
  // And and_6 has open pins: In_1=D2, In_2=undriven_2, out=open
  // And and_7 has open pins: In_1=d_ff_as_4_q, In_2=undriven, out=open
  // And and_8 has open pins: In_1=D3, In_2=undriven_2, out=open
  // Or or_2 has open pins: In_1=undriven_6, In_2=undriven_7, out=open
  // Or or_3 has open pins: In_1=undriven_3, In_2=undriven_8, out=open
  // Or or_4 has open pins: In_1=undriven_4, In_2=undriven_9, out=open
  // Or or_5 has open pins: In_1=undriven_5, In_2=undriven_10, out=open
  D_FF_AS d_ff_as_1 (.Set(1'b0), .D(undriven_14), .C(CLK), .Clr(RES), .Q(d_ff_as_1_q));  // open: nQ
  D_FF_AS d_ff_as_2 (.Set(1'b0), .D(undriven_11), .C(CLK), .Clr(RES), .Q(d_ff_as_2_q));  // open: nQ
  D_FF_AS d_ff_as_3 (.Set(1'b0), .D(undriven_12), .C(CLK), .Clr(RES), .Q(d_ff_as_3_q));  // open: nQ
  D_FF_AS d_ff_as_4 (.Set(1'b0), .D(undriven_13), .C(CLK), .Clr(RES), .Q(d_ff_as_4_q));  // open: nQ
  assign Q0 = undriven_15 ? d_ff_as_1_q : 1'bz;  // Driver driver_1
  assign Q1 = undriven_15 ? d_ff_as_2_q : 1'bz;  // Driver driver_2
  assign Q2 = undriven_15 ? d_ff_as_3_q : 1'bz;  // Driver driver_3
  assign Q3 = undriven_15 ? d_ff_as_4_q : 1'bz;  // Driver driver_4

  // Notes on the sheet:
  //   D0: pin 14
  //   VCC: pin 16, default 1
  //   GND: pin 8
  //   RES: pin 15, default 1
  //   Q0: pin 3
  //   D1: pin 13
  //   Q1: pin 4
  //   D2: pin 12
  //   Q2: pin 5
  //   D3: pin 11
  //   Q3: pin 6
  //   CLK: pin 7
  //   DE1: pin 9
  //   DE2: pin 10
  //   OE1: pin 1
  //   OE2: pin 2
endmodule

/* Test case:
OE1 OE2 RES CLK DE1 DE2 D0 D1 D2 D3 Q0 Q1 Q2 Q3

 0   0   1   x   x   x  x  x  x  x  0  0  0  0 
 0   0   0   1   x   x  x  x  x  x  0  0  0  0 
 0   0   0   0   x   x  x  x  x  x  0  0  0  0 

#clear ff
 0   0   0   c   0   0  0  0  0  0  0  0  0  0 

 0   0   0   c   1   x  x  x  x  x  0  0  0  0 
 0   0   0   c   x   1  x  x  x  x  0  0  0  0 


loop (n,16)
 0   0   0   c   0   0  bits(4,n)  bits(4,n) 
end loop

#clear ff
 0   0   0   c   0   0  0  0  0  0  0  0  0  0 


 0   1   x   x   x   x  x  x  x  x  z  z  z  z 
 1   0   x   x   x   x  x  x  x  x  z  z  z  z 
 1   1   x   x   x   x  x  x  x  x  z  z  z  z 
*/
