// Digital circuit 74373-D-inc.dig as structural Verilog
// transparent d latch
module _74373_D_inc (
  input  D,
  input  G,
  output Q
);

  wire undriven, undriven_2;

  // And and_1 has open pins: In_1=G, In_2=D, out=open
  // And and_2 has open pins: In_1=G, In_2=D, out=open
  RS_FF_AS rs_ff_as_1 (.S(undriven), .R(undriven_2), .Q(Q));  // open: nQ
endmodule
