// Digital circuit 7476.dig as structural Verilog
// dual J-K flip-flops with preset and clear
module _7476 (
  input  _1J,
  input  _1nCLK,
  input  _1K,
  input  _1nC,
  input  _1nS,
  input  _2J,
  input  _2nCLK,
  input  _2K,
  input  _2nC,
  input  _2nS,
  input  VCC,
  input  GND,
  output _1Q,
  output _1nQ,
  output _2Q,
  output _2nQ
);

  wire jk_ff_as_1_nq, jk_ff_as_2_nq, undriven, undriven_2;

  PowerSupply powersupply_1 (.VDD(VCC), .GND(GND));
  JK_FF_AS jk_ff_as_1 (.Set(~_1nS), .J(_1J), .C(~_1nCLK), .K(_1K), .Clr(~_1nC), .Q(_1Q), .nQ(jk_ff_as_1_nq));
  JK_FF_AS jk_ff_as_2 (.Set(~_2nS), .J(_2J), .C(~_2nCLK), .K(_2K), .Clr(~_2nC), .Q(_2Q), .nQ(jk_ff_as_2_nq));
  // And and_1 has open pins: In_1=_1nS, In_2=_1nC, out=open
  // And and_2 has open pins: In_1=_2nS, In_2=_2nC, out=open
  // Or or_1 has open pins: In_1=jk_ff_as_1_nq, In_2=undriven, out=open
  // Or or_2 has open pins: In_1=jk_ff_as_2_nq, In_2=undriven_2, out=open

  // Notes on the sheet:
  //   _1J: Set, pin 4
  //   _1Q: pin 15
  //   _1nQ: pin 14
  //   _1nCLK: Clock, pin 1
  //   _1K: Kill, pin 16
  //   _1nC: not clear, pin 3
  //   _1nS: not set, pin 2
  //   _2J: Set, pin 9
  //   _2Q: pin 11
  //   _2nQ: pin 10
  //   _2nCLK: Clock, pin 6
  //   _2K: Kill, pin 12
  //   _2nC: not clear, pin 8
  //   _2nS: not set, pin 7
  //   VCC: pin 5, default 1
  //   GND: pin 13
endmodule

/* Test case Flip Flop #1:
1~C 1~S 1J 1K 1~CLK 1Q 1~Q
0 1 X X X 0 1
1 0 X X X 1 0
0 0 X X X 1 1
1 1 1 0 C 1 0
1 1 0 1 C 0 1

# Tests for "no change" and "toggle" states
1 1 0 1 C 0 1
1 1 0 0 C 0 1
1 1 1 1 C 1 0
1 1 0 0 C 1 0
1 1 1 1 C 0 1
*/

/* Test case Flip Flop #2:
2~C 2~S 2J 2K 2~CLK 2Q 2~Q
0 1 X X X 0 1
1 0 X X X 1 0
0 0 X X X 1 1
1 1 1 0 C 1 0
1 1 0 1 C 0 1

# Tests for "no change" and "toggle" states
1 1 0 1 C 0 1
1 1 0 0 C 0 1
1 1 1 1 C 1 0
1 1 0 0 C 1 0
1 1 1 1 C 0 1
*/
