// Digital circuit 74189.dig as structural Verilog
// 64-Bit Random Access Memory with 3-STATE Outputs
module _74189 (
  input  A0,
  input  A1,
  input  A2,
  input  A3,
  input  D0,
  input  D1,
  input  D2,
  input  D3,
  input  nCS,
  input  nWE,
  input  VCC,
  input  GND,
  output Q0,
  output Q1,
  output Q2,
  output Q3
);

  wire undriven_2, undriven_3;
  wire [3:0] undriven;

  // And and_1 has open pins: In_1=nWE, In_2=nCS, out=open
  // And and_2 has open pins: In_1=nWE, In_2=nCS, out=open
  // Not not_1 has open pins: in={D3, D2, D1, D0}, out=open
  RAMDualPort #(.AddrBits(4), .Bits(4)) ramdualport_1 (
    .A({A3, A2, A1, A0}), .Din(undriven), .str(undriven_2), .C(undriven_2), .ld(undriven_3),
    .D({Q3, Q2, Q1, Q0}));
  PowerSupply powersupply_1 (.VDD(VCC), .GND(GND));

  // Notes on the sheet:
  //   A0: pin 1
  //   A1: pin 15
  //   A2: pin 14
  //   A3: pin 13
  //   D0: pin 4
  //   D1: pin 6
  //   D2: pin 10
  //   D3: pin 12
  //   Q0: pin 5
  //   Q1: pin 7
  //   Q2: pin 9
  //   Q3: pin 11
  //   nCS: pin 2, default 1
  //   nWE: pin 3, default 1
  //   VCC: pin 16, default 1
  //   GND: pin 8
endmodule
