// Digital circuit 74670-D-inc.dig as structural Verilog
// unclocked 4 bit D-latch
module _74670_D_inc (
  input  [3:0] D,
  input  G,
  output [3:0] Q
);

  wire undriven, undriven_2, undriven_3, undriven_4, undriven_5, undriven_6, undriven_7, undriven_8;

  // And and_1 has open pins: In_1=G, In_2=D[0], out=open
  // And and_2 has open pins: In_1=G, In_2=D[0], out=open
  // And and_3 has open pins: In_1=G, In_2=D[1], out=open
  // And and_4 has open pins: In_1=G, In_2=D[1], out=open
  // And and_5 has open pins: In_1=G, In_2=D[2], out=open
  // And and_6 has open pins: In_1=G, In_2=D[2], out=open
  // And and_7 has open pins: In_1=G, In_2=D[3], out=open
  // And and_8 has open pins: In_1=G, In_2=D[3], out=open
  RS_FF_AS rs_ff_as_1 (.S(undriven), .R(undriven_5), .Q(Q[0]));  // open: nQ
  RS_FF_AS rs_ff_as_2 (.S(undriven_2), .R(undriven_6), .Q(Q[1]));  // open: nQ
  RS_FF_AS rs_ff_as_3 (.S(undriven_3), .R(undriven_7), .Q(Q[2]));  // open: nQ
  RS_FF_AS rs_ff_as_4 (.S(undriven_4), .R(undriven_8), .Q(Q[3]));  // open: nQ
endmodule
