// Digital circuit 74670.dig as structural Verilog
// 3-state 4-by-4 Register File
module _74670 (
  input  D1,
  input  D2,
  input  D3,
  input  D4,
  input  WA,
  input  WB,
  input  RA,
  input  RB,
  input  nGR,
  input  nGW,
  input  VCC,
  input  GND,
  output Q1,
  output Q2,
  output Q3,
  output Q4
);

  wire demultiplexer_1_out_0, demultiplexer_1_out_1, demultiplexer_1_out_2, demultiplexer_1_out_3, undriven;
  wire [3:0] _74670_d_inc_1_q, _74670_d_inc_2_q, _74670_d_inc_3_q, _74670_d_inc_4_q, multiplexer_1_out;

  // Not not_1 has open pins: in=nGW, out=open
  Demultiplexer #(.Selector_Bits(2)) demultiplexer_1 (
    .sel({WB, WA}), .in(undriven), .out_0(demultiplexer_1_out_0), .out_1(demultiplexer_1_out_1),
    .out_2(demultiplexer_1_out_2), .out_3(demultiplexer_1_out_3));
  _74670_D_inc _74670_d_inc_1 (.D({D4, D3, D2, D1}), .G(demultiplexer_1_out_0), .Q(_74670_d_inc_1_q));
  _74670_D_inc _74670_d_inc_2 (.D({D4, D3, D2, D1}), .G(demultiplexer_1_out_1), .Q(_74670_d_inc_2_q));
  _74670_D_inc _74670_d_inc_3 (.D({D4, D3, D2, D1}), .G(demultiplexer_1_out_2), .Q(_74670_d_inc_3_q));
  _74670_D_inc _74670_d_inc_4 (.D({D4, D3, D2, D1}), .G(demultiplexer_1_out_3), .Q(_74670_d_inc_4_q));
  PowerSupply powersupply_1 (.VDD(VCC), .GND(GND));
  Multiplexer #(.Selector_Bits(2), .Bits(4)) multiplexer_1 (
    .sel({RB, RA}), .in_0(_74670_d_inc_1_q), .in_1(_74670_d_inc_2_q), .in_2(_74670_d_inc_3_q),
    .in_3(_74670_d_inc_4_q), .out(multiplexer_1_out));
  assign {Q4, Q3, Q2, Q1} = ~nGR ? multiplexer_1_out : 4'bz;  // DriverInvSel driverinvsel_1

  // Notes on the sheet:
  //   Q1: pin 10
  //   Q2: pin 9
  //   Q3: pin 7
  //   Q4: pin 6
  //   D1: pin 15
  //   D2: pin 1
  //   D3: pin 2
  //   D4: pin 3
  //   WA: pin 14
  //   WB: pin 13
  //   RA: pin 5
  //   RB: pin 4
  //   nGR: pin 11, default 1
  //   nGW: pin 12, default 1
  //   VCC: pin 16, default 1
  //   GND: pin 8
endmodule
