// Digital circuit 7489.dig as structural Verilog
// 64-bit RAM
module _7489 (
  input  A0,
  input  A1,
  input  A2,
  input  A3,
  input  D1,
  input  D2,
  input  D3,
  input  D4,
  input  nWE,
  input  nME,
  input  VCC,
  input  GND,
  output S4,
  output S1,
  output S2,
  output S3
);

  wire undriven, undriven_2, undriven_3, undriven_5;
  wire [3:0] undriven_4;

  // Not not_1 has open pins: in=nWE, out=open
  // Not not_2 has open pins: in=nME, out=open
  PowerSupply powersupply_1 (.VDD(VCC), .GND(GND));
  // And and_1 has open pins: In_1=undriven, In_2=undriven_2, out=open
  // Or or_1 has open pins: In_1=undriven, In_2=undriven_2, out=open
  // Not not_3 has open pins: in={D4, D3, D2, D1}, out=open
  RAMDualPort #(.AddrBits(4), .Bits(4), .Addr_Bits(4)) ramdualport_1 (
    .A({A3, A2, A1, A0}), .Din(undriven_4), .str(undriven_3), .C(undriven_3), .ld(undriven_5),
    .D({S4, S3, S2, S1}));

  // Notes on the sheet:
  //   S4: pin 11
  //   S1: pin 5
  //   S2: pin 7
  //   S3: pin 9
  //   A0: pin 1
  //   A1: pin 15
  //   A2: pin 14
  //   A3: pin 13
  //   D1: pin 4
  //   D2: pin 6
  //   D3: pin 10
  //   D4: pin 12
  //   nWE: pin 3
  //   nME: pin 2
  //   VCC: pin 16, default 1
  //   GND: pin 8
endmodule
