// Digital circuit 74150.dig as structural Verilog
// 4-line to 16-line data selectors/multiplexers
module _74150 (
  input  A,
  input  C,
  input  B,
  input  S,
  input  E0,
  input  E1,
  input  E2,
  input  E3,
  input  E4,
  input  E5,
  input  E6,
  input  E7,
  input  E8,
  input  E9,
  input  E10,
  input  E11,
  input  E12,
  input  E13,
  input  E14,
  input  E15,
  input  D,
  input  VCC,
  input  GND,
  output W
);

  wire multiplexer_1_out, undriven;

  Multiplexer #(.Selector_Bits(4)) multiplexer_1 (
    .sel({D, C, B, A}), .in_0(E0), .in_1(E1), .in_2(E2), .in_3(E3), .in_4(E4), .in_5(E5), .in_6(E6),
    .in_7(E7), .in_8(E8), .in_9(E9), .in_10(E10), .in_11(E11), .in_12(E12), .in_13(E13), .in_14(E14),
    .in_15(E15), .out(multiplexer_1_out));
  PowerSupply powersupply_1 (.VDD(VCC), .GND(GND));
  // Not not_1 has open pins: in=multiplexer_1_out, out=open
  // Or or_1 has open pins: In_1=S, In_2=undriven, out=open

  // Notes on the sheet:
  //   W: pin 10
  //   A: pin 15
  //   C: pin 13
  //   B: pin 14
  //   S: Strobe, pin 9
  //   E0: pin 8
  //   E1: pin 7
  //   E2: pin 6
  //   E3: pin 5
  //   E4: pin 4
  //   E5: pin 3
  //   E6: pin 2
  //   E7: pin 1
  //   E8: pin 23
  //   E9: pin 22
  //   E10: pin 21
  //   E11: pin 20
  //   E12: pin 19
  //   E13: pin 18
  //   E14: pin 17
  //   E15: pin 16
  //   D: pin 11
  //   VCC: pin 24, default 1
  //   GND: pin 12
endmodule
