// Digital circuit 74165.dig as structural Verilog
// parallel-load 8-bit shift register
module _74165 (
  input  nLD,
  input  A,
  input  INH,
  input  CLK,
  input  SER,
  input  B,
  input  C,
  input  D,
  input  E,
  input  F,
  input  G,
  input  H,
  input  VCC,
  input  GND,
  output QH,
  output nQH
);

  wire d_ff_as_1_q, d_ff_as_2_q, d_ff_as_3_q, d_ff_as_4_q, d_ff_as_5_q, d_ff_as_6_q, d_ff_as_7_q, undriven,
       undriven_2, undriven_3, undriven_4, undriven_5, undriven_6, undriven_7, undriven_8, undriven_9,
       undriven_10, undriven_11, undriven_12, undriven_13, undriven_14, undriven_15, undriven_16,
       undriven_17, undriven_18;

  PowerSupply powersupply_1 (.VDD(VCC), .GND(GND));
  // Not not_1 has open pins: in=nLD, out=open
  // Or or_1 has open pins: In_1=INH, In_2=CLK, out=open
  // NAnd nand_1 has open pins: In_1=A, In_2=undriven_18, out=open
  // And and_1 has open pins: In_1=undriven_2, In_2=undriven_18, out=open
  D_FF_AS d_ff_as_1 (.Set(~undriven_2), .D(SER), .C(undriven), .Clr(undriven_3), .Q(d_ff_as_1_q));  // open: nQ
  // NAnd nand_2 has open pins: In_1=B, In_2=undriven_18, out=open
  // And and_2 has open pins: In_1=undriven_4, In_2=undriven_18, out=open
  D_FF_AS d_ff_as_2 (.Set(~undriven_4), .D(d_ff_as_1_q), .C(undriven), .Clr(undriven_5), .Q(d_ff_as_2_q));  // open: nQ
  // NAnd nand_3 has open pins: In_1=C, In_2=undriven_18, out=open
  // And and_3 has open pins: In_1=undriven_6, In_2=undriven_18, out=open
  D_FF_AS d_ff_as_3 (.Set(~undriven_6), .D(d_ff_as_2_q), .C(undriven), .Clr(undriven_7), .Q(d_ff_as_3_q));  // open: nQ
  // NAnd nand_4 has open pins: In_1=D, In_2=undriven_18, out=open
  // And and_4 has open pins: In_1=undriven_8, In_2=undriven_18, out=open
  D_FF_AS d_ff_as_4 (.Set(~undriven_8), .D(d_ff_as_3_q), .C(undriven), .Clr(undriven_9), .Q(d_ff_as_4_q));  // open: nQ
  // NAnd nand_5 has open pins: In_1=E, In_2=undriven_18, out=open
  // And and_5 has open pins: In_1=undriven_10, In_2=undriven_18, out=open
  D_FF_AS d_ff_as_5 (
    .Set(~undriven_10), .D(d_ff_as_4_q), .C(undriven), .Clr(undriven_11), .Q(d_ff_as_5_q));  // open: nQ
  // NAnd nand_6 has open pins: In_1=F, In_2=undriven_18, out=open
  // And and_6 has open pins: In_1=undriven_12, In_2=undriven_18, out=open
  D_FF_AS d_ff_as_6 (
    .Set(~undriven_12), .D(d_ff_as_5_q), .C(undriven), .Clr(undriven_13), .Q(d_ff_as_6_q));  // open: nQ
  // NAnd nand_7 has open pins: In_1=G, In_2=undriven_18, out=open
  // And and_7 has open pins: In_1=undriven_14, In_2=undriven_18, out=open
  D_FF_AS d_ff_as_7 (
    .Set(~undriven_14), .D(d_ff_as_6_q), .C(undriven), .Clr(undriven_15), .Q(d_ff_as_7_q));  // open: nQ
  // NAnd nand_8 has open pins: In_1=H, In_2=undriven_18, out=open
  // And and_8 has open pins: In_1=undriven_16, In_2=undriven_18, out=open
  D_FF_AS d_ff_as_8 (.Set(~undriven_16), .D(d_ff_as_7_q), .C(undriven), .Clr(undriven_17), .Q(QH), .nQ(nQH));

  // Notes on the sheet:
  //   nLD: pin 1
  //   A: pin 11
  //   INH: pin 15
  //   CLK: pin 2
  //   SER: pin 10
  //   B: pin 12
  //   C: pin 13
  //   D: pin 14
  //   E: pin 3
  //   F: pin 4
  //   G: pin 5
  //   H: pin 6
  //   QH: pin 9
  //   nQH: pin 7
  //   VCC: pin 16, default 1
  //   GND: pin 8
endmodule
