// Digital circuit 74166.dig as structural Verilog
// 8-Bit Parallel-In/Serial-Out Shift Register
module _74166 (
  input  nLD,
  input  A,
  input  INH,
  input  CLK,
  input  SER,
  input  B,
  input  C,
  input  D,
  input  E,
  input  F,
  input  G,
  input  H,
  input  VCC,
  input  GND,
  input  nCLR,
  output QH
);

  wire d_ff_as_1_q, d_ff_as_2_q, d_ff_as_3_q, d_ff_as_4_q, d_ff_as_5_q, d_ff_as_6_q, d_ff_as_7_q, undriven,
       undriven_2, undriven_3, undriven_4, undriven_5, undriven_6, undriven_7, undriven_8, undriven_9,
       undriven_10, undriven_11, undriven_12, undriven_13, undriven_14, undriven_15, undriven_16,
       undriven_17, undriven_18, undriven_19, undriven_20, undriven_21, undriven_22, undriven_23,
       undriven_24, undriven_25, undriven_26, undriven_27;

  // Not not_1 has open pins: in=nCLR, out=open
  // Or or_1 has open pins: In_1=undriven, In_2=undriven_3, out=open
  // And and_1 has open pins: In_1=SER, In_2=nLD, out=open
  PowerSupply powersupply_1 (.VDD(VCC), .GND(GND));
  D_FF_AS d_ff_as_1 (.Set(1'b0), .D(undriven_2), .C(undriven_19), .Clr(undriven_10), .Q(d_ff_as_1_q));  // open: nQ
  // And and_2 has open pins: In_1=undriven_21, In_2=A, out=open
  // Not not_2 has open pins: in=nLD, out=open
  // Or or_2 has open pins: In_1=undriven_4, In_2=undriven_6, out=open
  // And and_3 has open pins: In_1=d_ff_as_1_q, In_2=nLD, out=open
  D_FF_AS d_ff_as_2 (.Set(1'b0), .D(undriven_5), .C(undriven_19), .Clr(undriven_10), .Q(d_ff_as_2_q));  // open: nQ
  // And and_4 has open pins: In_1=undriven_21, In_2=B, out=open
  // And and_5 has open pins: In_1=d_ff_as_2_q, In_2=nLD, out=open
  // Or or_3 has open pins: In_1=undriven_7, In_2=undriven_9, out=open
  // And and_6 has open pins: In_1=undriven_21, In_2=C, out=open
  D_FF_AS d_ff_as_3 (.Set(1'b0), .D(undriven_8), .C(undriven_19), .Clr(undriven_10), .Q(d_ff_as_3_q));  // open: nQ
  // And and_7 has open pins: In_1=d_ff_as_3_q, In_2=nLD, out=open
  // Or or_4 has open pins: In_1=undriven_11, In_2=undriven_13, out=open
  // And and_8 has open pins: In_1=undriven_21, In_2=D, out=open
  D_FF_AS d_ff_as_4 (.Set(1'b0), .D(undriven_12), .C(undriven_19), .Clr(undriven_10), .Q(d_ff_as_4_q));  // open: nQ
  // Or or_5 has open pins: In_1=undriven_14, In_2=undriven_16, out=open
  // And and_9 has open pins: In_1=d_ff_as_4_q, In_2=nLD, out=open
  D_FF_AS d_ff_as_5 (.Set(1'b0), .D(undriven_15), .C(undriven_19), .Clr(undriven_10), .Q(d_ff_as_5_q));  // open: nQ
  // And and_10 has open pins: In_1=undriven_21, In_2=E, out=open
  // Or or_6 has open pins: In_1=undriven_17, In_2=undriven_20, out=open
  // And and_11 has open pins: In_1=d_ff_as_5_q, In_2=nLD, out=open
  D_FF_AS d_ff_as_6 (.Set(1'b0), .D(undriven_18), .C(undriven_19), .Clr(undriven_10), .Q(d_ff_as_6_q));  // open: nQ
  // And and_12 has open pins: In_1=undriven_21, In_2=F, out=open
  // And and_13 has open pins: In_1=d_ff_as_6_q, In_2=nLD, out=open
  // Or or_7 has open pins: In_1=undriven_22, In_2=undriven_24, out=open
  // And and_14 has open pins: In_1=undriven_21, In_2=G, out=open
  D_FF_AS d_ff_as_7 (.Set(1'b0), .D(undriven_23), .C(undriven_19), .Clr(undriven_10), .Q(d_ff_as_7_q));  // open: nQ
  // And and_15 has open pins: In_1=d_ff_as_7_q, In_2=nLD, out=open
  // Or or_8 has open pins: In_1=undriven_25, In_2=undriven_27, out=open
  // And and_16 has open pins: In_1=undriven_21, In_2=H, out=open
  D_FF_AS d_ff_as_8 (.Set(1'b0), .D(undriven_26), .C(undriven_19), .Clr(undriven_10), .Q(QH));  // open: nQ
  // Or or_9 has open pins: In_1=INH, In_2=CLK, out=open

  // Notes on the sheet:
  //   nLD: pin 15, default 1
  //   A: pin 2
  //   INH: pin 6
  //   CLK: pin 7
  //   SER: pin 1
  //   B: pin 3
  //   C: pin 4
  //   D: pin 5
  //   E: pin 10
  //   F: pin 11
  //   G: pin 12
  //   H: pin 14
  //   QH: pin 13
  //   VCC: pin 16, default 1
  //   GND: pin 8
  //   nCLR: pin 9, default 1
endmodule
