// Digital circuit 28c256.dig as structural Verilog
// 256K (32K x 8) Paged Parallel EEPROM;
// DATA Polling for End of Write Detection not implemented!
module _28c256 (
  input  nCE,
  input  nOE,
  input  nWE,
  input  VCC,
  input  GND,
  input  I_O0,
  input  I_O1,
  input  I_O2,
  input  I_O3,
  input  I_O4,
  input  I_O5,
  input  I_O6,
  input  I_O7,
  input  A0,
  input  A1,
  input  A2,
  input  A3,
  input  A4,
  input  A5,
  input  A6,
  input  A7,
  input  A8,
  input  A9,
  input  A10,
  input  A11,
  input  A12,
  input  A13,
  input  A14
);

  wire undriven;
  wire [7:0] eeprom_d;

  EEPROM #(.AddrBits(15), .Bits(8)) eeprom (
    .A({A14, A13, A12, A11, A10, A9, A8, A7, A6, A5, A4, A3, A2, A1, A0}), .CS(~nCE), .WE(~nWE), .OE(~nOE),
    .D(eeprom_d));
  // NOr nor_1 has open pins: In_1=nCE, In_2=nOE, out=open
  PowerSupply powersupply_1 (.VDD(VCC), .GND(GND));
  BusSplitter #(.Bits(8)) bussplitter_1 (
    .D(eeprom_d), .OE(undriven), .D0(I_O0), .D1(I_O1), .D2(I_O2), .D3(I_O3), .D4(I_O4), .D5(I_O5), .D6(I_O6),
    .D7(I_O7));

  // Notes on the sheet:
  //   nCE: pin 20, default 1
  //   nOE: pin 22, default 1
  //   nWE: pin 27, default 1
  //   VCC: pin 28, default 1
  //   GND: pin 14
  //   I_O0: pin 11
  //   I_O1: pin 12
  //   I_O2: pin 13
  //   I_O3: pin 15
  //   I_O4: pin 16
  //   I_O5: pin 17
  //   I_O6: pin 18
  //   I_O7: pin 19
  //   A0: pin 10
  //   A1: pin 9
  //   A2: pin 8
  //   A3: pin 7
  //   A4: pin 6
  //   A5: pin 5
  //   A6: pin 4
  //   A7: pin 3
  //   A8: pin 25
  //   A9: pin 24
  //   A10: pin 21
  //   A11: pin 23
  //   A12: pin 2
  //   A13: pin 26
  //   A14: pin 1
  //   contents of eeprom (hex, n*v repeats v):
  //   55,56,aa,55,d5,80,0,0,3
endmodule
