// Digital circuit GAL2v3.dig as structural Verilog
// Simple GAL with two inputs and three macrocells. 
// Each cell can be combinatorial or used as a flip-flop 
// buffered (combinatorial, registered). The component 
// is programmed via the FG-Fets, which can be 
// programmed. For simplicity, the FG-Fets can be 
// programmed with the [P] key.
// {{de Einfaches GAL mit zwei Eingängen und drei
// Makrozellen. Jede Zelle kann kombinatorisch oder
// als mit Flip-Flop gepuffert (combinatorial, registered)
// verwendet werden. Programmiert wird der Baustein
// über die FG-Fets, die Programmiert werden können. 
// Zur Vereinfachung können die FG-Fets mit der Taste 
// [P] programmiert werden.}}
module GAL2v3 (
  input  A,
  input  B,
  input  Clock,
  output Q_0,
  output Q_1,
  output Q_2
);

  wire fgnfet_1_d, fgnfet_3_d, fgnfet_5_d, fgnfet_7_d, fgnfet_9_d, fgnfet_11_d, fgnfet_13_d, fgnfet_15_d,
       fgnfet_17_d, fgnfet_19_d, fgnfet_21_d, fgnfet_23_d, fgnfet_25_d, fgnfet_27_d, fgnfet_29_d, MC0_q,
       MC1_q, MC2_q, pullup_16_out, pullup_17_out, pullup_18_out, undriven, undriven_2, undriven_3,
       undriven_4, undriven_5, undriven_6, undriven_7, undriven_8;

  // Not not_1 has open pins: in=A, out=open
  FGNFET #(.Blown("true")) fgnfet_1 (.G(A), .D(fgnfet_1_d), .S(1'b0));
  FGNFET #(.Blown("true")) fgnfet_2 (.G(undriven), .D(fgnfet_1_d), .S(1'b0));
  FGNFET fgnfet_3 (.G(A), .D(fgnfet_3_d), .S(1'b0));
  FGNFET fgnfet_4 (.G(undriven), .D(fgnfet_3_d), .S(1'b0));
  FGNFET fgnfet_5 (.G(A), .D(fgnfet_5_d), .S(1'b0));
  FGNFET fgnfet_6 (.G(undriven), .D(fgnfet_5_d), .S(1'b0));
  FGNFET fgnfet_7 (.G(A), .D(fgnfet_7_d), .S(1'b0));
  FGNFET fgnfet_8 (.G(undriven), .D(fgnfet_7_d), .S(1'b0));
  FGNFET fgnfet_9 (.G(A), .D(fgnfet_9_d), .S(1'b0));
  FGNFET fgnfet_10 (.G(undriven), .D(fgnfet_9_d), .S(1'b0));
  FGNFET #(.Blown("true")) fgnfet_11 (.G(A), .D(fgnfet_11_d), .S(1'b0));
  FGNFET #(.Blown("true")) fgnfet_12 (.G(undriven), .D(fgnfet_11_d), .S(1'b0));
  FGNFET #(.Blown("true")) fgnfet_13 (.G(A), .D(fgnfet_13_d), .S(1'b0));
  FGNFET #(.Blown("true")) fgnfet_14 (.G(undriven), .D(fgnfet_13_d), .S(1'b0));
  FGNFET fgnfet_15 (.G(A), .D(fgnfet_15_d), .S(1'b0));
  FGNFET fgnfet_16 (.G(undriven), .D(fgnfet_15_d), .S(1'b0));
  FGNFET fgnfet_17 (.G(A), .D(fgnfet_17_d), .S(1'b0));
  FGNFET fgnfet_18 (.G(undriven), .D(fgnfet_17_d), .S(1'b0));
  FGNFET fgnfet_19 (.G(A), .D(fgnfet_19_d), .S(1'b0));
  FGNFET fgnfet_20 (.G(undriven), .D(fgnfet_19_d), .S(1'b0));
  FGNFET #(.Blown("true")) fgnfet_21 (.G(A), .D(fgnfet_21_d), .S(1'b0));
  FGNFET #(.Blown("true")) fgnfet_22 (.G(undriven), .D(fgnfet_21_d), .S(1'b0));
  FGNFET #(.Blown("true")) fgnfet_23 (.G(A), .D(fgnfet_23_d), .S(1'b0));
  FGNFET #(.Blown("true")) fgnfet_24 (.G(undriven), .D(fgnfet_23_d), .S(1'b0));
  FGNFET #(.Blown("true")) fgnfet_25 (.G(A), .D(fgnfet_25_d), .S(1'b0));
  FGNFET #(.Blown("true")) fgnfet_26 (.G(undriven), .D(fgnfet_25_d), .S(1'b0));
  FGNFET fgnfet_27 (.G(A), .D(fgnfet_27_d), .S(1'b0));
  FGNFET fgnfet_28 (.G(undriven), .D(fgnfet_27_d), .S(1'b0));
  FGNFET fgnfet_29 (.G(A), .D(fgnfet_29_d), .S(1'b0));
  FGNFET fgnfet_30 (.G(undriven), .D(fgnfet_29_d), .S(1'b0));
  FGNFET #(.Blown("true")) fgnfet_31 (.G(B), .D(fgnfet_1_d), .S(1'b0));
  FGNFET fgnfet_32 (.G(B), .D(fgnfet_3_d), .S(1'b0));
  FGNFET fgnfet_33 (.G(B), .D(fgnfet_5_d), .S(1'b0));
  FGNFET fgnfet_34 (.G(B), .D(fgnfet_7_d), .S(1'b0));
  FGNFET fgnfet_35 (.G(B), .D(fgnfet_9_d), .S(1'b0));
  FGNFET #(.Blown("true")) fgnfet_36 (.G(B), .D(fgnfet_11_d), .S(1'b0));
  FGNFET #(.Blown("true")) fgnfet_37 (.G(B), .D(fgnfet_13_d), .S(1'b0));
  FGNFET fgnfet_38 (.G(B), .D(fgnfet_15_d), .S(1'b0));
  FGNFET fgnfet_39 (.G(B), .D(fgnfet_17_d), .S(1'b0));
  FGNFET fgnfet_40 (.G(B), .D(fgnfet_19_d), .S(1'b0));
  FGNFET #(.Blown("true")) fgnfet_41 (.G(B), .D(fgnfet_21_d), .S(1'b0));
  FGNFET #(.Blown("true")) fgnfet_42 (.G(B), .D(fgnfet_23_d), .S(1'b0));
  FGNFET #(.Blown("true")) fgnfet_43 (.G(B), .D(fgnfet_25_d), .S(1'b0));
  FGNFET fgnfet_44 (.G(B), .D(fgnfet_27_d), .S(1'b0));
  FGNFET fgnfet_45 (.G(B), .D(fgnfet_29_d), .S(1'b0));
  // Not not_2 has open pins: in=B, out=open
  FGNFET #(.Blown("true")) fgnfet_46 (.G(undriven_2), .D(fgnfet_1_d), .S(1'b0));
  FGNFET fgnfet_47 (.G(undriven_2), .D(fgnfet_3_d), .S(1'b0));
  FGNFET fgnfet_48 (.G(undriven_2), .D(fgnfet_5_d), .S(1'b0));
  FGNFET fgnfet_49 (.G(undriven_2), .D(fgnfet_7_d), .S(1'b0));
  FGNFET fgnfet_50 (.G(undriven_2), .D(fgnfet_9_d), .S(1'b0));
  FGNFET #(.Blown("true")) fgnfet_51 (.G(undriven_2), .D(fgnfet_11_d), .S(1'b0));
  FGNFET #(.Blown("true")) fgnfet_52 (.G(undriven_2), .D(fgnfet_13_d), .S(1'b0));
  FGNFET fgnfet_53 (.G(undriven_2), .D(fgnfet_15_d), .S(1'b0));
  FGNFET fgnfet_54 (.G(undriven_2), .D(fgnfet_17_d), .S(1'b0));
  FGNFET fgnfet_55 (.G(undriven_2), .D(fgnfet_19_d), .S(1'b0));
  FGNFET #(.Blown("true")) fgnfet_56 (.G(undriven_2), .D(fgnfet_21_d), .S(1'b0));
  FGNFET #(.Blown("true")) fgnfet_57 (.G(undriven_2), .D(fgnfet_23_d), .S(1'b0));
  FGNFET #(.Blown("true")) fgnfet_58 (.G(undriven_2), .D(fgnfet_25_d), .S(1'b0));
  FGNFET fgnfet_59 (.G(undriven_2), .D(fgnfet_27_d), .S(1'b0));
  FGNFET fgnfet_60 (.G(undriven_2), .D(fgnfet_29_d), .S(1'b0));
  // Not not_3 has open pins: in=Q_2, out=open
  FGNFET #(.Blown("true")) fgnfet_61 (.G(Q_2), .D(fgnfet_1_d), .S(1'b0));
  FGNFET fgnfet_62 (.G(Q_2), .D(fgnfet_3_d), .S(1'b0));
  FGNFET fgnfet_63 (.G(Q_2), .D(fgnfet_5_d), .S(1'b0));
  FGNFET fgnfet_64 (.G(Q_2), .D(fgnfet_7_d), .S(1'b0));
  FGNFET fgnfet_65 (.G(Q_2), .D(fgnfet_9_d), .S(1'b0));
  FGNFET #(.Blown("true")) fgnfet_66 (.G(Q_2), .D(fgnfet_11_d), .S(1'b0));
  FGNFET #(.Blown("true")) fgnfet_67 (.G(Q_2), .D(fgnfet_13_d), .S(1'b0));
  FGNFET fgnfet_68 (.G(Q_2), .D(fgnfet_15_d), .S(1'b0));
  FGNFET fgnfet_69 (.G(Q_2), .D(fgnfet_17_d), .S(1'b0));
  FGNFET fgnfet_70 (.G(Q_2), .D(fgnfet_19_d), .S(1'b0));
  FGNFET fgnfet_71 (.G(Q_2), .D(fgnfet_21_d), .S(1'b0));
  FGNFET #(.Blown("true")) fgnfet_72 (.G(Q_2), .D(fgnfet_23_d), .S(1'b0));
  FGNFET #(.Blown("true")) fgnfet_73 (.G(Q_2), .D(fgnfet_25_d), .S(1'b0));
  FGNFET fgnfet_74 (.G(Q_2), .D(fgnfet_27_d), .S(1'b0));
  FGNFET fgnfet_75 (.G(Q_2), .D(fgnfet_29_d), .S(1'b0));
  FGNFET #(.Blown("true")) fgnfet_76 (.G(undriven_3), .D(fgnfet_1_d), .S(1'b0));
  FGNFET #(.Blown("true")) fgnfet_77 (.G(Q_1), .D(fgnfet_1_d), .S(1'b0));
  FGNFET fgnfet_78 (.G(undriven_3), .D(fgnfet_3_d), .S(1'b0));
  FGNFET fgnfet_79 (.G(Q_1), .D(fgnfet_3_d), .S(1'b0));
  FGNFET fgnfet_80 (.G(undriven_3), .D(fgnfet_5_d), .S(1'b0));
  FGNFET fgnfet_81 (.G(Q_1), .D(fgnfet_5_d), .S(1'b0));
  FGNFET fgnfet_82 (.G(undriven_3), .D(fgnfet_7_d), .S(1'b0));
  FGNFET fgnfet_83 (.G(Q_1), .D(fgnfet_7_d), .S(1'b0));
  FGNFET fgnfet_84 (.G(undriven_3), .D(fgnfet_9_d), .S(1'b0));
  FGNFET fgnfet_85 (.G(Q_1), .D(fgnfet_9_d), .S(1'b0));
  FGNFET #(.Blown("true")) fgnfet_86 (.G(undriven_3), .D(fgnfet_11_d), .S(1'b0));
  FGNFET fgnfet_87 (.G(Q_1), .D(fgnfet_11_d), .S(1'b0));
  FGNFET #(.Blown("true")) fgnfet_88 (.G(undriven_3), .D(fgnfet_13_d), .S(1'b0));
  FGNFET #(.Blown("true")) fgnfet_89 (.G(Q_1), .D(fgnfet_13_d), .S(1'b0));
  FGNFET fgnfet_90 (.G(undriven_3), .D(fgnfet_15_d), .S(1'b0));
  FGNFET fgnfet_91 (.G(Q_1), .D(fgnfet_15_d), .S(1'b0));
  FGNFET fgnfet_92 (.G(undriven_3), .D(fgnfet_17_d), .S(1'b0));
  FGNFET fgnfet_93 (.G(Q_1), .D(fgnfet_17_d), .S(1'b0));
  FGNFET fgnfet_94 (.G(undriven_3), .D(fgnfet_19_d), .S(1'b0));
  FGNFET fgnfet_95 (.G(Q_1), .D(fgnfet_19_d), .S(1'b0));
  FGNFET #(.Blown("true")) fgnfet_96 (.G(undriven_3), .D(fgnfet_21_d), .S(1'b0));
  FGNFET #(.Blown("true")) fgnfet_97 (.G(Q_1), .D(fgnfet_21_d), .S(1'b0));
  FGNFET fgnfet_98 (.G(undriven_3), .D(fgnfet_23_d), .S(1'b0));
  FGNFET #(.Blown("true")) fgnfet_99 (.G(Q_1), .D(fgnfet_23_d), .S(1'b0));
  FGNFET fgnfet_100 (.G(undriven_3), .D(fgnfet_25_d), .S(1'b0));
  FGNFET fgnfet_101 (.G(Q_1), .D(fgnfet_25_d), .S(1'b0));
  FGNFET fgnfet_102 (.G(undriven_3), .D(fgnfet_27_d), .S(1'b0));
  FGNFET fgnfet_103 (.G(Q_1), .D(fgnfet_27_d), .S(1'b0));
  FGNFET fgnfet_104 (.G(undriven_3), .D(fgnfet_29_d), .S(1'b0));
  FGNFET fgnfet_105 (.G(Q_1), .D(fgnfet_29_d), .S(1'b0));
  // Not not_4 has open pins: in=Q_1, out=open
  FGNFET #(.Blown("true")) fgnfet_106 (.G(undriven_4), .D(fgnfet_1_d), .S(1'b0));
  FGNFET fgnfet_107 (.G(undriven_4), .D(fgnfet_3_d), .S(1'b0));
  FGNFET fgnfet_108 (.G(undriven_4), .D(fgnfet_5_d), .S(1'b0));
  FGNFET fgnfet_109 (.G(undriven_4), .D(fgnfet_7_d), .S(1'b0));
  FGNFET fgnfet_110 (.G(undriven_4), .D(fgnfet_9_d), .S(1'b0));
  FGNFET #(.Blown("true")) fgnfet_111 (.G(undriven_4), .D(fgnfet_11_d), .S(1'b0));
  FGNFET fgnfet_112 (.G(undriven_4), .D(fgnfet_13_d), .S(1'b0));
  FGNFET fgnfet_113 (.G(undriven_4), .D(fgnfet_15_d), .S(1'b0));
  FGNFET fgnfet_114 (.G(undriven_4), .D(fgnfet_17_d), .S(1'b0));
  FGNFET fgnfet_115 (.G(undriven_4), .D(fgnfet_19_d), .S(1'b0));
  FGNFET fgnfet_116 (.G(undriven_4), .D(fgnfet_21_d), .S(1'b0));
  FGNFET #(.Blown("true")) fgnfet_117 (.G(undriven_4), .D(fgnfet_23_d), .S(1'b0));
  FGNFET #(.Blown("true")) fgnfet_118 (.G(undriven_4), .D(fgnfet_25_d), .S(1'b0));
  FGNFET fgnfet_119 (.G(undriven_4), .D(fgnfet_27_d), .S(1'b0));
  FGNFET fgnfet_120 (.G(undriven_4), .D(fgnfet_29_d), .S(1'b0));
  // Not not_5 has open pins: in=Q_0, out=open
  FGNFET fgnfet_121 (.G(Q_0), .D(fgnfet_1_d), .S(1'b0));
  FGNFET fgnfet_122 (.G(Q_0), .D(fgnfet_3_d), .S(1'b0));
  FGNFET fgnfet_123 (.G(Q_0), .D(fgnfet_5_d), .S(1'b0));
  FGNFET fgnfet_124 (.G(Q_0), .D(fgnfet_7_d), .S(1'b0));
  FGNFET fgnfet_125 (.G(Q_0), .D(fgnfet_9_d), .S(1'b0));
  FGNFET #(.Blown("true")) fgnfet_126 (.G(Q_0), .D(fgnfet_11_d), .S(1'b0));
  FGNFET fgnfet_127 (.G(Q_0), .D(fgnfet_13_d), .S(1'b0));
  FGNFET fgnfet_128 (.G(Q_0), .D(fgnfet_15_d), .S(1'b0));
  FGNFET fgnfet_129 (.G(Q_0), .D(fgnfet_17_d), .S(1'b0));
  FGNFET fgnfet_130 (.G(Q_0), .D(fgnfet_19_d), .S(1'b0));
  FGNFET #(.Blown("true")) fgnfet_131 (.G(Q_0), .D(fgnfet_21_d), .S(1'b0));
  FGNFET fgnfet_132 (.G(Q_0), .D(fgnfet_23_d), .S(1'b0));
  FGNFET #(.Blown("true")) fgnfet_133 (.G(Q_0), .D(fgnfet_25_d), .S(1'b0));
  FGNFET fgnfet_134 (.G(Q_0), .D(fgnfet_27_d), .S(1'b0));
  FGNFET fgnfet_135 (.G(Q_0), .D(fgnfet_29_d), .S(1'b0));
  PullUp pullup_1 (.out(fgnfet_1_d));
  FGNFET #(.Blown("true")) fgnfet_136 (.G(undriven_5), .D(fgnfet_1_d), .S(1'b0));
  PullUp pullup_2 (.out(fgnfet_3_d));
  FGNFET fgnfet_137 (.G(undriven_5), .D(fgnfet_3_d), .S(1'b0));
  PullUp pullup_3 (.out(fgnfet_5_d));
  FGNFET fgnfet_138 (.G(undriven_5), .D(fgnfet_5_d), .S(1'b0));
  PullUp pullup_4 (.out(fgnfet_7_d));
  FGNFET fgnfet_139 (.G(undriven_5), .D(fgnfet_7_d), .S(1'b0));
  PullUp pullup_5 (.out(fgnfet_9_d));
  FGNFET fgnfet_140 (.G(undriven_5), .D(fgnfet_9_d), .S(1'b0));
  PullUp pullup_6 (.out(fgnfet_11_d));
  FGNFET fgnfet_141 (.G(undriven_5), .D(fgnfet_11_d), .S(1'b0));
  PullUp pullup_7 (.out(fgnfet_13_d));
  FGNFET #(.Blown("true")) fgnfet_142 (.G(undriven_5), .D(fgnfet_13_d), .S(1'b0));
  PullUp pullup_8 (.out(fgnfet_15_d));
  FGNFET fgnfet_143 (.G(undriven_5), .D(fgnfet_15_d), .S(1'b0));
  PullUp pullup_9 (.out(fgnfet_17_d));
  FGNFET fgnfet_144 (.G(undriven_5), .D(fgnfet_17_d), .S(1'b0));
  PullUp pullup_10 (.out(fgnfet_19_d));
  FGNFET fgnfet_145 (.G(undriven_5), .D(fgnfet_19_d), .S(1'b0));
  PullUp pullup_11 (.out(fgnfet_21_d));
  FGNFET fgnfet_146 (.G(undriven_5), .D(fgnfet_21_d), .S(1'b0));
  PullUp pullup_12 (.out(fgnfet_23_d));
  FGNFET #(.Blown("true")) fgnfet_147 (.G(undriven_5), .D(fgnfet_23_d), .S(1'b0));
  PullUp pullup_13 (.out(fgnfet_25_d));
  FGNFET #(.Blown("true")) fgnfet_148 (.G(undriven_5), .D(fgnfet_25_d), .S(1'b0));
  PullUp pullup_14 (.out(fgnfet_27_d));
  FGNFET fgnfet_149 (.G(undriven_5), .D(fgnfet_27_d), .S(1'b0));
  PullUp pullup_15 (.out(fgnfet_29_d));
  FGNFET fgnfet_150 (.G(undriven_5), .D(fgnfet_29_d), .S(1'b0));
  // Or or_1 has open pins: In_1=fgnfet_1_d, In_2=fgnfet_3_d, In_3=fgnfet_5_d, In_4=fgnfet_7_d, In_5=fgnfet_9_d, out=open
  // Or or_2 has open pins: In_1=fgnfet_11_d, In_2=fgnfet_13_d, In_3=fgnfet_15_d, In_4=fgnfet_17_d, In_5=fgnfet_19_d, out=open
  // Or or_3 has open pins: In_1=fgnfet_21_d, In_2=fgnfet_23_d, In_3=fgnfet_25_d, In_4=fgnfet_27_d, In_5=fgnfet_29_d, out=open
  D_FF MC0 (.D(undriven_6), .C(Clock), .Q(MC0_q));  // open: nQ
  D_FF MC1 (.D(undriven_7), .C(Clock), .Q(MC1_q));  // open: nQ
  D_FF MC2 (.D(undriven_8), .C(Clock), .Q(MC2_q));  // open: nQ
  PullUp pullup_16 (.out(pullup_16_out));
  FGNFET #(.Blown("true")) fgnfet_151 (.G(1'b1), .D(pullup_16_out), .S(1'b0));
  Multiplexer multiplexer_1 (.sel(pullup_16_out), .in_0(undriven_6), .in_1(MC0_q), .out(Q_0));
  PullUp pullup_17 (.out(pullup_17_out));
  FGNFET #(.Blown("true")) fgnfet_152 (.G(1'b1), .D(pullup_17_out), .S(1'b0));
  Multiplexer multiplexer_2 (.sel(pullup_17_out), .in_0(undriven_7), .in_1(MC1_q), .out(Q_1));
  PullUp pullup_18 (.out(pullup_18_out));
  FGNFET #(.Blown("true")) fgnfet_153 (.G(1'b1), .D(pullup_18_out), .S(1'b0));
  Multiplexer multiplexer_3 (.sel(pullup_18_out), .in_0(undriven_8), .in_1(MC2_q), .out(Q_2));

  // Notes on the sheet:
  //   A: First freely configurable input.
  //   {{de Erster frei konfigurierbarer Eingang.}}
  //   B: Second freely configurable input.
  //   {{de Zweiter frei konfigurierbarer Eingang.}}
  //   Q_0: output bit 0
  //   {{de Das 0. Ausgangsbit.}}
  //   Q_1: output bit 1
  //   {{de Das 1. Ausgangsbit.}}
  //   Q_2: output bit 2
  //   {{de Das 2. Ausgangsbit.}}
endmodule

/* Test case Counter:
          A B Clock Q_2 Q_1 Q_0
          0 0 0      0   0   0
repeat(8) 0 0 C     bits(3,n+1)
repeat(8) 1 0 C     bits(3,n+1)
*/
