// Digital circuit PAL2v3.dig as structural Verilog
// Simple PAL with two inputs and three macrocells. 
// Each cell can be combinatorial or used as a flip-flop 
// buffered (combinatorial, registered). The component 
// is programmed via the diodes, which can be burned 
// or programmed. For simplicity, the diodes can be 
// programmed with the [P] key.
// {{de Einfaches PAL mit zwei Eingängen und drei
// Makrozellen. Jede Zelle kann kombinatorisch oder
// als mit Flip-Flop gepuffert (combinatorial, registered)
// verwendet werden. Programmiert wird der Baustein
// über die Dioden, die "durchgebrannt" bzw. 
// Programmiert werden können. Zur Vereinfachung 
// können die Dioden mit der Taste [P] programmiert 
// werden.}}
module PAL2v3 (
  input  A,
  input  B,
  input  Clock,
  output Y_0,
  output Y_1,
  output Y_2
);

  wire diodebackward_1_out, diodebackward_3_out, diodebackward_5_out, diodebackward_7_out,
       diodebackward_9_out, diodebackward_11_out, diodebackward_13_out, diodebackward_15_out,
       diodebackward_17_out, diodebackward_19_out, diodebackward_21_out, diodebackward_23_out,
       diodebackward_25_out, diodebackward_27_out, diodebackward_29_out, MC0_q, MC1_q, MC2_q, pullup_16_out,
       pullup_17_out, pullup_18_out, undriven, undriven_2, undriven_3, undriven_4, undriven_5, undriven_6,
       undriven_7, undriven_8;

  // Not not_1 has open pins: in=A, out=open
  DiodeBackward #(.Blown("true")) diodebackward_1 (.in(A), .out(diodebackward_1_out));
  DiodeBackward #(.Blown("true")) diodebackward_2 (.in(undriven), .out(diodebackward_1_out));
  DiodeBackward diodebackward_3 (.in(A), .out(diodebackward_3_out));
  DiodeBackward diodebackward_4 (.in(undriven), .out(diodebackward_3_out));
  DiodeBackward diodebackward_5 (.in(A), .out(diodebackward_5_out));
  DiodeBackward diodebackward_6 (.in(undriven), .out(diodebackward_5_out));
  DiodeBackward diodebackward_7 (.in(A), .out(diodebackward_7_out));
  DiodeBackward diodebackward_8 (.in(undriven), .out(diodebackward_7_out));
  DiodeBackward diodebackward_9 (.in(A), .out(diodebackward_9_out));
  DiodeBackward diodebackward_10 (.in(undriven), .out(diodebackward_9_out));
  DiodeBackward #(.Blown("true")) diodebackward_11 (.in(A), .out(diodebackward_11_out));
  DiodeBackward #(.Blown("true")) diodebackward_12 (.in(undriven), .out(diodebackward_11_out));
  DiodeBackward #(.Blown("true")) diodebackward_13 (.in(A), .out(diodebackward_13_out));
  DiodeBackward #(.Blown("true")) diodebackward_14 (.in(undriven), .out(diodebackward_13_out));
  DiodeBackward diodebackward_15 (.in(A), .out(diodebackward_15_out));
  DiodeBackward diodebackward_16 (.in(undriven), .out(diodebackward_15_out));
  DiodeBackward diodebackward_17 (.in(A), .out(diodebackward_17_out));
  DiodeBackward diodebackward_18 (.in(undriven), .out(diodebackward_17_out));
  DiodeBackward diodebackward_19 (.in(A), .out(diodebackward_19_out));
  DiodeBackward diodebackward_20 (.in(undriven), .out(diodebackward_19_out));
  DiodeBackward #(.Blown("true")) diodebackward_21 (.in(A), .out(diodebackward_21_out));
  DiodeBackward #(.Blown("true")) diodebackward_22 (.in(undriven), .out(diodebackward_21_out));
  DiodeBackward #(.Blown("true")) diodebackward_23 (.in(A), .out(diodebackward_23_out));
  DiodeBackward #(.Blown("true")) diodebackward_24 (.in(undriven), .out(diodebackward_23_out));
  DiodeBackward #(.Blown("true")) diodebackward_25 (.in(A), .out(diodebackward_25_out));
  DiodeBackward #(.Blown("true")) diodebackward_26 (.in(undriven), .out(diodebackward_25_out));
  DiodeBackward diodebackward_27 (.in(A), .out(diodebackward_27_out));
  DiodeBackward diodebackward_28 (.in(undriven), .out(diodebackward_27_out));
  DiodeBackward diodebackward_29 (.in(A), .out(diodebackward_29_out));
  DiodeBackward diodebackward_30 (.in(undriven), .out(diodebackward_29_out));
  // Not not_2 has open pins: in=B, out=open
  DiodeBackward #(.Blown("true")) diodebackward_31 (.in(B), .out(diodebackward_1_out));
  DiodeBackward #(.Blown("true")) diodebackward_32 (.in(undriven_2), .out(diodebackward_1_out));
  DiodeBackward diodebackward_33 (.in(B), .out(diodebackward_3_out));
  DiodeBackward diodebackward_34 (.in(undriven_2), .out(diodebackward_3_out));
  DiodeBackward diodebackward_35 (.in(B), .out(diodebackward_5_out));
  DiodeBackward diodebackward_36 (.in(undriven_2), .out(diodebackward_5_out));
  DiodeBackward diodebackward_37 (.in(B), .out(diodebackward_7_out));
  DiodeBackward diodebackward_38 (.in(undriven_2), .out(diodebackward_7_out));
  DiodeBackward diodebackward_39 (.in(B), .out(diodebackward_9_out));
  DiodeBackward diodebackward_40 (.in(undriven_2), .out(diodebackward_9_out));
  DiodeBackward #(.Blown("true")) diodebackward_41 (.in(B), .out(diodebackward_11_out));
  DiodeBackward #(.Blown("true")) diodebackward_42 (.in(undriven_2), .out(diodebackward_11_out));
  DiodeBackward #(.Blown("true")) diodebackward_43 (.in(B), .out(diodebackward_13_out));
  DiodeBackward #(.Blown("true")) diodebackward_44 (.in(undriven_2), .out(diodebackward_13_out));
  DiodeBackward diodebackward_45 (.in(B), .out(diodebackward_15_out));
  DiodeBackward diodebackward_46 (.in(undriven_2), .out(diodebackward_15_out));
  DiodeBackward diodebackward_47 (.in(B), .out(diodebackward_17_out));
  DiodeBackward diodebackward_48 (.in(undriven_2), .out(diodebackward_17_out));
  DiodeBackward diodebackward_49 (.in(B), .out(diodebackward_19_out));
  DiodeBackward diodebackward_50 (.in(undriven_2), .out(diodebackward_19_out));
  DiodeBackward #(.Blown("true")) diodebackward_51 (.in(B), .out(diodebackward_21_out));
  DiodeBackward #(.Blown("true")) diodebackward_52 (.in(undriven_2), .out(diodebackward_21_out));
  DiodeBackward #(.Blown("true")) diodebackward_53 (.in(B), .out(diodebackward_23_out));
  DiodeBackward #(.Blown("true")) diodebackward_54 (.in(undriven_2), .out(diodebackward_23_out));
  DiodeBackward #(.Blown("true")) diodebackward_55 (.in(B), .out(diodebackward_25_out));
  DiodeBackward #(.Blown("true")) diodebackward_56 (.in(undriven_2), .out(diodebackward_25_out));
  DiodeBackward diodebackward_57 (.in(B), .out(diodebackward_27_out));
  DiodeBackward diodebackward_58 (.in(undriven_2), .out(diodebackward_27_out));
  DiodeBackward diodebackward_59 (.in(B), .out(diodebackward_29_out));
  DiodeBackward diodebackward_60 (.in(undriven_2), .out(diodebackward_29_out));
  // Not not_3 has open pins: in=Y_0, out=open
  DiodeBackward #(.Blown("true")) diodebackward_61 (.in(Y_0), .out(diodebackward_1_out));
  DiodeBackward diodebackward_62 (.in(undriven_3), .out(diodebackward_1_out));
  DiodeBackward diodebackward_63 (.in(Y_0), .out(diodebackward_3_out));
  DiodeBackward diodebackward_64 (.in(undriven_3), .out(diodebackward_3_out));
  DiodeBackward diodebackward_65 (.in(Y_0), .out(diodebackward_5_out));
  DiodeBackward diodebackward_66 (.in(undriven_3), .out(diodebackward_5_out));
  DiodeBackward diodebackward_67 (.in(Y_0), .out(diodebackward_7_out));
  DiodeBackward diodebackward_68 (.in(undriven_3), .out(diodebackward_7_out));
  DiodeBackward diodebackward_69 (.in(Y_0), .out(diodebackward_9_out));
  DiodeBackward diodebackward_70 (.in(undriven_3), .out(diodebackward_9_out));
  DiodeBackward diodebackward_71 (.in(Y_0), .out(diodebackward_11_out));
  DiodeBackward #(.Blown("true")) diodebackward_72 (.in(undriven_3), .out(diodebackward_11_out));
  DiodeBackward #(.Blown("true")) diodebackward_73 (.in(Y_0), .out(diodebackward_13_out));
  DiodeBackward diodebackward_74 (.in(undriven_3), .out(diodebackward_13_out));
  DiodeBackward diodebackward_75 (.in(Y_0), .out(diodebackward_15_out));
  DiodeBackward diodebackward_76 (.in(undriven_3), .out(diodebackward_15_out));
  DiodeBackward diodebackward_77 (.in(Y_0), .out(diodebackward_17_out));
  DiodeBackward diodebackward_78 (.in(undriven_3), .out(diodebackward_17_out));
  DiodeBackward diodebackward_79 (.in(Y_0), .out(diodebackward_19_out));
  DiodeBackward diodebackward_80 (.in(undriven_3), .out(diodebackward_19_out));
  DiodeBackward diodebackward_81 (.in(Y_0), .out(diodebackward_21_out));
  DiodeBackward #(.Blown("true")) diodebackward_82 (.in(undriven_3), .out(diodebackward_21_out));
  DiodeBackward #(.Blown("true")) diodebackward_83 (.in(Y_0), .out(diodebackward_23_out));
  DiodeBackward diodebackward_84 (.in(undriven_3), .out(diodebackward_23_out));
  DiodeBackward #(.Blown("true")) diodebackward_85 (.in(Y_0), .out(diodebackward_25_out));
  DiodeBackward #(.Blown("true")) diodebackward_86 (.in(undriven_3), .out(diodebackward_25_out));
  DiodeBackward diodebackward_87 (.in(Y_0), .out(diodebackward_27_out));
  DiodeBackward diodebackward_88 (.in(undriven_3), .out(diodebackward_27_out));
  DiodeBackward diodebackward_89 (.in(Y_0), .out(diodebackward_29_out));
  DiodeBackward diodebackward_90 (.in(undriven_3), .out(diodebackward_29_out));
  // Not not_4 has open pins: in=Y_1, out=open
  DiodeBackward #(.Blown("true")) diodebackward_91 (.in(Y_1), .out(diodebackward_1_out));
  DiodeBackward #(.Blown("true")) diodebackward_92 (.in(undriven_4), .out(diodebackward_1_out));
  DiodeBackward diodebackward_93 (.in(Y_1), .out(diodebackward_3_out));
  DiodeBackward diodebackward_94 (.in(undriven_4), .out(diodebackward_3_out));
  DiodeBackward diodebackward_95 (.in(Y_1), .out(diodebackward_5_out));
  DiodeBackward diodebackward_96 (.in(undriven_4), .out(diodebackward_5_out));
  DiodeBackward diodebackward_97 (.in(Y_1), .out(diodebackward_7_out));
  DiodeBackward diodebackward_98 (.in(undriven_4), .out(diodebackward_7_out));
  DiodeBackward diodebackward_99 (.in(Y_1), .out(diodebackward_9_out));
  DiodeBackward diodebackward_100 (.in(undriven_4), .out(diodebackward_9_out));
  DiodeBackward #(.Blown("true")) diodebackward_101 (.in(Y_1), .out(diodebackward_11_out));
  DiodeBackward diodebackward_102 (.in(undriven_4), .out(diodebackward_11_out));
  DiodeBackward diodebackward_103 (.in(Y_1), .out(diodebackward_13_out));
  DiodeBackward #(.Blown("true")) diodebackward_104 (.in(undriven_4), .out(diodebackward_13_out));
  DiodeBackward diodebackward_105 (.in(Y_1), .out(diodebackward_15_out));
  DiodeBackward diodebackward_106 (.in(undriven_4), .out(diodebackward_15_out));
  DiodeBackward diodebackward_107 (.in(Y_1), .out(diodebackward_17_out));
  DiodeBackward diodebackward_108 (.in(undriven_4), .out(diodebackward_17_out));
  DiodeBackward diodebackward_109 (.in(Y_1), .out(diodebackward_19_out));
  DiodeBackward diodebackward_110 (.in(undriven_4), .out(diodebackward_19_out));
  DiodeBackward diodebackward_111 (.in(Y_1), .out(diodebackward_21_out));
  DiodeBackward #(.Blown("true")) diodebackward_112 (.in(undriven_4), .out(diodebackward_21_out));
  DiodeBackward #(.Blown("true")) diodebackward_113 (.in(Y_1), .out(diodebackward_23_out));
  DiodeBackward #(.Blown("true")) diodebackward_114 (.in(undriven_4), .out(diodebackward_23_out));
  DiodeBackward #(.Blown("true")) diodebackward_115 (.in(Y_1), .out(diodebackward_25_out));
  DiodeBackward diodebackward_116 (.in(undriven_4), .out(diodebackward_25_out));
  DiodeBackward diodebackward_117 (.in(Y_1), .out(diodebackward_27_out));
  DiodeBackward diodebackward_118 (.in(undriven_4), .out(diodebackward_27_out));
  DiodeBackward diodebackward_119 (.in(Y_1), .out(diodebackward_29_out));
  DiodeBackward diodebackward_120 (.in(undriven_4), .out(diodebackward_29_out));
  // Not not_5 has open pins: in=Y_2, out=open
  DiodeBackward #(.Blown("true")) diodebackward_121 (.in(Y_2), .out(diodebackward_1_out));
  DiodeBackward #(.Blown("true")) diodebackward_122 (.in(undriven_5), .out(diodebackward_1_out));
  DiodeBackward diodebackward_123 (.in(Y_2), .out(diodebackward_3_out));
  DiodeBackward diodebackward_124 (.in(undriven_5), .out(diodebackward_3_out));
  DiodeBackward diodebackward_125 (.in(Y_2), .out(diodebackward_5_out));
  DiodeBackward diodebackward_126 (.in(undriven_5), .out(diodebackward_5_out));
  DiodeBackward diodebackward_127 (.in(Y_2), .out(diodebackward_7_out));
  DiodeBackward diodebackward_128 (.in(undriven_5), .out(diodebackward_7_out));
  DiodeBackward diodebackward_129 (.in(Y_2), .out(diodebackward_9_out));
  DiodeBackward diodebackward_130 (.in(undriven_5), .out(diodebackward_9_out));
  DiodeBackward #(.Blown("true")) diodebackward_131 (.in(Y_2), .out(diodebackward_11_out));
  DiodeBackward #(.Blown("true")) diodebackward_132 (.in(undriven_5), .out(diodebackward_11_out));
  DiodeBackward #(.Blown("true")) diodebackward_133 (.in(Y_2), .out(diodebackward_13_out));
  DiodeBackward #(.Blown("true")) diodebackward_134 (.in(undriven_5), .out(diodebackward_13_out));
  DiodeBackward diodebackward_135 (.in(Y_2), .out(diodebackward_15_out));
  DiodeBackward diodebackward_136 (.in(undriven_5), .out(diodebackward_15_out));
  DiodeBackward diodebackward_137 (.in(Y_2), .out(diodebackward_17_out));
  DiodeBackward diodebackward_138 (.in(undriven_5), .out(diodebackward_17_out));
  DiodeBackward diodebackward_139 (.in(Y_2), .out(diodebackward_19_out));
  DiodeBackward diodebackward_140 (.in(undriven_5), .out(diodebackward_19_out));
  DiodeBackward #(.Blown("true")) diodebackward_141 (.in(Y_2), .out(diodebackward_21_out));
  DiodeBackward diodebackward_142 (.in(undriven_5), .out(diodebackward_21_out));
  DiodeBackward diodebackward_143 (.in(Y_2), .out(diodebackward_23_out));
  DiodeBackward #(.Blown("true")) diodebackward_144 (.in(undriven_5), .out(diodebackward_23_out));
  DiodeBackward diodebackward_145 (.in(Y_2), .out(diodebackward_25_out));
  DiodeBackward #(.Blown("true")) diodebackward_146 (.in(undriven_5), .out(diodebackward_25_out));
  DiodeBackward diodebackward_147 (.in(Y_2), .out(diodebackward_27_out));
  DiodeBackward diodebackward_148 (.in(undriven_5), .out(diodebackward_27_out));
  DiodeBackward diodebackward_149 (.in(Y_2), .out(diodebackward_29_out));
  DiodeBackward diodebackward_150 (.in(undriven_5), .out(diodebackward_29_out));
  PullUp pullup_1 (.out(diodebackward_1_out));
  PullUp pullup_2 (.out(diodebackward_3_out));
  PullUp pullup_3 (.out(diodebackward_5_out));
  PullUp pullup_4 (.out(diodebackward_7_out));
  PullUp pullup_5 (.out(diodebackward_9_out));
  PullUp pullup_6 (.out(diodebackward_11_out));
  PullUp pullup_7 (.out(diodebackward_13_out));
  PullUp pullup_8 (.out(diodebackward_15_out));
  PullUp pullup_9 (.out(diodebackward_17_out));
  PullUp pullup_10 (.out(diodebackward_19_out));
  PullUp pullup_11 (.out(diodebackward_21_out));
  PullUp pullup_12 (.out(diodebackward_23_out));
  PullUp pullup_13 (.out(diodebackward_25_out));
  PullUp pullup_14 (.out(diodebackward_27_out));
  PullUp pullup_15 (.out(diodebackward_29_out));
  // Or or_1 has open pins: In_1=diodebackward_1_out, In_2=diodebackward_3_out, In_3=diodebackward_5_out, In_4=diodebackward_7_out, In_5=diodebackward_9_out, out=open
  // Or or_2 has open pins: In_1=diodebackward_11_out, In_2=diodebackward_13_out, In_3=diodebackward_15_out, In_4=diodebackward_17_out, In_5=diodebackward_19_out, out=open
  // Or or_3 has open pins: In_1=diodebackward_21_out, In_2=diodebackward_23_out, In_3=diodebackward_25_out, In_4=diodebackward_27_out, In_5=diodebackward_29_out, out=open
  D_FF MC0 (.D(undriven_6), .C(Clock), .Q(MC0_q));  // open: nQ
  D_FF MC1 (.D(undriven_7), .C(Clock), .Q(MC1_q));  // open: nQ
  D_FF MC2 (.D(undriven_8), .C(Clock), .Q(MC2_q));  // open: nQ
  PullUp pullup_16 (.out(pullup_16_out));
  DiodeBackward #(.Blown("true")) diodebackward_151 (.in(1'b0), .out(pullup_16_out));
  Multiplexer multiplexer_1 (.sel(pullup_16_out), .in_0(undriven_6), .in_1(MC0_q), .out(Y_0));
  PullUp pullup_17 (.out(pullup_17_out));
  DiodeBackward #(.Blown("true")) diodebackward_152 (.in(1'b0), .out(pullup_17_out));
  Multiplexer multiplexer_2 (.sel(pullup_17_out), .in_0(undriven_7), .in_1(MC1_q), .out(Y_1));
  PullUp pullup_18 (.out(pullup_18_out));
  DiodeBackward #(.Blown("true")) diodebackward_153 (.in(1'b0), .out(pullup_18_out));
  Multiplexer multiplexer_3 (.sel(pullup_18_out), .in_0(undriven_8), .in_1(MC2_q), .out(Y_2));

  // Notes on the sheet:
  //   A: First freely configurable input.
  //   {{de Erster frei konfigurierbarer Eingang.}}
  //   B: Second freely configurable input.
  //   {{de Zweiter frei konfigurierbarer Eingang.}}
  //   Y_0: output bit 0
  //   {{de Das 0. Ausgangsbit.}}
  //   Y_1: output bit 1
  //   {{de Das 1. Ausgangsbit.}}
  //   Y_2: output bit 2
  //   {{de Das 2. Ausgangsbit.}}
endmodule

/* Test case Counter:
A B Clock Y_2 Y_1 Y_0
0 0 0     0   0   0
repeat(8) 0 0 C bits(3,n+1)
*/
