// Digital circuit PLA.dig as structural Verilog
// Typical PLA device with an AND and an OR matrix.
// The component is programmed via the diodes, which 
// can be burned or programmed. For simplicity, the 
// diodes can be programmed with the [P] key.
// {{de Typischer PLA Baustein mit einer UND und einer 
// ODER Matrix.
// Programmiert wird der Baustein
// über die Dioden, die "durchgebrannt" bzw. 
// Programmiert werden können. Zur Vereinfachung 
// können die Dioden mit der Taste [P] programmiert 
// werden.}}
module PLA (
  input  A,
  input  B,
  input  C,
  input  D,
  output Y_0,
  output Y_1,
  output Y_2,
  output Y_3
);

  wire diodebackward_1_out, diodebackward_3_out, diodebackward_5_out, diodebackward_7_out,
       diodebackward_9_out, diodebackward_11_out, undriven, undriven_2, undriven_3, undriven_4;

  // Not not_1 has open pins: in=A, out=open
  DiodeBackward diodebackward_1 (.in(A), .out(diodebackward_1_out));
  DiodeBackward #(.Blown("true")) diodebackward_2 (.in(undriven), .out(diodebackward_1_out));
  DiodeBackward #(.Blown("true")) diodebackward_3 (.in(A), .out(diodebackward_3_out));
  DiodeBackward diodebackward_4 (.in(undriven), .out(diodebackward_3_out));
  DiodeBackward #(.Blown("true")) diodebackward_5 (.in(A), .out(diodebackward_5_out));
  DiodeBackward #(.Blown("true")) diodebackward_6 (.in(undriven), .out(diodebackward_5_out));
  DiodeBackward diodebackward_7 (.in(A), .out(diodebackward_7_out));
  DiodeBackward #(.Blown("true")) diodebackward_8 (.in(undriven), .out(diodebackward_7_out));
  DiodeBackward #(.Blown("true")) diodebackward_9 (.in(A), .out(diodebackward_9_out));
  DiodeBackward #(.Blown("true")) diodebackward_10 (.in(undriven), .out(diodebackward_9_out));
  DiodeBackward diodebackward_11 (.in(A), .out(diodebackward_11_out));
  DiodeBackward diodebackward_12 (.in(undriven), .out(diodebackward_11_out));
  // Not not_2 has open pins: in=B, out=open
  DiodeBackward #(.Blown("true")) diodebackward_13 (.in(B), .out(diodebackward_1_out));
  DiodeBackward diodebackward_14 (.in(undriven_2), .out(diodebackward_1_out));
  DiodeBackward diodebackward_15 (.in(B), .out(diodebackward_3_out));
  DiodeBackward #(.Blown("true")) diodebackward_16 (.in(undriven_2), .out(diodebackward_3_out));
  DiodeBackward #(.Blown("true")) diodebackward_17 (.in(B), .out(diodebackward_5_out));
  DiodeBackward #(.Blown("true")) diodebackward_18 (.in(undriven_2), .out(diodebackward_5_out));
  DiodeBackward #(.Blown("true")) diodebackward_19 (.in(B), .out(diodebackward_7_out));
  DiodeBackward #(.Blown("true")) diodebackward_20 (.in(undriven_2), .out(diodebackward_7_out));
  DiodeBackward #(.Blown("true")) diodebackward_21 (.in(B), .out(diodebackward_9_out));
  DiodeBackward #(.Blown("true")) diodebackward_22 (.in(undriven_2), .out(diodebackward_9_out));
  DiodeBackward diodebackward_23 (.in(B), .out(diodebackward_11_out));
  DiodeBackward diodebackward_24 (.in(undriven_2), .out(diodebackward_11_out));
  // Not not_3 has open pins: in=C, out=open
  DiodeBackward #(.Blown("true")) diodebackward_25 (.in(C), .out(diodebackward_1_out));
  DiodeBackward #(.Blown("true")) diodebackward_26 (.in(undriven_3), .out(diodebackward_1_out));
  DiodeBackward #(.Blown("true")) diodebackward_27 (.in(C), .out(diodebackward_3_out));
  DiodeBackward #(.Blown("true")) diodebackward_28 (.in(undriven_3), .out(diodebackward_3_out));
  DiodeBackward diodebackward_29 (.in(C), .out(diodebackward_5_out));
  DiodeBackward #(.Blown("true")) diodebackward_30 (.in(undriven_3), .out(diodebackward_5_out));
  DiodeBackward #(.Blown("true")) diodebackward_31 (.in(C), .out(diodebackward_7_out));
  DiodeBackward #(.Blown("true")) diodebackward_32 (.in(undriven_3), .out(diodebackward_7_out));
  DiodeBackward diodebackward_33 (.in(C), .out(diodebackward_9_out));
  DiodeBackward #(.Blown("true")) diodebackward_34 (.in(undriven_3), .out(diodebackward_9_out));
  DiodeBackward diodebackward_35 (.in(C), .out(diodebackward_11_out));
  DiodeBackward diodebackward_36 (.in(undriven_3), .out(diodebackward_11_out));
  // Not not_4 has open pins: in=D, out=open
  DiodeBackward #(.Blown("true")) diodebackward_37 (.in(D), .out(diodebackward_1_out));
  DiodeBackward #(.Blown("true")) diodebackward_38 (.in(undriven_4), .out(diodebackward_1_out));
  DiodeBackward #(.Blown("true")) diodebackward_39 (.in(D), .out(diodebackward_3_out));
  DiodeBackward #(.Blown("true")) diodebackward_40 (.in(undriven_4), .out(diodebackward_3_out));
  DiodeBackward diodebackward_41 (.in(D), .out(diodebackward_5_out));
  DiodeBackward #(.Blown("true")) diodebackward_42 (.in(undriven_4), .out(diodebackward_5_out));
  DiodeBackward #(.Blown("true")) diodebackward_43 (.in(D), .out(diodebackward_7_out));
  DiodeBackward #(.Blown("true")) diodebackward_44 (.in(undriven_4), .out(diodebackward_7_out));
  DiodeBackward #(.Blown("true")) diodebackward_45 (.in(D), .out(diodebackward_9_out));
  DiodeBackward #(.Blown("true")) diodebackward_46 (.in(undriven_4), .out(diodebackward_9_out));
  DiodeBackward diodebackward_47 (.in(D), .out(diodebackward_11_out));
  DiodeBackward diodebackward_48 (.in(undriven_4), .out(diodebackward_11_out));
  PullUp pullup_1 (.out(diodebackward_1_out));
  PullUp pullup_2 (.out(diodebackward_3_out));
  PullUp pullup_3 (.out(diodebackward_5_out));
  PullUp pullup_4 (.out(diodebackward_7_out));
  PullUp pullup_5 (.out(diodebackward_9_out));
  PullUp pullup_6 (.out(diodebackward_11_out));
  DiodeForward diodeforward_1 (.in(diodebackward_1_out), .out(Y_0));
  DiodeForward diodeforward_2 (.in(diodebackward_3_out), .out(Y_0));
  DiodeForward #(.Blown("true")) diodeforward_3 (.in(diodebackward_5_out), .out(Y_0));
  DiodeForward #(.Blown("true")) diodeforward_4 (.in(diodebackward_7_out), .out(Y_0));
  DiodeForward #(.Blown("true")) diodeforward_5 (.in(diodebackward_9_out), .out(Y_0));
  DiodeForward diodeforward_6 (.in(diodebackward_11_out), .out(Y_0));
  PullDown pulldown_1 (.out(Y_0));
  DiodeForward #(.Blown("true")) diodeforward_7 (.in(diodebackward_1_out), .out(Y_1));
  DiodeForward #(.Blown("true")) diodeforward_8 (.in(diodebackward_3_out), .out(Y_1));
  DiodeForward diodeforward_9 (.in(diodebackward_5_out), .out(Y_1));
  DiodeForward #(.Blown("true")) diodeforward_10 (.in(diodebackward_7_out), .out(Y_1));
  DiodeForward #(.Blown("true")) diodeforward_11 (.in(diodebackward_9_out), .out(Y_1));
  DiodeForward diodeforward_12 (.in(diodebackward_11_out), .out(Y_1));
  PullDown pulldown_2 (.out(Y_1));
  DiodeForward #(.Blown("true")) diodeforward_13 (.in(diodebackward_1_out), .out(Y_2));
  DiodeForward #(.Blown("true")) diodeforward_14 (.in(diodebackward_3_out), .out(Y_2));
  DiodeForward diodeforward_15 (.in(diodebackward_5_out), .out(Y_2));
  DiodeForward diodeforward_16 (.in(diodebackward_7_out), .out(Y_2));
  DiodeForward #(.Blown("true")) diodeforward_17 (.in(diodebackward_9_out), .out(Y_2));
  DiodeForward diodeforward_18 (.in(diodebackward_11_out), .out(Y_2));
  PullDown pulldown_3 (.out(Y_2));
  DiodeForward #(.Blown("true")) diodeforward_19 (.in(diodebackward_1_out), .out(Y_3));
  DiodeForward #(.Blown("true")) diodeforward_20 (.in(diodebackward_3_out), .out(Y_3));
  DiodeForward #(.Blown("true")) diodeforward_21 (.in(diodebackward_5_out), .out(Y_3));
  DiodeForward diodeforward_22 (.in(diodebackward_7_out), .out(Y_3));
  DiodeForward diodeforward_23 (.in(diodebackward_9_out), .out(Y_3));
  DiodeForward diodeforward_24 (.in(diodebackward_11_out), .out(Y_3));
  PullDown pulldown_4 (.out(Y_3));

  // Notes on the sheet:
  //   A: First freely configurable input.
  //   {{de Erster frei konfigurierbarer Eingang.}}
  //   B: Second freely configurable input.
  //   {{de Zweiter frei konfigurierbarer Eingang.}}
  //   C: Third freely configurable input.
  //   {{de Dritter frei konfigurierbarer Eingang.}}
  //   D: Fourth freely configurable input.
  //   {{de Vierter frei konfigurierbarer Eingang.}}
  //   Y_0: output bit 0
  //   {{de Das 0. Ausgangsbit.}}
  //   Y_1: output bit 1
  //   {{de Das 1. Ausgangsbit.}}
  //   Y_2: output bit 2
  //   {{de Das 2. Ausgangsbit.}}
  //   Y_3: output bit 3
  //   {{de Das 3. Ausgangsbit.}}
  //   AND Matrix {{de UND matrix}}
  //   OR Matrix {{de ODER Matrix}}
endmodule

/* Test case Y_0=A xor B:
# y_0 = A xor B

A B C D  Y_0
0 0 x x  0 
0 1 x x  1 
1 0 x x  1 
1 1 x x  0 
*/

/* Test case Y_1 = C and D:
# y_1 = C and D

A B C D  Y_1
x x 0 0   0
x x 0 1   0
x x 1 0   0
x x 1 1   1
*/

/* Test case Y_2 = A or (C and D):
# Y_2 = A or (C and D)

A B C D  Y_2
0 x 0 0   0  
0 x 0 1   0  
0 x 1 0   0   
0 x 1 1   1   
1 x 0 0   1  
1 x 0 1   1  
1 x 1 0   1   
1 x 1 1   1   
*/

/* Test case Y_3 = A or C:
# y_3 = A or C

A B C D  Y_3
0 x 0 x   0
0 x 1 x   1
1 x 0 x   1
1 x 1 x   1
*/
