// Digital circuit ALU.dig as structural Verilog
// Arithmetic Logical unit.
// Performs all arithmetic operations.
// Used for arithmetic processor instructions as well as for 
// calculating memory addresses.
// {{de Arithmetisch Logische Einheit. 
// Führt alle arithmetischen Operationen durch. 
// Wird sowohl für arithmetische Prozessorbefehle 
// als auch für die Berechnung der Adressen 
// bei der Speicheradressierung verwendet.}}
module ALU (
  input  [15:0] A,
  input  [15:0] B,
  input  [4:0] Op,
  input  Ci,
  output [15:0] Y,
  output Zero,
  output Neg,
  output Carry
);

  wire add_1_c_o, asr_1_p2, lsl_1_p2, lsl_1_p4, lsr_1_p5, sub_1_c_o;
  wire [15:0] add_1_s, asr_1_p3, lsl_1_p3, lsl_1_p5, lsl_1_p6, lsl_1_p7, lsr_1_p4, sub_1_s, swap_1_p2,
       swapn_1_p2;
  wire [31:0] mul_1_mul;

  // And and_1 has open pins: In_1=Op[4], In_2=Ci, out=open
  Add #(.Bits(16)) add_1 (.a(A), .b(B), .c_i(lsl_1_p2), .s(add_1_s), .c_o(add_1_c_o));
  Sub #(.Bits(16)) sub_1 (.a(A), .b(B), .c_i(lsl_1_p2), .s(sub_1_s), .c_o(sub_1_c_o));
  // And and_2 has open pins: In_1=A, In_2=B, out=open
  // Or or_1 has open pins: In_1=A, In_2=B, out=open
  // XOr xor_1 has open pins: In_1=A, In_2=B, out=open
  // LSL lsl_1: pin names not known; wires that end beside it: A, lsl_1_p2, lsl_1_p3, lsl_1_p4, lsl_1_p5, lsl_1_p6, lsl_1_p7
  // LSR lsr_1: pin names not known; wires that end beside it: lsl_1_p2, A, lsl_1_p2, lsr_1_p4, lsr_1_p5
  // ASR asr_1: pin names not known; wires that end beside it: A, asr_1_p2, asr_1_p3
  // SWAP swap_1: pin names not known; wires that end beside it: A, swap_1_p2
  // SWAPN swapn_1: pin names not known; wires that end beside it: A, swapn_1_p2
  Mul #(.Bits(16)) mul_1 (.a(A), .b(B), .mul(mul_1_mul));
  Multiplexer #(.Selector_Bits(4)) multiplexer_1 (
    .sel(Op[3:0]), .in_0(1'b0), .in_1(add_1_c_o), .in_2(sub_1_c_o), .in_3(1'b0), .in_4(1'b0), .in_5(1'b0),
    .in_6(lsl_1_p4), .in_7(lsr_1_p5), .in_8(asr_1_p2), .in_9(1'b0), .in_10(1'b0), .in_11(1'b0), .in_12(1'b0),
    .in_13(1'b0), .in_14(1'b0), .in_15(1'b0), .out(Carry));
  Multiplexer #(.Selector_Bits(4), .Bits(16)) multiplexer_2 (
    .sel(Op[3:0]), .in_0(B), .in_1(add_1_s), .in_2(sub_1_s), .in_3(lsl_1_p5), .in_4(lsl_1_p6),
    .in_5(lsl_1_p7), .in_6(lsl_1_p3), .in_7(lsr_1_p4), .in_8(asr_1_p3), .in_9(swap_1_p2), .in_10(swapn_1_p2),
    .in_11(mul_1_mul[15:0]), .in_12({16{1'b0}}), .in_13({16{1'b0}}), .in_14({16{1'b0}}), .in_15({16{1'b0}}),
    .out(Y));
  Comparator #(.Signed("true"), .Bits(16)) comparator_1 (.a(Y), .b({16{1'b0}}), .eq(Zero), .lt(Neg));  // open: gt

  // Other names for the same wires on the sheet: sel[3:0] = Op[3:0]

  // Notes on the sheet:
  //   A: first operand
  //   {{de Erster Operand}}
  //   B: second operand
  //   {{de Zweiter Operand}}
  //   Op: selected operation
  //   {{de Operationswahl}}
  //   Y: result of the operation
  //   {{de Ergebnis der Operation}}
  //   Zero: Zero-flag. Is high if the relult is zero.
  //   {{de Zero-Flag; Ist High wenn das Ergebnis Null ist.}}
  //   Neg: Is high if the result is negative.
  //   {{de Ist High wenn das Ergebnis negativ ist.}}
  //   Carry: Is high if there has been a carry.
  //   {{de Ist High wenn es einen Übertrag gegeben hat.}}
  //   Ci: carry input
  //   {{de Der Eingang für den Übertrag}}
endmodule
