// Digital circuit GPI.dig as structural Verilog
// Component for a general purpose input.
// {{de Element für ein allgemeines EIngaberegister.}}
module GPI (
  input  [15:0] A,
  input  R,
  input  In0,
  input  In1,
  input  In2,
  input  In3,
  output [15:0] D
);

  wire comparator_1_eq, undriven;

  Comparator #(.Bits(16)) comparator_1 (.a(A), .b(16'h14), .eq(comparator_1_eq));  // open: gt, lt
  // And and_1 has open pins: In_1=comparator_1_eq, In_2=R, out=open
  assign D = undriven ? {{12{1'b0}}, In3, In2, In1, In0} : 16'bz;  // Driver driver_1

  // Notes on the sheet:
  //   A: address bus {{de Addressbus}}
  //   R: Raed Enable {{de Lesefreigabe}}
  //   D: Output {{de Ausgabe}}
endmodule
