// Digital circuit GPO.dig as structural Verilog
// Component contaning a general purpose output.
// {{de Element für ein allgemeines Ausgaberegister.
// Seine Adresse ist 0x15}}
module GPO (
  input  [15:0] D,
  input  [15:0] A,
  input  C,
  input  W,
  output O0,
  output O1,
  output O2,
  output O3,
  output O4,
  output O5,
  output O6,
  output O7,
  output O8,
  output O9,
  output OA,
  output OB,
  output OC,
  output OD,
  output OE,
  output OF
);

  wire comparator_1_eq, undriven;

  Comparator #(.Bits(16)) comparator_1 (.a(A), .b(16'h15), .eq(comparator_1_eq));  // open: gt, lt
  // And and_1 has open pins: In_1=comparator_1_eq, In_2=W, out=open
  Register #(.Bits(16)) register_1 (
    .D(D), .C(C), .en(undriven), .Q({OF, OE, OD, OC, OB, OA, O9, O8, O7, O6, O5, O4, O3, O2, O1, O0}));

  // Notes on the sheet:
  //   D: data bus {{de Datenbus}}
  //   A: address bus {{de Adressbus}}
  //   W: Write Enable {{de Schreibfreigabe}}
endmodule
