// Digital circuit Graphics.dig as structural Verilog
// Eine einfache "Grafikkarte". 
// Contains a graphics RAM to display the actual graphics. 
// This graphics RAM is configured to display 20x20 pixels. 
// The required 800 bytes of memory are maped to the 
// address 0x8000 in the address space.
// {{de Enthält ein Grafik-RAM um die eigentliche 
// Grafik anzuzeigen. Dieses Grafik-RAM ist auf die 
// Darstellung von 20x20 Pixel konfiguriert. 
// Die erforderlichen 800 Bytes Speicher  werden 
// ab Adresse 0x8000 in den Adressbereich 
// eingeblendet.}}
module Graphics (
  input  [15:0] A,
  input  R,
  input  C,
  input  W,
  output [15:0] D
);

  wire Bank_q, comparator_1_lt, comparator_2_eq, comparator_2_gt, undriven, undriven_2, undriven_3,
       undriven_4;

  Comparator #(.Bits(16)) comparator_1 (.a(A), .b(16'h8320), .lt(comparator_1_lt));  // open: gt, eq
  Comparator #(.Bits(16)) comparator_2 (.a(A), .b(16'h7fff), .gt(comparator_2_gt), .eq(comparator_2_eq));  // open: lt
  // And and_1 has open pins: In_1=comparator_1_lt, In_2=comparator_2_gt, out=open
  // And and_2 has open pins: In_1=comparator_2_eq, In_2=W, out=open
  // And and_3 has open pins: In_1=undriven, In_2=W, out=open
  // And and_4 has open pins: In_1=undriven, In_2=R, out=open
  Register Bank (.D(D[0]), .C(C), .en(undriven_2), .Q(Bank_q));
  GraphicCard #(.AddrBits(16), .graphicHeight(20), .graphicWidth(20), .Bits(16), .Addr_Bits(16)) graphiccard_1 (
    .A(A[9:0]), .str(undriven_3), .C(C), .ld(undriven_4), .B(Bank_q), .D(D));

  // Notes on the sheet:
  //   A: address {{de Adresse}}
  //   R: Read enable {{de Lesefreigabe}}
  //   D: bidirectional data port
  //   {{de Bidirektionaler Datenanschluss}}
  //   W: Write enable {{de Schreibfreigabe}}
endmodule
