// Digital circuit LedMatrix.dig as structural Verilog
module LedMatrix (
  input  [15:0] D,
  input  [15:0] A,
  input  C,
  input  W
);

  wire comparator_1_eq, comparator_2_eq, undriven, undriven_2;
  wire [15:0] register_1_q, register_2_q, register_3_q;

  Comparator #(.Bits(16)) comparator_1 (.a(A), .b(16'ha), .eq(comparator_1_eq));  // open: gt, lt
  Comparator #(.Bits(16)) comparator_2 (.a(A), .b(16'hb), .eq(comparator_2_eq));  // open: gt, lt
  // And and_1 has open pins: In_1=comparator_1_eq, In_2=W, out=open
  // And and_2 has open pins: In_1=W, In_2=comparator_2_eq, out=open
  Register #(.Bits(16)) register_1 (.D(D), .C(C), .en(undriven_2), .Q(register_1_q));
  Register #(.Bits(16)) register_2 (.D(D), .C(C), .en(undriven), .Q(register_2_q));
  Register #(.Bits(16)) register_3 (.D(register_1_q), .C(C), .en(undriven), .Q(register_3_q));
  LedMatrix #(.ledPersistence("true"), .colAddrBits(6), .rowDataBits(16)) ledmatrix_1 (
    .rows(register_3_q), .column(register_2_q[5:0]));

  // Notes on the sheet:
  //   D: data bus {{de Datenbus}}
  //   A: address bus {{de Adressbus}}
  //   W: Write Enable {{de Schreibfreigabe}}
endmodule
