// Digital circuit Terminal.dig as structural Verilog
// Terminal. The used address is 0x1F.
// {{de Terminal. Die Adresse ist 0x1F.}}
module Terminal (
  input  [15:0] D,
  input  [15:0] A,
  input  C,
  input  W
);

  wire comparator_1_eq, undriven;

  Comparator #(.Bits(16)) comparator_1 (.a(A), .b(16'h1f), .eq(comparator_1_eq));  // open: gt, lt
  // And and_1 has open pins: In_1=comparator_1_eq, In_2=W, out=open
  Terminal terminal_1 (.D(D), .C(C), .en(undriven));

  // Notes on the sheet:
  //   D: data bus {{de Datenbus}}
  //   A: address {{de Adressbus}}
  //   W: Write Enable {{de Schreibfreigabe}}
endmodule
