// Digital circuit ClockDiv.dig as structural Verilog
// Clock divider. Here the clock is divided by two, and the 
// memory access signals of the instruction register are generated. 
// A instruction word is alternately read et first and then executed.
// {{de Taktteiler. Hier wird der Takt durch zwei geteilt, und 
// es werden die Signale für den Speicherzugriff des 
// InstructionRegisters erzeugt. Jeweils abwechselnd 
// wird ein Befehlswort gelesen und dieses Befehlswort
// dann ausgeführt.}}
module ClockDiv (
  input  Clock,
  output S_in,
  output C_in,
  output C
);

  wire t_ff_1_nq, undriven;

  // Not not_1 has open pins: in=Clock, out=open
  T_FF #(.withEnable("false")) t_ff_1 (.C(undriven), .Q(S_in), .nQ(t_ff_1_nq));
  // And and_1 has open pins: In_1=Clock, In_2=S_in, out=open
  // And and_2 has open pins: In_1=t_ff_1_nq, In_2=Clock, out=open

  // Notes on the sheet:
  //   S_in: Signal to configure the processor for reading 
  //   the next instruction.
  //   {{de Signal welches den Prozessor für das Lesen 
  //   eines Befehlswortes konfiguriert.}}
  //   C_in: Clock signal to read the next instruction.
  //   {{de Taktsignal für das Lesen eines Befehlswortes}}
  //   C: Clock used to execute an instruction.
  //   {{de Takt der das Ausführen eines Befehlswortes 
  //   steuert.}}
endmodule
