// Digital circuit ControlMux.dig as structural Verilog
// Control unit for a simple processor.
// It works purely combinatorial.
// Since it is relatively complex (24 output bits), it is 
// implemented by a corresponding ROM component, 
// and not by 24 individual combinatorial circuits.
// {{de Leitwerk für einen einfachen Prozessor.
// Es arbeitet rein kombinatorisch, es handelt sich 
// also um ein einfaches Schaltnetz. 
// Da es vergleichsweise komplex ist (24 
// Ausgangsbits), wird es durch einen 
// entsprechenden ROM-Baustein 
// realisiert, und nicht durch 24 einzelne Schaltnetze.}}
module ControlMux (
  input  [6:0] Op,
  output [1:0] WDm,
  output WE,
  output imm,
  output absJmp,
  output [2:0] muxB,
  output srcToD,
  output muxA,
  output ALUToBus,
  output [4:0] ALUop,
  output storeFlags,
  output [2:0] Branch,
  output st,
  output ld,
  output ioW,
  output ioR
);

  wire [5:0] multiplexer_1_out;
  wire [23:8] Logic_d;

  Multiplexer #(.Bits(6)) multiplexer_1 (.sel(Op[6]), .in_0(Op[5:0]), .in_1({6{1'b0}}), .out(multiplexer_1_out));
  ROM #(.AddrBits(6), .Bits(24), .Addr_Bits(6)) Logic (
    .A(multiplexer_1_out), .sel(1'b1),
    .D({Logic_d[23], storeFlags, srcToD, Logic_d[20], ioR, ioW, Branch, ALUop, muxA, Logic_d[8], WE, ALUToBus, absJmp, muxB, st, ld}));
  Break #(.Cycles(600000)) Break (.brk(Logic_d[20]));
  // Or or_1 has open pins: In_1=ld, In_2=Logic_d[8], out=open
  // Or or_2 has open pins: In_1=ioR, In_2=Logic_d[8], out=open

  assign imm = Op[6];

  // Notes on the sheet:
  //   Op: The obcode and the immediate bit.
  //   {{de Der Opcode incl. Immediate Bit}}
  //   WE: The data bus value ist stored in a register.
  //   {{de Wert am Datenbus in Register speichern}}
  //   imm: Enables the storage of a constant value.
  //   {{de Aktiviert das Speichern der Konstanten}}
  //   absJmp: triggers a absolute jump
  //   {{de absoluten Sprung auslösen}}
  //   muxB: selector for mux B
  //   {{de Selektor für Mux B}}
  //   srcToD: Put source register to data bus
  //   {{de SourceRegister auf Datenbus legen}}
  //   muxA: selector for mux A
  //   {{de Selector für Mux A}}
  //   ALUToBus: ALU value is put on the data bus.
  //   {{de ALU auf den Datenbus legen}}
  //   ALUop: the operation of the ALU
  //   {{de Operation der ALU}}
  //   storeFlags: If set, the ALU performs an arithmetic operation so that the 
  //   flags must be stored.
  //   {{de Wenn gesetzt führt die ALU eine arithmetische Operation 
  //   aus, so dass die Flags gespeichert werden müssen.}}
  //   Branch: kind of branch
  //   {{de Art des bedingten Sprunges}}
  //   st: The RAM stores the data on the data bus.
  //   {{de Ram speichert Daten vom Datenbus}}
  //   ld: The RAM component puts its content to the 
  //   data bus.
  //   {{de Ram gibt Daten auf den Datenbus}}
  //   ioW: write to IO
  //   {{de Es wird auf die IO geschrieben}}
  //   ioR: read from IO
  //   {{de Es wird IO gelesen}}
  //   contents of Logic (hex, n*v repeats v):
  //   0,200080,4004c0,4044c0,4008c0,4048c0,400cc0,4010c0,4014c0,c4,d4,4004c4,4004d4,4044c4,
  //   4044d4,4008c4,4008d4,4048c4,4048d4,400cc4,400cd4,4010c4,4010d4,4014c4,4014d4,402cc0,
  //   402cc4,402cd4,400800,400804,400814,4018c0,401cc0,4058c0,405cc0,4020c0,24c0,28c0,20040a,
  //   689,200006,20001e,85,95,200406,685,8018,10018,18018,28018,30018,38018,1a4,20,24,20018,
  //   240004,24001c,240408,80284,80294,80688,100000,800020
endmodule
