// Digital circuit FlagsRW.dig as structural Verilog
// Stores the processor flags. In contrast to the simple 
// variant, the flags can be read and written via IO operations. 
// The flags can be found at IO address 0.
// {{de Speichert die Prozessorflags. Im Gegensatz zur 
// einfachen Variante können bei diesem Modul
// die Flags per IO Operation gelesen und geschrieben
// werden. Die Flags finden sich an IO Adresse 0.}}
module FlagsRW (
  input  Zi,
  input  Ni,
  input  Ci,
  input  C,
  input  store,
  input  [15:0] A,
  input  IOR,
  input  IOW,
  input  [15:0] Data,
  output Zo,
  output No,
  output Co
);

  wire comparator_1_eq, undriven, undriven_2, undriven_3;
  wire [15:0] multiplexer_1_out;
  wire [15:3] register_1_q;

  Comparator #(.Bits(16)) comparator_1 (.a(A), .b({16{1'b0}}), .eq(comparator_1_eq));  // open: gt, lt
  // And and_1 has open pins: In_1=IOW, In_2=comparator_1_eq, out=open
  // And and_2 has open pins: In_1=comparator_1_eq, In_2=IOR, out=open
  Multiplexer #(.Bits(16)) multiplexer_1 (
    .sel(undriven), .in_0({{13{1'b0}}, Ni, Zi, Ci}), .in_1(Data), .out(multiplexer_1_out));
  // Or or_1 has open pins: In_1=store, In_2=undriven, out=open
  Register #(.Bits(16)) register_1 (.D(multiplexer_1_out), .C(C), .en(undriven_2), .Q({register_1_q, No, Zo, Co}));
  assign Data = undriven_3 ? {register_1_q, No, Zo, Co} : 16'bz;  // Driver driver_1

  // Notes on the sheet:
  //   Zi: Zero In {{de Zero EIngang}}
  //   Zo: Zero Out {{de Zero Ausgang}}
  //   Ni: Negative In {{de negative Eingang}}
  //   No: Negative Out {{de negative Ausgang}}
  //   Ci: Carry In {{de Carry EIngang}}
  //   Co: Carry Out {{de Carry Ausgang}}
  //   store: The input which activates storing.
  //   It is set to one when performing an arithmetic operation.
  //   {{de Der Eingang welcher das Speichern aktiviert. 
  //   Es wird auf Eins gesetzt, wenn eine arithmetische 
  //   Operation ausgeführt wird.}}
  //   A: address {{de Adresse}}
  //   IOR: IO Read {{de Lesen von der IO}}
  //   IOW: IO Write {{de Schreiben auf die IO}}
endmodule
