// Digital circuit Interrupt.dig as structural Verilog
// Simple interrupt controller.
// If an interrupt is triggered, the controller is disabled: no 
// further interrupts can be triggered. Setting the input reti 
// releases the interrupt controller.
// {{de Einfacher Interrupt-Controller.
// Wird ein Interrupt ausgelöst, wird der Controller
// gesperrt: Es können keine weiteren Interrupts
// ausgelöst werden. Erst der Eingang reti gibt den 
// Interrupt-Controller wieder frei.}}
module Interrupt (
  input  C,
  input  [15:0] Next,
  input  rel,
  input  imm,
  input  abs,
  input  reti,
  input  intr,
  output [15:0] retAddr,
  output iEn
);

  wire intLock_nq, rising_1_out, undriven, undriven_2, undriven_3, undriven_4;

  Rising rising_1 (.Reset(iEn), .Set(intr), .Out(rising_1_out));
  // Not not_1 has open pins: in=imm, out=open
  // Not not_2 has open pins: in=rel, out=open
  // Not not_3 has open pins: in=abs, out=open
  // And and_1 has open pins: In_1=intLock_nq, In_2=rising_1_out, In_3=undriven, In_4=undriven_2, In_5=undriven_3, out=open
  JK_FF intLock (.J(undriven_4), .C(C), .K(reti), .nQ(intLock_nq));  // open: Q
  Register #(.Bits(16)) u_retAddr (.D(Next), .C(C), .en(undriven_4), .Q(retAddr));
  D_FF u_iEn (.D(undriven_4), .C(C), .Q(iEn));  // open: nQ

  // Notes on the sheet:
  //   retAddr: Return Address {{de Return Adresse}}
  //   iEn: interrupt trigger used by the PC
  //   {{de Interrupt-Freigabe für PC}}
  //   Next: The next commands address, that 
  //   is the return address.
  //   {{de Der nächste Befehl, also die 
  //   Rücksprungadresse.}}
  //   rel: relative jump
  //   If set, an interrupt is blocked.
  //   {{de relativer Sprung: 
  //   Wenn gesetzt, wird Interrupt verhindert.}}
  //   imm: immediate register:
  //   If set, an interrupt is blocked.
  //   {{de Immediate Register:
  //   Wenn gesetzt, wird Interrupt verhindert.}}
  //   abs: absoluite jump
  //   If set, an interrupt is blocked.
  //   {{de Absoluter Sprung:
  //   Wenn gesetzt, wird Interrupt verhindert.}}
  //   reti: return from interrupt. This signal is used to 
  //   release the interrupt controller.
  //   {{de return from interrupt. Über dieses Signal werden
  //   die Interrupts wieder freigegeben.}}
  //   intr: interrupt trigger {{de Interrupt Anforderung}}
endmodule
