// Digital circuit PC-HDL.dig as structural Verilog
// The program counter.
// Here the current program counter is stored.
// The various inputs can be used to influence how the 
// program counter is modified if a clock signal happens.
// {{de Der Programmzähler. 
// Hier wird der aktuelle Programmzähler gespeichert. 
// Über die verschiedenen Eingänge kann beeinflußt 
// werden, auf welche Weise der Programmzähler mit 
// dem Takt weiter geschaltet wird.}}
module PC_HDL (
  input  [15:0] ALU,
  input  C,
  input  abs,
  input  reset,
  input  rel,
  output [15:0] Next,
  output [15:0] PC
);

  wire undriven;
  wire [15:0] Add_ALU_s, multiplexer_1_out, multiplexer_2_out, multiplexer_3_out;

  Multiplexer #(.Bits(16)) multiplexer_1 (
    .sel(reset), .in_0(multiplexer_3_out), .in_1({16{1'b0}}), .out(multiplexer_1_out));
  // Not not_1 has open pins: in=C, out=open
  Register #(.Bits(16)) u_PC (.D(multiplexer_1_out), .C(undriven), .en(1'b1), .Q(PC));
  Add #(.Bits(16)) Add_One (.a(PC), .b(16'h1), .c_i(1'b0), .s(Next));  // open: c_o
  Add #(.Bits(16)) Add_ALU (.a(Next), .b(ALU), .c_i(1'b0), .s(Add_ALU_s));  // open: c_o
  Multiplexer #(.Bits(16)) multiplexer_2 (.sel(rel), .in_0(Next), .in_1(Add_ALU_s), .out(multiplexer_2_out));
  Multiplexer #(.Bits(16)) multiplexer_3 (.sel(abs), .in_0(multiplexer_2_out), .in_1(ALU), .out(multiplexer_3_out));

  // Notes on the sheet:
  //   ALU: current ALU output
  //   {{de Aktuelle ALU Ausgabe}}
  //   Next: Address of the next instruction to execute.
  //   {{de Adresse des nächsten auszuführenden Befehls.}}
  //   PC: Programm Counter
  //   {{de Programmzähler}}
  //   abs: Triggers a absolute jump.
  //   {{de absoluten Sprung auslösen}}
  //   rel: Triggers a relative jump.
  //   {{de relativen Spung auslösen}}
endmodule
