// Digital circuit Counter-D.dig as structural Verilog
module Counter_D (
  input  C,
  output Q_3,
  output Q_2,
  output Q_1,
  output Q_0
);

  wire undriven, undriven_2, undriven_3, undriven_4, undriven_5, undriven_6, undriven_7, undriven_8,
       undriven_9, undriven_10, undriven_11, undriven_12, undriven_13, undriven_14, undriven_15, undriven_16;

  // Not not_1 has open pins: in=Q_0, out=open
  // Not not_2 has open pins: in=Q_1, out=open
  // Not not_3 has open pins: in=Q_2, out=open
  // Not not_4 has open pins: in=Q_3, out=open
  // And and_1 has open pins: In_1=Q_0, In_2=Q_1, In_3=Q_2, In_4=undriven_13, out=open
  // And and_2 has open pins: In_1=undriven_16, In_2=Q_3, out=open
  // And and_3 has open pins: In_1=undriven_15, In_2=Q_3, out=open
  // And and_4 has open pins: In_1=undriven_14, In_2=Q_3, out=open
  // And and_5 has open pins: In_1=Q_0, In_2=Q_1, In_3=undriven_14, out=open
  // And and_6 has open pins: In_1=undriven_16, In_2=Q_2, out=open
  // And and_7 has open pins: In_1=undriven_15, In_2=Q_2, out=open
  // And and_8 has open pins: In_1=Q_0, In_2=undriven_15, out=open
  // And and_9 has open pins: In_1=undriven_16, In_2=Q_1, out=open
  // Or or_1 has open pins: In_1=undriven_3, In_2=undriven_4, In_3=undriven_7, out=open
  // Or or_2 has open pins: In_1=undriven_5, In_2=undriven_8, out=open
  // Or or_3 has open pins: In_1=undriven, In_2=undriven_2, In_3=undriven_6, In_4=undriven_9, out=open
  D_FF #(.Default(1)) q_3n (.D(undriven_12), .C(C), .Q(Q_3));  // open: nQ
  D_FF #(.Default(1)) q_2n (.D(undriven_10), .C(C), .Q(Q_2));  // open: nQ
  D_FF #(.Default(1)) q_1n (.D(undriven_11), .C(C), .Q(Q_1));  // open: nQ
  D_FF q_0n (.D(undriven_16), .C(C), .Q(Q_0));  // open: nQ

  // Other names for the same wires on the sheet: q_0n = Q_0; q_1n = Q_1; q_2n = Q_2; q_3n = Q_3
endmodule

/* Test case:
           C Q_3 Q_2 Q_1 Q_0
repeat(16) C bits(4,n-1)
*/
