// Digital circuit Counter-JK.dig as structural Verilog
module Counter_JK (
  input  C,
  output Q_0,
  output Q_1,
  output Q_2,
  output Q_3
);

  wire undriven, undriven_2;

  JK_FF q_0n (.J(1'b1), .C(C), .K(1'b1), .Q(Q_0));  // open: nQ
  JK_FF #(.Default(1)) q_1n (.J(Q_0), .C(C), .K(Q_0), .Q(Q_1));  // open: nQ
  // And and_1 has open pins: In_1=Q_0, In_2=Q_1, out=open
  JK_FF #(.Default(1)) q_2n (.J(undriven), .C(C), .K(undriven), .Q(Q_2));  // open: nQ
  // And and_2 has open pins: In_1=undriven, In_2=Q_2, out=open
  JK_FF #(.Default(1)) q_3n (.J(undriven_2), .C(C), .K(undriven_2), .Q(Q_3));  // open: nQ

  // Notes on the sheet:
  //   Asynchronous counter built with JK flip-flops
  //   {{de Synchroner Zähler aufgebaut mit JK-Flipflops}}
endmodule

/* Test case:
           C Q_3 Q_2 Q_1 Q_0
repeat(16) C bits(4,n-1)
*/
