// Digital circuit D-T.dig as structural Verilog
module D_T (
  input  D,
  input  C,
  output Q,
  output nQ
);

  wire delay_1_out, undriven, undriven_2, undriven_3, undriven_4, undriven_5;

  // Not not_1 has open pins: in=C, out=open
  // Not not_2 has open pins: in=D, out=open
  // And and_1 has open pins: In_1=delay_1_out, In_2=C, out=open
  Delay delay_1 (.in(undriven), .out(delay_1_out));
  // And and_2 has open pins: In_1=undriven_2, In_2=undriven_3, out=open
  // And and_3 has open pins: In_1=undriven_3, In_2=D, out=open
  // NOr nor_1 has open pins: In_1=undriven_4, In_2=nQ, out=open
  // NOr nor_2 has open pins: In_1=Q, In_2=undriven_5, out=open
endmodule

/* Test case:
C D Q ~Q
C 1 1  0
0 1 1  0
0 0 1  0
C 0 0  1
0 0 0  1
0 1 0  1
*/
