// Digital circuit D-TransmissionGate.dig as structural Verilog
module D_TransmissionGate (
  input  D,
  input  C,
  output Q,
  output nQ
);

  wire transgate_2_out2, undriven;

  // Not not_1 has open pins: in=C, out=open
  TransGate transgate_1 (.A(C), .nA(undriven), .out1(Q), .out2(D));
  TransGate transgate_2 (.A(undriven), .nA(C), .out1(Q), .out2(transgate_2_out2));
  // Not not_2 has open pins: in=Q, out=open
  // Not not_3 has open pins: in=nQ, out=open
endmodule

/* Test case:
C D Q ~Q
C 1 1  0
0 1 1  0
0 0 1  0
C 0 0  1
0 0 0  1
0 1 0  1
C 1 1  0
C 0 0  1
*/
