// Digital circuit D.dig as structural Verilog
module D (
  input  D,
  input  C,
  output Q,
  output nQ
);

  wire undriven, undriven_2, undriven_3;

  // Not not_1 has open pins: in=D, out=open
  // And and_1 has open pins: In_1=undriven, In_2=C, out=open
  // And and_2 has open pins: In_1=C, In_2=D, out=open
  // NOr nor_1 has open pins: In_1=undriven_2, In_2=nQ, out=open
  // NOr nor_2 has open pins: In_1=Q, In_2=undriven_3, out=open
endmodule

/* Test case:
C D Q ~Q
C 1 1  0
0 1 1  0
0 0 1  0
C 0 0  1
0 0 0  1
0 1 0  1
*/
