// Digital circuit D_NAND.dig as structural Verilog
module D_NAND (
  input  D,
  input  C,
  output Q,
  output nQ
);

  wire undriven, undriven_2;

  // NAnd nand_1 has open pins: In_1=D, In_2=C, out=open
  // NAnd nand_2 has open pins: In_1=undriven, In_2=C, out=open
  // NAnd nand_3 has open pins: In_1=undriven, In_2=nQ, out=open
  // NAnd nand_4 has open pins: In_1=Q, In_2=undriven_2, out=open
endmodule

/* Test case:
C D Q ~Q
C 1 1  0
0 1 1  0
0 0 1  0
C 0 0  1
0 0 0  1
0 1 0  1
*/
