// Digital circuit JK-MS.dig as structural Verilog
// Discrete Master-Slave JK flip-flop.
// The master flip-flop stores at a high at the clock signal, 
// the slave flip-flop at low at the clock signal. 
// The two feedback lines prevent the "not allowed" condition 
// on the master flip-flop.
// {{de Diskret aufgebautes Master-Slave JK-Flipflop.
// Das Master-Flipflop speichert bei einem High am 
// Taktsignal, das Slave-Flipflop bei Low am Taktsignal.
// Die obere und untere Rückkoppelleitung verhindern,
// das der verbotenen Zustand am Master-Flipflop
// auftritt.}}
module JK_MS (
  input  J,
  input  C,
  input  K,
  output Q,
  output nQ
);

  wire undriven, undriven_2, undriven_3, undriven_4, undriven_5, undriven_6, undriven_7;

  // And and_1 has open pins: In_1=nQ, In_2=J, In_3=C, out=open
  // Not not_1 has open pins: in=C, out=open
  // And and_2 has open pins: In_1=C, In_2=K, In_3=Q, out=open
  // NOr nor_1 has open pins: In_1=undriven, In_2=undriven_3, out=open
  // NOr nor_2 has open pins: In_1=undriven_4, In_2=undriven_2, out=open
  // And and_3 has open pins: In_1=undriven_4, In_2=undriven_5, out=open
  // And and_4 has open pins: In_1=undriven_5, In_2=undriven_3, out=open
  // NOr nor_3 has open pins: In_1=undriven_6, In_2=nQ, out=open
  // NOr nor_4 has open pins: In_1=Q, In_2=undriven_7, out=open

  // Notes on the sheet:
  //   J: Input to set the flip-flop.
  //   {{de Eingang zum Setzen des Flipflops.}}
  //   C: Clock input
  //   {{de Takteingang}}
  //   Q: The stored bit.
  //   {{de Das gespeicherte Bit.}}
  //   nQ: The inverted stored bit.
  //   {{de Das Inverse des gespeicherten Bits.}}
  //   K: Input to clear the flip-flop.
  //   {{de Eingang zum Löschen des Flipflops.}}
endmodule

/* Test case:
C J K Q ~Q
C 1 0 1 0
C 0 0 1 0
C 0 1 0 1
C 0 0 0 1
C 1 1 1 0
C 1 1 0 1
C 1 1 1 0
C 1 1 0 1
*/
