// Digital circuit JK-T.dig as structural Verilog
// Clock edges triggert JK flip-flop. 
// A rising edge at the clock input is converted into a pulse 
// whose duration is just sufficient to switch the flip-flop.
// {{de Taktflanken gesteuerters JK-Flipflop. Eine steigende
// Flanke am Takteingang wird in einem Impuls 
// umgeformt, der gerade ausreicht, um das Flipflop
// umzuschalten.}}
module JK_T (
  input  J,
  input  C,
  input  K,
  output Q,
  output nQ
);

  wire delay_1_out, undriven, undriven_2, undriven_3, undriven_4;

  // Not not_1 has open pins: in=C, out=open
  // And and_1 has open pins: In_1=delay_1_out, In_2=C, out=open
  Delay delay_1 (.in(undriven), .out(delay_1_out));
  // And and_2 has open pins: In_1=Q, In_2=K, In_3=undriven_2, out=open
  // And and_3 has open pins: In_1=undriven_2, In_2=J, In_3=nQ, out=open
  // NOr nor_1 has open pins: In_1=undriven_3, In_2=nQ, out=open
  // NOr nor_2 has open pins: In_1=Q, In_2=undriven_4, out=open

  // Notes on the sheet:
  //   J: Input to set the flip-flop
  //   {{de Eingang zum Setzen des Flipflops.}}
  //   Q: The bit stored in the flip-flop.
  //   {{de Das im Flipflop gespeicherte Bit.}}
  //   nQ: The inverted stored bit.
  //   {{de Das inverse gespeicherte Bit.}}
  //   C: Clock signal. On a rising edge, a short pulse is 
  //   generated on the flip-flop, which is just enough to 
  //   switch the Flopflop.
  //   {{de Taktsignal. Bei einer steigenden Flanke wird ein 
  //   kurzer Impuls am Flipflop erzeugt, der gerade 
  //   ausreicht, um das Flopflop umzuschalten.}}
  //   K: Input to clear the flip-flop.
  //   {{de Eingang zum Löschen des Flipflops.}}
endmodule

/* Test case:
C J K Q ~Q
C 1 0 1 0
C 0 0 1 0
C 0 1 0 1
C 0 0 0 1
C 1 1 1 0
C 1 1 0 1
C 1 1 1 0
C 1 1 0 1
*/
