// Digital circuit Prescaler.dig as structural Verilog
// Simple frequency divider. The divider ratios 
// are 1/2, 1/4, 1/8 and 1/16.
// {{de Einfacher Frequenzteiler. Möglich sind die 
// Teilerverhältnisse 1/2, 1/4, 1/8 und 1/16.}}
module Prescaler (
  input  Clock,
  input  A,
  input  B,
  output Y
);

  wire t_ff_1_q, t_ff_2_q, t_ff_3_q, t_ff_4_q, undriven, undriven_2, undriven_3, undriven_4, undriven_5,
       undriven_6;

  // Not not_1 has open pins: in=A, out=open
  // Not not_2 has open pins: in=B, out=open
  T_FF #(.withEnable("false")) t_ff_1 (.C(Clock), .Q(t_ff_1_q));  // open: nQ
  T_FF #(.withEnable("false")) t_ff_2 (.C(t_ff_1_q), .Q(t_ff_2_q));  // open: nQ
  // And and_1 has open pins: In_1=t_ff_1_q, In_2=undriven, In_3=undriven_2, out=open
  T_FF #(.withEnable("false")) t_ff_3 (.C(t_ff_2_q), .Q(t_ff_3_q));  // open: nQ
  // And and_2 has open pins: In_1=t_ff_2_q, In_2=A, In_3=undriven_2, out=open
  // And and_3 has open pins: In_1=t_ff_3_q, In_2=undriven, In_3=B, out=open
  T_FF #(.withEnable("false")) t_ff_4 (.C(t_ff_3_q), .Q(t_ff_4_q));  // open: nQ
  // And and_4 has open pins: In_1=t_ff_4_q, In_2=A, In_3=B, out=open
  // Or or_1 has open pins: In_1=undriven_6, In_2=undriven_5, In_3=undriven_4, In_4=undriven_3, out=open

  // Notes on the sheet:
  //   Clock: Hz: 20
  //   A: First bit of frequency selection
  //   {{de Erstes Bit der Frequenzwahl}}
  //   B: Second bit of frequency selection
  //   {{de zweites Bit der Frequenzwahl}}
  //   Y: Prescaler output
  //   {{de Prescaler Ausgabe}}
endmodule

/* Test case:
           Clock A B Y
repeat(16) C     0 0 (~n&1)
repeat(16) C     1 0 (~(n>>1)&1)
repeat(16) C     0 1 (~(n>>2)&1)
repeat(16) C     1 1 (~(n>>3)&1)
*/
