// Digital circuit RS-C.dig as structural Verilog
// A gated NOR SR latch.
// {{de Einfaches NOR RS-Flipflop mit Freigabeeingang.}}
module RS_C (
  input  S,
  input  C,
  input  R,
  output Q,
  output nQ
);

  wire undriven, undriven_2;

  // And and_1 has open pins: In_1=R, In_2=C, out=open
  // And and_2 has open pins: In_1=C, In_2=S, out=open
  // NOr nor_1 has open pins: In_1=undriven, In_2=nQ, out=open
  // NOr nor_2 has open pins: In_1=Q, In_2=undriven_2, out=open

  // Notes on the sheet:
  //   S: Set input
  //   {{de Set Eingang}}
  //   C: gate input
  //   {{de Freigabeeingang}}
  //   Q: The stored bit.
  //   {{de Das gespeicherte Bit}}
  //   nQ: The inverted stored bit.
  //   {{de Das inverse des gespeicherten Bits}}
  //   R: Reset input
  //   {{de Reset Eingang}}
endmodule

/* Test case:
R C S Q ~Q
1 C 0 0  1
X 0 X 0  1
0 C 1 1  0
X 0 X 1  0
*/
