// Digital circuit RS-MS-Simp.dig as structural Verilog
// Master Slave RS flip-flop.
// Built from two simple RS flip-flops and an inverter.
// {{de Master Slave RS-Flipflop. 
// Aufgebaut aus zwei einfachen RS-Flipflops und einem 
// Inverter.}}
module RS_MS_Simp (
  input  R,
  input  C,
  input  S,
  output Q,
  output nQ
);

  wire not_1_out, rs_c_1_nq, rs_c_1_q;

  RS_C rs_c_1 (.S(S), .C(C), .R(R), .Q(rs_c_1_q), .nQ(rs_c_1_nq));
  not not_1 (not_1_out, C);
  RS_C rs_c_2 (.S(rs_c_1_q), .C(not_1_out), .R(rs_c_1_nq), .Q(Q), .nQ(nQ));

  // Notes on the sheet:
  //   R: reset input
  //   {{de Reset Eingang}}
  //   C: Clock {{de Takteingang}}
  //   Q: The stored bit.
  //   {{de Das gespeicherte Bit.}}
  //   nQ: The inverted stored bit.
  //   {{de Das Inverse des gespeicherten Bits.}}
  //   S: set input
  //   {{de Set Eingang}}
endmodule

/* Test case:
R C S Q ~Q
1 C 0 0  1
X 0 X 0  1
0 C 1 1  0
X 0 X 1  0
*/
