// Digital circuit RS-MS.dig as structural Verilog
module RS_MS (
  input  S,
  input  C,
  input  R,
  output Q,
  output nQ
);

  wire undriven, undriven_2, undriven_3, undriven_4, undriven_5, undriven_6, undriven_7;

  // And and_1 has open pins: In_1=S, In_2=C, out=open
  // And and_2 has open pins: In_1=C, In_2=R, out=open
  // Not not_1 has open pins: in=C, out=open
  // NOr nor_1 has open pins: In_1=undriven, In_2=undriven_3, out=open
  // NOr nor_2 has open pins: In_1=undriven_4, In_2=undriven_2, out=open
  // And and_3 has open pins: In_1=undriven_4, In_2=undriven_5, out=open
  // And and_4 has open pins: In_1=undriven_5, In_2=undriven_3, out=open
  // NOr nor_3 has open pins: In_1=undriven_6, In_2=nQ, out=open
  // NOr nor_4 has open pins: In_1=Q, In_2=undriven_7, out=open
endmodule

/* Test case:
R C S Q ~Q
1 C 0 0  1
X 0 X 0  1
0 C 1 1  0
X 0 X 1  0
*/
