// Digital circuit RS.dig as structural Verilog
module RS (
  input  R,
  input  S,
  output Q,
  output nQ
);

  // NOr nor_1 has open pins: In_1=R, In_2=nQ, out=open
  // NOr nor_2 has open pins: In_1=Q, In_2=S, out=open
endmodule

/* Test case:
R S Q ~Q
1 0 0  1
0 0 0  1
0 1 1  0
0 0 1  0
*/
