// Digital circuit SPI.dig as structural Verilog
module SPI (
  input  D_i2,
  input  D_i3,
  input  D_i0,
  input  D_i1,
  input  Load,
  input  Clock,
  input  D_i3_2,
  input  D_i2_2,
  input  D_i1_2,
  input  D_i0_2,
  input  Load_2,
  output D_o3,
  output D_o0,
  output D_o2,
  output D_o1,
  output D_o3_2,
  output D_o2_2,
  output D_o1_2,
  output D_o0_2
);

  wire d_ff_1_q, d_ff_2_q, d_ff_3_q, d_ff_4_q, d_ff_5_q, d_ff_6_q, d_ff_7_q, d_ff_8_q, undriven;

  // Not not_1 has open pins: in=Load, out=open
  Multiplexer multiplexer_1 (.sel(undriven), .in_0(D_i3), .in_1(d_ff_8_q), .out(D_o3_2));
  Multiplexer multiplexer_2 (.sel(Load_2), .in_0(d_ff_7_q), .in_1(D_i3_2), .out(D_o3));
  D_FF d_ff_1 (.D(D_o3_2), .C(Clock), .Q(d_ff_1_q));  // open: nQ
  D_FF d_ff_2 (.D(D_o3), .C(Clock), .Q(d_ff_2_q));  // open: nQ
  Multiplexer multiplexer_3 (.sel(undriven), .in_0(D_i2), .in_1(d_ff_1_q), .out(D_o2_2));
  Multiplexer multiplexer_4 (.sel(Load_2), .in_0(d_ff_2_q), .in_1(D_i2_2), .out(D_o2));
  D_FF d_ff_3 (.D(D_o2_2), .C(Clock), .Q(d_ff_3_q));  // open: nQ
  D_FF d_ff_4 (.D(D_o2), .C(Clock), .Q(d_ff_4_q));  // open: nQ
  Multiplexer multiplexer_5 (.sel(undriven), .in_0(D_i1), .in_1(d_ff_3_q), .out(D_o1_2));
  Multiplexer multiplexer_6 (.sel(Load_2), .in_0(d_ff_4_q), .in_1(D_i1_2), .out(D_o1));
  D_FF d_ff_5 (.D(D_o1_2), .C(Clock), .Q(d_ff_5_q));  // open: nQ
  D_FF d_ff_6 (.D(D_o1), .C(Clock), .Q(d_ff_6_q));  // open: nQ
  Multiplexer multiplexer_7 (.sel(undriven), .in_0(D_i0), .in_1(d_ff_5_q), .out(D_o0_2));
  Multiplexer multiplexer_8 (.sel(Load_2), .in_0(d_ff_6_q), .in_1(D_i0_2), .out(D_o0));
  D_FF d_ff_7 (.D(D_o0_2), .C(Clock), .Q(d_ff_7_q));  // open: nQ
  D_FF d_ff_8 (.D(D_o0), .C(Clock), .Q(d_ff_8_q));  // open: nQ

  // Notes on the sheet:
  //   Master {{de Master}}
  //   Slave {{de Slave}}
endmodule
