// Digital circuit T-MS.dig as structural Verilog
module T_MS (
  input  C,
  output Q,
  output nQ
);

  wire undriven, undriven_2, undriven_3, undriven_4, undriven_5, undriven_6, undriven_7, undriven_8;

  // Not not_1 has open pins: in=C, out=open
  // And and_1 has open pins: In_1=nQ, In_2=undriven, out=open
  // Not not_2 has open pins: in=undriven, out=open
  // And and_2 has open pins: In_1=undriven, In_2=Q, out=open
  // NOr nor_1 has open pins: In_1=undriven_2, In_2=undriven_4, out=open
  // NOr nor_2 has open pins: In_1=undriven_5, In_2=undriven_3, out=open
  // And and_3 has open pins: In_1=undriven_5, In_2=undriven_6, out=open
  // And and_4 has open pins: In_1=undriven_6, In_2=undriven_4, out=open
  // NOr nor_3 has open pins: In_1=undriven_7, In_2=nQ, out=open
  // NOr nor_4 has open pins: In_1=Q, In_2=undriven_8, out=open
endmodule
