// Digital circuit muller-c.dig as structural Verilog
// A classic muller-C-element
// {{de Ein klassisches muller-c Element.}}
module muller_c (
  input  A,
  input  B,
  input  rst,
  output Y
);

  wire nfet_1_s, nfet_3_s, pfet_1_d, pfet_2_d, pullup_1_out;

  PFET pfet_1 (.G(A), .S(1'b1), .D(pfet_1_d));
  PFET pfet_2 (.G(B), .S(pfet_1_d), .D(pfet_2_d));
  NFET nfet_1 (.G(B), .D(pfet_2_d), .S(nfet_1_s));
  NFET nfet_2 (.G(A), .D(nfet_1_s), .S(1'b0));
  PullUp pullup_1 (.out(pullup_1_out));
  PFET pfet_3 (.G(Y), .S(pullup_1_out), .D(pfet_2_d));
  NFET nfet_3 (.G(Y), .D(pfet_2_d), .S(nfet_3_s));
  PullDown pulldown_1 (.out(nfet_3_s));
  // NOr nor_1 has open pins: In_1=pfet_2_d, In_2=rst, out=open
endmodule

/* Test case:
rst A B Y
 1  0 0 0
 1  1 0 0
 1  0 1 0
 1  1 1 0
 0  0 0 0
 0  0 1 0
 0  1 0 0
 0  1 1 1
 0  1 0 1
 0  0 1 1
 0  0 0 0
*/
