// Digital circuit muller-pipeline.dig as structural Verilog
module muller_pipeline (
  output c_1,
  output c_2,
  output c_3,
  output c_4
);

  wire reset_1_out, undriven, undriven_2, undriven_3, undriven_4, undriven_5;

  Reset #(.invertOutput("false")) reset_1 (.out(reset_1_out));
  // Or or_1 has open pins: In_1=c_4, In_2=reset_1_out, out=open
  muller_c muller_c_1 (.A(undriven), .B(undriven_2), .rst(reset_1_out), .Y(c_1));
  // Not not_1 has open pins: in=c_2, out=open
  // Not not_2 has open pins: in=c_3, out=open
  muller_c muller_c_2 (.A(undriven_3), .B(c_1), .rst(reset_1_out), .Y(c_2));
  muller_c muller_c_3 (.A(undriven_4), .B(c_2), .rst(reset_1_out), .Y(c_3));
  // Not not_3 has open pins: in=c_4, out=open
  muller_c muller_c_4 (.A(undriven_5), .B(c_3), .rst(reset_1_out), .Y(c_4));
  // Not not_4 has open pins: in=c_1, out=open

  // Notes on the sheet:
  //   Run circuit in single gate step mode.
  //   {{de Starte die Schaltung im Gatterschrittmodus.}}
endmodule
