// Digital circuit oscillator.dig as structural Verilog
module oscillator (
  output Q,
  output nQ
);

  wire C, delay_1_out, delay_2_out, reset_1_out, undriven, undriven_2, undriven_3, undriven_4;

  Reset reset_1 (.out(reset_1_out));
  // XOr xor_1 has open pins: In_1=reset_1_out, In_2=delay_1_out, out=open
  Delay #(.delayTime(2)) delay_1 (.in(C), .out(delay_1_out));
  // Not not_1 has open pins: in=C, out=open
  // Probe C on C
  Delay delay_2 (.in(undriven), .out(delay_2_out));
  // And and_1 has open pins: In_1=delay_2_out, In_2=C, out=open
  // And and_2 has open pins: In_1=Q, In_2=undriven_2, out=open
  // And and_3 has open pins: In_1=undriven_2, In_2=nQ, out=open
  // NOr nor_1 has open pins: In_1=undriven_3, In_2=nQ, out=open
  // NOr nor_2 has open pins: In_1=Q, In_2=undriven_4, out=open
endmodule
