// Digital circuit descrete.dig as structural Verilog
// Implementaion of a single cell of "Conways game of 
// life". This circuit is analyzed to create the truth table
// with 11 inputs and one output. Then the truth table 
// is exported to a hex file, and this hex file is imported
// into a LUT to speedup the cellular automaton.
// {{de Implementierung einer einzelnen Zelle von "Conways game of 
// life". Diese Schaltung wurde analysiert, um eine Wahrheitstabelle mit 11
// Eingängen und einem Ausgang zu erstellen. Diese wurde dann als 
// Hex-Datei exportiert und in eine LUT importiert, um den zellularen 
// Automaten zu beschleunigen.}}
module descrete (
  input  n1,
  input  n2,
  input  n3,
  input  n4,
  input  n5,
  input  n6,
  input  n7,
  input  n8,
  input  now,
  input  sel,
  input  init,
  output next
);

  wire comparator_1_eq, comparator_2_eq, undriven, undriven_2, undriven_3, undriven_4, undriven_5;
  wire [3:0] bitcount_1_out;

  BitCount #(.Bits(8)) bitcount_1 (.in({n8, n7, n6, n5, n4, n3, n2, n1}), .out(bitcount_1_out));
  Comparator #(.Bits(4)) comparator_1 (.a(4'b0011), .b(bitcount_1_out), .eq(comparator_1_eq));  // open: gt, lt
  Comparator #(.Bits(4)) comparator_2 (.a(4'b0010), .b(bitcount_1_out), .eq(comparator_2_eq));  // open: gt, lt
  // Or or_1 has open pins: In_1=comparator_1_eq, In_2=comparator_2_eq, out=open
  // Not not_1 has open pins: in=now, out=open
  // And and_1 has open pins: In_1=undriven_2, In_2=comparator_1_eq, out=open
  // And and_2 has open pins: In_1=now, In_2=undriven, out=open
  // Or or_2 has open pins: In_1=undriven_3, In_2=undriven_4, out=open
  Multiplexer multiplexer_1 (.sel(sel), .in_0(undriven_5), .in_1(init), .out(next));

  // Notes on the sheet:
  //   now: state of the cell, alive (HIGH) or dead (LOW)
  //   {{de Der aktuelle Zustand der Zelle.}}
  //   next: State of cell in the next generation.
  //   {{de Zustand der Zelle in der nächsten Generation}}
  //   sel: If high, the value given in input init is used as the
  //   next state. Is used to initialize the cell.
  //   {{de Wenn dieser Eingang auf high gesetzt wird,
  //   wird der init-Eingang verwendet um die Zelle zu
  //   initialisieren.}}
  //   init: The initial value of the cell. Is used if sel is high.
  //   {{de Der Anfangszustand der Zelle.
  //   Wird nur verwendet, wenn sel auf high gesetzt ist.}}
  //   neighbours {{de Nachbarn}}
  //   survive {{de überleben}}
  //   birth {{de Geburt}}
endmodule
