// Digital circuit multip_D_notWorking.dig as structural Verilog
module multip_D_notWorking (
  input  D,
  input  C,
  output Q
);

  wire undriven, undriven_2, undriven_3, undriven_4, undriven_5, undriven_6, undriven_7, undriven_8,
       undriven_9, undriven_10, undriven_11, undriven_12, undriven_13, undriven_14;

  // Not not_1 has open pins: in=D, out=open
  // And and_1 has open pins: In_1=undriven, In_2=C, out=open
  // And and_2 has open pins: In_1=C, In_2=D, out=open
  // NOr nor_1 has open pins: In_1=undriven_2, In_2=undriven_4, out=open
  // NOr nor_2 has open pins: In_1=undriven_5, In_2=undriven_3, out=open
  // Not not_2 has open pins: in=undriven_5, out=open
  // And and_3 has open pins: In_1=undriven_6, In_2=C, out=open
  // And and_4 has open pins: In_1=C, In_2=undriven_5, out=open
  // NOr nor_3 has open pins: In_1=undriven_7, In_2=undriven_9, out=open
  // NOr nor_4 has open pins: In_1=undriven_10, In_2=undriven_8, out=open
  // Not not_3 has open pins: in=undriven_10, out=open
  // And and_5 has open pins: In_1=undriven_11, In_2=C, out=open
  // And and_6 has open pins: In_1=C, In_2=undriven_10, out=open
  // NOr nor_5 has open pins: In_1=undriven_12, In_2=undriven_14, out=open
  // NOr nor_6 has open pins: In_1=Q, In_2=undriven_13, out=open
endmodule
