// Digital circuit multip_D_working_detail.dig as structural Verilog
module multip_D_working_detail (
  input  D,
  input  C,
  output D_2,
  output D_1,
  output D_0
);

  wire undriven, undriven_2, undriven_3, undriven_4, undriven_5, undriven_6, undriven_7, undriven_8,
       undriven_9, undriven_10, undriven_11, undriven_12, undriven_13, undriven_14, undriven_15, undriven_16,
       undriven_17, undriven_18, undriven_19, undriven_20, undriven_21, undriven_22, undriven_23,
       undriven_24, undriven_25, undriven_26, undriven_27;

  // And and_1 has open pins: In_1=D, In_2=C, out=open
  // Not not_1 has open pins: in=D, out=open
  // And and_2 has open pins: In_1=C, In_2=undriven, out=open
  // Not not_2 has open pins: in=C, out=open
  // NOr nor_1 has open pins: In_1=undriven_2, In_2=undriven_4, out=open
  // NOr nor_2 has open pins: In_1=undriven_5, In_2=undriven_3, out=open
  // And and_3 has open pins: In_1=undriven_5, In_2=undriven_6, out=open
  // And and_4 has open pins: In_1=undriven_6, In_2=undriven_4, out=open
  // NOr nor_3 has open pins: In_1=undriven_7, In_2=undriven_9, out=open
  // NOr nor_4 has open pins: In_1=D_0, In_2=undriven_8, out=open
  // And and_5 has open pins: In_1=D_0, In_2=C, out=open
  // Not not_3 has open pins: in=D_0, out=open
  // And and_6 has open pins: In_1=C, In_2=undriven_10, out=open
  // Not not_4 has open pins: in=C, out=open
  // NOr nor_5 has open pins: In_1=undriven_11, In_2=undriven_13, out=open
  // NOr nor_6 has open pins: In_1=undriven_14, In_2=undriven_12, out=open
  // And and_7 has open pins: In_1=undriven_14, In_2=undriven_15, out=open
  // And and_8 has open pins: In_1=undriven_15, In_2=undriven_13, out=open
  // NOr nor_7 has open pins: In_1=undriven_16, In_2=undriven_18, out=open
  // NOr nor_8 has open pins: In_1=D_1, In_2=undriven_17, out=open
  // And and_9 has open pins: In_1=D_1, In_2=C, out=open
  // Not not_5 has open pins: in=D_1, out=open
  // And and_10 has open pins: In_1=C, In_2=undriven_19, out=open
  // Not not_6 has open pins: in=C, out=open
  // NOr nor_9 has open pins: In_1=undriven_20, In_2=undriven_22, out=open
  // NOr nor_10 has open pins: In_1=undriven_23, In_2=undriven_21, out=open
  // And and_11 has open pins: In_1=undriven_23, In_2=undriven_24, out=open
  // And and_12 has open pins: In_1=undriven_24, In_2=undriven_22, out=open
  // NOr nor_11 has open pins: In_1=undriven_25, In_2=undriven_27, out=open
  // NOr nor_12 has open pins: In_1=D_2, In_2=undriven_26, out=open
endmodule

/* Test case:
C D D_0 D_1 D_2
# clear all bits
C 0  0   x   x
C 0  0   0   x
C 0  0   0   0

# fill with one
C 1  1   0   0
C 1  1   1   0
C 1  1   1   1

# fill with zero
C 0  0   1   1
C 0  0   0   1
C 0  0   0   0
*/
