// Digital circuit TafficLight1.dig as structural Verilog
module TafficLight1 (
  input  C
);

  wire undriven, z_m_0_nq, z_m_0_q, z_m_1_nq, z_m_1_q;

  JK_FF z_m_1 (.J(z_m_0_q), .C(C), .K(z_m_0_q), .Q(z_m_1_q), .nQ(z_m_1_nq));
  JK_FF z_m_0 (.J(1'b1), .C(C), .K(1'b1), .Q(z_m_0_q), .nQ(z_m_0_nq));
  // And and_1 has open pins: In_1=z_m_1_q, In_2=z_m_0_nq, out=open
  LED R (.in(z_m_1_nq));
  LED Y (.in(z_m_0_q));
  LED G (.in(undriven));
endmodule

/* Test case:
C R Y G
0 1 0 0
C 1 1 0
C 0 0 1
C 0 1 0
C 1 0 0
C 1 1 0
C 0 0 1
C 0 1 0
*/
