// Digital circuit TafficLight3.dig as structural Verilog
module TafficLight3 (
  input  C,
  input  F
);

  wire undriven, undriven_2, z_0_nq, z_0_q, z_1_nq, z_1_q;

  // Or or_1 has open pins: In_1=z_1_q, In_2=F, out=open
  JK_FF z_1 (.J(z_0_q), .C(C), .K(z_0_q), .Q(z_1_q), .nQ(z_1_nq));
  JK_FF z_0 (.J(undriven), .C(C), .K(1'b1), .Q(z_0_q), .nQ(z_0_nq));
  // And and_1 has open pins: In_1=z_1_q, In_2=z_0_nq, out=open
  LED R (.in(z_1_nq));
  LED Y (.in(z_0_q));
  LED G (.in(undriven_2));
endmodule

/* Test case:
C F  R Y G
0 0  1 0 0
C 0  1 1 0
C 0  0 0 1
C 0  0 1 0
C 0  1 0 0
C 0  1 1 0
# Fire signal goes high
C 1  0 0 1
C 1  0 1 0
# TL runs to red and then stops
C 1  1 0 0
C 1  1 0 0
C 1  1 0 0
# If fire signal goes low TL runs in the normal way
C 0  1 1 0
*/
