// Digital circuit splash.dig as structural Verilog
// Diskret aufgebautes Master-Slave JK-Flipflop.
// Das Master-Flipflop speichert bei einem High am 
// Taktsignal, das Slave-Flipflop bei Low am Taktsignal.
// Die obere und untere Rückkoppelleitung verhindern,
// das der verbotenen Zustand am Master-Flipflop
// auftritt..
module splash (
  input  J,
  input  C,
  input  K,
  output Q,
  output nQ
);

  wire undriven, undriven_2, undriven_3, undriven_4, undriven_5, undriven_6, undriven_7;

  // And and_1 has open pins: In_1=nQ, In_2=J, In_3=C, out=open
  // Not not_1 has open pins: in=C, out=open
  // And and_2 has open pins: In_1=C, In_2=K, In_3=Q, out=open
  // NOr nor_1 has open pins: In_1=undriven, In_2=undriven_2, out=open
  // NOr nor_2 has open pins: In_1=undriven_4, In_2=undriven_3, out=open
  // And and_3 has open pins: In_1=undriven_4, In_2=undriven_5, out=open
  // And and_4 has open pins: In_1=undriven_5, In_2=undriven_2, out=open
  // NOr nor_3 has open pins: In_1=undriven_6, In_2=nQ, out=open
  // NOr nor_4 has open pins: In_1=Q, In_2=undriven_7, out=open

  // Notes on the sheet:
  //   J: Eingang zum Setzen des Flipflops.
  //   C: Takteingang
  //   Q: Das im Flipflop gespeicherte Bit.
  //   nQ: Das inverse gespeicherte Bit.
  //   K: Eingang zum Löschen des Flipflops.
  //   LogicBLOX
  //   Circuit Simulator
endmodule
