// Digital circuit CounterSplitter.dig as structural Verilog
module CounterSplitter (
  input  clk,
  output [9:0] out_2
);

  wire counter_1_ovf, counter_2_ovf, undriven;
  wire [4:0] counter_1_out, counter_2_out;

  Counter #(.Bits(5)) counter_1 (.en(1'b1), .C(clk), .clr(1'b0), .out(counter_1_out), .ovf(counter_1_ovf));
  Counter #(.Bits(5)) counter_2 (.en(counter_1_ovf), .C(clk), .clr(1'b0), .out(counter_2_out), .ovf(counter_2_ovf));
  // Not not_1 has open pins: in=counter_2_ovf, out=open
  Break break_1 (.brk(counter_2_ovf));
  Register #(.Bits(10)) register_1 (.D({counter_2_out, counter_1_out}), .C(clk), .en(undriven), .Q(out_2));
endmodule
