// Digital circuit MS-JK-DIL.dig as structural Verilog
module MS_JK_DIL (
  input  J,
  input  C,
  input  K,
  output Q,
  output nQ
);

  wire undriven, undriven_2, undriven_3, undriven_4, undriven_5, undriven_6, undriven_7;

  // And and_1 has open pins: In_1=nQ, In_2=J, In_3=C, out=open
  // Not not_1 has open pins: in=C, out=open
  // And and_2 has open pins: In_1=C, In_2=K, In_3=Q, out=open
  // NOr nor_1 has open pins: In_1=undriven, In_2=undriven_3, out=open
  // NOr nor_2 has open pins: In_1=undriven_4, In_2=undriven_2, out=open
  // And and_3 has open pins: In_1=undriven_4, In_2=undriven_5, out=open
  // And and_4 has open pins: In_1=undriven_5, In_2=undriven_3, out=open
  // NOr nor_3 has open pins: In_1=undriven_6, In_2=nQ, out=open
  // NOr nor_4 has open pins: In_1=Q, In_2=undriven_7, out=open

  // Notes on the sheet:
  //   J: pin 1
  //   C: pin 2
  //   Q: pin 7
  //   nQ: pin 6
  //   K: pin 3
endmodule
