// Digital circuit analyzeBacktrack.dig as structural Verilog
module analyzeBacktrack (
  input  _1A,
  input  _1B,
  input  _2A,
  input  _2B,
  input  _3A,
  input  _3B,
  input  _4A,
  input  _4B,
  input  _4C,
  output _1Y,
  output _2Y,
  output _3Y,
  output _4Y
);

  // XOr xor_1 has open pins: In_1=_1A, In_2=_1B, out=open
  // XNOr xnor_1 has open pins: In_1=_2A, In_2=_2B, out=open
  // Or or_1 has open pins: In_1=_3A, In_2=_3B, out=open
  // And and_1 has open pins: In_1=_4A, In_2=_4B, In_3=_4C, out=open
endmodule
