// Digital circuit analyzeTestDFF.dig as structural Verilog
module analyzeTestDFF (
  input  C
);

  wire Q_0n, Q_1n, undriven, undriven_2, undriven_3, undriven_4, undriven_5;

  // Not not_1 has open pins: in=Q_0n, out=open
  // Not not_2 has open pins: in=Q_1n, out=open
  // And and_1 has open pins: In_1=Q_0n, In_2=undriven_4, out=open
  // And and_2 has open pins: In_1=undriven_5, In_2=Q_1n, out=open
  // Or or_1 has open pins: In_1=undriven, In_2=undriven_2, out=open
  D_FF u_Q_1n (.D(undriven_3), .C(C), .Q(Q_1n));  // open: nQ
  D_FF u_Q_0n (.D(undriven_5), .C(C), .Q(Q_0n));  // open: nQ
endmodule
