// Digital circuit multiBitInOutXOr.dig as structural Verilog
module multiBitInOutXOr (
  input  [3:0] A,
  input  [3:0] B,
  output [3:0] S
);

  // XOr xor_1 has open pins: In_1=A, In_2=B, out=open

  // Notes on the sheet:
  //   A: pin 1,2,3,4
  //   B: pin 5,6,7,8
  //   S: pin 9,10,11,12
endmodule
