// Digital circuit AllComponents.dig as structural Verilog
module AllComponents (
  input  [7:0] in8,
  input  in1,
  input  in1b,
  input  clk,
  input  [3:0] in4,
  input  [1:0] in2,
  input  [15:0] in_8,
  output U
);

  wire diodeforward_1_out, pullup_1_out, relay_1_p1, relaydt_1_p2;

  PowerSupply powersupply_1 (.VDD(1'b1), .GND(1'b0));
  Button button_1 ();  // open: out
  // RotEncoder rotencoder_1: pin names not known; wires that end beside it: 1'b1
  Reset reset_1 ();  // open: out
  DipSwitch dipswitch_1 ();  // open: out
  // And and_1 has open pins: In_1=in1, In_2=in1b, out=open
  // NAnd nand_1 has open pins: In_1=in1, In_2=in1b, out=open
  // Or or_1 has open pins: In_1=in1, In_2=in1b, out=open
  // NOr nor_1 has open pins: In_1=in1, In_2=in1b, out=open
  // XOr xor_1 has open pins: In_1=in1, In_2=in1b, out=open
  // XNOr xnor_1 has open pins: In_1=in1, In_2=in1b, out=open
  // Not not_1 has open pins: in=in1, out=open
  LookUpTable lookuptable_1 (.in0(in1), .in1(in1b));  // open: out
  Delay delay_1 (.in(in1));  // open: out
  LED led_1 (.in(in1));
  // Probe on in1
  LightBulb lightbulb_1 (.A(in1), .B(in1));
  Seven_Seg seven_seg_1 (.a(in1), .b(in1), .c(in1), .d(in1), .e(in1), .f(in1), .g(in1), .dp(in1));
  Seven_Seg_Hex seven_seg_hex_1 (.d(in4), .dp(in1));
  Keyboard keyboard_1 (.C(in1), .en(in1));  // open: D, av
  Terminal terminal_1 (.D(in8), .C(in1), .en(in1));
  LedMatrix #(.colAddrBits(4)) ledmatrix_1 (.rows(in8), .column(in4));
  BusSplitter #(.Bits(4)) bussplitter_1 (.D(in4), .OE(in1), .D0(in1), .D1(in1), .D2(in1), .D3(in1));
  Driver #(.Bits(4)) driver_1 (.in(in4), .en(in1));  // open: out
  DriverInvSel #(.Bits(4)) driverinvsel_1 (.in(in4), .en(in1));  // open: out
  Multiplexer #(.Bits(4)) multiplexer_1 (.sel(in1), .in_0(in4), .in_1(in4));  // open: out
  Demultiplexer demultiplexer_1 (.sel(in1), .in(in1));  // open: out_0, out_1
  Decoder decoder_1 (.sel(in1));  // open: out_0, out_1
  BitSelector #(.Selector_Bits(2)) bitselector_1 (.in(in4), .sel(in2));  // open: out
  PriorityEncoder priorityencoder_1 (.in0(in1), .in1(in1));  // open: num, any
  JK_FF jk_ff_1 (.J(in1), .C(clk), .K(in1));  // open: Q, nQ
  D_FF d_ff_1 (.D(in1), .C(clk));  // open: Q, nQ
  T_FF t_ff_1 (.T(in1), .C(clk));  // open: Q, nQ
  ROM #(.AddrBits(8), .Bits(8)) rom_1 (.A(in8), .sel(in1));  // open: D
  GraphicCard #(.graphicHeight(10), .graphicWidth(10), .Bits(8)) graphiccard_1 (
    .A(in8), .str(in1), .C(clk), .ld(in1), .B(in1), .D(in8));
  SixteenSeg sixteenseg_1 (.led(in_8), .dp(in1));
  Add #(.Bits(8)) add_1 (.a(in8), .b(in8), .c_i(relay_1_p1));  // open: s, c_o
  Sub #(.Bits(8)) sub_1 (.a(in8), .b(in8), .c_i(relay_1_p1));  // open: s, c_o
  Mul #(.Bits(8)) mul_1 (.a(in8), .b(in8));  // open: mul
  BarrelShifter #(.Bits(8)) barrelshifter_1 (.in(in8), .shift(in4));  // open: out
  Comparator #(.Bits(8)) comparator_1 (.a(in8), .b(in8));  // open: gt, eq, lt
  Neg #(.Bits(8)) neg_1 (.in(in8));  // open: out
  BitExtender bitextender_1 (.in(in8));  // open: out
  BitCount #(.Bits(8)) bitcount_1 (.in(in8));  // open: out
  Break break_1 (.brk(relay_1_p1));
  DiodeForward diodeforward_1 (.in(relay_1_p1), .out(diodeforward_1_out));
  PullDown pulldown_1 (.out(diodeforward_1_out));
  PullUp pullup_1 (.out(pullup_1_out));
  DiodeBackward diodebackward_1 (.in(relay_1_p1), .out(pullup_1_out));
  // Relay relay_1: pin names not known; wires that end beside it: relay_1_p1, relay_1_p1, relay_1_p1, relay_1_p1, relay_1_p1, relay_1_p1
  // RelayDT relaydt_1: pin names not known; wires that end beside it: relay_1_p1, relaydt_1_p2, relay_1_p1, relay_1_p1, relay_1_p1
  Switch switch_1 (.A(relay_1_p1), .B(relay_1_p1));
  Fuse fuse_1 (.A(relay_1_p1), .B(relay_1_p1));
  PFET pfet_1 (.G(relay_1_p1), .S(relay_1_p1), .D(relay_1_p1));
  NFET nfet_1 (.G(relay_1_p1), .D(relay_1_p1), .S(relay_1_p1));
  FGPFET fgpfet_1 (.G(relay_1_p1), .S(relay_1_p1), .D(relay_1_p1));
  FGNFET fgnfet_1 (.G(relay_1_p1), .D(relay_1_p1), .S(relay_1_p1));
  TransGate transgate_1 (.A(relay_1_p1), .nA(relaydt_1_p2), .out1(relay_1_p1), .out2(relay_1_p1));
  // Not not_2 has open pins: in=relay_1_p1, out=open
  // PolarityAwareLED polarityawareled_1: pin names not known; wires that end beside it: relay_1_p1, relay_1_p1
  // RGBLED rgbled_1: pin names not known; wires that end beside it: relay_1_p1, relay_1_p1

  assign U = in1;

  // Other names for the same wires on the sheet: zz[7:0] = in8

  // Notes on the sheet:
  //   All Components available in LogicBLOX
endmodule
