// Digital circuit counter.dig as structural Verilog
module counter (
  input  en,
  input  C,
  output [3:0] Q,
  output ov
);

  wire undriven, undriven_2, undriven_3, undriven_4, undriven_5, undriven_6, undriven_7, undriven_8,
       undriven_9, undriven_10, undriven_11, undriven_12, undriven_13, undriven_14, undriven_15, undriven_16,
       undriven_17, undriven_18, undriven_19, undriven_20, undriven_21;

  // Not not_1 has open pins: in=en, out=open
  // Not not_2 has open pins: in=Q[0], out=open
  // Not not_3 has open pins: in=Q[1], out=open
  // Not not_4 has open pins: in=Q[2], out=open
  // Not not_5 has open pins: in=Q[3], out=open
  // And and_1 has open pins: In_1=Q[0], In_2=Q[1], In_3=Q[2], In_4=en, out=open
  // And and_2 has open pins: In_1=undriven_20, In_2=Q[3], out=open
  // And and_3 has open pins: In_1=Q[3], In_2=undriven_21, out=open
  // And and_4 has open pins: In_1=Q[0], In_2=Q[1], In_3=undriven_18, In_4=en, out=open
  // And and_5 has open pins: In_1=undriven_20, In_2=Q[2], out=open
  // And and_6 has open pins: In_1=undriven_19, In_2=Q[2], out=open
  // And and_7 has open pins: In_1=Q[2], In_2=undriven_21, out=open
  // And and_8 has open pins: In_1=Q[0], In_2=undriven_19, In_3=undriven_17, In_4=en, out=open
  // And and_9 has open pins: In_1=undriven_20, In_2=Q[1], out=open
  // And and_10 has open pins: In_1=Q[1], In_2=undriven_21, out=open
  // And and_11 has open pins: In_1=Q[0], In_2=undriven_21, out=open
  // And and_12 has open pins: In_1=undriven_20, In_2=en, out=open
  // And and_13 has open pins: In_1=Q[0], In_2=en, In_3=Q[3], out=open
  // Or or_1 has open pins: In_1=undriven, In_2=undriven_2, In_3=undriven_8, out=open
  // Or or_2 has open pins: In_1=undriven_5, In_2=undriven_6, In_3=undriven_10, out=open
  // Or or_3 has open pins: In_1=undriven_7, In_2=undriven_11, out=open
  // Or or_4 has open pins: In_1=undriven_3, In_2=undriven_4, In_3=undriven_9, In_4=undriven_12, out=open
  D_FF Q_3n (.D(undriven_13), .C(C), .Q(Q[3]));  // open: nQ
  D_FF Q_2n (.D(undriven_16), .C(C), .Q(Q[2]));  // open: nQ
  D_FF Q_1n (.D(undriven_14), .C(C), .Q(Q[1]));  // open: nQ
  D_FF Q_0n (.D(undriven_15), .C(C), .Q(Q[0]));  // open: nQ
  // Pins of 1 and 4 bits meet at Q

  // Other names for the same wires on the sheet: Q_0n = Q[0]; Q_1n = Q[1]; Q_2n = Q[2]; Q_3n = Q[3]
endmodule
