// Digital circuit counter2Bit3.dig as structural Verilog
module counter2Bit3 (
  input  C,
  output Q1,
  output Q0
);

  wire undriven, undriven_2, undriven_3;

  // Not not_1 has open pins: in=Q0, out=open
  // Not not_2 has open pins: in=Q1, out=open
  // And and_1 has open pins: In_1=undriven_3, In_2=undriven_2, out=open
  D_FF Q_1n (.D(Q0), .C(C), .Q(Q1));  // open: nQ
  D_FF Q_0n (.D(undriven), .C(C), .Q(Q0));  // open: nQ

  // Other names for the same wires on the sheet: Q_0n = Q0; Q_1n = Q1
endmodule
