// Digital circuit decoder.dig as structural Verilog
module decoder (
  input  D_0,
  input  D_1,
  input  D_2,
  input  D_3,
  output d,
  output c,
  output b,
  output a,
  output e,
  output f,
  output g
);

  wire undriven, undriven_2, undriven_3, undriven_4, undriven_5, undriven_6, undriven_7, undriven_8,
       undriven_9, undriven_10, undriven_11, undriven_12, undriven_13, undriven_14, undriven_15, undriven_16,
       undriven_17, undriven_18, undriven_19, undriven_20, undriven_21, undriven_22, undriven_23,
       undriven_24, undriven_25, undriven_26, undriven_27, undriven_28, undriven_29, undriven_30,
       undriven_31, undriven_32, undriven_33, undriven_34, undriven_35, undriven_36, undriven_37,
       undriven_38, undriven_39;

  // Not not_1 has open pins: in=D_3, out=open
  // Not not_2 has open pins: in=D_2, out=open
  // Not not_3 has open pins: in=D_1, out=open
  // Not not_4 has open pins: in=D_0, out=open
  // And and_1 has open pins: In_1=undriven_39, In_2=D_1, out=open
  // And and_2 has open pins: In_1=undriven_39, In_2=D_2, In_3=D_0, out=open
  // And and_3 has open pins: In_1=D_3, In_2=undriven_38, In_3=undriven_37, out=open
  // And and_4 has open pins: In_1=D_3, In_2=undriven_36, out=open
  // And and_5 has open pins: In_1=undriven_38, In_2=undriven_36, out=open
  // And and_6 has open pins: In_1=D_2, In_2=D_1, out=open
  // And and_7 has open pins: In_1=undriven_39, In_2=undriven_37, In_3=undriven_36, out=open
  // And and_8 has open pins: In_1=undriven_39, In_2=D_1, In_3=D_0, out=open
  // And and_9 has open pins: In_1=D_3, In_2=undriven_37, In_3=D_0, out=open
  // And and_10 has open pins: In_1=undriven_38, In_2=undriven_36, out=open
  // And and_11 has open pins: In_1=undriven_38, In_2=undriven_37, out=open
  // And and_12 has open pins: In_1=undriven_39, In_2=D_2, out=open
  // And and_13 has open pins: In_1=D_3, In_2=undriven_38, out=open
  // And and_14 has open pins: In_1=undriven_38, In_2=D_0, out=open
  // And and_15 has open pins: In_1=undriven_38, In_2=undriven_37, out=open
  // And and_16 has open pins: In_1=undriven_37, In_2=D_0, out=open
  // And and_17 has open pins: In_1=undriven_39, In_2=undriven_38, In_3=undriven_36, out=open
  // And and_18 has open pins: In_1=D_3, In_2=undriven_37, out=open
  // And and_19 has open pins: In_1=D_2, In_2=undriven_37, In_3=D_0, out=open
  // And and_20 has open pins: In_1=undriven_38, In_2=D_1, In_3=D_0, out=open
  // And and_21 has open pins: In_1=D_2, In_2=D_1, In_3=undriven_36, out=open
  // And and_22 has open pins: In_1=D_3, In_2=D_1, out=open
  // And and_23 has open pins: In_1=D_3, In_2=D_2, out=open
  // And and_24 has open pins: In_1=undriven_38, In_2=undriven_36, out=open
  // And and_25 has open pins: In_1=D_1, In_2=undriven_36, out=open
  // And and_26 has open pins: In_1=undriven_39, In_2=D_2, In_3=undriven_37, out=open
  // And and_27 has open pins: In_1=D_3, In_2=undriven_38, out=open
  // And and_28 has open pins: In_1=D_3, In_2=D_1, out=open
  // And and_29 has open pins: In_1=D_2, In_2=undriven_36, out=open
  // And and_30 has open pins: In_1=undriven_37, In_2=undriven_36, out=open
  // And and_31 has open pins: In_1=D_3, In_2=undriven_38, out=open
  // And and_32 has open pins: In_1=undriven_39, In_2=D_2, In_3=undriven_37, out=open
  // And and_33 has open pins: In_1=D_3, In_2=D_0, out=open
  // And and_34 has open pins: In_1=undriven_38, In_2=D_1, out=open
  // And and_35 has open pins: In_1=D_1, In_2=undriven_36, out=open
  // Or or_1 has open pins: In_1=undriven, In_2=undriven_2, In_3=undriven_3, In_4=undriven_21, In_5=undriven_28, In_6=undriven_35, out=open
  // Or or_2 has open pins: In_1=undriven_4, In_2=undriven_5, In_3=undriven_6, In_4=undriven_22, In_5=undriven_29, out=open
  // Or or_3 has open pins: In_1=undriven_7, In_2=undriven_8, In_3=undriven_9, In_4=undriven_23, In_5=undriven_30, out=open
  // Or or_4 has open pins: In_1=undriven_10, In_2=undriven_11, In_3=undriven_12, In_4=undriven_24, In_5=undriven_31, out=open
  // Or or_5 has open pins: In_1=undriven_13, In_2=undriven_14, In_3=undriven_25, In_4=undriven_32, out=open
  // Or or_6 has open pins: In_1=undriven_15, In_2=undriven_16, In_3=undriven_17, In_4=undriven_26, In_5=undriven_33, out=open
  // Or or_7 has open pins: In_1=undriven_18, In_2=undriven_19, In_3=undriven_20, In_4=undriven_27, In_5=undriven_34, out=open

  // Notes on the sheet:
  //   D_0: Bit 0 des Dekodereingangs.
  //   D_1: Bit 1 des Dekodereingangs.
  //   D_2: Bit 2 des Dekodereingangs.
  //   D_3: Bit 3 des Dekodereingangs.
endmodule
