// Digital circuit dif.dig as structural Verilog
module dif (
  input  Count,
  input  C,
  output Out
);

  wire p0_q, p1_nq;

  D_FF p0 (.D(Count), .C(C), .Q(p0_q));  // open: nQ
  D_FF p1 (.D(p0_q), .C(C), .nQ(p1_nq));  // open: Q
  // And and_1 has open pins: In_1=p0_q, In_2=p1_nq, out=open
endmodule
