// Digital circuit busTest.dig as structural Verilog
module busTest (
  input  [3:0] A,
  input  [3:0] B,
  output [3:0] S,
  output [3:0] U
);

  // XOr xor_1 has open pins: In_1=A, In_2=B, out=open
  // XNOr xnor_1 has open pins: In_1=B, In_2=A, out=open

  // Notes on the sheet:
  //   S: pin 9,10,11,12
  //   A: pin 1,2,3,4
  //   B: pin 5,6,7,8
  //   U: pin 13,14,15,16
endmodule
