// Digital circuit data.dig as structural Verilog
module data (
  input  C,
  output out_1,
  output out_3,
  output out_4,
  output out_5
);

  wire counter_1_ovf, undriven, undriven_2;

  Counter #(.Bits(4)) counter_1 (.en(1'b1), .C(C), .clr(1'b0), .ovf(counter_1_ovf));  // open: out
  JK_FF q_0n (.J(1'b1), .C(C), .K(1'b1), .Q(out_1));  // open: nQ
  Break break_1 (.brk(counter_1_ovf));
  JK_FF q_1n (.J(out_1), .C(C), .K(out_1), .Q(out_3));  // open: nQ
  // And and_1 has open pins: In_1=out_1, In_2=out_3, out=open
  JK_FF q_2n (.J(undriven), .C(C), .K(undriven), .Q(out_4));  // open: nQ
  // And and_2 has open pins: In_1=undriven, In_2=out_4, out=open
  JK_FF q_3n (.J(undriven_2), .C(C), .K(undriven_2), .Q(out_5));  // open: nQ

  // Notes on the sheet:
  //   Synchroner Zähler aus JK-Flipflops
endmodule
