// Digital circuit inner.dig as structural Verilog
module inner (
  input  A,
  input  B,
  output Y
);

  // And and_1 has open pins: In_1=A, In_2=B, out=open
  // Not not_1 has open pins: in=open, out=Y
endmodule
