// Digital circuit innerBit.dig as structural Verilog
module innerBit (
  input  A,
  input  B,
  output Y
);

  // And and_1 has open pins: In_1=A, In_2=1'b0, In_3=B, out=open
  // Pins of 1 and 2 bits meet at 2'b10
endmodule
