// Digital circuit mid.dig as structural Verilog
module mid (
  input  A,
  input  B,
  output Y
);

  wire inner_1_y, undriven, undriven_2;

  // Not not_1 has open pins: in=A, out=open
  // Not not_2 has open pins: in=B, out=open
  inner inner_1 (.A(undriven), .B(undriven_2), .Y(inner_1_y));
  // Not not_3 has open pins: in=inner_1_y, out=open
endmodule
