// Digital circuit mid2.dig as structural Verilog
module mid2 (
  input  A,
  input  B,
  output Y
);

  wire inner2_1_y, undriven, undriven_2;

  // Not not_1 has open pins: in=A, out=open
  // Not not_2 has open pins: in=B, out=open
  inner2 inner2_1 (.A(undriven), .B(undriven_2), .Y(inner2_1_y));
  // Not not_3 has open pins: in=inner2_1_y, out=open
endmodule
