// Digital circuit midBit.dig as structural Verilog
module midBit (
  input  A,
  input  B,
  output Y
);

  wire innerbit_1_y, undriven, undriven_2;

  // Not not_1 has open pins: in=A, out=open
  // Not not_2 has open pins: in=B, out=open
  innerBit innerbit_1 (.A(undriven), .B(undriven_2), .Y(innerbit_1_y));
  // Not not_3 has open pins: in=innerbit_1_y, out=open
endmodule
