// Digital circuit ArtixClockCascading.dig as structural Verilog
module ArtixClockCascading (
  input  Clk,
  output Y0
);

  // Not not_1 has open pins: in=Clk, out=open

  // Notes on the sheet:
  //   Y0: pin U16
  //   Clk: pin W5, Hz: 37000
  //   Board: BASYS3
endmodule
