// Digital circuit Clock.dig as structural Verilog
module Clock (
  input  Clk,
  output Y0
);

  // Not not_1 has open pins: in=Clk, out=open

  // Notes on the sheet:
  //   Y0: pin U16
  //   Clk: pin W5, Hz: 20
  //   Board: BASYS3
endmodule
