// Digital circuit Clock3.dig as structural Verilog
module Clock3 (
  input  C,
  output OV
);

  // Not not_1 has open pins: in=C, out=open

  // Notes on the sheet:
  //   OV: pin U18
  //   C: pin W5, Hz: 100000000
endmodule
