// Digital circuit adder4b.dig as structural Verilog
module adder4b (
  input  [3:0] A,
  input  [3:0] B,
  input  C_I,
  output [3:0] S,
  output C_O
);

  wire undriven, undriven_2, undriven_3, undriven_4, undriven_5, undriven_6, undriven_7, undriven_8,
       undriven_9, undriven_10, undriven_11, undriven_12, undriven_13, undriven_14, undriven_15, undriven_16,
       undriven_17, undriven_18, undriven_19, undriven_20, undriven_21, undriven_22, undriven_23,
       undriven_24, undriven_25, undriven_26, undriven_27, undriven_28, undriven_29, undriven_30,
       undriven_31, undriven_32, undriven_33, undriven_34, undriven_35, undriven_36, undriven_37,
       undriven_38, undriven_39, undriven_40, undriven_41, undriven_42, undriven_43, undriven_44,
       undriven_45, undriven_46, undriven_47, undriven_48, undriven_49, undriven_50, undriven_51,
       undriven_52, undriven_53, undriven_54, undriven_55, undriven_56, undriven_57, undriven_58,
       undriven_59, undriven_60, undriven_61, undriven_62, undriven_63, undriven_64, undriven_65,
       undriven_66, undriven_67, undriven_68, undriven_69, undriven_70, undriven_71, undriven_72,
       undriven_73, undriven_74, undriven_75, undriven_76, undriven_77, undriven_78, undriven_79,
       undriven_80, undriven_81, undriven_82, undriven_83, undriven_84, undriven_85, undriven_86,
       undriven_87, undriven_88, undriven_89, undriven_90, undriven_91, undriven_92, undriven_93,
       undriven_94, undriven_95, undriven_96, undriven_97, undriven_98, undriven_99, undriven_100,
       undriven_101, undriven_102, undriven_103, undriven_104, undriven_105, undriven_106, undriven_107,
       undriven_108, undriven_109, undriven_110, undriven_111, undriven_112, undriven_113, undriven_114,
       undriven_115, undriven_116, undriven_117, undriven_118, undriven_119, undriven_120, undriven_121,
       undriven_122, undriven_123, undriven_124, undriven_125, undriven_126, undriven_127, undriven_128,
       undriven_129, undriven_130, undriven_131, undriven_132, undriven_133, undriven_134, undriven_135,
       undriven_136, undriven_137, undriven_138, undriven_139, undriven_140, undriven_141, undriven_142,
       undriven_143, undriven_144;

  // Not not_1 has open pins: in=A[3], out=open
  // Not not_2 has open pins: in=A[2], out=open
  // Not not_3 has open pins: in=A[1], out=open
  // Not not_4 has open pins: in=A[0], out=open
  // Not not_5 has open pins: in=B[3], out=open
  // Not not_6 has open pins: in=B[2], out=open
  // Not not_7 has open pins: in=B[1], out=open
  // Not not_8 has open pins: in=B[0], out=open
  // Not not_9 has open pins: in=C_I, out=open
  // And and_1 has open pins: In_1=undriven_141, In_2=undriven_144, In_3=undriven_138, In_4=undriven_139, In_5=B[3], In_6=undriven_136, out=open
  // And and_2 has open pins: In_1=A[0], In_2=undriven_144, In_3=B[1], In_4=B[2], In_5=undriven_140, In_6=C_I, out=open
  // And and_3 has open pins: In_1=undriven_141, In_2=A[3], In_3=undriven_138, In_4=undriven_139, In_5=undriven_140, In_6=undriven_136, out=open
  // And and_4 has open pins: In_1=A[0], In_2=A[3], In_3=B[1], In_4=B[2], In_5=B[3], In_6=C_I, out=open
  // And and_5 has open pins: In_1=undriven_141, In_2=undriven_143, In_3=undriven_144, In_4=undriven_138, In_5=B[3], In_6=undriven_136, out=open
  // And and_6 has open pins: In_1=A[0], In_2=A[2], In_3=undriven_144, In_4=B[1], In_5=undriven_140, In_6=C_I, out=open
  // And and_7 has open pins: In_1=undriven_141, In_2=undriven_143, In_3=A[3], In_4=undriven_138, In_5=undriven_140, In_6=undriven_136, out=open
  // And and_8 has open pins: In_1=A[0], In_2=A[2], In_3=A[3], In_4=B[1], In_5=B[3], In_6=C_I, out=open
  // And and_9 has open pins: In_1=undriven_141, In_2=undriven_142, In_3=undriven_144, In_4=undriven_139, In_5=B[3], In_6=undriven_136, out=open
  // And and_10 has open pins: In_1=A[0], In_2=A[1], In_3=undriven_144, In_4=B[2], In_5=undriven_140, In_6=C_I, out=open
  // And and_11 has open pins: In_1=undriven_141, In_2=undriven_142, In_3=A[3], In_4=undriven_139, In_5=undriven_140, In_6=undriven_136, out=open
  // And and_12 has open pins: In_1=A[0], In_2=A[1], In_3=A[3], In_4=B[2], In_5=B[3], In_6=C_I, out=open
  // And and_13 has open pins: In_1=undriven_141, In_2=undriven_142, In_3=undriven_143, In_4=undriven_144, In_5=B[3], In_6=undriven_136, out=open
  // And and_14 has open pins: In_1=A[0], In_2=A[1], In_3=A[2], In_4=undriven_144, In_5=undriven_140, In_6=C_I, out=open
  // And and_15 has open pins: In_1=undriven_141, In_2=undriven_142, In_3=undriven_143, In_4=A[3], In_5=undriven_140, In_6=undriven_136, out=open
  // And and_16 has open pins: In_1=A[0], In_2=A[1], In_3=A[2], In_4=A[3], In_5=B[3], In_6=C_I, out=open
  // And and_17 has open pins: In_1=undriven_141, In_2=undriven_144, In_3=undriven_137, In_4=undriven_138, In_5=undriven_139, In_6=B[3], out=open
  // And and_18 has open pins: In_1=A[0], In_2=undriven_144, In_3=B[0], In_4=B[1], In_5=B[2], In_6=undriven_140, out=open
  // And and_19 has open pins: In_1=undriven_141, In_2=A[3], In_3=undriven_137, In_4=undriven_138, In_5=undriven_139, In_6=undriven_140, out=open
  // And and_20 has open pins: In_1=A[0], In_2=A[3], In_3=B[0], In_4=B[1], In_5=B[2], In_6=B[3], out=open
  // And and_21 has open pins: In_1=undriven_141, In_2=undriven_143, In_3=undriven_144, In_4=undriven_137, In_5=undriven_138, In_6=B[3], out=open
  // And and_22 has open pins: In_1=A[0], In_2=A[2], In_3=undriven_144, In_4=B[0], In_5=B[1], In_6=undriven_140, out=open
  // And and_23 has open pins: In_1=undriven_141, In_2=undriven_143, In_3=A[3], In_4=undriven_137, In_5=undriven_138, In_6=undriven_140, out=open
  // And and_24 has open pins: In_1=A[0], In_2=A[2], In_3=A[3], In_4=B[0], In_5=B[1], In_6=B[3], out=open
  // And and_25 has open pins: In_1=undriven_141, In_2=undriven_142, In_3=undriven_144, In_4=undriven_137, In_5=undriven_139, In_6=B[3], out=open
  // And and_26 has open pins: In_1=A[0], In_2=A[1], In_3=undriven_144, In_4=B[0], In_5=B[2], In_6=undriven_140, out=open
  // And and_27 has open pins: In_1=undriven_141, In_2=undriven_142, In_3=A[3], In_4=undriven_137, In_5=undriven_139, In_6=undriven_140, out=open
  // And and_28 has open pins: In_1=A[0], In_2=A[1], In_3=A[3], In_4=B[0], In_5=B[2], In_6=B[3], out=open
  // And and_29 has open pins: In_1=undriven_141, In_2=undriven_142, In_3=undriven_143, In_4=undriven_144, In_5=undriven_137, In_6=B[3], out=open
  // And and_30 has open pins: In_1=A[0], In_2=A[1], In_3=A[2], In_4=undriven_144, In_5=B[0], In_6=undriven_140, out=open
  // And and_31 has open pins: In_1=undriven_141, In_2=undriven_142, In_3=undriven_143, In_4=A[3], In_5=undriven_137, In_6=undriven_140, out=open
  // And and_32 has open pins: In_1=A[0], In_2=A[1], In_3=A[2], In_4=A[3], In_5=B[0], In_6=B[3], out=open
  // And and_33 has open pins: In_1=undriven_142, In_2=undriven_144, In_3=undriven_137, In_4=undriven_139, In_5=B[3], In_6=undriven_136, out=open
  // And and_34 has open pins: In_1=A[1], In_2=undriven_144, In_3=B[0], In_4=B[2], In_5=undriven_140, In_6=C_I, out=open
  // And and_35 has open pins: In_1=undriven_142, In_2=A[3], In_3=undriven_137, In_4=undriven_139, In_5=undriven_140, In_6=undriven_136, out=open
  // And and_36 has open pins: In_1=A[1], In_2=A[3], In_3=B[0], In_4=B[2], In_5=B[3], In_6=C_I, out=open
  // And and_37 has open pins: In_1=undriven_142, In_2=undriven_143, In_3=undriven_144, In_4=undriven_137, In_5=B[3], In_6=undriven_136, out=open
  // And and_38 has open pins: In_1=A[1], In_2=A[2], In_3=undriven_144, In_4=B[0], In_5=undriven_140, In_6=C_I, out=open
  // And and_39 has open pins: In_1=undriven_142, In_2=undriven_143, In_3=A[3], In_4=undriven_137, In_5=undriven_140, In_6=undriven_136, out=open
  // And and_40 has open pins: In_1=A[1], In_2=A[2], In_3=A[3], In_4=B[0], In_5=B[3], In_6=C_I, out=open
  // And and_41 has open pins: In_1=undriven_142, In_2=undriven_144, In_3=undriven_138, In_4=undriven_139, In_5=B[3], out=open
  // And and_42 has open pins: In_1=A[1], In_2=undriven_144, In_3=B[1], In_4=B[2], In_5=undriven_140, out=open
  // And and_43 has open pins: In_1=undriven_142, In_2=A[3], In_3=undriven_138, In_4=undriven_139, In_5=undriven_140, out=open
  // And and_44 has open pins: In_1=A[1], In_2=A[3], In_3=B[1], In_4=B[2], In_5=B[3], out=open
  // And and_45 has open pins: In_1=undriven_142, In_2=undriven_143, In_3=undriven_144, In_4=undriven_138, In_5=B[3], out=open
  // And and_46 has open pins: In_1=A[1], In_2=A[2], In_3=undriven_144, In_4=B[1], In_5=undriven_140, out=open
  // And and_47 has open pins: In_1=undriven_142, In_2=undriven_143, In_3=A[3], In_4=undriven_138, In_5=undriven_140, out=open
  // And and_48 has open pins: In_1=A[1], In_2=A[2], In_3=A[3], In_4=B[1], In_5=B[3], out=open
  // And and_49 has open pins: In_1=undriven_143, In_2=undriven_144, In_3=undriven_137, In_4=undriven_138, In_5=B[3], In_6=undriven_136, out=open
  // And and_50 has open pins: In_1=A[2], In_2=undriven_144, In_3=B[0], In_4=B[1], In_5=undriven_140, In_6=C_I, out=open
  // And and_51 has open pins: In_1=undriven_143, In_2=A[3], In_3=undriven_137, In_4=undriven_138, In_5=undriven_140, In_6=undriven_136, out=open
  // And and_52 has open pins: In_1=A[2], In_2=A[3], In_3=B[0], In_4=B[1], In_5=B[3], In_6=C_I, out=open
  // And and_53 has open pins: In_1=undriven_143, In_2=undriven_144, In_3=undriven_139, In_4=B[3], out=open
  // And and_54 has open pins: In_1=A[2], In_2=undriven_144, In_3=B[2], In_4=undriven_140, out=open
  // And and_55 has open pins: In_1=undriven_143, In_2=A[3], In_3=undriven_139, In_4=undriven_140, out=open
  // And and_56 has open pins: In_1=A[2], In_2=A[3], In_3=B[2], In_4=B[3], out=open
  // And and_57 has open pins: In_1=undriven_144, In_2=B[0], In_3=B[1], In_4=B[2], In_5=undriven_140, In_6=C_I, out=open
  // And and_58 has open pins: In_1=undriven_144, In_2=undriven_137, In_3=undriven_138, In_4=undriven_139, In_5=B[3], In_6=undriven_136, out=open
  // And and_59 has open pins: In_1=A[3], In_2=undriven_137, In_3=undriven_138, In_4=undriven_139, In_5=undriven_140, In_6=undriven_136, out=open
  // And and_60 has open pins: In_1=A[3], In_2=B[0], In_3=B[1], In_4=B[2], In_5=B[3], In_6=C_I, out=open
  // And and_61 has open pins: In_1=undriven_141, In_2=undriven_143, In_3=undriven_138, In_4=B[2], In_5=undriven_136, out=open
  // And and_62 has open pins: In_1=A[0], In_2=undriven_143, In_3=B[1], In_4=undriven_139, In_5=C_I, out=open
  // And and_63 has open pins: In_1=undriven_141, In_2=A[2], In_3=undriven_138, In_4=undriven_139, In_5=undriven_136, out=open
  // And and_64 has open pins: In_1=A[0], In_2=A[2], In_3=B[1], In_4=B[2], In_5=C_I, out=open
  // And and_65 has open pins: In_1=undriven_141, In_2=undriven_142, In_3=undriven_143, In_4=B[2], In_5=undriven_136, out=open
  // And and_66 has open pins: In_1=A[0], In_2=A[1], In_3=undriven_143, In_4=undriven_139, In_5=C_I, out=open
  // And and_67 has open pins: In_1=undriven_141, In_2=undriven_142, In_3=A[2], In_4=undriven_139, In_5=undriven_136, out=open
  // And and_68 has open pins: In_1=A[0], In_2=A[1], In_3=A[2], In_4=B[2], In_5=C_I, out=open
  // And and_69 has open pins: In_1=undriven_141, In_2=undriven_143, In_3=undriven_137, In_4=undriven_138, In_5=B[2], out=open
  // And and_70 has open pins: In_1=A[0], In_2=undriven_143, In_3=B[0], In_4=B[1], In_5=undriven_139, out=open
  // And and_71 has open pins: In_1=undriven_141, In_2=A[2], In_3=undriven_137, In_4=undriven_138, In_5=undriven_139, out=open
  // And and_72 has open pins: In_1=A[0], In_2=A[2], In_3=B[0], In_4=B[1], In_5=B[2], out=open
  // And and_73 has open pins: In_1=undriven_141, In_2=undriven_142, In_3=undriven_143, In_4=undriven_137, In_5=B[2], out=open
  // And and_74 has open pins: In_1=A[0], In_2=A[1], In_3=undriven_143, In_4=B[0], In_5=undriven_139, out=open
  // And and_75 has open pins: In_1=undriven_141, In_2=undriven_142, In_3=A[2], In_4=undriven_137, In_5=undriven_139, out=open
  // And and_76 has open pins: In_1=A[0], In_2=A[1], In_3=A[2], In_4=B[0], In_5=B[2], out=open
  // And and_77 has open pins: In_1=undriven_142, In_2=undriven_143, In_3=undriven_137, In_4=B[2], In_5=undriven_136, out=open
  // And and_78 has open pins: In_1=A[1], In_2=undriven_143, In_3=B[0], In_4=undriven_139, In_5=C_I, out=open
  // And and_79 has open pins: In_1=undriven_142, In_2=A[2], In_3=undriven_137, In_4=undriven_139, In_5=undriven_136, out=open
  // And and_80 has open pins: In_1=A[1], In_2=A[2], In_3=B[0], In_4=B[2], In_5=C_I, out=open
  // And and_81 has open pins: In_1=undriven_142, In_2=undriven_143, In_3=undriven_138, In_4=B[2], out=open
  // And and_82 has open pins: In_1=A[1], In_2=undriven_143, In_3=B[1], In_4=undriven_139, out=open
  // And and_83 has open pins: In_1=undriven_142, In_2=A[2], In_3=undriven_138, In_4=undriven_139, out=open
  // And and_84 has open pins: In_1=A[1], In_2=A[2], In_3=B[1], In_4=B[2], out=open
  // And and_85 has open pins: In_1=undriven_143, In_2=B[0], In_3=B[1], In_4=undriven_139, In_5=C_I, out=open
  // And and_86 has open pins: In_1=undriven_143, In_2=undriven_137, In_3=undriven_138, In_4=B[2], In_5=undriven_136, out=open
  // And and_87 has open pins: In_1=A[2], In_2=undriven_137, In_3=undriven_138, In_4=undriven_139, In_5=undriven_136, out=open
  // And and_88 has open pins: In_1=A[2], In_2=B[0], In_3=B[1], In_4=B[2], In_5=C_I, out=open
  // And and_89 has open pins: In_1=undriven_141, In_2=undriven_142, In_3=B[1], In_4=undriven_136, out=open
  // And and_90 has open pins: In_1=A[0], In_2=undriven_142, In_3=undriven_138, In_4=C_I, out=open
  // And and_91 has open pins: In_1=undriven_141, In_2=A[1], In_3=undriven_138, In_4=undriven_136, out=open
  // And and_92 has open pins: In_1=A[0], In_2=A[1], In_3=B[1], In_4=C_I, out=open
  // And and_93 has open pins: In_1=undriven_141, In_2=undriven_142, In_3=undriven_137, In_4=B[1], out=open
  // And and_94 has open pins: In_1=A[0], In_2=undriven_142, In_3=B[0], In_4=undriven_138, out=open
  // And and_95 has open pins: In_1=undriven_141, In_2=A[1], In_3=undriven_137, In_4=undriven_138, out=open
  // And and_96 has open pins: In_1=A[0], In_2=A[1], In_3=B[0], In_4=B[1], out=open
  // And and_97 has open pins: In_1=undriven_142, In_2=B[0], In_3=undriven_138, In_4=C_I, out=open
  // And and_98 has open pins: In_1=undriven_142, In_2=undriven_137, In_3=B[1], In_4=undriven_136, out=open
  // And and_99 has open pins: In_1=A[1], In_2=undriven_137, In_3=undriven_138, In_4=undriven_136, out=open
  // And and_100 has open pins: In_1=A[1], In_2=B[0], In_3=B[1], In_4=C_I, out=open
  // And and_101 has open pins: In_1=undriven_141, In_2=undriven_137, In_3=C_I, out=open
  // And and_102 has open pins: In_1=undriven_141, In_2=B[0], In_3=undriven_136, out=open
  // And and_103 has open pins: In_1=A[0], In_2=undriven_137, In_3=undriven_136, out=open
  // And and_104 has open pins: In_1=A[0], In_2=B[0], In_3=C_I, out=open
  // And and_105 has open pins: In_1=A[0], In_2=B[1], In_3=B[2], In_4=B[3], In_5=C_I, out=open
  // And and_106 has open pins: In_1=A[0], In_2=A[3], In_3=B[1], In_4=B[2], In_5=C_I, out=open
  // And and_107 has open pins: In_1=A[0], In_2=A[2], In_3=B[1], In_4=B[3], In_5=C_I, out=open
  // And and_108 has open pins: In_1=A[0], In_2=A[2], In_3=A[3], In_4=B[1], In_5=C_I, out=open
  // And and_109 has open pins: In_1=A[0], In_2=A[1], In_3=B[2], In_4=B[3], In_5=C_I, out=open
  // And and_110 has open pins: In_1=A[0], In_2=A[1], In_3=A[3], In_4=B[2], In_5=C_I, out=open
  // And and_111 has open pins: In_1=A[0], In_2=A[1], In_3=A[2], In_4=B[3], In_5=C_I, out=open
  // And and_112 has open pins: In_1=A[0], In_2=A[1], In_3=A[2], In_4=A[3], In_5=C_I, out=open
  // And and_113 has open pins: In_1=A[0], In_2=B[0], In_3=B[1], In_4=B[2], In_5=B[3], out=open
  // And and_114 has open pins: In_1=A[0], In_2=A[3], In_3=B[0], In_4=B[1], In_5=B[2], out=open
  // And and_115 has open pins: In_1=A[0], In_2=A[2], In_3=B[0], In_4=B[1], In_5=B[3], out=open
  // And and_116 has open pins: In_1=A[0], In_2=A[2], In_3=A[3], In_4=B[0], In_5=B[1], out=open
  // And and_117 has open pins: In_1=A[0], In_2=A[1], In_3=B[0], In_4=B[2], In_5=B[3], out=open
  // And and_118 has open pins: In_1=A[0], In_2=A[1], In_3=A[3], In_4=B[0], In_5=B[2], out=open
  // And and_119 has open pins: In_1=A[0], In_2=A[1], In_3=A[2], In_4=B[0], In_5=B[3], out=open
  // And and_120 has open pins: In_1=A[0], In_2=A[1], In_3=A[2], In_4=A[3], In_5=B[0], out=open
  // And and_121 has open pins: In_1=A[1], In_2=B[0], In_3=B[2], In_4=B[3], In_5=C_I, out=open
  // And and_122 has open pins: In_1=A[1], In_2=A[3], In_3=B[0], In_4=B[2], In_5=C_I, out=open
  // And and_123 has open pins: In_1=A[1], In_2=A[2], In_3=B[0], In_4=B[3], In_5=C_I, out=open
  // And and_124 has open pins: In_1=A[1], In_2=A[2], In_3=A[3], In_4=B[0], In_5=C_I, out=open
  // And and_125 has open pins: In_1=A[1], In_2=B[1], In_3=B[2], In_4=B[3], out=open
  // And and_126 has open pins: In_1=A[1], In_2=A[3], In_3=B[1], In_4=B[2], out=open
  // And and_127 has open pins: In_1=A[1], In_2=A[2], In_3=B[1], In_4=B[3], out=open
  // And and_128 has open pins: In_1=A[1], In_2=A[2], In_3=A[3], In_4=B[1], out=open
  // And and_129 has open pins: In_1=A[2], In_2=B[0], In_3=B[1], In_4=B[3], In_5=C_I, out=open
  // And and_130 has open pins: In_1=A[2], In_2=A[3], In_3=B[0], In_4=B[1], In_5=C_I, out=open
  // And and_131 has open pins: In_1=A[2], In_2=B[2], In_3=B[3], out=open
  // And and_132 has open pins: In_1=A[2], In_2=A[3], In_3=B[2], out=open
  // And and_133 has open pins: In_1=A[3], In_2=B[0], In_3=B[1], In_4=B[2], In_5=C_I, out=open
  // And and_134 has open pins: In_1=A[3], In_2=B[3], out=open
  // And and_135 has open pins: In_1=B[0], In_2=B[1], In_3=B[2], In_4=B[3], In_5=C_I, out=open
  // Or or_1 has open pins: In_1=undriven_51, In_2=undriven_52, In_3=undriven_72, In_4=undriven_77, out=open
  // Or or_2 has open pins: In_1=undriven_45, In_2=undriven_46, In_3=undriven_47, In_4=undriven_48, In_5=undriven_49, In_6=undriven_50, In_7=undriven_71, In_8=undriven_76, In_9=undriven_81, In_10=undriven_85, In_11=undriven_89, In_12=undriven_93, out=open
  // Or or_3 has open pins: In_1=undriven_31, In_2=undriven_32, In_3=undriven_33, In_4=undriven_34, In_5=undriven_35, In_6=undriven_36, In_7=undriven_37, In_8=undriven_38, In_9=undriven_39, In_10=undriven_40, In_11=undriven_41, In_12=undriven_42, In_13=undriven_43, In_14=undriven_44, In_15=undriven_70, In_16=undriven_75, In_17=undriven_80, In_18=undriven_84, In_19=undriven_88, In_20=undriven_92, In_21=undriven_96, In_22=undriven_99, In_23=undriven_102, In_24=undriven_105, In_25=undriven_108, In_26=undriven_111, In_27=undriven_114, In_28=undriven_117, out=open
  // Or or_4 has open pins: In_1=undriven_53, In_2=undriven_54, In_3=undriven_55, In_4=undriven_56, In_5=undriven_57, In_6=undriven_58, In_7=undriven_59, In_8=undriven_60, In_9=undriven_61, In_10=undriven_62, In_11=undriven_63, In_12=undriven_64, In_13=undriven_65, In_14=undriven_66, In_15=undriven_67, In_16=undriven_68, In_17=undriven_73, In_18=undriven_78, In_19=undriven_82, In_20=undriven_86, In_21=undriven_90, In_22=undriven_94, In_23=undriven_97, In_24=undriven_100, In_25=undriven_103, In_26=undriven_106, In_27=undriven_109, In_28=undriven_112, In_29=undriven_115, In_30=undriven_118, In_31=undriven_120, out=open
  // Or or_5 has open pins: In_1=undriven, In_2=undriven_2, In_3=undriven_3, In_4=undriven_4, In_5=undriven_5, In_6=undriven_6, In_7=undriven_7, In_8=undriven_8, In_9=undriven_9, In_10=undriven_10, In_11=undriven_11, In_12=undriven_12, In_13=undriven_13, In_14=undriven_14, In_15=undriven_15, In_16=undriven_16, In_17=undriven_17, In_18=undriven_18, In_19=undriven_19, In_20=undriven_20, In_21=undriven_21, In_22=undriven_22, In_23=undriven_23, In_24=undriven_24, In_25=undriven_25, In_26=undriven_26, In_27=undriven_27, In_28=undriven_28, In_29=undriven_29, In_30=undriven_30, In_31=undriven_69, In_32=undriven_74, In_33=undriven_79, In_34=undriven_83, In_35=undriven_87, In_36=undriven_91, In_37=undriven_95, In_38=undriven_98, In_39=undriven_101, In_40=undriven_104, In_41=undriven_107, In_42=undriven_110, In_43=undriven_113, In_44=undriven_116, In_45=undriven_119, In_46=undriven_121, In_47=undriven_122, In_48=undriven_123, In_49=undriven_124, In_50=undriven_125, In_51=undriven_126, In_52=undriven_127, In_53=undriven_128, In_54=undriven_129, In_55=undriven_130, In_56=undriven_131, In_57=undriven_132, In_58=undriven_133, In_59=undriven_134, In_60=undriven_135, out=open
endmodule

/* Test case:
A B C_I C_O S
loop(a,16)
loop(b,16)
(a) (b) 0 ((a+b)>>4) ((a+b)&0xf)
(a) (b) 1 ((a+b+1)>>4) ((a+b+1)&0xf)
end loop
end loop
*/
