// Digital circuit avoidVarRangeMerge.dig as structural Verilog
module avoidVarRangeMerge (
  input  [7:0] A,
  input  [7:0] B,
  output [3:0] Y
);

  // And and_1 has open pins: In_1=A, In_2=B, out=open
endmodule

/* Test case:
A B Y
0 0 0
0 1 0
1 0 0
1 1 1

0 0 0
0 255 0
255 0 0
255 255 15
*/
