// Digital circuit circular.dig as structural Verilog
module circular (
  input  A,
  input  C,
  output X
);

  wire A_nq, B_nq, C_nq, Q_A, Q_B, undriven, undriven_2, undriven_3;

  // XOr xor_1 has open pins: In_1=A_nq, In_2=A, out=open
  D_FF u_A (.D(undriven), .C(C), .Q(Q_A), .nQ(A_nq));
  // XOr xor_2 has open pins: In_1=B_nq, In_2=Q_A, out=open
  D_FF B (.D(undriven_2), .C(C), .Q(Q_B), .nQ(B_nq));
  // XOr xor_3 has open pins: In_1=C_nq, In_2=Q_B, out=open
  D_FF u_C (.D(undriven_3), .C(C), .Q(X), .nQ(C_nq));
endmodule

/* Test case:
C A X
C 0 1
C 0 1
C 0 1
C 0 0
C 0 1
C 0 1
C 0 1
C 0 0
C 1 1
C 1 1
C 1 0
C 1 0
C 1 1
C 1 1
C 1 0
C 1 0
*/
