// Digital circuit comb.dig as structural Verilog
module comb (
  input  A,
  input  B,
  input  C,
  output X,
  output Y,
  output Z,
  output Aident
);

  wire undriven, undriven_2, undriven_3, undriven_4, undriven_5;

  // Not not_1 has open pins: in=A, out=open
  // Not not_2 has open pins: in=C, out=open
  // Or or_1 has open pins: In_1=A, In_2=C, out=open
  // Or or_2 has open pins: In_1=Z, In_2=C, out=open
  // NOr nor_1 has open pins: In_1=B, In_2=C, out=open
  // Or or_3 has open pins: In_1=B, In_2=undriven_5, out=open
  // And and_1 has open pins: In_1=undriven, In_2=undriven_2, In_3=1'b1, In_4=undriven_3, In_5=Y, out=open
  D_FF d_ff_1 (.D(undriven_4), .C(1'b1), .Q(X));  // open: nQ

  assign Aident = A;
endmodule
