// Digital circuit combBits.dig as structural Verilog
module combBits (
  input  [1:0] A,
  input  [1:0] B,
  input  [1:0] C,
  output [1:0] X,
  output [1:0] Y,
  output [1:0] Z,
  output [1:0] Aident
);

  wire [1:0] undriven, undriven_2, undriven_3, undriven_4, undriven_5;

  // Not not_1 has open pins: in=A, out=open
  // Not not_2 has open pins: in=C, out=open
  // Or or_1 has open pins: In_1=A, In_2=C, out=open
  // Or or_2 has open pins: In_1=Z, In_2=C, out=open
  // NOr nor_1 has open pins: In_1=B, In_2=C, out=open
  // Or or_3 has open pins: In_1=B, In_2=undriven_5, out=open
  // And and_1 has open pins: In_1=undriven, In_2=undriven_2, In_3=2'b01, In_4=undriven_3, In_5=Y, out=open
  D_FF #(.Bits(2)) d_ff_1 (.D(undriven_4), .C(1'b1), .Q(X));  // open: nQ

  assign Aident = A;
endmodule
