// Digital circuit inputInvert2.dig as structural Verilog
module inputInvert2 (
  input  A,
  input  B,
  input  C,
  output Y
);

  wire undriven;

  // And and_1 has open pins: In_1=A, In_2=B, out=open
  // Or or_1 has open pins: In_1=undriven, In_2=C, out=open
endmodule

/* Test case:
A B C Y
0 0 0 1
0 0 1 1
0 1 0 1
0 1 1 1
1 0 0 1
1 0 1 1
1 1 0 0
1 1 1 1
*/
