// Digital circuit naming.dig as structural Verilog
// Simple test circuit
// used to test comments.
module naming (
  input  S0,
  input  S1,
  output S2,
  output S3
);

  wire undriven;

  // NOr nor_1 has open pins: In_1=S0, In_2=S1, out=open
  // XOr xor_1 has open pins: In_1=S0, In_2=undriven, out=open
  // XOr xor_2 has open pins: In_1=undriven, In_2=S1, out=open

  // Notes on the sheet:
  //   S2: first output
  //   S0: First input
  //   This is a far longer text.
  //   S1: Second input
  //   S3: second output
  //   also with a longer text
endmodule

/* Test case:
S0 S1 S2 S3
0  0  1  1
0  1  0  1
1  0  1  0
1  1  1  1
*/
