// Digital circuit naming2.dig as structural Verilog
// Simple test circuit
// used to test comments.
module naming2 (
  input  AA,
  input  S1,
  input  C,
  output S2,
  output S3
);

  wire aa_t;

  // And and_1 has open pins: In_1=AA, In_2=S1, out=open
  D_FF d_ff_1 (.D(aa_t), .C(C), .Q(S2));  // open: nQ
  D_FF d_ff_2 (.D(aa_t), .C(C), .nQ(S3));  // open: Q

  // Notes on the sheet:
  //   S2: first output
  //   AA: First input
  //   This is a far longer text.
  //   S1: Second input
  //   S3: second output
  //   also with a longer text
endmodule

/* Test case:
AA S1 C S2 S3
0  0  C 0  1
0  1  C 0  1
1  0  C 0  1
1  1  C 1  0
*/
