// Digital circuit splitter.dig as structural Verilog
module splitter (
  input  [3:0] A,
  output [1:0] X
);

  // And and_1 has open pins: In_1=A[1:0], In_2=A[3:2], out=open
endmodule

/* Test case:
 A  X
 0  0
 1  1
 2  2
 3  3
 4  0
 5  0
 6  2
 7  2
 8  0
 9  1
10  0
11  1
12  0
13  0
14  0
15  0
*/
