// Digital circuit splitter3.dig as structural Verilog
module splitter3 (
  input  [3:0] A,
  input  [3:0] B,
  output [3:0] S
);

  // And and_1 has open pins: In_1=A[1:0], In_2=B[1:0], out=open
  // Or or_1 has open pins: In_1=A[3:2], In_2=B[3:2], out=open
endmodule

/* Test case:
A B S
loop(a,16)
loop(b,16)
(a) (b) (((a&b)&3) | ((a|b)&12))
end loop
end loop
*/
