// Digital circuit readOutput.dig as structural Verilog
module readOutput (
  input  A,
  input  B,
  output Y,
  output Z
);

  // And and_1 has open pins: In_1=A, In_2=B, out=open
  // Not not_1 has open pins: in=Y, out=open
endmodule
