// Digital circuit splitter3.dig as structural Verilog
module splitter3 (
  input  [3:0] A,
  input  [3:0] B,
  output [7:0] Y,
  output [7:0] Z
);

  // Not not_1 has open pins: in={B, A}, out=open

  assign Y = {B, A};
endmodule
