// Digital circuit xorNegBus.dig as structural Verilog
module xorNegBus (
  input  [1:0] A,
  input  [1:0] B,
  output [1:0] Y
);

  wire [1:0] undriven, undriven_2;

  // And and_1 has open pins: In_1=A, In_2=B, out=open
  // And and_2 has open pins: In_1=A, In_2=B, out=open
  // Or or_1 has open pins: In_1=undriven, In_2=undriven_2, out=open
endmodule
