// Digital circuit 03_fastRuntimeButton.dig as structural Verilog
module _03_fastRuntimeButton (
  input  clk
);

  wire A_out, counter_1_ovf, driver_1_out, undriven;

  Button A (.out(A_out));
  Counter #(.Bits(32)) counter_1 (.en(1'b1), .C(clk), .clr(1'b0), .ovf(counter_1_ovf));  // open: out
  // Or or_1 has open pins: In_1=A_out, In_2=counter_1_ovf, out=open
  assign driver_1_out = undriven ? 1'b1 : 1'bz;  // Driver driver_1
  // also tied to GND on the sheet: driver_1_out

  // Notes on the sheet:
  //   clk: Hz: 500000
  //   Shows a runtime error.
  //   Press the button to create 
  //   the error.
endmodule
