// Digital circuit 08_twoFastClocks.dig as structural Verilog
module _08_twoFastClocks (
  input  clk,
  input  clk_2,
  output out_1
);

  // And and_1 has open pins: In_1=clk, In_2=clk_2, out=open

  // Notes on the sheet:
  //   clk: Hz: 500000
  //   clk_2: Hz: 500000
  //   Must generate an error as 
  //   two fast clocks are used.
endmodule
