// Digital circuit 09_analysis.dig as structural Verilog
module _09_analysis (
  input  A,
  input  B,
  input  C,
  output Y
);

  wire undriven, undriven_2, undriven_3, undriven_4, undriven_5, undriven_6;

  // Not not_1 has open pins: in=A, out=open
  // Not not_2 has open pins: in=C, out=open
  // Or or_1 has open pins: In_1=A, In_2=C, out=open
  // Or or_2 has open pins: In_1=undriven_6, In_2=C, out=open
  // Or or_3 has open pins: In_1=B, In_2=C, out=open
  // Or or_4 has open pins: In_1=B, In_2=undriven_5, out=open
  // And and_1 has open pins: In_1=undriven, In_2=undriven_2, In_3=undriven_3, In_4=undriven_4, out=open
endmodule
