// Digital circuit 10_74xx.dig as structural Verilog
module _10_74xx (
  input  C0,
  input  C2,
  output C1
);

  // And and_1 has open pins: In_1=C0, In_2=C2, out=open

  // Notes on the sheet:
  //   C1: Pin 27, pin 27
  //   C0: Pin 26, pin 26, default 1
  //   C2: Pin 28, pin 28, default 1
endmodule
