// Digital circuit 12_groupEdit.dig as structural Verilog
module _12_groupEdit (
  input  A,
  input  B,
  input  A_2,
  input  B_2,
  output C,
  output C_2
);

  // And and_1 has open pins: In_1=A_2, In_2=B_2, out=open
  // And and_2 has open pins: In_1=A, In_2=B, out=open
endmodule
