// Digital circuit 14_inputInvert.dig as structural Verilog
module _14_inputInvert (
  input  A,
  input  B,
  output Y
);

  // And and_1 has open pins: In_1=A, In_2=open, out=open
endmodule

/* Test case:
A B Y
0 0 0
0 1 0
1 0 1
1 1 0
*/
