// Digital circuit probe.dig as structural Verilog
module probe (
  input  A,
  input  B,
  output Y
);

  wire Probe1_y, Probe2_y, undriven;

  // Not not_1 has open pins: in=B, out=open
  pr1 Probe1 (.A(A), .B(B), .Y(Probe1_y));
  pr1 Probe2 (.A(A), .B(undriven), .Y(Probe2_y));
  // XOr xor_1 has open pins: In_1=Probe1_y, In_2=Probe2_y, out=open
endmodule
