// Digital circuit probeNest.dig as structural Verilog
module probeNest (
  input  A,
  input  B,
  output Y
);

  wire Nest_y, Probe1_y, undriven;

  // Not not_1 has open pins: in=B, out=open
  pr1 Probe1 (.A(A), .B(B), .Y(Probe1_y));
  probe Nest (.A(A), .B(undriven), .Y(Nest_y));
  // XOr xor_1 has open pins: In_1=Probe1_y, In_2=Nest_y, out=open
endmodule
