// Digital circuit selectInnerLongName.dig as structural Verilog
// AndWithLongName
module selectInnerLongName (
  input  A,
  input  B,
  output Out
);

  // And and_1 has open pins: In_1=A, In_2=B, out=open
endmodule
