// Digital circuit shapes.dig as structural Verilog
module shapes (
  input  in_1,
  input  clk,
  output out_2
);

  wire polarityawareled_1_p4, polarityawareled_1_p5, pullup_1_out, relay_1_p2, rotencoder_1_p1;

  // And and_1 is placed but not wired
  Register register_1 ();  // open: D, C, en, Q
  Add add_1 ();  // open: a, b, c_i, s, c_o
  LED led_1 (.in(polarityawareled_1_p4));
  Button button_1 ();  // open: out
  // Probe MW on polarityawareled_1_p5
  ROM rom_1 ();  // open: A, sel, D
  // NAnd nand_1 is placed but not wired
  // PolarityAwareLED polarityawareled_1: pin names not known; wires that end beside it: out_2, in_1, 1'b1, polarityawareled_1_p4, polarityawareled_1_p5, clk, 1'b0, 1'b1
  LightBulb lightbulb_1 ();  // open: A, B
  BusSplitter bussplitter_1 ();  // open: D, OE, D0
  Sub sub_1 ();  // open: a, b, c_i, s, c_o
  // Or or_1 is placed but not wired
  Seven_Seg seven_seg_1 ();  // open: a, b, c, d, e, f, g, dp
  Delay delay_1 ();  // open: in, out
  RAMDualPort ramdualport_1 ();  // open: A, Din, str, C, ld, D
  Mul mul_1 ();  // open: a, b, mul
  // NOr nor_1 is placed but not wired
  Seven_Seg_Hex seven_seg_hex_1 ();  // open: d, dp
  RAMSinglePort ramsingleport_1 ();  // open: A, str, C, ld, D
  SixteenSeg sixteenseg_1 ();  // open: led, dp
  Driver driver_1 ();  // open: in, en, out
  DriverInvSel driverinvsel_1 ();  // open: in, en, out
  Counter counter_1 ();  // open: en, C, clr, out, ovf
  Comparator comparator_1 ();  // open: a, b, gt, eq, lt
  // XOr xor_1 is placed but not wired
  Driver driver_2 ();  // open: in, en, out
  Switch switch_1 ();  // open: A, B
  GraphicCard graphiccard_1 ();  // open: A, str, C, ld, B, D
  Neg neg_1 ();  // open: in, out
  // XNOr xnor_1 is placed but not wired
  Reset reset_1 ();  // open: out
  Break break_1 ();  // open: brk
  DriverInvSel driverinvsel_2 ();  // open: in, en, out
  Terminal terminal_1 ();  // open: D, C, en
  Keyboard keyboard_1 ();  // open: C, en, D, av
  RAMSinglePortSel ramsingleportsel_1 ();  // open: A, CS, WE, OE, D
  BitCount bitcount_1 ();  // open: in, out
  // Not not_1 is placed but not wired
  // RotEncoder rotencoder_1: pin names not known; wires that end beside it: rotencoder_1_p1
  LookUpTable lookuptable_1 ();  // open: in0, in1, out
  MS_JK_DIL ms_jk_dil_1 ();  // open: J, C, Q, nQ, K
  MS_JK_DIL ms_jk_dil_2 ();  // open: J, C, Q, nQ, K
  Multiplexer multiplexer_1 ();  // open: sel, in_0, in_1, out
  RS_FF rs_ff_1 ();  // open: S, C, R, Q, nQ
  RS_FF_AS rs_ff_as_1 ();  // open: S, R, Q, nQ
  T_FF t_ff_1 ();  // open: T, C, Q, nQ
  Demultiplexer demultiplexer_1 ();  // open: sel, in, out_0, out_1
  JK_FF jk_ff_1 ();  // open: J, C, K, Q, nQ
  D_FF_AS d_ff_as_1 ();  // open: Set, D, C, Clr, Q, nQ
  DiodeForward diodeforward_1 ();  // open: in, out
  DiodeBackward diodebackward_1 ();  // open: in, out
  TransGate transgate_1 ();  // open: A, nA, out1, out2
  Decoder decoder_1 ();  // open: sel, out_0, out_1
  PullUp pullup_1 (.out(pullup_1_out));
  // Relay relay_1: pin names not known; wires that end beside it: pullup_1_out, relay_1_p2
  BitSelector bitselector_1 ();  // open: in, sel, out
  D_FF d_ff_1 ();  // open: D, C, Q, nQ
  JK_FF_AS jk_ff_as_1 ();  // open: Set, J, C, K, Clr, Q, nQ
  FGNFET fgnfet_1 ();  // open: G, D, S
  PullDown pulldown_1 (.out(relay_1_p2));
  NFET nfet_1 ();  // open: G, D, S
  FGPFET fgpfet_1 ();  // open: G, S, D
  PFET pfet_1 ();  // open: G, S, D

  // Notes on the sheet:
  //   Logisch
  //   IO
  //   Leitungen
  //   Speicher
  //   Arithmetik
  //   Multiplexer
  //   Flipflops
  //   PLD
  //   Test
endmodule
