// Digital circuit 74181-74182.dig as structural Verilog
module _74181_74182 (
  input  M,
  input  [3:0] S,
  input  [15:0] A,
  input  [15:0] B,
  input  C,
  output [16:0] F
);

  wire _74181_1_p1, _74181_1_p17, _74181_1_p18, _74181_2_p2, _74181_2_p17, _74181_2_p18, _74181_3_p2,
       _74181_3_p17, _74181_3_p18, _74181_4_p2, _74181_4_p18, _74181_4_p19, _74181_4_p24;

  // Not not_1 has open pins: in=C, out=open
  // _74181 _74181_1: pin names not known; wires that end beside it: _74181_1_p1, _74181_1_p1, A[0], A[1], A[2], A[3], B[0], B[1], B[2], B[3], S[0], S[1], S[2], S[3], M, 1'b1, _74181_1_p17, _74181_1_p18, F[0], F[1], F[2], F[3]
  // _74181 _74181_2: pin names not known; wires that end beside it: 1'b0, _74181_2_p2, A[4], A[5], A[6], A[7], B[4], B[5], B[6], B[7], S[0], S[1], S[2], S[3], M, 1'b1, _74181_2_p17, _74181_2_p18, F[4], F[5], F[6], F[7]
  // _74181 _74181_3: pin names not known; wires that end beside it: 1'b0, _74181_3_p2, A[8], A[9], A[10], A[11], B[8], B[9], B[10], B[11], S[0], S[1], S[2], S[3], M, 1'b1, _74181_3_p17, _74181_3_p18, F[8], F[9], F[10], F[11]
  // _74181 _74181_4: pin names not known; wires that end beside it: 1'b0, _74181_4_p2, A[12], A[13], A[14], A[15], B[12], B[13], B[14], B[15], S[0], S[1], S[2], S[3], M, 1'b1, 1'b0, _74181_4_p18, _74181_4_p19, F[12], F[13], F[14], F[15], _74181_4_p24, F[16]
  _74182 _74182_1 (
    .C_n(_74181_1_p1), .nG0(_74181_1_p17), .nP0(_74181_1_p18), .nG1(_74181_2_p17), .nP1(_74181_2_p18),
    .nG2(_74181_3_p17), .nP2(_74181_3_p18), .nG3(_74181_4_p18), .nP3(_74181_4_p19), .VCC(1'b1), .GND(1'b0),
    .C_n_plus_z(_74181_4_p2), .C_n_plus_y(_74181_3_p2), .C_n_plus_x(_74181_2_p2));  // open: nP, nG
  // Not not_2 has open pins: in=_74181_4_p24, out=open

  // Notes on the sheet:
  //   S: default 9
  //   16-Bit adder with four 74181 alu's
  //   and a 74182 carry generator
endmodule

/* Test case:
S M C A B F

9 0 0 0x0000 0x0000 0x00000
9 0 0 0x000f 0x0001 0x00010
9 0 0 0x00f0 0x0010 0x00100
9 0 0 0x00ff 0x0001 0x00100
9 0 0 0x0f00 0x0100 0x01000
9 0 0 0x0f0f 0x0101 0x01010
9 0 0 0x0ff0 0x0010 0x01000
9 0 0 0x0fff 0x0001 0x01000
9 0 0 0xf000 0x1000 0x10000
9 0 0 0xf00f 0x1001 0x10010
9 0 0 0xf0f0 0x1010 0x10100
9 0 0 0xf0ff 0x1011 0x10110
9 0 0 0xff00 0x1100 0x11000
9 0 0 0xff0f 0x1101 0x11010
9 0 0 0xfff0 0x1110 0x11100
9 0 0 0xffff 0x1111 0x11110

9 0 1 0x0000 0x0000 0x00001
9 0 1 0x000f 0x0001 0x00011
9 0 1 0x00f0 0x0010 0x00101
9 0 1 0x00ff 0x0001 0x00101
9 0 1 0x0f00 0x0100 0x01001
9 0 1 0x0f0f 0x0101 0x01011
9 0 1 0x0ff0 0x0010 0x01001
9 0 1 0x0fff 0x0001 0x01001
9 0 1 0xf000 0x1000 0x10001
9 0 1 0xf00f 0x1001 0x10011
9 0 1 0xf0f0 0x1010 0x10101
9 0 1 0xf0ff 0x1011 0x10111
9 0 1 0xff00 0x1100 0x11001
9 0 1 0xff0f 0x1101 0x11011
9 0 1 0xfff0 0x1110 0x11101
9 0 1 0xffff 0x1111 0x11111



loop (n,1<<12)
  let a=random(1<<16);
  let b=random(1<<16);
  9 0 0 (a) (b) (a+b)
end loop

loop (n,1<<12)
  let a=random(1<<16);
  let b=random(1<<16);
  9 0 1 (a) (b) (a+b+1)
end loop
*/
