// Digital circuit TwoTestCases.dig as structural Verilog
module TwoTestCases (
  input  C
);

  wire G_q, R_q, undriven, undriven_2, Y_q;

  // And and_1 has open pins: In_1=Y_q, In_2=R_q, out=open
  // Not not_1 has open pins: in=undriven, out=open
  JK_FF R (.J(Y_q), .C(C), .K(Y_q), .Q(R_q));  // open: nQ
  JK_FF Y (.J(1'b1), .C(C), .K(1'b1), .Q(Y_q));  // open: nQ
  JK_FF G (.J(undriven), .C(C), .K(undriven_2), .Q(G_q));  // open: nQ
  LED R_2 (.in(R_q));
  LED Y_2 (.in(Y_q));
  LED G_2 (.in(G_q));
endmodule

/* Test case Test 1:
C R Y G
0 0 0 0
C 0 1 0
C 1 0 0
C 1 1 0
C 0 0 1
C 0 1 0
C 1 0 0
C 1 1 0
C 0 0 1
C 0 1 0
*/

/* Test case Test 2:
C R Y G
0 0 0 0
C 0 1 0
C 1 0 0
C 1 1 0
C 0 0 1
C 0 1 0
C 1 0 0
C 1 1 0
C 0 0 1
C 0 1 0
*/
