// Digital circuit FullSub.dig as structural Verilog
// FullSub
module FullSub (
  input  A_i,
  input  B_i,
  input  BO_i_1,
  output BO_i,
  output S_i
);

  wire halfadder_1_c, halfadder_1_s, halfsub_1_bo;

  HalfAdder halfadder_1 (.A(B_i), .B(BO_i_1), .S(halfadder_1_s), .C(halfadder_1_c));
  HalfSub halfsub_1 (.A(A_i), .B(halfadder_1_s), .S(S_i), .BO(halfsub_1_bo));
  // Or or_1 has open pins: In_1=halfsub_1_bo, In_2=halfadder_1_c, out=open
endmodule

/* Test case:
A_i B_i BO_i-1  BO_i S_i
 0   0   0        0   0
 0   0   1        1   1
 0   1   0        1   1
 0   1   1        1   0
 1   0   0        0   1
 1   0   1        0   0
 1   1   0        0   0
 1   1   1        1   1
*/
