// Digital circuit HalfSub.dig as structural Verilog
module HalfSub (
  input  A,
  input  B,
  output S,
  output BO
);

  wire undriven;

  // Not not_1 has open pins: in=A, out=open
  // XOr xor_1 has open pins: In_1=A, In_2=B, out=open
  // And and_1 has open pins: In_1=undriven, In_2=B, out=open
endmodule

/* Test case:
A B BO S
0 0 0  0
0 1 1  1
1 0 0  1
1 1 0  0
*/
