// Digital circuit fullAdder.dig as structural Verilog
module fullAdder (
  input  A,
  input  B,
  input  Ci,
  output Co,
  output S
);

  wire halfadder_1_c, halfadder_1_s, halfadder_2_c;

  halfAdder halfadder_1 (.A(A), .B(B), .S(halfadder_1_s), .C(halfadder_1_c));
  halfAdder halfadder_2 (.A(Ci), .B(halfadder_1_s), .S(S), .C(halfadder_2_c));
  // Or or_1 has open pins: In_1=halfadder_2_c, In_2=halfadder_1_c, out=open
endmodule

/* Test case:
 A  B  Ci    Co  S
 0  0  0     0   0
 0  0  1     0   1
 0  1  0     0   1
 0  1  1     1   0
 1  0  0     0   1
 1  0  1     1   0
 1  1  0     1   0
 1  1  1     1   1
*/
