// Digital circuit halfAdder.dig as structural Verilog
module halfAdder (
  input  A,
  input  B,
  output S,
  output C
);

  // XOr xor_1 has open pins: In_1=A, In_2=B, out=open
  // And and_1 has open pins: In_1=A, In_2=B, out=open
endmodule
