// Digital circuit d-ff.dig as structural Verilog
module d_ff (
  input  D,
  input  C,
  output nQ,
  output Q
);

  wire delay_1_out, nfet_1_s, nfet_4_s, not_1_out, pfet_1_d, pfet_4_d;

  not not_1 (not_1_out, C);
  Delay delay_1 (.in(C), .out(delay_1_out));
  PFET pfet_1 (.G(not_1_out), .S(1'b1), .D(pfet_1_d));
  PFET pfet_2 (.G(D), .S(pfet_1_d), .D(nQ));
  NFET nfet_1 (.G(D), .D(nQ), .S(nfet_1_s));
  NFET nfet_2 (.G(delay_1_out), .D(nfet_1_s), .S(1'b0));
  PFET pfet_3 (.G(nQ), .S(1'b1), .D(Q));
  NFET nfet_3 (.G(nQ), .D(Q), .S(1'b0));
  PFET pfet_4 (.G(delay_1_out), .S(1'b1), .D(pfet_4_d));
  PFET pfet_5 (.G(Q), .S(pfet_4_d), .D(nQ));
  NFET nfet_4 (.G(Q), .D(nQ), .S(nfet_4_s));
  NFET nfet_5 (.G(not_1_out), .D(nfet_4_s), .S(1'b0));
endmodule

/* Test case:
C D Q ~Q
1 0 0 1
0 0 0 1
0 1 0 1
0 0 0 1
1 1 1 0
0 1 1 0
0 0 1 0
1 0 0 1
0 0 0 1
*/
