// Digital circuit simpleTest1.dig as structural Verilog
module simpleTest1 (
  input  _2A,
  input  _2B,
  input  _1A,
  input  _1B,
  output _2Y,
  output _1Y
);

  // And and_1 has open pins: In_1=_1A, In_2=_1B, out=open
  // XOr xor_1 has open pins: In_1=_2A, In_2=_2B, out=open
endmodule

/* Test case AND:
1A 1B 1Y
0  0  0
0  1  1
1  0  0
1  1  0
 
*/

/* Test case XOR:
2A 2B 2Y
0  0  1
0  1  0
1  0  0
1  1  1
 
*/
