// Digital circuit inner.dig as structural Verilog
module inner (
  input  A,
  input  T,
  input  B,
  output Y
);

  // XOr xor_1 has open pins: In_1=A, In_2=B, out=open
endmodule

/* Test case:
A B T Y
0 0 0 0
0 1 0 1
1 0 0 1
1 1 0 0
0 0 1 0
0 1 1 1
1 0 1 1
1 1 1 0
*/
