// Digital circuit Adder.dig as structural Verilog
module Adder (
  input  A,
  input  B,
  input  c_i,
  output S,
  output c_o
);

  wire undriven, undriven_2, undriven_3;

  // XOr xor_1 has open pins: In_1=A, In_2=B, out=open
  // And and_1 has open pins: In_1=A, In_2=B, out=open
  // XOr xor_2 has open pins: In_1=c_i, In_2=undriven_2, out=open
  // And and_2 has open pins: In_1=c_i, In_2=undriven_2, out=open
  // Or or_1 has open pins: In_1=undriven_3, In_2=undriven, out=open

  // Notes on the sheet:
  //   c_i: carry in
  //   S: sum
  //   c_o: carry out
endmodule

/* Test case:
A B c_i c_o S
loop (a,2)
loop (b,2)
loop (c,2)
(a) (b) (c) bits(2,a+b+c)
end loop
end loop
end loop
*/
