// Digital circuit transGate.dig as structural Verilog
module transGate (
  input  A,
  input  [7:0] B,
  output [7:0] Y
);

  wire not_1_out;

  not not_1 (not_1_out, A);
  TransGate #(.Bits(8)) transgate_1 (.A(A), .nA(not_1_out), .out1(B), .out2(Y));
endmodule

/* Test case:
A B Y
0 0 z 
0 7 z 
1 0 0 
1 7 7 
*/
