// Digital circuit crossTest.dig as structural Verilog
module crossTest (
  input  A,
  input  B,
  output Y
);

  wire cross_1_p3;

  // cross cross_1: pin names not known; wires that end beside it: A, B, cross_1_p3
  and and_1 (Y, cross_1_p3, B);
endmodule

/* Test case:
A B Y
0 z 0
1 z 1
*/
