// Digital circuit crossTestError.dig as structural Verilog
module crossTestError (
  input  A,
  input  B,
  output Y
);

  wire crosse_1_p3;

  // crossE crosse_1: pin names not known; wires that end beside it: A, B, crosse_1_p3
  and and_1 (Y, crosse_1_p3, B);
endmodule

/* Test case:
A B Y
0 z 0
1 z 1
*/
