// Digital circuit doubleTest.dig as structural Verilog
module doubleTest (
  input  A,
  input  B,
  output Y1,
  output Y2
);

  wire double_1_p3, double_1_p4, double_1_p5, double_1_p6;

  // double double_1: pin names not known; wires that end beside it: A, B, double_1_p3, double_1_p4, double_1_p5, double_1_p6, Y1, Y2
  // XOr xor_1 has open pins: In_1=double_1_p3, In_2=double_1_p4, out=open
  // XNOr xnor_1 has open pins: In_1=double_1_p5, In_2=double_1_p6, out=open
endmodule

/* Test case:
A B Y1 Y2
0 0 0  1
0 1 1  0
1 0 1  0
1 1 0  1
*/
