// Digital circuit transtest2.dig as structural Verilog
module transtest2 (
  input  A,
  input  B,
  output Y
);

  wire trans2_1_p3, trans2_1_p4;

  // trans2 trans2_1: pin names not known; wires that end beside it: A, B, trans2_1_p3, trans2_1_p4, Y
  // XOr xor_1 has open pins: In_1=trans2_1_p3, In_2=trans2_1_p4, out=open
endmodule

/* Test case:
A B Y
0 0 0
0 1 1
1 0 1
1 1 0
*/
