// Digital circuit transtestLabel.dig as structural Verilog
module transtestLabel (
  input  A,
  input  B,
  output Y
);

  wire _1, _2;

  // trans trans_1: pin names not known; wires that end beside it: A, B, _1, _2, Y
  // XOr xor_1 has open pins: In_1=_1, In_2=_2, out=open

  // Other names for the same wires on the sheet: _3 = A; _4 = B
endmodule

/* Test case:
A B Y
0 0 0
0 1 1
1 0 1
1 1 0
*/
