// Digital circuit multiPort.dig as structural Verilog
module multiPort (
  input  A,
  output Y,
  output Z
);

  // Not not_1 has open pins: in=A, out=open

  assign Z = Y;
endmodule

/* Test case:
A Y Z
0 1 1
1 0 0
*/
