// Digital circuit naming-inc.dig as structural Verilog
module naming_inc (
  input  A,
  input  B,
  output Y
);

  // XOr xor_1 has open pins: In_1=A, In_2=B, out=open
endmodule

/* Test case:
A B Y
0 0 0
0 1 1
1 0 1
1 1 0
*/
