// Digital circuit simpleANDNAND.dig as structural Verilog
module simpleANDNAND (
  input  A,
  input  B,
  input  C,
  output Y
);

  wire undriven;

  // And and_1 has open pins: In_1=A, In_2=B, out=open
  // NAnd nand_1 has open pins: In_1=undriven, In_2=C, out=open
endmodule

/* Test case:
A B C Y
0 0 0 1
0 0 1 1
0 1 0 1
0 1 1 1
1 0 0 1
1 0 1 1
1 1 0 1
1 1 1 0
*/
