// Digital circuit xorMulitInput.dig as structural Verilog
module xorMulitInput (
  input  A,
  input  B,
  input  C,
  output Y1,
  output Y2
);

  wire undriven;

  // XOr xor_1 has open pins: In_1=A, In_2=B, out=open
  // XOr xor_2 has open pins: In_1=undriven, In_2=C, out=open
  // XOr xor_3 has open pins: In_1=C, In_2=B, In_3=A, out=open
endmodule

/* Test case:
A  B  C Y1 Y2
0  0  0 0  0
0  0  1 1  1
0  1  0 1  1
0  1  1 0  0
1  0  0 1  1
1  0  1 0  0
1  1  0 0  0
1  1  1 1  1
 
*/
